// Logisim project cpu24.circ as structural Verilog: 39 circuits, main circuit ◇单周期MIPS
module \单周期MIPS  (
  input  IR1,
  input  IR2,
  input  IR3,
  output RegWrite,
  output MemWrite,
  output [31:0] PC,
  output [31:0] IR,
  output [31:0] RDin,
  output [31:0] MDin,
  output [31:0] LedData
);

  wire Alu_SRC, and_1_out, and_2_out, and_3_out, and_5_out, Beq, BLTZ, Bne, Branch, CLK, clock_2_out,
       comparator_1_eq, comparator_1_lt, comparator_2_lt, comparator_3_eq, d_ff_1_q, Equal, Go, halt, IR1_t,
       IR2_t, IR3_t, IRA, IRB, IRC, JAL, JMP, JR, LB, Ledin, MemToReg, nand_1_out, not_1_out, not_2_out,
       not_3_out, not_4_out, SignedExt, SRAV, SysCall, W1, W2, W3, \单周期硬布线控制器_1_regdst ;
  wire [3:0] AluOP;
  wire [4:0] multiplexer_4_out, multiplexer_5_out, multiplexer_6_out, multiplexer_7_out, multiplexer_10_out;
  wire [7:0] multiplexer_12_out;
  wire [12:0] CNT_num;
  wire [15:0] \总周期数 ;
  wire [31:0] adder_1_out, adder_2_out, bit_extender_1_out, bit_extender_2_out, bit_extender_3_out,
       multiplexer_1_out, multiplexer_2_out, multiplexer_3_out, multiplexer_8_out, multiplexer_9_out,
       multiplexer_13_out, multiplexer_14_out, ram_1_data, result, rs, shifter_1_out;

  Clock #(.highDuration(1), .lowDuration(1)) clock_1 ();  // open: out
  Button _1 (.out(IRA));
  Button _2 (.out(IRB));
  Button _3 (.out(IRC));
  Button \u_继续运行  (.out(Go));
  LED #(.active("true")) led_1 (.in(W1));
  LED #(.active("true")) led_2 (.in(W2));
  LED #(.active("true")) led_3 (.in(W3));
  D_Flip_Flop #(.trigger("high"), .Pre_Clr_Positions("LEGACY"), .NegatePresetClear("false"), .enable("true"), .NewFFLayout("false")) d_ff_1 (.Q(d_ff_1_q));  // open: clk, D, Qn, preset, en, reset
  // Probe on 13'h58
  Multiplexer #(.select(1), .width(32), .disabled("Z"), .enable("false")) multiplexer_1 (
    .in0(adder_1_out), .in1(adder_2_out), .out(multiplexer_1_out), .sel(Branch));
  Multiplexer #(.select(1), .width(32), .disabled("Z"), .enable("false")) multiplexer_2 (
    .in0(multiplexer_1_out), .in1({4'b0000, IR[25:0], 2'b00}), .out(multiplexer_2_out), .sel(JMP));
  Hex_Digit_Display hex_digit_display_1 (.value(LedData[31:28]));  // open: dp
  Comparator #(.width(13), .mode("twosComplement")) comparator_1 (
    .a(CNT_num), .b(13'h58), .eq(comparator_1_eq), .lt(comparator_1_lt));  // open: gt
  Clock #(.highDuration(1), .lowDuration(1)) clock_2 (.out(clock_2_out));
  Multiplexer #(.select(1), .width(32), .disabled("Z"), .enable("false")) multiplexer_3 (
    .in0(multiplexer_2_out), .in1(rs), .out(multiplexer_3_out), .sel(JR));
  not not_1 (not_1_out, halt);
  Hex_Digit_Display hex_digit_display_2 (.value(LedData[23:20]));  // open: dp
  Hex_Digit_Display hex_digit_display_3 (.value(LedData[27:24]));  // open: dp
  Counter #(.width(13), .max('h1fff), .ongoal("stay"), .trigger("rising"), .behavior("old")) counter_1 (
    .count(comparator_1_lt), .Q(CNT_num), .clk(clock_2_out));  // open: load, D, carry, clr, preset
  Register #(.width(32), .trigger("rising"), .Select("low")) u_PC (
    .D(multiplexer_3_out), .en(not_1_out), .Q(PC), .clk(CLK));  // open: clr
  Hex_Digit_Display hex_digit_display_4 (.value(LedData[19:16]));  // open: dp
  Hex_Digit_Display hex_digit_display_5 (.value(LedData[15:12]));  // open: dp
  nand nand_1 (nand_1_out, d_ff_1_q, comparator_1_eq);
  // Probe on PC
  Adder #(.width(32)) adder_1 (.a(PC), .b(32'h4), .out(adder_1_out));  // open: cin, cout
  Hex_Digit_Display hex_digit_display_6 (.value(LedData[11:8]));  // open: dp
  Hex_Digit_Display hex_digit_display_7 (.value(LedData[7:4]));  // open: dp
  // Probe on \总周期数 
  assign CLK = nand_1_out ? clock_2_out : 1'bz;  // Controlled_Buffer controlled_buffer_1
  Pull_Resistor #(.pull(1)) pull_resistor_1 (.node(CLK));
  // Mips_Probe mips_probe_1: pin names not known; wires that end beside it: IR, IR[20:16]
  ROM #(.addrWidth(10), .dataWidth(32), .Select("high")) rom_1 (.addr(PC[11:2]), .data(IR));
  Hex_Digit_Display hex_digit_display_8 (.value(LedData[3:0]));  // open: dp
  \单周期硬布线控制器  \u_单周期硬布线控制器_1  (
    .Func(IR[5:0]), .OP(IR[31:26]), .ALU_OP(AluOP), .MemToReg(MemToReg), .MemWrite(MemWrite),
    .ALU_SRC(Alu_SRC), .RegWrite(RegWrite), .SysCALL(SysCall), .SignedExt(SignedExt),
    .RegDst(\单周期硬布线控制器_1_regdst ), .JR(JR), .JMP(JMP), .Beq(Beq), .JAL(JAL), .Bne(Bne), .SRAV(SRAV), .LB(LB),
    .BLTZ(BLTZ));
  Multiplexer #(.select(1), .width(5), .disabled("Z"), .enable("false")) multiplexer_4 (
    .in0(IR[25:21]), .in1(5'b00010), .out(multiplexer_4_out), .sel(SysCall));
  Multiplexer #(.select(1), .width(5), .disabled("Z"), .enable("false")) multiplexer_5 (
    .in0(IR[20:16]), .in1(5'b00100), .out(multiplexer_5_out), .sel(SysCall));
  Multiplexer #(.select(1), .width(5), .disabled("Z"), .enable("false")) multiplexer_6 (
    .in0(IR[20:16]), .in1(IR[15:11]), .out(multiplexer_6_out), .sel(\单周期硬布线控制器_1_regdst ));
  or or_1 (IR1_t, IR1, IRA);
  Multiplexer #(.select(1), .width(5), .disabled("Z"), .enable("false")) multiplexer_7 (
    .in0(multiplexer_6_out), .in1({5{1'b1}}), .out(multiplexer_7_out), .sel(JAL));
  assign bit_extender_1_out = {{16{1'b0}}, IR[15:0]};  // Bit_Extender bit_extender_1
  assign bit_extender_2_out = {{16{IR[15]}}, IR[15:0]};  // Bit_Extender bit_extender_2
  or or_2 (IR2_t, IR2, IRB);
  Multiplexer #(.select(1), .width(32), .disabled("Z"), .enable("false")) multiplexer_8 (
    .in0(bit_extender_1_out), .in1(bit_extender_2_out), .out(multiplexer_8_out), .sel(SignedExt));
  Shifter #(.width(32), .shift("ll")) shifter_1 (.in(bit_extender_2_out), .\dist (5'b00010), .out(shifter_1_out));
  MIPS_Regifile mips_regifile_1 (
    .Din(RDin), .Clk(CLK), .R1(rs), .R2(MDin), .WE(RegWrite), .W_num(multiplexer_7_out),
    .R1_num(multiplexer_4_out), .R2_num(multiplexer_5_out));
  Adder #(.width(32)) adder_2 (.a(shifter_1_out), .b(adder_1_out), .out(adder_2_out));  // open: cin, cout
  or or_3 (IR3_t, IR3, IRC);
  Multiplexer #(.select(1), .width(32), .disabled("Z"), .enable("false")) multiplexer_9 (
    .in0(MDin), .in1(multiplexer_8_out), .out(multiplexer_9_out), .sel(Alu_SRC));
  Comparator #(.width(32), .mode("twosComplement")) comparator_2 (
    .a(rs), .b({32{1'b0}}), .lt(comparator_2_lt));  // open: gt, eq
  Multiplexer #(.select(1), .width(5), .disabled("Z"), .enable("false")) multiplexer_10 (
    .in0(IR[10:6]), .in1(rs[4:0]), .out(multiplexer_10_out), .sel(SRAV));
  MIPS_ALU mips_alu_1 (
    .X(rs), .Y(multiplexer_9_out), .AluOP(AluOP), .Equal(Equal), .Result(result), .shamt(multiplexer_10_out));  // open: Result_2
  Multiplexer #(.select(1), .width(32), .disabled("Z"), .enable("false")) multiplexer_11 (
    .in0(multiplexer_14_out), .in1(bit_extender_3_out), .out(RDin), .sel(LB));
  and and_1 (and_1_out, BLTZ, comparator_2_lt);
  and and_2 (and_2_out, Equal, Beq);
  not not_2 (not_2_out, Equal);
  and and_3 (and_3_out, not_2_out, Bne);
  Comparator #(.width(32), .mode("twosComplement")) comparator_3 (
    .a(32'h22), .b(rs), .eq(comparator_3_eq));  // open: gt, lt
  or or_4 (Branch, and_1_out, and_2_out, and_3_out);
  not not_3 (not_3_out, comparator_3_eq);
  Register #(.width(32), .trigger("rising"), .Select("low")) register_1 (
    .D(MDin), .en(Ledin), .Q(LedData), .clk(CLK));  // open: clr
  assign bit_extender_3_out = {{24{multiplexer_12_out[7]}}, multiplexer_12_out};  // Bit_Extender bit_extender_3
  and and_4 (Ledin, SysCall, comparator_3_eq);
  Register #(.width(1), .trigger("rising"), .Select("low")) register_2 (
    .D(SysCall), .en(and_5_out), .Q(halt), .clk(CLK), .clr(Go));
  and and_5 (and_5_out, SysCall, not_3_out);
  RAM #(.addrWidth(10), .dataWidth(32), .bus("separate"), .Select("high")) ram_1 (
    .addr(result[11:2]), .din(MDin), .data(ram_1_data), .str(MemWrite), .clk(CLK), .ld(1'b1));  // open: sel, clr
  Multiplexer #(.select(2), .width(8), .disabled("Z"), .enable("false")) multiplexer_12 (
    .in0(multiplexer_14_out[7:0]), .in1(multiplexer_14_out[15:8]), .in2(multiplexer_14_out[23:16]),
    .in3(multiplexer_14_out[31:24]), .out(multiplexer_12_out), .sel(result[1:0]));
  Multiplexer #(.select(1), .width(32), .disabled("Z"), .enable("false")) multiplexer_13 (
    .in0(result), .in1(ram_1_data), .out(multiplexer_13_out), .sel(MemToReg));
  Multiplexer #(.select(1), .width(32), .disabled("Z"), .enable("false")) multiplexer_14 (
    .in0(multiplexer_13_out), .in1(adder_1_out), .out(multiplexer_14_out), .sel(JAL));
  not not_4 (not_4_out, halt);
  Counter #(.width(16), .max('hffff), .ongoal("stay"), .trigger("rising"), .behavior("old")) counter_2 (
    .count(not_4_out), .Q(\总周期数 ), .clk(CLK));  // open: load, D, carry, clr, preset

  // Notes on the sheet:
  //   中断源
  //   中断等待指示
  //   总复位信号应将除ROM以外所有存储组件全部清零
  //   控制位
  //   暂停节拍，不能为0
  //   用这个时钟源需要去掉电路中的其他时钟源
  //   戳工具置1进入计数暂停模式，ctrl+k时钟自动运行到对应节拍暂停
  //   ctrl+k关闭时钟连续运行，将控制位置零，进入单步调试模式调试
  //   数码管输出
  //   数码管输出应该用寄存器锁存，否则显示数据只能一闪而过
  //   可计数暂停的时钟源
  //   指令存储器
  //   contents of rom_1 (hex, n*v repeats v):
  //   20110001 8000c05 20110001 20120002 20130003 8000c09 20110001 20120002 20130003 8000c0d 20110001
  //   20120002 20130003 8000c11 20110001 20120002 20130003 c000cf9 20100001 20110001 118fc0 112020
  //   20020022 c 118882 12200001 8000c15 112020 20020022 c 20110001 118880 112020 20020022 c 12200001
  //   8000c1f 20110001 118fc0 112020 20020022 c 1188c3 112020 20020022 c 118903 112020 20020022 c 118903
  //   112020 20020022 c 118903 112020 20020022 c 118903 112020 20020022 c 118903 112020 20020022 c 118903
  //   112020 20020022 c 118903 112020 20020022 c 20100001 109fc0 139fc3 8021 2012000c 24160003 26100001
  //   3210000f 20080008 20090001 139900 2709825 132020 20020022 c 1094022 1500fff9 22100001 2018000f
  //   2188024 108700 20080008 20090001 139902 2709825 132021 20020022 c 1094022 1500fff9 108702 2c9b022
  //   12c00001 8000c50 4020 1084027 84400 3508ffff 82021 20020022 c 2010ffff 20110000 ae300000 22100001
  //   22310004 ae300000 22100001 22310004 ae300000 22100001 22310004 ae300000 22100001 22310004 ae300000
  //   22100001 22310004 ae300000 22100001 22310004 ae300000 22100001 22310004 ae300000 22100001 22310004
  //   ae300000 22100001 22310004 ae300000 22100001 22310004 ae300000 22100001 22310004 ae300000 22100001
  //   22310004 ae300000 22100001 22310004 ae300000 22100001 22310004 ae300000 22100001 22310004 ae300000
  //   22100001 22310004 22100001 8020 2011003c 8e130000 8e340000 274402a 11000002 ae330000 ae140000
  //   2231fffc 1611fff8 102020 20020022 c 22100004 2011003c 1611fff2 20020032 c 20080001 20090003 20110876
  //   118d00 112020 20020022 c 200b0008 1118807 1318807 112020 20020022 c 216bffff 1560fff9 2002000a c
  //   2008ffff 20117777 112020 20020022 c 200b0010 2288826 112020 20020022 c 216bffff 1560fffa 2002000a c
  //   20090000 200b0010 34118483 20120404 118c00 129400 36318281 22520404 ad310000 2328820 21290004
  //   216bffff 1560fffb 200b0020 20090000 81310000 112020 20020022 c 21290001 216bffff 1560fff9 2002000a c
  //   2011fff1 112020 20020022 c 22310001 620fffb 2002000a c 2002000a c 20100000 22100001 102020 20020022
  //   c 22100002 102020 20020022 c 22100003 102020 20020022 c 22100004 102020 20020022 c 22100005 102020
  //   20020022 c 22100006 102020 20020022 c 22100007 102020 20020022 c 22100008 102020 20020022 20020022 c
  //   3e00008
  //   指令字
  //   rs
  //   rt
  //   rd
  //   OP
  //   Func
  //   RegDst
  //   为方便自动评测，需要输出PC，IR，寄存器堆写如数据RDin
  //   RAM写使能MemWrite、RAM写入数据MDin等信号
endmodule

// 单周期硬布线控制器
module \单周期硬布线控制器  (
  input  [5:0] OP,
  input  [5:0] Func,
  output [3:0] ALU_OP,
  output MemToReg,
  output MemWrite,
  output ALU_SRC,
  output RegWrite,
  output SysCALL,
  output SignedExt,
  output RegDst,
  output Beq,
  output Bne,
  output JR,
  output JMP,
  output JAL,
  output SRAV,
  output LB,
  output BLTZ
);

  \运算控制器自动生成  \u_运算控制器自动生成_1  (
    .OP0(OP[0]), .OP1(OP[1]), .OP2(OP[2]), .OP3(OP[3]), .OP4(OP[4]), .OP5(OP[5]), .F0(Func[0]), .F1(Func[1]),
    .F2(Func[2]), .F3(Func[3]), .F4(Func[4]), .F5(Func[5]), .S0(ALU_OP[0]), .S1(ALU_OP[1]), .S2(ALU_OP[2]),
    .S3(ALU_OP[3]));
  \控制信号自动生成  \u_控制信号自动生成_1  (
    .OP0(OP[0]), .OP1(OP[1]), .OP2(OP[2]), .MemToReg(MemToReg), .OP3(OP[3]), .OP4(OP[4]), .OP5(OP[5]),
    .MemWrite(MemWrite), .F0(Func[0]), .F1(Func[1]), .F2(Func[2]), .F3(Func[3]), .F4(Func[4]), .F5(Func[5]),
    .ALU_SRC(ALU_SRC), .RegWrite(RegWrite), .SysCALL(SysCALL), .SignedExt(SignedExt), .RegDst(RegDst),
    .BEQ(Beq), .BNE(Bne), .JR(JR), .JUMP(JMP), .JAL(JAL), .SRAV(SRAV), .LB(LB), .BLTZ(BLTZ));

  // Other names for the same wires on the sheet: OP_CODE[5:0] = OP

  // Notes on the sheet:
  //   运算器控制器，根据指令生成运算器功能选择信号
  //   控制信号生成，产生数据通路需要的其他控制信号
endmodule

// 运算器控制器
module \运算控制器自动生成  (
  input  OP0,
  input  OP1,
  input  OP2,
  input  OP3,
  input  OP4,
  input  OP5,
  input  F0,
  input  F1,
  input  F2,
  input  F3,
  input  F4,
  input  F5,
  output S0,
  output S1,
  output S2,
  output S3
);

  wire and_1_out, and_2_out, and_3_out, and_4_out, and_5_out, and_6_out, and_7_out, and_8_out, and_9_out,
       and_10_out, and_11_out, and_12_out, and_13_out, and_14_out, and_15_out, and_16_out, and_17_out,
       and_18_out, and_19_out, and_20_out, and_21_out, and_22_out, and_23_out, and_24_out, and_25_out,
       and_26_out, and_27_out, and_28_out, and_29_out, and_30_out, and_31_out, and_32_out, and_33_out,
       and_34_out, and_35_out, and_36_out, and_37_out, and_38_out, and_39_out, not_1_out, not_2_out,
       not_3_out, not_4_out, not_5_out, not_6_out, not_7_out, not_8_out, not_9_out, not_10_out, not_11_out,
       not_12_out, not_13_out, not_14_out, not_15_out, not_16_out, not_17_out, not_18_out, not_19_out,
       not_20_out, not_21_out, not_22_out, not_23_out, not_24_out, not_25_out, not_26_out, not_27_out,
       not_28_out, not_29_out, not_30_out, not_31_out, not_32_out, not_33_out, not_34_out, not_35_out,
       not_36_out, not_37_out, not_38_out, not_39_out, not_40_out, not_41_out, not_42_out, not_43_out,
       not_44_out, not_45_out, not_46_out, not_47_out, not_48_out, not_49_out, not_50_out, not_51_out,
       not_52_out, not_53_out, not_54_out, not_55_out, not_56_out, not_57_out, not_58_out, not_59_out,
       not_60_out, not_61_out, not_62_out, not_63_out, not_64_out, not_65_out, not_66_out, not_67_out,
       not_68_out, not_69_out, not_70_out, not_71_out, not_72_out, not_73_out, not_74_out, not_75_out,
       not_76_out, not_77_out, not_78_out, not_79_out, not_80_out, not_81_out, not_82_out, not_83_out,
       not_84_out, not_85_out, not_86_out, not_87_out, not_88_out, not_89_out, not_90_out, not_91_out,
       not_92_out, not_93_out, not_94_out, not_95_out, not_96_out, not_97_out, not_98_out, not_99_out,
       not_100_out, not_101_out, not_102_out, not_103_out, not_104_out, not_105_out, not_106_out,
       not_107_out, not_108_out, not_109_out, not_110_out, not_111_out, not_112_out, not_113_out,
       not_114_out, not_115_out, not_116_out, not_117_out, not_118_out, not_119_out, not_120_out,
       not_121_out, not_122_out, not_123_out, not_124_out, not_125_out, not_126_out, not_127_out,
       not_128_out, not_129_out, not_130_out, not_131_out, not_132_out, not_133_out, not_134_out,
       not_135_out, not_136_out, not_137_out, not_138_out, not_139_out, not_140_out, not_141_out,
       not_142_out, not_143_out, not_144_out, not_145_out, not_146_out, not_147_out, not_148_out,
       not_149_out, not_150_out, not_151_out, not_152_out, not_153_out, not_154_out, not_155_out,
       not_156_out, not_157_out, not_158_out, not_159_out, not_160_out, not_161_out, not_162_out,
       not_163_out, not_164_out, not_165_out, not_166_out, not_167_out, not_168_out, not_169_out,
       not_170_out, not_171_out, not_172_out, not_173_out, not_174_out, not_175_out, not_176_out,
       not_177_out, not_178_out, not_179_out, not_180_out, not_181_out, not_182_out, not_183_out,
       not_184_out, not_185_out, not_186_out, not_187_out, not_188_out, not_189_out, not_190_out,
       not_191_out, not_192_out, not_193_out, not_194_out, not_195_out, not_196_out, not_197_out,
       not_198_out, not_199_out, not_200_out, not_201_out, not_202_out, not_203_out, not_204_out,
       not_205_out, not_206_out, not_207_out, not_208_out, not_209_out, not_210_out, not_211_out,
       not_212_out, not_213_out, not_214_out, not_215_out, not_216_out, not_217_out, not_218_out,
       not_219_out, not_220_out, not_221_out, not_222_out, not_223_out, not_224_out, not_225_out,
       not_226_out, not_227_out, not_228_out, not_229_out, not_230_out, not_231_out, not_232_out,
       not_233_out, not_234_out, not_235_out, not_236_out, not_237_out, not_238_out, not_239_out,
       not_240_out, not_241_out, not_242_out, not_243_out, not_244_out, not_245_out, not_246_out,
       not_247_out, not_248_out, not_249_out, not_250_out, not_251_out, not_252_out, not_253_out,
       not_254_out, not_255_out, not_256_out, not_257_out, not_258_out, not_259_out, not_260_out,
       not_261_out, not_262_out, not_263_out, not_264_out, not_265_out, not_266_out, not_267_out,
       not_268_out, not_269_out, not_270_out, not_271_out, not_272_out, not_273_out;

  not not_1 (not_1_out, OP5);
  not not_2 (not_2_out, OP4);
  not not_3 (not_3_out, OP3);
  not not_4 (not_4_out, OP2);
  not not_5 (not_5_out, OP1);
  not not_6 (not_6_out, OP0);
  not not_7 (not_7_out, F5);
  not not_8 (not_8_out, F4);
  not not_9 (not_9_out, F3);
  not not_10 (not_10_out, F2);
  not not_11 (not_11_out, OP5);
  not not_12 (not_12_out, OP4);
  not not_13 (not_13_out, OP3);
  not not_14 (not_14_out, OP2);
  not not_15 (not_15_out, OP1);
  not not_16 (not_16_out, OP0);
  not not_17 (not_17_out, F4);
  not not_18 (not_18_out, F3);
  not not_19 (not_19_out, F2);
  not not_20 (not_20_out, F1);
  not not_21 (not_21_out, F0);
  not not_22 (not_22_out, OP5);
  not not_23 (not_23_out, OP4);
  not not_24 (not_24_out, OP3);
  not not_25 (not_25_out, OP2);
  not not_26 (not_26_out, OP1);
  not not_27 (not_27_out, OP0);
  not not_28 (not_28_out, F4);
  not not_29 (not_29_out, F3);
  not not_30 (not_30_out, F2);
  not not_31 (not_31_out, F1);
  not not_32 (not_32_out, OP5);
  not not_33 (not_33_out, OP4);
  not not_34 (not_34_out, OP3);
  not not_35 (not_35_out, OP2);
  not not_36 (not_36_out, OP1);
  not not_37 (not_37_out, OP0);
  not not_38 (not_38_out, F4);
  not not_39 (not_39_out, F3);
  not not_40 (not_40_out, F1);
  not not_41 (not_41_out, F0);
  not not_42 (not_42_out, OP5);
  not not_43 (not_43_out, OP4);
  not not_44 (not_44_out, OP3);
  not not_45 (not_45_out, OP2);
  not not_46 (not_46_out, OP1);
  not not_47 (not_47_out, OP0);
  not not_48 (not_48_out, F4);
  not not_49 (not_49_out, F2);
  not not_50 (not_50_out, F0);
  not not_51 (not_51_out, OP5);
  not not_52 (not_52_out, OP4);
  not not_53 (not_53_out, OP2);
  not not_54 (not_54_out, OP1);
  not not_55 (not_55_out, OP0);
  not not_56 (not_56_out, OP5);
  not not_57 (not_57_out, OP4);
  not not_58 (not_58_out, OP1);
  not not_59 (not_59_out, OP0);
  not not_60 (not_60_out, OP5);
  not not_61 (not_61_out, OP4);
  not not_62 (not_62_out, OP2);
  not not_63 (not_63_out, OP1);
  not not_64 (not_64_out, OP5);
  not not_65 (not_65_out, OP4);
  not not_66 (not_66_out, OP2);
  not not_67 (not_67_out, OP0);
  not not_68 (not_68_out, OP4);
  not not_69 (not_69_out, OP3);
  not not_70 (not_70_out, OP2);
  not not_71 (not_71_out, OP4);
  not not_72 (not_72_out, OP2);
  not not_73 (not_73_out, OP5);
  not not_74 (not_74_out, OP4);
  not not_75 (not_75_out, OP3);
  not not_76 (not_76_out, OP2);
  not not_77 (not_77_out, OP1);
  not not_78 (not_78_out, OP0);
  not not_79 (not_79_out, F5);
  not not_80 (not_80_out, F4);
  not not_81 (not_81_out, F3);
  not not_82 (not_82_out, OP5);
  not not_83 (not_83_out, OP4);
  not not_84 (not_84_out, OP3);
  not not_85 (not_85_out, OP2);
  not not_86 (not_86_out, OP1);
  not not_87 (not_87_out, OP0);
  not not_88 (not_88_out, F4);
  not not_89 (not_89_out, F3);
  not not_90 (not_90_out, F0);
  not not_91 (not_91_out, OP4);
  not not_92 (not_92_out, OP3);
  not not_93 (not_93_out, OP2);
  not not_94 (not_94_out, OP1);
  not not_95 (not_95_out, OP0);
  not not_96 (not_96_out, OP5);
  not not_97 (not_97_out, OP4);
  not not_98 (not_98_out, OP3);
  not not_99 (not_99_out, OP2);
  not not_100 (not_100_out, OP1);
  not not_101 (not_101_out, OP0);
  not not_102 (not_102_out, F5);
  not not_103 (not_103_out, F4);
  not not_104 (not_104_out, F3);
  not not_105 (not_105_out, F2);
  not not_106 (not_106_out, F0);
  not not_107 (not_107_out, OP5);
  not not_108 (not_108_out, OP4);
  not not_109 (not_109_out, OP3);
  not not_110 (not_110_out, OP2);
  not not_111 (not_111_out, OP1);
  not not_112 (not_112_out, OP0);
  not not_113 (not_113_out, F4);
  not not_114 (not_114_out, F3);
  not not_115 (not_115_out, F2);
  not not_116 (not_116_out, F0);
  not not_117 (not_117_out, OP5);
  not not_118 (not_118_out, OP4);
  not not_119 (not_119_out, OP3);
  not not_120 (not_120_out, OP2);
  not not_121 (not_121_out, OP1);
  not not_122 (not_122_out, OP0);
  not not_123 (not_123_out, F4);
  not not_124 (not_124_out, F3);
  not not_125 (not_125_out, F1);
  not not_126 (not_126_out, F0);
  not not_127 (not_127_out, OP5);
  not not_128 (not_128_out, OP4);
  not not_129 (not_129_out, OP3);
  not not_130 (not_130_out, OP2);
  not not_131 (not_131_out, OP1);
  not not_132 (not_132_out, OP0);
  not not_133 (not_133_out, F4);
  not not_134 (not_134_out, F3);
  not not_135 (not_135_out, OP5);
  not not_136 (not_136_out, OP4);
  not not_137 (not_137_out, OP3);
  not not_138 (not_138_out, OP2);
  not not_139 (not_139_out, OP1);
  not not_140 (not_140_out, OP0);
  not not_141 (not_141_out, F4);
  not not_142 (not_142_out, F2);
  not not_143 (not_143_out, F0);
  not not_144 (not_144_out, OP5);
  not not_145 (not_145_out, OP4);
  not not_146 (not_146_out, OP1);
  not not_147 (not_147_out, OP0);
  not not_148 (not_148_out, OP5);
  not not_149 (not_149_out, OP4);
  not not_150 (not_150_out, OP2);
  not not_151 (not_151_out, OP0);
  not not_152 (not_152_out, OP5);
  not not_153 (not_153_out, OP4);
  not not_154 (not_154_out, OP3);
  not not_155 (not_155_out, OP2);
  not not_156 (not_156_out, OP1);
  not not_157 (not_157_out, OP0);
  not not_158 (not_158_out, F4);
  not not_159 (not_159_out, F3);
  not not_160 (not_160_out, F2);
  not not_161 (not_161_out, F1);
  not not_162 (not_162_out, F0);
  not not_163 (not_163_out, OP5);
  not not_164 (not_164_out, OP4);
  not not_165 (not_165_out, OP3);
  not not_166 (not_166_out, OP2);
  not not_167 (not_167_out, OP1);
  not not_168 (not_168_out, OP0);
  not not_169 (not_169_out, F4);
  not not_170 (not_170_out, F3);
  not not_171 (not_171_out, F2);
  not not_172 (not_172_out, F1);
  not not_173 (not_173_out, OP5);
  not not_174 (not_174_out, OP4);
  not not_175 (not_175_out, OP3);
  not not_176 (not_176_out, OP2);
  not not_177 (not_177_out, OP1);
  not not_178 (not_178_out, OP0);
  not not_179 (not_179_out, F4);
  not not_180 (not_180_out, F3);
  not not_181 (not_181_out, F2);
  not not_182 (not_182_out, F0);
  not not_183 (not_183_out, OP5);
  not not_184 (not_184_out, OP4);
  not not_185 (not_185_out, OP3);
  not not_186 (not_186_out, OP2);
  not not_187 (not_187_out, OP1);
  not not_188 (not_188_out, OP0);
  not not_189 (not_189_out, F4);
  not not_190 (not_190_out, F3);
  not not_191 (not_191_out, F1);
  not not_192 (not_192_out, F0);
  not not_193 (not_193_out, OP5);
  not not_194 (not_194_out, OP4);
  not not_195 (not_195_out, OP3);
  not not_196 (not_196_out, OP2);
  not not_197 (not_197_out, OP1);
  not not_198 (not_198_out, OP0);
  not not_199 (not_199_out, F4);
  not not_200 (not_200_out, F2);
  not not_201 (not_201_out, OP5);
  not not_202 (not_202_out, OP4);
  not not_203 (not_203_out, OP2);
  not not_204 (not_204_out, OP1);
  not not_205 (not_205_out, OP0);
  not not_206 (not_206_out, OP5);
  not not_207 (not_207_out, OP4);
  not not_208 (not_208_out, OP1);
  not not_209 (not_209_out, OP0);
  not not_210 (not_210_out, OP5);
  not not_211 (not_211_out, OP4);
  not not_212 (not_212_out, OP2);
  not not_213 (not_213_out, OP1);
  not not_214 (not_214_out, OP4);
  not not_215 (not_215_out, OP3);
  not not_216 (not_216_out, OP2);
  not not_217 (not_217_out, OP4);
  not not_218 (not_218_out, OP2);
  not not_219 (not_219_out, OP4);
  not not_220 (not_220_out, OP3);
  not not_221 (not_221_out, OP2);
  not not_222 (not_222_out, OP1);
  not not_223 (not_223_out, OP0);
  not not_224 (not_224_out, OP5);
  not not_225 (not_225_out, OP4);
  not not_226 (not_226_out, OP3);
  not not_227 (not_227_out, OP2);
  not not_228 (not_228_out, OP1);
  not not_229 (not_229_out, OP0);
  not not_230 (not_230_out, F4);
  not not_231 (not_231_out, F3);
  not not_232 (not_232_out, F1);
  not not_233 (not_233_out, OP5);
  not not_234 (not_234_out, OP4);
  not not_235 (not_235_out, OP3);
  not not_236 (not_236_out, OP2);
  not not_237 (not_237_out, OP1);
  not not_238 (not_238_out, OP0);
  not not_239 (not_239_out, F4);
  not not_240 (not_240_out, F3);
  not not_241 (not_241_out, OP5);
  not not_242 (not_242_out, OP4);
  not not_243 (not_243_out, OP3);
  not not_244 (not_244_out, OP2);
  not not_245 (not_245_out, OP1);
  not not_246 (not_246_out, OP0);
  not not_247 (not_247_out, F4);
  not not_248 (not_248_out, F2);
  not not_249 (not_249_out, F0);
  not not_250 (not_250_out, OP5);
  not not_251 (not_251_out, OP4);
  not not_252 (not_252_out, OP3);
  not not_253 (not_253_out, OP2);
  not not_254 (not_254_out, OP1);
  not not_255 (not_255_out, OP0);
  not not_256 (not_256_out, F4);
  not not_257 (not_257_out, F2);
  not not_258 (not_258_out, OP5);
  not not_259 (not_259_out, OP4);
  not not_260 (not_260_out, OP2);
  not not_261 (not_261_out, OP0);
  not not_262 (not_262_out, OP5);
  not not_263 (not_263_out, OP4);
  not not_264 (not_264_out, OP1);
  not not_265 (not_265_out, OP5);
  not not_266 (not_266_out, OP4);
  not not_267 (not_267_out, OP3);
  not not_268 (not_268_out, OP2);
  not not_269 (not_269_out, OP1);
  not not_270 (not_270_out, OP0);
  not not_271 (not_271_out, F4);
  not not_272 (not_272_out, F3);
  not not_273 (not_273_out, F0);
  and and_1 (and_1_out, not_1_out, not_2_out, not_3_out, not_4_out, not_5_out, not_6_out, not_7_out, not_8_out, not_9_out, not_10_out, F1, F0);
  and and_2 (and_2_out, not_11_out, not_12_out, not_13_out, not_14_out, not_15_out, not_16_out, F5, not_17_out, not_18_out, not_19_out, not_20_out, not_21_out);
  and and_3 (and_3_out, not_22_out, not_23_out, not_24_out, not_25_out, not_26_out, not_27_out, F5, not_28_out, not_29_out, not_30_out, not_31_out, F0);
  and and_4 (and_4_out, not_32_out, not_33_out, not_34_out, not_35_out, not_36_out, not_37_out, F5, not_38_out, not_39_out, F2, not_40_out, not_41_out);
  and and_5 (and_5_out, not_42_out, not_43_out, not_44_out, not_45_out, not_46_out, not_47_out, F5, not_48_out, F3, not_49_out, F1, not_50_out);
  and and_6 (and_6_out, not_51_out, not_52_out, OP3, not_53_out, not_54_out, not_55_out);
  and and_7 (and_7_out, not_56_out, not_57_out, OP3, OP2, not_58_out, not_59_out);
  and and_8 (and_8_out, not_60_out, not_61_out, OP3, not_62_out, not_63_out, OP0);
  and and_9 (and_9_out, not_64_out, not_65_out, OP3, not_66_out, OP1, not_67_out);
  and and_10 (and_10_out, OP5, not_68_out, not_69_out, not_70_out, OP1, OP0);
  and and_11 (and_11_out, OP5, not_71_out, OP3, not_72_out, OP1, OP0);
  and and_12 (and_12_out, not_73_out, not_74_out, not_75_out, not_76_out, not_77_out, not_78_out, not_79_out, not_80_out, not_81_out, F2, F1, F0);
  and and_13 (and_13_out, not_82_out, not_83_out, not_84_out, not_85_out, not_86_out, not_87_out, F5, not_88_out, not_89_out, F2, F1, not_90_out);
  and and_14 (and_14_out, OP5, not_91_out, not_92_out, not_93_out, not_94_out, not_95_out);
  and and_15 (and_15_out, not_96_out, not_97_out, not_98_out, not_99_out, not_100_out, not_101_out, not_102_out, not_103_out, not_104_out, not_105_out, F1, not_106_out);
  and and_16 (and_16_out, not_107_out, not_108_out, not_109_out, not_110_out, not_111_out, not_112_out, F5, not_113_out, not_114_out, not_115_out, F1, not_116_out);
  and and_17 (and_17_out, not_117_out, not_118_out, not_119_out, not_120_out, not_121_out, not_122_out, F5, not_123_out, not_124_out, F2, not_125_out, not_126_out);
  and and_18 (and_18_out, not_127_out, not_128_out, not_129_out, not_130_out, not_131_out, not_132_out, F5, not_133_out, not_134_out, F2, F1, F0);
  and and_19 (and_19_out, not_135_out, not_136_out, not_137_out, not_138_out, not_139_out, not_140_out, F5, not_141_out, F3, not_142_out, F1, not_143_out);
  and and_20 (and_20_out, not_144_out, not_145_out, OP3, OP2, not_146_out, not_147_out);
  and and_21 (and_21_out, not_148_out, not_149_out, OP3, not_150_out, OP1, not_151_out);
  and and_22 (and_22_out, not_152_out, not_153_out, not_154_out, not_155_out, not_156_out, not_157_out, F5, not_158_out, not_159_out, not_160_out, not_161_out, not_162_out);
  and and_23 (and_23_out, not_163_out, not_164_out, not_165_out, not_166_out, not_167_out, not_168_out, F5, not_169_out, not_170_out, not_171_out, not_172_out, F0);
  and and_24 (and_24_out, not_173_out, not_174_out, not_175_out, not_176_out, not_177_out, not_178_out, F5, not_179_out, not_180_out, not_181_out, F1, not_182_out);
  and and_25 (and_25_out, not_183_out, not_184_out, not_185_out, not_186_out, not_187_out, not_188_out, F5, not_189_out, not_190_out, F2, not_191_out, not_192_out);
  and and_26 (and_26_out, not_193_out, not_194_out, not_195_out, not_196_out, not_197_out, not_198_out, F5, not_199_out, F3, not_200_out, F1, F0);
  and and_27 (and_27_out, not_201_out, not_202_out, OP3, not_203_out, not_204_out, not_205_out);
  and and_28 (and_28_out, not_206_out, not_207_out, OP3, OP2, not_208_out, not_209_out);
  and and_29 (and_29_out, not_210_out, not_211_out, OP3, not_212_out, not_213_out, OP0);
  and and_30 (and_30_out, OP5, not_214_out, not_215_out, not_216_out, OP1, OP0);
  and and_31 (and_31_out, OP5, not_217_out, OP3, not_218_out, OP1, OP0);
  and and_32 (and_32_out, OP5, not_219_out, not_220_out, not_221_out, not_222_out, not_223_out);
  and and_33 (and_33_out, not_224_out, not_225_out, not_226_out, not_227_out, not_228_out, not_229_out, F5, not_230_out, not_231_out, F2, not_232_out, F0);
  and and_34 (and_34_out, not_233_out, not_234_out, not_235_out, not_236_out, not_237_out, not_238_out, F5, not_239_out, not_240_out, F2, F1, F0);
  and and_35 (and_35_out, not_241_out, not_242_out, not_243_out, not_244_out, not_245_out, not_246_out, F5, not_247_out, F3, not_248_out, F1, not_249_out);
  and and_36 (and_36_out, not_250_out, not_251_out, not_252_out, not_253_out, not_254_out, not_255_out, F5, not_256_out, F3, not_257_out, F1, F0);
  and and_37 (and_37_out, not_258_out, not_259_out, OP3, not_260_out, OP1, not_261_out);
  and and_38 (and_38_out, not_262_out, not_263_out, OP3, OP2, not_264_out, OP0);
  and and_39 (and_39_out, not_265_out, not_266_out, not_267_out, not_268_out, not_269_out, not_270_out, F5, not_271_out, not_272_out, F2, F1, not_273_out);
  or or_1 (S1, and_15_out, and_16_out, and_17_out, and_18_out, and_19_out, and_20_out, and_21_out);
  or or_2 (S2, and_22_out, and_23_out, and_24_out, and_25_out, and_26_out, and_27_out, and_28_out, and_29_out, and_30_out, and_31_out, and_32_out);
  or or_3 (S3, and_33_out, and_34_out, and_35_out, and_36_out, and_37_out, and_38_out, and_39_out);
  or or_4 (S0, and_1_out, and_2_out, and_3_out, and_4_out, and_5_out, and_6_out, and_7_out, and_8_out, and_9_out, and_10_out, and_11_out, and_12_out, and_13_out, and_14_out);
endmodule

// 控制信号生成
module \控制信号自动生成  (
  input  OP0,
  input  OP1,
  input  OP2,
  input  OP3,
  input  OP4,
  input  OP5,
  input  F0,
  input  F1,
  input  F2,
  input  F3,
  input  F4,
  input  F5,
  output MemToReg,
  output MemWrite,
  output ALU_SRC,
  output RegWrite,
  output SysCALL,
  output SignedExt,
  output RegDst,
  output BEQ,
  output BNE,
  output JR,
  output JUMP,
  output JAL,
  output SRAV,
  output LB,
  output BLTZ
);

  wire and_1_out, and_2_out, and_4_out, and_5_out, and_6_out, and_7_out, and_8_out, and_9_out, and_10_out,
       and_11_out, and_12_out, and_13_out, and_14_out, and_15_out, and_16_out, and_18_out, and_19_out,
       and_20_out, and_21_out, and_22_out, and_23_out, and_24_out, and_25_out, and_26_out, and_30_out,
       and_31_out, not_1_out, not_2_out, not_3_out, not_4_out, not_5_out, not_6_out, not_7_out, not_8_out,
       not_9_out, not_10_out, not_11_out, not_12_out, not_13_out, not_14_out, not_15_out, not_16_out,
       not_17_out, not_18_out, not_19_out, not_20_out, not_21_out, not_22_out, not_23_out, not_24_out,
       not_25_out, not_26_out, not_27_out, not_28_out, not_29_out, not_30_out, not_31_out, not_32_out,
       not_33_out, not_34_out, not_35_out, not_36_out, not_37_out, not_38_out, not_39_out, not_40_out,
       not_41_out, not_42_out, not_43_out, not_44_out, not_45_out, not_46_out, not_47_out, not_48_out,
       not_49_out, not_50_out, not_51_out, not_52_out, not_53_out, not_54_out, not_55_out, not_56_out,
       not_57_out, not_58_out, not_59_out, not_60_out, not_61_out, not_62_out, not_63_out, not_64_out,
       not_65_out, not_66_out, not_67_out, not_68_out, not_69_out, not_70_out, not_71_out, not_72_out,
       not_73_out, not_74_out, not_75_out, not_76_out, not_77_out, not_78_out, not_79_out, not_80_out,
       not_81_out, not_82_out, not_83_out, not_84_out, not_85_out, not_86_out, not_87_out, not_88_out,
       not_89_out, not_90_out, not_91_out, not_92_out, not_93_out, not_94_out, not_95_out, not_96_out,
       not_97_out, not_98_out, not_99_out, not_100_out, not_101_out, not_102_out, not_103_out, not_104_out,
       not_105_out, not_106_out, not_107_out, not_108_out, not_109_out, not_110_out, not_111_out,
       not_112_out, not_113_out, not_114_out, not_115_out, not_116_out, not_117_out, not_118_out,
       not_119_out, not_120_out, not_121_out, not_122_out, not_123_out, not_124_out, not_125_out,
       not_126_out, not_127_out, not_128_out, not_129_out, not_130_out, not_131_out, not_132_out,
       not_133_out, not_134_out, not_135_out, not_136_out, not_137_out, not_138_out, not_139_out,
       not_140_out, not_141_out, not_142_out, not_143_out, not_144_out, not_145_out, not_146_out,
       not_147_out, not_148_out, not_149_out, not_150_out, not_151_out, not_152_out, not_153_out,
       not_154_out, not_155_out, not_156_out, not_157_out, not_158_out, not_159_out, not_160_out,
       not_161_out, not_162_out, not_163_out, not_164_out, not_165_out, not_166_out, not_167_out,
       not_168_out, not_169_out, not_170_out, not_171_out, not_172_out, not_173_out, not_174_out,
       not_175_out, not_176_out, not_177_out, not_178_out, not_179_out, not_180_out, not_181_out,
       not_182_out, not_183_out, not_184_out, not_185_out, not_186_out, not_187_out, not_188_out,
       not_189_out, not_190_out, not_191_out, not_192_out, not_193_out, not_194_out, not_195_out,
       not_196_out, not_197_out, not_198_out, not_199_out, not_200_out, not_201_out, not_202_out,
       not_203_out, not_204_out;

  not not_1 (not_1_out, OP0);
  not not_2 (not_2_out, OP1);
  not not_3 (not_3_out, OP2);
  not not_4 (not_4_out, OP3);
  not not_5 (not_5_out, OP4);
  not not_6 (not_6_out, OP2);
  not not_7 (not_7_out, OP3);
  not not_8 (not_8_out, OP4);
  not not_9 (not_9_out, OP2);
  not not_10 (not_10_out, OP4);
  not not_11 (not_11_out, OP0);
  not not_12 (not_12_out, OP1);
  not not_13 (not_13_out, OP2);
  not not_14 (not_14_out, OP3);
  not not_15 (not_15_out, OP4);
  not not_16 (not_16_out, OP0);
  not not_17 (not_17_out, OP2);
  not not_18 (not_18_out, OP4);
  not not_19 (not_19_out, OP5);
  not not_20 (not_20_out, OP1);
  not not_21 (not_21_out, OP4);
  not not_22 (not_22_out, OP5);
  not not_23 (not_23_out, OP2);
  not not_24 (not_24_out, OP4);
  not not_25 (not_25_out, OP0);
  not not_26 (not_26_out, OP1);
  not not_27 (not_27_out, OP2);
  not not_28 (not_28_out, OP3);
  not not_29 (not_29_out, OP4);
  not not_30 (not_30_out, F0);
  not not_31 (not_31_out, F2);
  not not_32 (not_32_out, F3);
  not not_33 (not_33_out, F4);
  not not_34 (not_34_out, OP0);
  not not_35 (not_35_out, OP1);
  not not_36 (not_36_out, OP2);
  not not_37 (not_37_out, OP3);
  not not_38 (not_38_out, OP4);
  not not_39 (not_39_out, F1);
  not not_40 (not_40_out, F3);
  not not_41 (not_41_out, F4);
  not not_42 (not_42_out, OP0);
  not not_43 (not_43_out, OP1);
  not not_44 (not_44_out, OP2);
  not not_45 (not_45_out, OP3);
  not not_46 (not_46_out, OP4);
  not not_47 (not_47_out, F3);
  not not_48 (not_48_out, F4);
  not not_49 (not_49_out, OP0);
  not not_50 (not_50_out, OP1);
  not not_51 (not_51_out, OP2);
  not not_52 (not_52_out, OP3);
  not not_53 (not_53_out, OP4);
  not not_54 (not_54_out, F2);
  not not_55 (not_55_out, F4);
  not not_56 (not_56_out, OP0);
  not not_57 (not_57_out, OP1);
  not not_58 (not_58_out, OP2);
  not not_59 (not_59_out, OP3);
  not not_60 (not_60_out, OP4);
  not not_61 (not_61_out, F3);
  not not_62 (not_62_out, F4);
  not not_63 (not_63_out, F5);
  not not_64 (not_64_out, OP0);
  not not_65 (not_65_out, OP1);
  not not_66 (not_66_out, OP2);
  not not_67 (not_67_out, OP3);
  not not_68 (not_68_out, OP4);
  not not_69 (not_69_out, OP0);
  not not_70 (not_70_out, OP2);
  not not_71 (not_71_out, OP4);
  not not_72 (not_72_out, OP5);
  not not_73 (not_73_out, OP1);
  not not_74 (not_74_out, OP4);
  not not_75 (not_75_out, OP5);
  not not_76 (not_76_out, OP2);
  not not_77 (not_77_out, OP3);
  not not_78 (not_78_out, OP4);
  not not_79 (not_79_out, OP0);
  not not_80 (not_80_out, OP1);
  not not_81 (not_81_out, OP2);
  not not_82 (not_82_out, OP3);
  not not_83 (not_83_out, OP4);
  not not_84 (not_84_out, OP5);
  not not_85 (not_85_out, F0);
  not not_86 (not_86_out, F1);
  not not_87 (not_87_out, F4);
  not not_88 (not_88_out, F5);
  not not_89 (not_89_out, OP0);
  not not_90 (not_90_out, OP1);
  not not_91 (not_91_out, OP2);
  not not_92 (not_92_out, OP3);
  not not_93 (not_93_out, OP4);
  not not_94 (not_94_out, OP0);
  not not_95 (not_95_out, OP2);
  not not_96 (not_96_out, OP4);
  not not_97 (not_97_out, OP5);
  not not_98 (not_98_out, OP1);
  not not_99 (not_99_out, OP2);
  not not_100 (not_100_out, OP4);
  not not_101 (not_101_out, OP5);
  not not_102 (not_102_out, OP2);
  not not_103 (not_103_out, OP4);
  not not_104 (not_104_out, OP0);
  not not_105 (not_105_out, OP1);
  not not_106 (not_106_out, OP2);
  not not_107 (not_107_out, OP3);
  not not_108 (not_108_out, OP4);
  not not_109 (not_109_out, OP5);
  not not_110 (not_110_out, F0);
  not not_111 (not_111_out, F2);
  not not_112 (not_112_out, F3);
  not not_113 (not_113_out, F4);
  not not_114 (not_114_out, OP0);
  not not_115 (not_115_out, OP1);
  not not_116 (not_116_out, OP2);
  not not_117 (not_117_out, OP3);
  not not_118 (not_118_out, OP4);
  not not_119 (not_119_out, OP5);
  not not_120 (not_120_out, F1);
  not not_121 (not_121_out, F3);
  not not_122 (not_122_out, F4);
  not not_123 (not_123_out, OP0);
  not not_124 (not_124_out, OP1);
  not not_125 (not_125_out, OP2);
  not not_126 (not_126_out, OP3);
  not not_127 (not_127_out, OP4);
  not not_128 (not_128_out, OP5);
  not not_129 (not_129_out, F3);
  not not_130 (not_130_out, F4);
  not not_131 (not_131_out, OP0);
  not not_132 (not_132_out, OP1);
  not not_133 (not_133_out, OP2);
  not not_134 (not_134_out, OP3);
  not not_135 (not_135_out, OP4);
  not not_136 (not_136_out, OP5);
  not not_137 (not_137_out, F2);
  not not_138 (not_138_out, F4);
  not not_139 (not_139_out, OP0);
  not not_140 (not_140_out, OP1);
  not not_141 (not_141_out, OP2);
  not not_142 (not_142_out, OP3);
  not not_143 (not_143_out, OP4);
  not not_144 (not_144_out, OP5);
  not not_145 (not_145_out, F3);
  not not_146 (not_146_out, F4);
  not not_147 (not_147_out, F5);
  not not_148 (not_148_out, OP0);
  not not_149 (not_149_out, OP1);
  not not_150 (not_150_out, OP3);
  not not_151 (not_151_out, OP4);
  not not_152 (not_152_out, OP5);
  not not_153 (not_153_out, OP1);
  not not_154 (not_154_out, OP3);
  not not_155 (not_155_out, OP4);
  not not_156 (not_156_out, OP5);
  not not_157 (not_157_out, OP0);
  not not_158 (not_158_out, OP1);
  not not_159 (not_159_out, OP2);
  not not_160 (not_160_out, OP3);
  not not_161 (not_161_out, OP4);
  not not_162 (not_162_out, OP5);
  not not_163 (not_163_out, F0);
  not not_164 (not_164_out, F1);
  not not_165 (not_165_out, F2);
  not not_166 (not_166_out, F4);
  not not_167 (not_167_out, F5);
  not not_168 (not_168_out, OP0);
  not not_169 (not_169_out, OP2);
  not not_170 (not_170_out, OP3);
  not not_171 (not_171_out, OP4);
  not not_172 (not_172_out, OP5);
  not not_173 (not_173_out, F0);
  not not_174 (not_174_out, F1);
  not not_175 (not_175_out, F2);
  not not_176 (not_176_out, F4);
  not not_177 (not_177_out, F5);
  not not_178 (not_178_out, OP2);
  not not_179 (not_179_out, OP3);
  not not_180 (not_180_out, OP4);
  not not_181 (not_181_out, OP5);
  not not_182 (not_182_out, OP2);
  not not_183 (not_183_out, OP3);
  not not_184 (not_184_out, OP4);
  not not_185 (not_185_out, OP5);
  not not_186 (not_186_out, OP0);
  not not_187 (not_187_out, OP1);
  not not_188 (not_188_out, OP2);
  not not_189 (not_189_out, OP3);
  not not_190 (not_190_out, OP4);
  not not_191 (not_191_out, OP5);
  not not_192 (not_192_out, F3);
  not not_193 (not_193_out, F4);
  not not_194 (not_194_out, F5);
  not not_195 (not_195_out, OP4);
  not not_196 (not_196_out, OP3);
  not not_197 (not_197_out, OP2);
  not not_198 (not_198_out, OP1);
  not not_199 (not_199_out, OP0);
  not not_200 (not_200_out, OP1);
  not not_201 (not_201_out, OP2);
  not not_202 (not_202_out, OP3);
  not not_203 (not_203_out, OP4);
  not not_204 (not_204_out, OP5);
  and and_1 (and_1_out, not_1_out, not_2_out, not_3_out, not_4_out, not_5_out, OP5);
  and and_2 (and_2_out, OP0, OP1, not_6_out, not_7_out, not_8_out, OP5);
  and and_3 (MemWrite, OP0, OP1, not_9_out, OP3, not_10_out, OP5);
  and and_4 (and_4_out, not_11_out, not_12_out, not_13_out, not_14_out, not_15_out, OP5);
  and and_5 (and_5_out, not_16_out, not_17_out, OP3, not_18_out, not_19_out);
  and and_6 (and_6_out, not_20_out, OP3, not_21_out, not_22_out);
  and and_7 (and_7_out, OP0, OP1, not_23_out, not_24_out, OP5);
  and and_8 (and_8_out, not_25_out, not_26_out, not_27_out, not_28_out, not_29_out, not_30_out, not_31_out, not_32_out, not_33_out);
  and and_9 (and_9_out, not_34_out, not_35_out, not_36_out, not_37_out, not_38_out, not_39_out, not_40_out, not_41_out, F5);
  and and_10 (and_10_out, not_42_out, not_43_out, not_44_out, not_45_out, not_46_out, F2, not_47_out, not_48_out, F5);
  and and_11 (and_11_out, not_49_out, not_50_out, not_51_out, not_52_out, not_53_out, F1, not_54_out, F3, not_55_out, F5);
  and and_12 (and_12_out, not_56_out, not_57_out, not_58_out, not_59_out, not_60_out, F0, F1, not_61_out, not_62_out, not_63_out);
  and and_13 (and_13_out, not_64_out, not_65_out, not_66_out, not_67_out, not_68_out, OP5);
  and and_14 (and_14_out, not_69_out, not_70_out, OP3, not_71_out, not_72_out);
  and and_15 (and_15_out, not_73_out, OP3, not_74_out, not_75_out);
  and and_16 (and_16_out, OP0, OP1, not_76_out, not_77_out, not_78_out);
  and and_17 (SysCALL, not_79_out, not_80_out, not_81_out, not_82_out, not_83_out, not_84_out, not_85_out, not_86_out, F2, F3, not_87_out, not_88_out);
  and and_18 (and_18_out, not_89_out, not_90_out, not_91_out, not_92_out, not_93_out, OP5);
  and and_19 (and_19_out, not_94_out, not_95_out, OP3, not_96_out, not_97_out);
  and and_20 (and_20_out, not_98_out, not_99_out, OP3, not_100_out, not_101_out);
  and and_21 (and_21_out, OP0, OP1, not_102_out, not_103_out, OP5);
  and and_22 (and_22_out, not_104_out, not_105_out, not_106_out, not_107_out, not_108_out, not_109_out, not_110_out, not_111_out, not_112_out, not_113_out);
  and and_23 (and_23_out, not_114_out, not_115_out, not_116_out, not_117_out, not_118_out, not_119_out, not_120_out, not_121_out, not_122_out, F5);
  and and_24 (and_24_out, not_123_out, not_124_out, not_125_out, not_126_out, not_127_out, not_128_out, F2, not_129_out, not_130_out, F5);
  and and_25 (and_25_out, not_131_out, not_132_out, not_133_out, not_134_out, not_135_out, not_136_out, F1, not_137_out, F3, not_138_out, F5);
  and and_26 (and_26_out, not_139_out, not_140_out, not_141_out, not_142_out, not_143_out, not_144_out, F0, F1, not_145_out, not_146_out, not_147_out);
  and and_27 (BEQ, not_148_out, not_149_out, OP2, not_150_out, not_151_out, not_152_out);
  and and_28 (BNE, OP0, not_153_out, OP2, not_154_out, not_155_out, not_156_out);
  and and_29 (JR, not_157_out, not_158_out, not_159_out, not_160_out, not_161_out, not_162_out, not_163_out, not_164_out, not_165_out, F3, not_166_out, not_167_out);
  and and_30 (and_30_out, not_168_out, not_169_out, not_170_out, not_171_out, not_172_out, not_173_out, not_174_out, not_175_out, F3, not_176_out, not_177_out);
  and and_31 (and_31_out, OP1, not_178_out, not_179_out, not_180_out, not_181_out);
  and and_32 (JAL, OP0, OP1, not_182_out, not_183_out, not_184_out, not_185_out);
  and and_33 (SRAV, not_186_out, not_187_out, not_188_out, not_189_out, not_190_out, not_191_out, F0, F1, F2, not_192_out, not_193_out, not_194_out);
  and and_34 (LB, OP5, not_195_out, not_196_out, not_197_out, not_198_out, not_199_out);
  and and_35 (BLTZ, OP0, not_200_out, not_201_out, not_202_out, not_203_out, not_204_out);
  or or_1 (MemToReg, and_1_out, and_2_out);
  or or_2 (ALU_SRC, and_4_out, and_5_out, and_6_out, and_7_out);
  or or_3 (RegWrite, and_8_out, and_9_out, and_10_out, and_11_out, and_12_out, and_13_out, and_14_out, and_15_out, and_16_out);
  or or_4 (SignedExt, and_18_out, and_19_out, and_20_out, and_21_out);
  or or_5 (RegDst, and_22_out, and_23_out, and_24_out, and_25_out, and_26_out);
  or or_6 (JUMP, and_30_out, and_31_out);
endmodule

// ALU
module MIPS_ALU (
  input  [4:0] shamt,
  input  [31:0] X,
  input  [31:0] Y,
  input  [3:0] AluOP,
  output Equal,
  output [31:0] Result,
  output [31:0] Result_2
);

  wire [0:0] comparator_1_lt, comparator_2_lt;
  wire [31:0] adder_1_out, AND_out, divider_1_out, divider_1_rem, multiplier_1_cout, multiplier_1_out,
       NOR_out, OR_out, shifter_1_out, shifter_2_out, shifter_3_out, subtractor_1_out, XOR_out;

  assign AND_out = X & Y;  // AND_Gate AND, 32 bits wide
  assign OR_out = X | Y;  // OR_Gate OR, 32 bits wide
  Shifter #(.width(32), .shift("ll")) shifter_1 (.in(Y), .\dist (shamt), .out(shifter_1_out));
  Shifter #(.width(32), .shift("ar")) shifter_2 (.in(Y), .\dist (shamt), .out(shifter_2_out));
  Shifter #(.width(32), .shift("lr")) shifter_3 (.in(Y), .\dist (shamt), .out(shifter_3_out));
  Multiplier #(.width(32)) multiplier_1 (.a(X), .b(Y), .out(multiplier_1_out), .cout(multiplier_1_cout));  // open: cin
  Divider #(.width(32)) divider_1 (.a(X), .b(Y), .out(divider_1_out), .rem(divider_1_rem));  // open: upper
  Adder #(.width(32)) adder_1 (.a(X), .b(Y), .out(adder_1_out));  // open: cin, cout
  Subtractor #(.width(32)) subtractor_1 (.a(X), .b(Y), .out(subtractor_1_out));  // open: bin, bout
  assign XOR_out = X ^ Y;  // XOR_Gate XOR, 32 bits wide
  assign NOR_out = ~(X | Y);  // NOR_Gate NOR, 32 bits wide
  Comparator #(.width(32), .mode("twosComplement")) comparator_1 (
    .a(X), .b(Y), .eq(Equal), .lt(comparator_1_lt[0]));  // open: gt
  Comparator #(.width(32), .mode("unsigned")) comparator_2 (.a(X), .b(Y), .lt(comparator_2_lt[0]));  // open: gt, eq
  Multiplexer #(.select(4), .width(32), .disabled("Z"), .enable("false")) multiplexer_1 (
    .in0(shifter_1_out), .in1(shifter_2_out), .in2(shifter_3_out), .in3(multiplier_1_out),
    .in4(divider_1_out), .in5(adder_1_out), .in6(subtractor_1_out), .in7(AND_out), .in8(OR_out),
    .in9(XOR_out), .in10(NOR_out), .in11({{31{1'b0}}, comparator_1_lt[0]}),
    .in12({{31{1'b0}}, comparator_2_lt[0]}), .in13({32{1'b0}}), .in14({32{1'b0}}), .in15({32{1'b0}}),
    .out(Result), .sel(AluOP));
  Multiplexer #(.select(4), .width(32), .disabled("Z"), .enable("false")) multiplexer_2 (
    .in0({32{1'b0}}), .in1({32{1'b0}}), .in2({32{1'b0}}), .in3(multiplier_1_cout), .in4(divider_1_rem),
    .in5({32{1'b0}}), .in6({32{1'b0}}), .in7({32{1'b0}}), .in8({32{1'b0}}), .in9({32{1'b0}}),
    .in10({32{1'b0}}), .in11({32{1'b0}}), .in12({32{1'b0}}), .in13({32{1'b0}}), .in14({32{1'b0}}),
    .in15({32{1'b0}}), .out(Result_2), .sel(AluOP));

  // Other names for the same wires on the sheet: Result2[31:0] = Result_2; S[3:0] = AluOP

  // Notes on the sheet:
  //   不要改变此引脚区域内容，也不要改变ALU封装形式
  //   输入引脚
  //   输出引脚
endmodule

module MIPS_Regifile (
  input  [31:0] Din,
  input  Clk,
  input  WE,
  input  [4:0] R1_num,
  input  [4:0] W_num,
  input  [4:0] R2_num,
  output [31:0] R1,
  output [31:0] R2
);

  // RegisterFile registerfile_1: pin names not known; wires that end beside it: Din, Clk, WE, W_num, R1_num, R2_num, R1, R2
endmodule

module \MIPS_Regifile_下降沿  (
  input  [31:0] Din,
  input  Clk,
  input  WE,
  input  [4:0] R1_num,
  input  [4:0] W_num,
  input  [4:0] R2_num,
  output [31:0] R1,
  output [31:0] R2
);

  // RegisterFile registerfile_1: pin names not known; wires that end beside it: Din, Clk, WE, W_num, R1_num, R2_num, R1, R2
endmodule

module \理想流水线  (
  output RegWrite,
  output MemWrite,
  output [31:0] IF_PC,
  output [31:0] ID_PC,
  output [31:0] EX_PC,
  output [31:0] M_PC,
  output [31:0] WB_PC,
  output [31:0] RDin,
  output [31:0] MDin,
  output [31:0] LedData
);

  wire Alu_SRC, and_1_out, and_2_out, and_3_out, and_5_out, Beq, BLTZ, Bne, Branch, CLK, clock_1_out,
       clock_2_out, comparator_1_lt, comparator_2_eq, comparator_2_lt, comparator_3_eq, d_ff_1_q, Equal, Go,
       halt, ID_MemWrite, ID_RegWrite, IR1, IR2, IR3, JAL, JMP, JR, LB, Ledin, MemToReg, nand_1_out,
       not_1_out, not_2_out, not_3_out, not_4_out, RegDst, RST, SignedExt, SRAV, SysCall, W1, W2, W3,
       \理想流水接口ex_mem_1_ex_memtoreg , \理想流水接口ex_mem_1_ex_regwrite , \理想流水接口ex_mem_1_ex_syscall ,
       \理想流水接口id_ex_1_ex_alusrc , \理想流水接口id_ex_1_ex_memtoreg , \理想流水接口id_ex_1_ex_memwrite ,
       \理想流水接口id_ex_1_ex_regwrite , \理想流水接口id_ex_1_ex_syscall , \理想流水接口mem_wb_1_ex_memtoreg ;
  wire [3:0] AluOP, \理想流水接口id_ex_1_ex_aluop ;
  wire [4:0] multiplexer_4_out, multiplexer_5_out, multiplexer_6_out, multiplexer_7_out, multiplexer_10_out,
       \理想流水接口ex_mem_1_ex_writereg , \理想流水接口id_ex_1_ex_shamt , \理想流水接口id_ex_1_ex_writereg ,
       \理想流水接口mem_wb_1_ex_writereg ;
  wire [5:0] Func;
  wire [7:0] multiplexer_12_out, multiplexer_14_out, multiplexer_14_out_2, multiplexer_14_out_3,
       multiplexer_14_out_4;
  wire [12:0] CNT_num;
  wire [15:0] \LoadUse次数 , \总周期数 , \插入气泡数 , \无条件分支数 , \条件分支成功数 ;
  wire [31:0] adder_1_out, adder_2_out, bit_extender_1_out, bit_extender_2_out, bit_extender_3_out, EX_IR,
       IF_IR, MEM_IR, mips_alu_1_result, mips_regifile_1_r1, mips_regifile_1_r2, multiplexer_1_out,
       multiplexer_2_out, multiplexer_3_out, multiplexer_8_out, multiplexer_9_out, multiplexer_13_out,
       ram_1_data, result, rs, shifter_1_out, WB_IR, \理想流水接口ex_mem_1_ex_rs , \理想流水接口id_ex_1_ex_imm ,
       \理想流水接口id_ex_1_ex_rs , \理想流水接口id_ex_1_ex_rt , \理想流水接口id_ex_1_ex_signimm ,
       \理想流水接口mem_wb_1_ex_aluresult , \理想流水接口mem_wb_1_ex_memresult ;
  wire [31:6] ID_IR;

  Button \u_总复位  (.out(RST));
  Button _1 (.out(IR1));
  Button _2 (.out(IR2));
  Button _3 (.out(IR3));
  // Probe on \总周期数 
  // Probe on \总周期数 
  Button \u_继续运行  (.out(Go));
  LED #(.active("true")) led_1 (.in(W1));
  LED #(.active("true")) led_2 (.in(W2));
  LED #(.active("true")) led_3 (.in(W3));
  not not_1 (not_1_out, halt);
  Hex_Digit_Display hex_digit_display_1 (.value(LedData[31:28]));  // open: dp
  // Probe on IF_PC[19:0]
  // Mips_Probe mips_probe_1: pin names not known; wires that end beside it: IF_IR
  Counter #(.width(16), .max('hffff), .ongoal("stay"), .trigger("rising"), .behavior("old")) counter_1 (
    .count(not_1_out), .Q(\总周期数 ), .clk(CLK));  // open: load, D, carry, clr, preset
  Hex_Digit_Display hex_digit_display_2 (.value(LedData[23:20]));  // open: dp
  Hex_Digit_Display hex_digit_display_3 (.value(LedData[27:24]));  // open: dp
  // Probe on ID_PC[19:0]
  // Mips_Probe mips_probe_2: pin names not known; wires that end beside it: {ID_IR, Func}
  Hex_Digit_Display hex_digit_display_4 (.value(LedData[15:12]));  // open: dp
  Hex_Digit_Display hex_digit_display_5 (.value(LedData[19:16]));  // open: dp
  Multiplexer #(.select(1), .width(32), .disabled("Z"), .enable("false")) multiplexer_1 (
    .in0(adder_1_out), .in1(adder_2_out), .out(multiplexer_1_out), .sel(Branch));
  Hex_Digit_Display hex_digit_display_6 (.value(LedData[11:8]));  // open: dp
  Hex_Digit_Display hex_digit_display_7 (.value(LedData[7:4]));  // open: dp
  Clock #(.highDuration(1), .lowDuration(1)) clock_1 (.out(clock_1_out));
  // Probe on EX_PC[19:0]
  // Mips_Probe mips_probe_3: pin names not known; wires that end beside it: clock_1_out, EX_IR, CLK
  Comparator #(.width(32), .mode("twosComplement")) comparator_1 (
    .a(rs), .b({32{1'b0}}), .lt(comparator_1_lt));  // open: gt, eq
  Multiplexer #(.select(1), .width(32), .disabled("Z"), .enable("false")) multiplexer_2 (
    .in0(multiplexer_1_out), .in1({4'b0000, ID_IR[25:6], Func, 2'b00}), .out(multiplexer_2_out), .sel(JMP));
  Multiplexer #(.select(1), .width(32), .disabled("Z"), .enable("false")) multiplexer_3 (
    .in0(multiplexer_2_out), .in1(\理想流水接口id_ex_1_ex_rs ), .out(multiplexer_3_out), .sel(JR));
  not not_2 (not_2_out, halt);
  Hex_Digit_Display hex_digit_display_8 (.value(LedData[3:0]));  // open: dp
  Register #(.width(32), .trigger("rising"), .Select("low")) PC (
    .D(multiplexer_3_out), .en(not_2_out), .Q(IF_PC), .clk(CLK));  // open: clr
  // Probe on \总周期数 
  // Probe on M_PC[19:0]
  // Mips_Probe mips_probe_4: pin names not known; wires that end beside it: MEM_IR
  and and_1 (and_1_out, BLTZ, comparator_1_lt);
  and and_2 (and_2_out, Equal, Beq);
  not not_3 (not_3_out, Equal);
  and and_3 (and_3_out, not_3_out, Bne);
  // Probe on \总周期数 
  // Probe on \无条件分支数 
  // Probe on \条件分支成功数 
  // Probe on \插入气泡数 
  // Probe on \LoadUse次数 
  or or_1 (Branch, and_1_out, and_2_out, and_3_out);
  Adder #(.width(32)) adder_1 (.a(IF_PC), .b(32'h4), .out(adder_1_out));  // open: cin, cout
  // Probe on IF_PC[11:0]
  // Probe on WB_PC[19:0]
  // Mips_Probe mips_probe_5: pin names not known; wires that end beside it: WB_IR
  // Mips_Probe mips_probe_6: pin names not known; wires that end beside it: IF_IR
  ROM #(.addrWidth(10), .dataWidth(32), .Select("high")) rom_1 (.addr(IF_PC[11:2]), .data(IF_IR));
  // Probe on EX_PC[11:0]
  // Probe on ID_PC[11:0]
  \理想流水接口IF_ID  \u_理想流水接口if_id_1  (.IF_IR(IF_IR), .ID_IR({ID_IR, Func}), .IF_PC(IF_PC), .ID_PC(ID_PC), .CLK(CLK));
  // Probe on M_PC[11:0]
  D_Flip_Flop #(.trigger("high"), .Pre_Clr_Positions("LEGACY"), .NegatePresetClear("false"), .enable("true"), .NewFFLayout("false")) d_ff_1 (.Q(d_ff_1_q));  // open: clk, D, Qn, preset, en, reset
  // Probe on 13'hc
  // Probe on WB_PC[11:0]
  Comparator #(.width(13), .mode("twosComplement")) comparator_2 (
    .a(CNT_num), .b(13'hc), .eq(comparator_2_eq), .lt(comparator_2_lt));  // open: gt
  Clock #(.highDuration(1), .lowDuration(1)) clock_2 (.out(clock_2_out));
  nand nand_1 (nand_1_out, d_ff_1_q, comparator_2_eq);
  Counter #(.width(13), .max('h1fff), .ongoal("stay"), .trigger("rising"), .behavior("old")) counter_2 (
    .count(comparator_2_lt), .Q(CNT_num), .clk(clock_2_out));  // open: load, D, carry, clr, preset
  \单周期硬布线控制器  \u_单周期硬布线控制器_1  (
    .Func(Func), .OP(ID_IR[31:26]), .ALU_OP(AluOP), .MemToReg(MemToReg), .MemWrite(ID_MemWrite),
    .ALU_SRC(Alu_SRC), .RegWrite(ID_RegWrite), .SysCALL(SysCall), .SignedExt(SignedExt), .RegDst(RegDst),
    .JR(JR), .JMP(JMP), .Beq(Beq), .JAL(JAL), .Bne(Bne), .SRAV(SRAV), .LB(LB), .BLTZ(BLTZ));
  Multiplexer #(.select(1), .width(5), .disabled("Z"), .enable("false")) multiplexer_4 (
    .in0(ID_IR[25:21]), .in1(5'b00010), .out(multiplexer_4_out), .sel(SysCall));
  Multiplexer #(.select(1), .width(5), .disabled("Z"), .enable("false")) multiplexer_5 (
    .in0(ID_IR[20:16]), .in1(5'b00100), .out(multiplexer_5_out), .sel(SysCall));
  assign bit_extender_1_out = {{16{1'b0}}, {ID_IR[15:6], Func}};  // Bit_Extender bit_extender_1
  assign bit_extender_2_out = {{16{ID_IR[15]}}, {ID_IR[15:6], Func}};  // Bit_Extender bit_extender_2
  Multiplexer #(.select(1), .width(5), .disabled("Z"), .enable("false")) multiplexer_6 (
    .in0(ID_IR[20:16]), .in1(ID_IR[15:11]), .out(multiplexer_6_out), .sel(RegDst));
  assign CLK = nand_1_out ? clock_2_out : 1'bz;  // Controlled_Buffer controlled_buffer_1
  Multiplexer #(.select(1), .width(5), .disabled("Z"), .enable("false")) multiplexer_7 (
    .in0(multiplexer_6_out), .in1({5{1'b1}}), .out(multiplexer_7_out), .sel(JAL));
  Pull_Resistor #(.pull(1)) pull_resistor_1 (.node(CLK));
  Multiplexer #(.select(1), .width(32), .disabled("Z"), .enable("false")) multiplexer_8 (
    .in0(bit_extender_1_out), .in1(bit_extender_2_out), .out(multiplexer_8_out), .sel(SignedExt));
  MIPS_Regifile mips_regifile_1 (
    .Din(RDin), .Clk(CLK), .R1(mips_regifile_1_r1), .R2(mips_regifile_1_r2), .WE(RegWrite),
    .W_num(\理想流水接口mem_wb_1_ex_writereg ), .R1_num(multiplexer_4_out), .R2_num(multiplexer_5_out));
  \理想流水接口ID_EX  \u_理想流水接口id_ex_1  (
    .ID_RegWrite(ID_RegWrite), .ID_MemtoReg(MemToReg), .ID_MemWrite(ID_MemWrite), .ID_AluOP(AluOP),
    .ID_AluSrc(Alu_SRC), .ID_SignImm(bit_extender_2_out), .ID_WriteReg(multiplexer_7_out),
    .EX_RegWrite(\理想流水接口id_ex_1_ex_regwrite ), .EX_MemtoReg(\理想流水接口id_ex_1_ex_memtoreg ),
    .EX_MemWrite(\理想流水接口id_ex_1_ex_memwrite ), .EX_AluOP(\理想流水接口id_ex_1_ex_aluop ),
    .EX_AluSrc(\理想流水接口id_ex_1_ex_alusrc ), .EX_SignImm(\理想流水接口id_ex_1_ex_signimm ),
    .EX_WriteReg(\理想流水接口id_ex_1_ex_writereg ), .CLK(CLK), .ID_rs(mips_regifile_1_r1),
    .EX_rs(\理想流水接口id_ex_1_ex_rs ), .ID_rt(mips_regifile_1_r2), .EX_rt(\理想流水接口id_ex_1_ex_rt ),
    .ID_shamt(ID_IR[10:6]), .EX_shamt(\理想流水接口id_ex_1_ex_shamt ), .ID_Imm(multiplexer_8_out),
    .EX_Imm(\理想流水接口id_ex_1_ex_imm ), .ID_PC(ID_PC), .EX_PC(EX_PC), .ID_IR({ID_IR, Func}), .EX_IR(EX_IR),
    .ID_Syscall(SysCall), .EX_Syscall(\理想流水接口id_ex_1_ex_syscall ));
  Multiplexer #(.select(1), .width(32), .disabled("Z"), .enable("false")) multiplexer_9 (
    .in0(\理想流水接口id_ex_1_ex_rt ), .in1(\理想流水接口id_ex_1_ex_imm ), .out(multiplexer_9_out),
    .sel(\理想流水接口id_ex_1_ex_alusrc ));
  Shifter #(.width(32), .shift("ll")) shifter_1 (
    .in(\理想流水接口id_ex_1_ex_signimm ), .\dist (5'b00010), .out(shifter_1_out));
  Multiplexer #(.select(1), .width(5), .disabled("Z"), .enable("false")) multiplexer_10 (
    .in0(\理想流水接口id_ex_1_ex_shamt ), .in1(rs[4:0]), .out(multiplexer_10_out), .sel(SRAV));
  Adder #(.width(32)) adder_2 (.a(shifter_1_out), .b(EX_PC), .out(adder_2_out));  // open: cin, cout
  MIPS_ALU mips_alu_1 (
    .X(\理想流水接口id_ex_1_ex_rs ), .Y(multiplexer_9_out), .AluOP(\理想流水接口id_ex_1_ex_aluop ), .Equal(Equal),
    .Result(mips_alu_1_result), .shamt(multiplexer_10_out));  // open: Result_2
  Multiplexer #(.select(1), .width(32), .disabled("Z"), .enable("false")) multiplexer_11 (
    .in0({multiplexer_14_out_4, multiplexer_14_out_3, multiplexer_14_out_2, multiplexer_14_out}),
    .in1(bit_extender_3_out), .out(RDin), .sel(LB));
  \理想流水接口EX_MEM  \u_理想流水接口ex_mem_1  (
    .ID_RegWrite(\理想流水接口id_ex_1_ex_regwrite ), .ID_MemtoReg(\理想流水接口id_ex_1_ex_memtoreg ),
    .ID_MemWrite(\理想流水接口id_ex_1_ex_memwrite ), .ID_result(mips_alu_1_result),
    .ID_MDin(\理想流水接口id_ex_1_ex_rt ), .ID_PC(EX_PC), .ID_WriteReg(\理想流水接口id_ex_1_ex_writereg ),
    .EX_RegWrite(\理想流水接口ex_mem_1_ex_regwrite ), .EX_MemtoReg(\理想流水接口ex_mem_1_ex_memtoreg ),
    .EX_MemWrite(MemWrite), .EX_result(result), .EX_MDin(MDin), .EX_PC(M_PC),
    .EX_WriteReg(\理想流水接口ex_mem_1_ex_writereg ), .CLK(CLK), .ID_IR(EX_IR), .EX_IR(MEM_IR),
    .ID_rs(\理想流水接口id_ex_1_ex_rs ), .EX_rs(\理想流水接口ex_mem_1_ex_rs ), .ID_Syscall(\理想流水接口id_ex_1_ex_syscall ),
    .EX_Syscall(\理想流水接口ex_mem_1_ex_syscall ));
  assign bit_extender_3_out = {{24{multiplexer_12_out[7]}}, multiplexer_12_out};  // Bit_Extender bit_extender_3
  Multiplexer #(.select(2), .width(8), .disabled("Z"), .enable("false")) multiplexer_12 (
    .in0(multiplexer_14_out), .in1(multiplexer_14_out_2), .in2(multiplexer_14_out_3),
    .in3(multiplexer_14_out_4), .out(multiplexer_12_out), .sel(result[1:0]));
  Register #(.width(32), .trigger("rising"), .Select("low")) register_1 (
    .D(MDin), .en(Ledin), .Q(LedData), .clk(CLK));  // open: clr
  RAM #(.addrWidth(10), .dataWidth(32), .bus("separate"), .Select("high")) ram_1 (
    .addr(result[11:2]), .din(MDin), .data(ram_1_data), .str(MemWrite), .clk(CLK), .ld(1'b1));  // open: sel, clr
  \理想流水接口MEM_WB  \u_理想流水接口mem_wb_1  (
    .ID_RegWrite(\理想流水接口ex_mem_1_ex_regwrite ), .ID_MemtoReg(\理想流水接口ex_mem_1_ex_memtoreg ),
    .ID_AluResult(result), .ID_MemResult(ram_1_data), .ID_PC(M_PC),
    .ID_WriteReg(\理想流水接口ex_mem_1_ex_writereg ), .EX_RegWrite(RegWrite),
    .EX_MemtoReg(\理想流水接口mem_wb_1_ex_memtoreg ), .EX_AluResult(\理想流水接口mem_wb_1_ex_aluresult ),
    .EX_MemResult(\理想流水接口mem_wb_1_ex_memresult ), .EX_PC(WB_PC), .EX_WriteReg(\理想流水接口mem_wb_1_ex_writereg ),
    .CLK(CLK), .ID_IR(MEM_IR), .EX_IR(WB_IR), .ID_rs(\理想流水接口ex_mem_1_ex_rs ),
    .ID_Syscall(\理想流水接口ex_mem_1_ex_syscall ));  // open: EX_rs, EX_Syscall
  Comparator #(.width(32), .mode("twosComplement")) comparator_3 (
    .a(32'h22), .b(\理想流水接口ex_mem_1_ex_rs ), .eq(comparator_3_eq));  // open: gt, lt
  Multiplexer #(.select(1), .width(32), .disabled("Z"), .enable("false")) multiplexer_13 (
    .in0(\理想流水接口mem_wb_1_ex_aluresult ), .in1(\理想流水接口mem_wb_1_ex_memresult ), .out(multiplexer_13_out),
    .sel(\理想流水接口mem_wb_1_ex_memtoreg ));
  and and_4 (Ledin, \理想流水接口ex_mem_1_ex_syscall , comparator_3_eq);
  and and_5 (and_5_out, \理想流水接口ex_mem_1_ex_syscall , not_4_out);
  not not_4 (not_4_out, comparator_3_eq);
  Multiplexer #(.select(1), .width(32), .disabled("Z"), .enable("false")) multiplexer_14 (
    .in0(multiplexer_13_out), .in1(WB_PC),
    .out({multiplexer_14_out_4, multiplexer_14_out_3, multiplexer_14_out_2, multiplexer_14_out}), .sel(JAL));
  Register #(.width(1), .trigger("rising"), .Select("low")) register_2 (
    .D(\理想流水接口ex_mem_1_ex_syscall ), .en(and_5_out), .Q(halt), .clk(CLK), .clr(Go));

  // Other names for the same wires on the sheet: ID_IR[5:0] = Func; OP[5:0] = ID_IR[31:26]; IR[31:0] = IF_IR;
  //   MEM_PC[31:0] = M_PC; PC[31:0] = IF_PC

  // Notes on the sheet:
  //   中断源
  //   时空图监测，可删除
  //   中断等待指示
  //   数码管输出
  //   指令存储器
  //   指令字
  //   contents of rom_1 (hex, n*v repeats v):
  //   20100000 20110000 20120000 20130000 36100000 36310001 36520002 36730003 ae100000 ae110004 ae120008
  //   ae13000c 2002000a 20110000 20120000 20130000 c
  //   控制位
  //   流水调试日志用
  //   暂停节拍，不能为0
  //   OP
  //   Func
  //   戳工具置1进入计数暂停模式，ctrl+k时钟自动运行到对应节拍暂停
  //   ctrl+k关闭时钟连续运行，将控制位置零，进入单步调试模式调试
  //   用这个时钟源需要去掉电路中的其他时钟源
  //   rs
  //   rt
  //   shamt
  //   rt
  //   rd
  //   可计数暂停的时钟源
  //   为方便自动评测，需要输出流水线各段保存的PC值，注意是PC不是PC+4，另外ID段寄存器写入信息，Mem段内存写入信息也要输出
endmodule

module \气泡流水线  (
  output RegWrite,
  output MemWrite,
  output [31:0] IF_PC,
  output [31:0] ID_PC,
  output [31:0] EX_PC,
  output [31:0] M_PC,
  output [31:0] WB_PC,
  output [31:0] RDin,
  output [31:0] MDin,
  output [31:0] LedData
);

  wire and_1_out, and_2_out, and_3_out, and_4_out, and_6_out, Branch, BranchTaken, CLK, clock_1_out,
       clock_2_out, comparator_1_eq, comparator_1_lt, comparator_2_lt, comparator_3_eq, d_ff_1_q, Equal,
       EX_Beq, EX_BLTZ, EX_Bne, EX_JMP, EX_JR, Go, halt, ID_Alu_SRC, ID_Beq, ID_BLTZ, ID_Bne, ID_JAL, ID_JMP,
       ID_JR, ID_LB, ID_MemToReg, ID_MemWrite, ID_RegDst, ID_RegWrite, ID_SRAV, ID_SysCall, IR1, IR2, IR3,
       Ledin, nand_1_out, not_1_out, not_2_out, not_3_out, RST, SignedExt, Stall, W1, W2, W3, WB_LB,
       \气泡流水接口ex_mem_1_mem_jal , \气泡流水接口ex_mem_1_mem_lb , \气泡流水接口ex_mem_1_mem_memtoreg ,
       \气泡流水接口ex_mem_1_mem_regwrite , \气泡流水接口ex_mem_1_mem_syscall , \气泡流水接口id_ex_1_ex_alusrc ,
       \气泡流水接口id_ex_1_ex_jal , \气泡流水接口id_ex_1_ex_lb , \气泡流水接口id_ex_1_ex_memtoreg ,
       \气泡流水接口id_ex_1_ex_memwrite , \气泡流水接口id_ex_1_ex_regwrite , \气泡流水接口id_ex_1_ex_srav ,
       \气泡流水接口id_ex_1_ex_syscall , \气泡流水接口mem_wb_1_p8 , \气泡流水接口mem_wb_1_p15 , \气泡流水接口mem_wb_1_p16 ,
       \相关处理逻辑_1_flush ;
  wire [3:0] ID_AluOP, \气泡流水接口id_ex_1_ex_aluop ;
  wire [4:0] EX_WriteReg, MEM_WriteReg, multiplexer_4_out, multiplexer_5_out, multiplexer_6_out,
       multiplexer_7_out, multiplexer_10_out, \气泡流水接口id_ex_1_ex_shamt , \气泡流水接口mem_wb_1_p21 ;
  wire [5:0] Func;
  wire [7:0] multiplexer_13_out, multiplexer_13_out_2, multiplexer_13_out_3, multiplexer_13_out_4,
       multiplexer_14_out;
  wire [12:0] CNT_num;
  wire [15:0] \LoadUse次数 , \总周期数 , \插入气泡数 , \无条件分支数 , \条件分支成功数 ;
  wire [31:0] adder_1_out, adder_2_out, bit_extender_1_out, bit_extender_2_out, bit_extender_3_out, EX_IR,
       EX_RS, IF_IR, MEM_IR, mips_alu_1_result, \mips_regifile_下降沿_1_r1 , \mips_regifile_下降沿_1_r2 ,
       multiplexer_1_out, multiplexer_2_out, multiplexer_3_out, multiplexer_8_out, multiplexer_9_out,
       multiplexer_12_out, ram_1_data, result, shifter_1_out, WB_IR, \气泡流水接口ex_mem_1_mem_pc ,
       \气泡流水接口ex_mem_1_mem_result , \气泡流水接口ex_mem_1_mem_rs , \气泡流水接口id_ex_1_ex_addr , \气泡流水接口id_ex_1_ex_imm ,
       \气泡流水接口id_ex_1_ex_pc_2 , \气泡流水接口id_ex_1_ex_rt , \气泡流水接口id_ex_1_ex_signimm , \气泡流水接口if_id_1_id_pc ,
       \气泡流水接口mem_wb_1_p19 , \气泡流水接口mem_wb_1_p20 ;
  wire [31:6] ID_IR;

  Button \u_总复位  (.out(RST));
  Button _1 (.out(IR1));
  Button _2 (.out(IR2));
  Button _3 (.out(IR3));
  // Probe on \总周期数 
  // Probe on \总周期数 
  Button \u_继续运行  (.out(Go));
  LED #(.active("true")) led_1 (.in(W1));
  LED #(.active("true")) led_2 (.in(W2));
  LED #(.active("true")) led_3 (.in(W3));
  Hex_Digit_Display hex_digit_display_1 (.value(LedData[31:28]));  // open: dp
  // Probe on IF_PC[19:0]
  // Mips_Probe mips_probe_1: pin names not known; wires that end beside it: IF_IR
  Hex_Digit_Display hex_digit_display_2 (.value(LedData[27:24]));  // open: dp
  Hex_Digit_Display hex_digit_display_3 (.value(LedData[23:20]));  // open: dp
  // Probe on ID_PC[19:0]
  // Mips_Probe mips_probe_2: pin names not known; wires that end beside it: {ID_IR, Func}
  Hex_Digit_Display hex_digit_display_4 (.value(LedData[19:16]));  // open: dp
  Hex_Digit_Display hex_digit_display_5 (.value(LedData[15:12]));  // open: dp
  Hex_Digit_Display hex_digit_display_6 (.value(LedData[11:8]));  // open: dp
  Hex_Digit_Display hex_digit_display_7 (.value(LedData[7:4]));  // open: dp
  Clock #(.highDuration(1), .lowDuration(1)) clock_1 (.out(clock_1_out));
  // Probe on EX_PC[19:0]
  // Mips_Probe mips_probe_3: pin names not known; wires that end beside it: clock_1_out, EX_IR, CLK
  Multiplexer #(.select(1), .width(32), .disabled("Z"), .enable("false")) multiplexer_1 (
    .in0(adder_1_out), .in1(adder_2_out), .out(multiplexer_1_out), .sel(Branch));
  Hex_Digit_Display hex_digit_display_8 (.value(LedData[3:0]));  // open: dp
  Multiplexer #(.select(1), .width(32), .disabled("Z"), .enable("false")) multiplexer_2 (
    .in0(multiplexer_1_out), .in1(\气泡流水接口id_ex_1_ex_addr ), .out(multiplexer_2_out), .sel(EX_JMP));
  // Probe on \总周期数 
  // Probe on M_PC[19:0]
  // Mips_Probe mips_probe_4: pin names not known; wires that end beside it: MEM_IR
  and and_1 (and_1_out, ~halt, ~Stall);  // AND_Gate
  Register #(.width(32), .trigger("rising"), .Select("low")) PC (
    .D(multiplexer_3_out), .en(and_1_out), .Q(IF_PC), .clk(CLK));  // open: clr
  Multiplexer #(.select(1), .width(32), .disabled("Z"), .enable("false")) multiplexer_3 (
    .in0(multiplexer_2_out), .in1(EX_RS), .out(multiplexer_3_out), .sel(EX_JR));
  // Probe on \总周期数 
  // Probe on \无条件分支数 
  // Probe on \条件分支成功数 
  // Probe on \插入气泡数 
  // Probe on \LoadUse次数 
  // Probe on IF_PC[11:0]
  // Probe on WB_PC[19:0]
  // Mips_Probe mips_probe_5: pin names not known; wires that end beside it: WB_IR
  Counter #(.width(16), .max('hffff), .ongoal("stay"), .trigger("rising"), .behavior("old")) counter_1 (
    .count(Stall), .Q(\插入气泡数 ), .clk(CLK));  // open: load, D, carry, clr, preset
  \单周期硬布线控制器  \u_单周期硬布线控制器_1  (
    .Func(Func), .OP(ID_IR[31:26]), .ALU_OP(ID_AluOP), .MemToReg(ID_MemToReg), .MemWrite(ID_MemWrite),
    .ALU_SRC(ID_Alu_SRC), .RegWrite(ID_RegWrite), .SysCALL(ID_SysCall), .SignedExt(SignedExt),
    .RegDst(ID_RegDst), .JR(ID_JR), .JMP(ID_JMP), .Beq(ID_Beq), .JAL(ID_JAL), .Bne(ID_Bne), .SRAV(ID_SRAV),
    .LB(ID_LB), .BLTZ(ID_BLTZ));
  Adder #(.width(32)) adder_1 (.a(IF_PC), .b(32'h4), .out(adder_1_out));  // open: cin, cout
  // Probe on ID_PC[11:0]
  // Probe on EX_PC[11:0]
  // Mips_Probe mips_probe_6: pin names not known; wires that end beside it: IF_IR
  ROM #(.addrWidth(10), .dataWidth(32), .Select("high")) rom_1 (.addr(IF_PC[11:2]), .data(IF_IR));
  // Probe on M_PC[11:0]
  D_Flip_Flop #(.trigger("high"), .Pre_Clr_Positions("LEGACY"), .NegatePresetClear("false"), .enable("true"), .NewFFLayout("false")) d_ff_1 (.Q(d_ff_1_q));  // open: clk, D, Qn, preset, en, reset
  // Probe on 13'h9f
  \相关处理逻辑  \u_相关处理逻辑_1  (
    .EX_RegWrite(\气泡流水接口id_ex_1_ex_regwrite ), .BranchTaken(BranchTaken), .Instr({ID_IR, Func}),
    .MEM_RegWrite(\气泡流水接口ex_mem_1_mem_regwrite ), .EX_WriteReg_num(EX_WriteReg),
    .MEM_WriteReg_num(MEM_WriteReg), .Stall(Stall), .Flush(\相关处理逻辑_1_flush ), .R1(multiplexer_4_out),
    .R2(multiplexer_5_out));
  \气泡流水接口IF_ID  \u_气泡流水接口if_id_1  (
    .IF_IR(IF_IR), .IF_PC(adder_1_out), .ID_IR({ID_IR, Func}), .ID_PC(\气泡流水接口if_id_1_id_pc ), .CLK(CLK),
    .\同步清零_气泡_高电平有效 (BranchTaken), .\使能端_为高电平时忽略时钟输入 (Stall), .IF_monitor(IF_PC), .ID_monitor(ID_PC));  // open: IF_PredictJump, ID_PredictJump
  // Probe on WB_PC[11:0]
  Comparator #(.width(13), .mode("twosComplement")) comparator_1 (
    .a(CNT_num), .b(13'h9f), .eq(comparator_1_eq), .lt(comparator_1_lt));  // open: gt
  Clock #(.highDuration(1), .lowDuration(1)) clock_2 (.out(clock_2_out));
  Counter #(.width(16), .max('hffff), .ongoal("stay"), .trigger("rising"), .behavior("old")) counter_2 (
    .count(not_1_out), .Q(\总周期数 ), .clk(CLK));  // open: load, D, carry, clr, preset
  not not_1 (not_1_out, halt);
  nand nand_1 (nand_1_out, d_ff_1_q, comparator_1_eq);
  Counter #(.width(13), .max('h1fff), .ongoal("stay"), .trigger("rising"), .behavior("old")) counter_3 (
    .count(comparator_1_lt), .Q(CNT_num), .clk(clock_2_out));  // open: load, D, carry, clr, preset
  // Probe on {ID_IR, Func}
  assign CLK = nand_1_out ? clock_2_out : 1'bz;  // Controlled_Buffer controlled_buffer_1
  Multiplexer #(.select(1), .width(5), .disabled("Z"), .enable("false")) multiplexer_4 (
    .in0(ID_IR[25:21]), .in1(5'b00010), .out(multiplexer_4_out), .sel(ID_SysCall));
  Multiplexer #(.select(1), .width(5), .disabled("Z"), .enable("false")) multiplexer_5 (
    .in0(ID_IR[20:16]), .in1(5'b00100), .out(multiplexer_5_out), .sel(ID_SysCall));
  Multiplexer #(.select(1), .width(5), .disabled("Z"), .enable("false")) multiplexer_6 (
    .in0(ID_IR[20:16]), .in1(ID_IR[15:11]), .out(multiplexer_6_out), .sel(ID_RegDst));
  Pull_Resistor #(.pull(1)) pull_resistor_1 (.node(CLK));
  // Probe on multiplexer_4_out
  // Probe on multiplexer_5_out
  assign bit_extender_1_out = {{16{1'b0}}, {ID_IR[15:6], Func}};  // Bit_Extender bit_extender_1
  assign bit_extender_2_out = {{16{ID_IR[15]}}, {ID_IR[15:6], Func}};  // Bit_Extender bit_extender_2
  Multiplexer #(.select(1), .width(5), .disabled("Z"), .enable("false")) multiplexer_7 (
    .in0(multiplexer_6_out), .in1({5{1'b1}}), .out(multiplexer_7_out), .sel(ID_JAL));
  Comparator #(.width(32), .mode("twosComplement")) comparator_2 (
    .a(EX_RS), .b({32{1'b0}}), .lt(comparator_2_lt));  // open: gt, eq
  Multiplexer #(.select(1), .width(32), .disabled("Z"), .enable("false")) multiplexer_8 (
    .in0(bit_extender_1_out), .in1(bit_extender_2_out), .out(multiplexer_8_out), .sel(SignedExt));
  \MIPS_Regifile_下降沿  \mips_regifile_下降沿_1  (
    .Din(RDin), .Clk(CLK), .R1(\mips_regifile_下降沿_1_r1 ), .R2(\mips_regifile_下降沿_1_r2 ), .WE(RegWrite),
    .W_num(\气泡流水接口mem_wb_1_p21 ), .R1_num(multiplexer_4_out), .R2_num(multiplexer_5_out));
  not not_2 (not_2_out, Equal);
  and and_2 (and_2_out, EX_BLTZ, comparator_2_lt);
  and and_3 (and_3_out, Equal, EX_Beq);
  and and_4 (and_4_out, not_2_out, EX_Bne);
  \气泡流水接口ID_EX  \u_气泡流水接口id_ex_1  (
    .ID_RegWrite(ID_RegWrite), .ID_MemToReg(ID_MemToReg), .ID_JAL(ID_JAL), .ID_LB(ID_LB),
    .ID_MemWrite(ID_MemWrite), .ID_Beq(ID_Beq), .ID_Bne(ID_Bne), .ID_JMP(ID_JMP), .ID_JR(ID_JR),
    .ID_BLTZ(ID_BLTZ), .ID_Syscall(ID_SysCall), .ID_AluOP(ID_AluOP), .ID_AluSRC(ID_Alu_SRC),
    .ID_SRAV(ID_SRAV), .ID_RS(\mips_regifile_下降沿_1_r1 ), .ID_RT(\mips_regifile_下降沿_1_r2 ),
    .ID_shamt(ID_IR[10:6]), .ID_Imm(multiplexer_8_out), .ID_SignImm(bit_extender_2_out),
    .ID_PC(\气泡流水接口if_id_1_id_pc ), .ID_WriteReg(multiplexer_7_out), .ID_IR({ID_IR, Func}), .CLK(CLK),
    .EX_RegWrite(\气泡流水接口id_ex_1_ex_regwrite ), .EX_MemToReg(\气泡流水接口id_ex_1_ex_memtoreg ),
    .EX_JAL(\气泡流水接口id_ex_1_ex_jal ), .EX_LB(\气泡流水接口id_ex_1_ex_lb ),
    .EX_MemWrite(\气泡流水接口id_ex_1_ex_memwrite ), .EX_Beq(EX_Beq), .EX_PC(EX_Bne), .EX_JMP(EX_JMP),
    .EX_JR(EX_JR), .ID_BLTZ_2(EX_BLTZ), .EX_Syscall(\气泡流水接口id_ex_1_ex_syscall ),
    .EX_AluOP(\气泡流水接口id_ex_1_ex_aluop ), .EX_AluSRC(\气泡流水接口id_ex_1_ex_alusrc ),
    .EX_SRAV(\气泡流水接口id_ex_1_ex_srav ), .EX_RS(EX_RS), .EX_RT(\气泡流水接口id_ex_1_ex_rt ),
    .EX_shamt(\气泡流水接口id_ex_1_ex_shamt ), .EX_Imm(\气泡流水接口id_ex_1_ex_imm ),
    .EX_SignImm(\气泡流水接口id_ex_1_ex_signimm ), .EX_PC_2(\气泡流水接口id_ex_1_ex_pc_2 ), .EX_WriteReg(EX_WriteReg),
    .EX_IR(EX_IR), .\同步清零_气泡_高电平有效 (\相关处理逻辑_1_flush ), .ID_addr({4'b0000, ID_IR[25:6], Func, 2'b00}),
    .EX_addr(\气泡流水接口id_ex_1_ex_addr ), .ID_monitor(ID_PC), .EX_monitor(EX_PC));  // open: 使能端_为高电平时忽略时钟输入
  or or_1 (Branch, and_2_out, and_3_out, and_4_out);
  // Probe on EX_WriteReg
  // Probe on EX_WriteReg
  Multiplexer #(.select(1), .width(32), .disabled("Z"), .enable("false")) multiplexer_9 (
    .in0(\气泡流水接口id_ex_1_ex_rt ), .in1(\气泡流水接口id_ex_1_ex_imm ), .out(multiplexer_9_out),
    .sel(\气泡流水接口id_ex_1_ex_alusrc ));
  // Probe on \气泡流水接口id_ex_1_ex_pc_2 
  Multiplexer #(.select(1), .width(5), .disabled("Z"), .enable("false")) multiplexer_10 (
    .in0(\气泡流水接口id_ex_1_ex_shamt ), .in1(EX_RS[4:0]), .out(multiplexer_10_out), .sel(\气泡流水接口id_ex_1_ex_srav ));
  Shifter #(.width(32), .shift("ll")) shifter_1 (
    .in(\气泡流水接口id_ex_1_ex_signimm ), .\dist (5'b00010), .out(shifter_1_out));
  // Probe on EX_RS
  MIPS_ALU mips_alu_1 (
    .X(EX_RS), .Y(multiplexer_9_out), .AluOP(\气泡流水接口id_ex_1_ex_aluop ), .Equal(Equal),
    .Result(mips_alu_1_result), .shamt(multiplexer_10_out));  // open: Result_2
  Adder #(.width(32)) adder_2 (.a(shifter_1_out), .b(\气泡流水接口id_ex_1_ex_pc_2 ), .out(adder_2_out));  // open: cin, cout
  // Probe on adder_2_out
  or or_2 (BranchTaken, Branch, EX_JMP);
  \气泡流水接口EX_MEM  \u_气泡流水接口ex_mem_1  (
    .EX_RegWrite(\气泡流水接口id_ex_1_ex_regwrite ), .EX_MemToReg(\气泡流水接口id_ex_1_ex_memtoreg ),
    .EX_JAL(\气泡流水接口id_ex_1_ex_jal ), .EX_LB(\气泡流水接口id_ex_1_ex_lb ),
    .EX_MemWrite(\气泡流水接口id_ex_1_ex_memwrite ), .EX_Syscall(\气泡流水接口id_ex_1_ex_syscall ),
    .EX_MDin(\气泡流水接口id_ex_1_ex_rt ), .EX_PC(\气泡流水接口id_ex_1_ex_pc_2 ), .EX_WriteReg(EX_WriteReg),
    .EX_IR(EX_IR), .CLK(CLK), .MEM_RegWrite(\气泡流水接口ex_mem_1_mem_regwrite ),
    .MEM_MemToReg(\气泡流水接口ex_mem_1_mem_memtoreg ), .MEM_JAL(\气泡流水接口ex_mem_1_mem_jal ),
    .MEM_LB(\气泡流水接口ex_mem_1_mem_lb ), .MEM_MemWrite(MemWrite), .MEM_Syscall(\气泡流水接口ex_mem_1_mem_syscall ),
    .MEM_MDin(MDin), .MEM_PC(\气泡流水接口ex_mem_1_mem_pc ), .MEM_WriteReg(MEM_WriteReg), .MEM_IR(MEM_IR),
    .EX_result(mips_alu_1_result), .MEM_result(\气泡流水接口ex_mem_1_mem_result ), .EX_RS(EX_RS),
    .MEM_RS(\气泡流水接口ex_mem_1_mem_rs ), .EX_monitor(EX_PC), .MEM_monitor(M_PC));  // open: 同步清零_气泡_高电平有效, 使能端_低电平有效_stall_高电平有效
  // Probe on \气泡流水接口ex_mem_1_mem_rs 
  // Probe on MEM_WriteReg
  Register #(.width(32), .trigger("rising"), .Select("low")) register_1 (
    .D(MDin), .en(Ledin), .Q(LedData), .clk(CLK));  // open: clr
  // Probe on MEM_WriteReg
  // Probe on RDin
  RAM #(.addrWidth(10), .dataWidth(32), .bus("separate"), .Select("high")) ram_1 (
    .addr(\气泡流水接口ex_mem_1_mem_result [11:2]), .din(MDin), .data(ram_1_data), .str(MemWrite), .clk(CLK),
    .ld(1'b1));  // open: sel, clr
  // 气泡流水接口MEM_WB 气泡流水接口mem_wb_1: pin names not known; wires that end beside it: \气泡流水接口ex_mem_1_mem_regwrite , \气泡流水接口ex_mem_1_mem_memtoreg , \气泡流水接口ex_mem_1_mem_jal , \气泡流水接口ex_mem_1_mem_lb , \气泡流水接口ex_mem_1_mem_result , ram_1_data, \气泡流水接口ex_mem_1_mem_pc , \气泡流水接口mem_wb_1_p8 , MEM_WriteReg, MEM_IR, M_PC, \气泡流水接口mem_wb_1_p8 , CLK, RegWrite, \气泡流水接口mem_wb_1_p15 , \气泡流水接口mem_wb_1_p16 , WB_LB, result, \气泡流水接口mem_wb_1_p19 , \气泡流水接口mem_wb_1_p20 , \气泡流水接口mem_wb_1_p21 , WB_IR, WB_PC
  Multiplexer #(.select(1), .width(32), .disabled("Z"), .enable("false")) multiplexer_11 (
    .in0({multiplexer_13_out_4, multiplexer_13_out_3, multiplexer_13_out_2, multiplexer_13_out}),
    .in1(bit_extender_3_out), .out(RDin), .sel(WB_LB));
  assign bit_extender_3_out = {{24{multiplexer_14_out[7]}}, multiplexer_14_out};  // Bit_Extender bit_extender_3
  Multiplexer #(.select(1), .width(32), .disabled("Z"), .enable("false")) multiplexer_12 (
    .in0(result), .in1(\气泡流水接口mem_wb_1_p19 ), .out(multiplexer_12_out), .sel(\气泡流水接口mem_wb_1_p15 ));
  Multiplexer #(.select(1), .width(32), .disabled("Z"), .enable("false")) multiplexer_13 (
    .in0(multiplexer_12_out), .in1(\气泡流水接口mem_wb_1_p20 ),
    .out({multiplexer_13_out_4, multiplexer_13_out_3, multiplexer_13_out_2, multiplexer_13_out}),
    .sel(\气泡流水接口mem_wb_1_p16 ));
  Multiplexer #(.select(2), .width(8), .disabled("Z"), .enable("false")) multiplexer_14 (
    .in0(multiplexer_13_out), .in1(multiplexer_13_out_2), .in2(multiplexer_13_out_3),
    .in3(multiplexer_13_out_4), .out(multiplexer_14_out), .sel(result[1:0]));
  Comparator #(.width(32), .mode("twosComplement")) comparator_3 (
    .a(32'h22), .b(\气泡流水接口ex_mem_1_mem_rs ), .eq(comparator_3_eq));  // open: gt, lt
  and and_5 (Ledin, \气泡流水接口ex_mem_1_mem_syscall , comparator_3_eq);
  and and_6 (and_6_out, \气泡流水接口ex_mem_1_mem_syscall , not_3_out);
  not not_3 (not_3_out, comparator_3_eq);
  Register #(.width(1), .trigger("rising"), .Select("low")) register_2 (
    .D(\气泡流水接口ex_mem_1_mem_syscall ), .en(and_6_out), .Q(halt), .clk(CLK), .clr(Go));

  // Other names for the same wires on the sheet: ID_IR[5:0] = Func; OP[5:0] = ID_IR[31:26]; IR[31:0] = IF_IR;
  //   MEM_PC[31:0] = M_PC; PC[31:0] = IF_PC

  // Notes on the sheet:
  //   中断源
  //   时空图监测，可删除
  //   中断等待指示
  //   数码管输出
  //   指令存储器
  //   控制位
  //   指令字
  //   contents of rom_1 (hex, n*v repeats v):
  //   20110001 8000c05 20110001 20120002 20130003 8000c09 20110001 20120002 20130003 8000c0d 20110001
  //   20120002 20130003 8000c11 20110001 20120002 20130003 c000cb8 20100001 20110001 118fc0 112020
  //   20020022 c 118882 12200001 8000c15 112020 20020022 c 20110001 118880 112020 20020022 c 12200001
  //   8000c1f 20110001 118fc0 112020 20020022 c 1188c3 112020 20020022 c 118903 112020 20020022 c 118903
  //   112020 20020022 c 118903 112020 20020022 c 118903 112020 20020022 c 118903 112020 20020022 c 118903
  //   112020 20020022 c 118903 112020 20020022 c 20100001 109fc0 139fc3 8021 2012000c 24160003 26100001
  //   3210000f 20080008 20090001 139900 2709825 132020 20020022 c 1094022 1500fff9 22100001 2018000f
  //   2188024 108700 20080008 20090001 139902 2709825 132021 20020022 c 1094022 1500fff9 108702 2c9b022
  //   12c00001 8000c50 4020 1084027 84400 3508ffff 82021 20020022 c 2010ffff 20110000 ae300000 22100001
  //   22310004 ae300000 22100001 22310004 ae300000 22100001 22310004 ae300000 22100001 22310004 ae300000
  //   22100001 22310004 ae300000 22100001 22310004 ae300000 22100001 22310004 ae300000 22100001 22310004
  //   ae300000 22100001 22310004 ae300000 22100001 22310004 ae300000 22100001 22310004 ae300000 22100001
  //   22310004 ae300000 22100001 22310004 ae300000 22100001 22310004 ae300000 22100001 22310004 ae300000
  //   22100001 22310004 22100001 8020 2011003c 8e130000 8e340000 274402a 11000002 ae330000 ae140000
  //   2231fffc 1611fff8 102020 20020022 c 22100004 2011003c 1611fff2 20020032 c 20100000 22100001 102020
  //   20020022 c 22100002 102020 20020022 c 22100003 102020 20020022 c 22100004 102020 20020022 c 22100005
  //   102020 20020022 c 22100006 102020 20020022 c 22100007 102020 20020022 c 22100008 102020 20020022
  //   20020022 c 3e00008
  //   流水调试日志用
  //   暂停节拍，不能为0
  //   戳工具置1进入计数暂停模式，ctrl+k时钟自动运行到对应节拍暂停
  //   ctrl+k关闭时钟连续运行，将控制位置零，进入单步调试模式调试
  //   Func
  //   OP
  //   rs
  //   rt
  //   shamt
  //   rt
  //   rd
  //   可计数暂停的时钟源
  //   为方便自动评测，需要输出流水线各段保存的PC值，注意是PC不是PC+4，另外ID段寄存器写入信息，Mem段内存写入信息也要输出
endmodule
module \重定向流水线  (
  output RegWrite,
  output MemWrite,
  output [31:0] IF_PC,
  output [31:0] ID_PC,
  output [31:0] EX_PC,
  output [31:0] M_PC,
  output [31:0] WB_PC,
  output [31:0] RDin,
  output [31:0] MDin,
  output [31:0] LedData
);

  wire and_1_out, and_2_out, and_3_out, and_4_out, and_6_out, Branch, BranchTaken, CLK, clock_1_out,
       clock_2_out, comparator_1_eq, comparator_1_lt, comparator_2_lt, comparator_3_eq, d_ff_1_q, Equal,
       EX_Beq, EX_BLTZ, EX_Bne, EX_JMP, EX_JR, Go, halt, ID_Alu_SRC, ID_Beq, ID_BLTZ, ID_Bne, ID_JAL, ID_JMP,
       ID_JR, ID_LB, ID_MemToReg, ID_MemWrite, ID_RegDst, ID_RegWrite, ID_SRAV, ID_SysCall, IR1, IR2, IR3,
       Ledin, LoadUse, nand_1_out, not_1_out, not_2_out, not_3_out, RST, SignedExt, Stall, W1, W2, W3, WB_LB,
       \相关处理逻辑_重定向_1_flush , \重定向流水接口ex_mem_1_mem_jal , \重定向流水接口ex_mem_1_mem_lb ,
       \重定向流水接口ex_mem_1_mem_memtoreg , \重定向流水接口ex_mem_1_mem_regwrite , \重定向流水接口ex_mem_1_mem_syscall ,
       \重定向流水接口id_ex_1_ex_alusrc , \重定向流水接口id_ex_1_ex_jal , \重定向流水接口id_ex_1_ex_lb ,
       \重定向流水接口id_ex_1_ex_memtoreg , \重定向流水接口id_ex_1_ex_memwrite , \重定向流水接口id_ex_1_ex_regwrite ,
       \重定向流水接口id_ex_1_ex_srav , \重定向流水接口id_ex_1_ex_syscall , \重定向流水接口mem_wb_1_wb_jal ,
       \重定向流水接口mem_wb_1_wb_memtoreg ;
  wire [1:0] \相关处理逻辑_重定向_1_rsf , \相关处理逻辑_重定向_1_rtf , \重定向流水接口id_ex_1_ex_rsf , \重定向流水接口id_ex_1_ex_rtf ;
  wire [3:0] ID_AluOP, \重定向流水接口id_ex_1_ex_aluop ;
  wire [4:0] EX_WriteReg, MEM_WriteReg, multiplexer_4_out, multiplexer_5_out, multiplexer_6_out,
       multiplexer_7_out, multiplexer_12_out, \重定向流水接口id_ex_1_ex_shamt , \重定向流水接口mem_wb_1_wb_writereg ;
  wire [5:0] Func;
  wire [7:0] multiplexer_15_out, multiplexer_16_out, multiplexer_16_out_2, multiplexer_16_out_3,
       multiplexer_16_out_4;
  wire [12:0] CNT_num;
  wire [15:0] \LoadUse次数 , \总周期数 , \插入气泡数 , \无条件分支数 , \条件分支成功数 ;
  wire [31:0] adder_1_out, adder_2_out, bit_extender_1_out, bit_extender_2_out, bit_extender_3_out, EX_IR,
       EX_RS, IF_IR, MEM_AluResult, MEM_IR, mips_alu_1_result, \mips_regifile_下降沿_1_r1 ,
       \mips_regifile_下降沿_1_r2 , multiplexer_1_out, multiplexer_2_out, multiplexer_3_out, multiplexer_8_out,
       multiplexer_10_out, multiplexer_11_out, multiplexer_14_out, ram_1_data, result, shifter_1_out, WB_IR,
       \气泡流水接口if_id_1_id_pc , \重定向流水接口ex_mem_1_mem_pc , \重定向流水接口ex_mem_1_mem_rs , \重定向流水接口id_ex_1_ex_addr ,
       \重定向流水接口id_ex_1_ex_imm , \重定向流水接口id_ex_1_ex_pc_2 , \重定向流水接口id_ex_1_ex_rs , \重定向流水接口id_ex_1_ex_rt ,
       \重定向流水接口id_ex_1_ex_signimm , \重定向流水接口mem_wb_1_wb_memresult , \重定向流水接口mem_wb_1_wb_pc ;
  wire [31:6] ID_IR;

  Button \u_总复位  (.out(RST));
  Button _1 (.out(IR1));
  Button _2 (.out(IR2));
  Button _3 (.out(IR3));
  // Probe on \总周期数 
  // Probe on \总周期数 
  Button \u_继续运行  (.out(Go));
  LED #(.active("true")) led_1 (.in(W1));
  LED #(.active("true")) led_2 (.in(W2));
  LED #(.active("true")) led_3 (.in(W3));
  Hex_Digit_Display hex_digit_display_1 (.value(LedData[31:28]));  // open: dp
  // Probe on IF_PC[19:0]
  // Mips_Probe mips_probe_1: pin names not known; wires that end beside it: IF_IR
  not not_1 (not_1_out, halt);
  Hex_Digit_Display hex_digit_display_2 (.value(LedData[27:24]));  // open: dp
  Hex_Digit_Display hex_digit_display_3 (.value(LedData[23:20]));  // open: dp
  // Probe on ID_PC[19:0]
  // Mips_Probe mips_probe_2: pin names not known; wires that end beside it: {ID_IR, Func}
  Counter #(.width(16), .max('hffff), .ongoal("stay"), .trigger("rising"), .behavior("old")) counter_1 (
    .count(not_1_out), .Q(\总周期数 ), .clk(CLK));  // open: load, D, carry, clr, preset
  Counter #(.width(16), .max('hffff), .ongoal("stay"), .trigger("rising"), .behavior("old")) counter_2 (
    .count(Stall), .Q(\插入气泡数 ), .clk(CLK));  // open: load, D, carry, clr, preset
  Counter #(.width(16), .max('hffff), .ongoal("stay"), .trigger("rising"), .behavior("old")) counter_3 (
    .count(EX_JMP), .Q(\无条件分支数 ), .clk(CLK));  // open: load, D, carry, clr, preset
  Counter #(.width(16), .max('hffff), .ongoal("stay"), .trigger("rising"), .behavior("old")) counter_4 (
    .count(Branch), .Q(\条件分支成功数 ), .clk(CLK));  // open: load, D, carry, clr, preset
  Counter #(.width(16), .max('hffff), .ongoal("stay"), .trigger("rising"), .behavior("old")) counter_5 (
    .count(LoadUse), .Q(\LoadUse次数 ), .clk(CLK));  // open: load, D, carry, clr, preset
  Hex_Digit_Display hex_digit_display_4 (.value(LedData[15:12]));  // open: dp
  Hex_Digit_Display hex_digit_display_5 (.value(LedData[19:16]));  // open: dp
  Multiplexer #(.select(1), .width(32), .disabled("Z"), .enable("false")) multiplexer_1 (
    .in0(adder_1_out), .in1(adder_2_out), .out(multiplexer_1_out), .sel(Branch));
  Hex_Digit_Display hex_digit_display_6 (.value(LedData[11:8]));  // open: dp
  Hex_Digit_Display hex_digit_display_7 (.value(LedData[7:4]));  // open: dp
  Clock #(.highDuration(1), .lowDuration(1)) clock_1 (.out(clock_1_out));
  // Probe on EX_PC[19:0]
  // Mips_Probe mips_probe_3: pin names not known; wires that end beside it: clock_1_out, EX_IR, CLK
  Multiplexer #(.select(1), .width(32), .disabled("Z"), .enable("false")) multiplexer_2 (
    .in0(multiplexer_1_out), .in1(\重定向流水接口id_ex_1_ex_addr ), .out(multiplexer_2_out), .sel(EX_JMP));
  Hex_Digit_Display hex_digit_display_8 (.value(LedData[3:0]));  // open: dp
  Multiplexer #(.select(1), .width(32), .disabled("Z"), .enable("false")) multiplexer_3 (
    .in0(multiplexer_2_out), .in1(EX_RS), .out(multiplexer_3_out), .sel(EX_JR));
  // Probe on \总周期数 
  // Probe on M_PC[19:0]
  // Mips_Probe mips_probe_4: pin names not known; wires that end beside it: MEM_IR
  and and_1 (and_1_out, ~halt, ~Stall);  // AND_Gate
  Register #(.width(32), .trigger("rising"), .Select("low")) PC (
    .D(multiplexer_3_out), .en(and_1_out), .Q(IF_PC), .clk(CLK));  // open: clr
  // Probe on multiplexer_3_out
  // Probe on \总周期数 
  // Probe on \无条件分支数 
  // Probe on \条件分支成功数 
  // Probe on \插入气泡数 
  // Probe on \LoadUse次数 
  // Probe on IF_PC[11:0]
  // Probe on WB_PC[19:0]
  // Mips_Probe mips_probe_5: pin names not known; wires that end beside it: WB_IR
  \单周期硬布线控制器  \u_单周期硬布线控制器_1  (
    .Func(Func), .OP(ID_IR[31:26]), .ALU_OP(ID_AluOP), .MemToReg(ID_MemToReg), .MemWrite(ID_MemWrite),
    .ALU_SRC(ID_Alu_SRC), .RegWrite(ID_RegWrite), .SysCALL(ID_SysCall), .SignedExt(SignedExt),
    .RegDst(ID_RegDst), .JR(ID_JR), .JMP(ID_JMP), .Beq(ID_Beq), .JAL(ID_JAL), .Bne(ID_Bne), .SRAV(ID_SRAV),
    .LB(ID_LB), .BLTZ(ID_BLTZ));
  Adder #(.width(32)) adder_1 (.a(IF_PC), .b(32'h4), .out(adder_1_out));  // open: cin, cout
  // Probe on EX_PC[11:0]
  // Probe on ID_PC[11:0]
  // Mips_Probe mips_probe_6: pin names not known; wires that end beside it: IF_IR
  ROM #(.addrWidth(10), .dataWidth(32), .Select("high")) rom_1 (.addr(IF_PC[11:2]), .data(IF_IR));
  // Probe on M_PC[11:0]
  D_Flip_Flop #(.trigger("high"), .Pre_Clr_Positions("LEGACY"), .NegatePresetClear("false"), .enable("true"), .NewFFLayout("false")) d_ff_1 (.Q(d_ff_1_q));  // open: clk, D, Qn, preset, en, reset
  // Probe on 13'h8f7
  \相关处理逻辑_重定向  \u_相关处理逻辑_重定向_1  (
    .R1(multiplexer_4_out), .Instr({ID_IR, Func}), .R2(multiplexer_5_out),
    .EX_RegWrite(\重定向流水接口id_ex_1_ex_regwrite ), .EX_WriteReg_num(EX_WriteReg),
    .EX_MemtoReg(\重定向流水接口id_ex_1_ex_memtoreg ), .BranchTaken(BranchTaken),
    .MEM_RegWrite(\重定向流水接口ex_mem_1_mem_regwrite ), .MEM_WriteReg_num(MEM_WriteReg), .Stall(Stall),
    .Flush(\相关处理逻辑_重定向_1_flush ), .RSF(\相关处理逻辑_重定向_1_rsf ), .RTF(\相关处理逻辑_重定向_1_rtf ), .LoadUse(LoadUse));
  \气泡流水接口IF_ID  \u_气泡流水接口if_id_1  (
    .IF_IR(IF_IR), .IF_PC(adder_1_out), .ID_IR({ID_IR, Func}), .ID_PC(\气泡流水接口if_id_1_id_pc ), .CLK(CLK),
    .\同步清零_气泡_高电平有效 (BranchTaken), .\使能端_为高电平时忽略时钟输入 (Stall), .IF_monitor(IF_PC), .ID_monitor(ID_PC));  // open: IF_PredictJump, ID_PredictJump
  // Probe on WB_PC[11:0]
  Comparator #(.width(13), .mode("twosComplement")) comparator_1 (
    .a(CNT_num), .b(13'h8f7), .eq(comparator_1_eq), .lt(comparator_1_lt));  // open: gt
  Clock #(.highDuration(1), .lowDuration(1)) clock_2 (.out(clock_2_out));
  nand nand_1 (nand_1_out, d_ff_1_q, comparator_1_eq);
  Counter #(.width(13), .max('h1fff), .ongoal("stay"), .trigger("rising"), .behavior("old")) counter_6 (
    .count(comparator_1_lt), .Q(CNT_num), .clk(clock_2_out));  // open: load, D, carry, clr, preset
  // Probe on {ID_IR, Func}
  assign CLK = nand_1_out ? clock_2_out : 1'bz;  // Controlled_Buffer controlled_buffer_1
  // Probe on \相关处理逻辑_重定向_1_rsf 
  // Probe on \相关处理逻辑_重定向_1_rtf 
  Multiplexer #(.select(1), .width(5), .disabled("Z"), .enable("false")) multiplexer_4 (
    .in0(ID_IR[25:21]), .in1(5'b00010), .out(multiplexer_4_out), .sel(ID_SysCall));
  Multiplexer #(.select(1), .width(5), .disabled("Z"), .enable("false")) multiplexer_5 (
    .in0(ID_IR[20:16]), .in1(5'b00100), .out(multiplexer_5_out), .sel(ID_SysCall));
  Multiplexer #(.select(1), .width(5), .disabled("Z"), .enable("false")) multiplexer_6 (
    .in0(ID_IR[20:16]), .in1(ID_IR[15:11]), .out(multiplexer_6_out), .sel(ID_RegDst));
  Pull_Resistor #(.pull(1)) pull_resistor_1 (.node(CLK));
  // Probe on multiplexer_4_out
  // Probe on multiplexer_5_out
  assign bit_extender_1_out = {{16{1'b0}}, {ID_IR[15:6], Func}};  // Bit_Extender bit_extender_1
  assign bit_extender_2_out = {{16{ID_IR[15]}}, {ID_IR[15:6], Func}};  // Bit_Extender bit_extender_2
  Multiplexer #(.select(1), .width(5), .disabled("Z"), .enable("false")) multiplexer_7 (
    .in0(multiplexer_6_out), .in1({5{1'b1}}), .out(multiplexer_7_out), .sel(ID_JAL));
  Comparator #(.width(32), .mode("twosComplement")) comparator_2 (
    .a(EX_RS), .b({32{1'b0}}), .lt(comparator_2_lt));  // open: gt, eq
  Multiplexer #(.select(1), .width(32), .disabled("Z"), .enable("false")) multiplexer_8 (
    .in0(bit_extender_1_out), .in1(bit_extender_2_out), .out(multiplexer_8_out), .sel(SignedExt));
  \MIPS_Regifile_下降沿  \mips_regifile_下降沿_1  (
    .Din(RDin), .Clk(CLK), .R1(\mips_regifile_下降沿_1_r1 ), .R2(\mips_regifile_下降沿_1_r2 ), .WE(RegWrite),
    .W_num(\重定向流水接口mem_wb_1_wb_writereg ), .R1_num(multiplexer_4_out), .R2_num(multiplexer_5_out));
  // Probe on \气泡流水接口if_id_1_id_pc 
  not not_2 (not_2_out, Equal);
  and and_2 (and_2_out, EX_BLTZ, comparator_2_lt);
  and and_3 (and_3_out, Equal, EX_Beq);
  and and_4 (and_4_out, not_2_out, EX_Bne);
  \重定向流水接口ID_EX  \u_重定向流水接口id_ex_1  (
    .ID_RegWrite(ID_RegWrite), .ID_MemToReg(ID_MemToReg), .ID_JAL(ID_JAL), .ID_LB(ID_LB),
    .ID_MemWrite(ID_MemWrite), .ID_Syscall(ID_SysCall), .ID_Beq(ID_Beq), .ID_Bne(ID_Bne), .ID_JMP(ID_JMP),
    .ID_JR(ID_JR), .ID_BLTZ(ID_BLTZ), .ID_AluOP(ID_AluOP), .ID_AluSRC(ID_Alu_SRC), .ID_SRAV(ID_SRAV),
    .ID_RSF(\相关处理逻辑_重定向_1_rsf ), .ID_RTF(\相关处理逻辑_重定向_1_rtf ), .ID_RS(\mips_regifile_下降沿_1_r1 ),
    .ID_RT(\mips_regifile_下降沿_1_r2 ), .ID_shamt(ID_IR[10:6]), .ID_Imm(multiplexer_8_out),
    .ID_SignImm(bit_extender_2_out), .ID_PC(\气泡流水接口if_id_1_id_pc ), .ID_WriteReg(multiplexer_7_out),
    .ID_IR({ID_IR, Func}), .ID_addr({4'b0000, ID_IR[25:6], Func, 2'b00}), .ID_monitor(ID_PC), .CLK(CLK),
    .EX_RegWrite(\重定向流水接口id_ex_1_ex_regwrite ), .EX_MemToReg(\重定向流水接口id_ex_1_ex_memtoreg ),
    .EX_JAL(\重定向流水接口id_ex_1_ex_jal ), .EX_LB(\重定向流水接口id_ex_1_ex_lb ),
    .EX_MemWrite(\重定向流水接口id_ex_1_ex_memwrite ), .EX_Syscall(\重定向流水接口id_ex_1_ex_syscall ), .EX_Beq(EX_Beq),
    .EX_PC(EX_Bne), .EX_JMP(EX_JMP), .EX_JR(EX_JR), .ID_BLTZ_2(EX_BLTZ),
    .EX_AluOP(\重定向流水接口id_ex_1_ex_aluop ), .EX_AluSRC(\重定向流水接口id_ex_1_ex_alusrc ),
    .EX_SRAV(\重定向流水接口id_ex_1_ex_srav ), .EX_RSF(\重定向流水接口id_ex_1_ex_rsf ), .EX_RTF(\重定向流水接口id_ex_1_ex_rtf ),
    .EX_RS(\重定向流水接口id_ex_1_ex_rs ), .EX_RT(\重定向流水接口id_ex_1_ex_rt ), .EX_shamt(\重定向流水接口id_ex_1_ex_shamt ),
    .EX_Imm(\重定向流水接口id_ex_1_ex_imm ), .EX_SignImm(\重定向流水接口id_ex_1_ex_signimm ),
    .EX_PC_2(\重定向流水接口id_ex_1_ex_pc_2 ), .EX_WriteReg(EX_WriteReg), .EX_IR(EX_IR),
    .EX_addr(\重定向流水接口id_ex_1_ex_addr ), .EX_monitor(EX_PC), .\同步清零_气泡_高电平有效 (\相关处理逻辑_重定向_1_flush ));  // open: 使能端_为高电平时忽略时钟输入, ID_PredictJump, EX_PredictJump
  or or_1 (Branch, and_2_out, and_3_out, and_4_out);
  // Probe on \重定向流水接口id_ex_1_ex_rsf 
  // Probe on \重定向流水接口id_ex_1_ex_rtf 
  // Probe on EX_WriteReg
  // Probe on \重定向流水接口id_ex_1_ex_addr 
  Multiplexer #(.select(2), .width(32), .disabled("Z"), .enable("false")) multiplexer_9 (
    .in0(\重定向流水接口id_ex_1_ex_rs ), .in1(MEM_AluResult), .in2(RDin), .out(EX_RS), .sel(\重定向流水接口id_ex_1_ex_rsf ));  // open: in3
  Multiplexer #(.select(2), .width(32), .disabled("Z"), .enable("false")) multiplexer_10 (
    .in0(\重定向流水接口id_ex_1_ex_rt ), .in1(MEM_AluResult), .in2(RDin), .out(multiplexer_10_out),
    .sel(\重定向流水接口id_ex_1_ex_rtf ));  // open: in3
  // Probe on \重定向流水接口id_ex_1_ex_pc_2 
  Multiplexer #(.select(1), .width(32), .disabled("Z"), .enable("false")) multiplexer_11 (
    .in0(multiplexer_10_out), .in1(\重定向流水接口id_ex_1_ex_imm ), .out(multiplexer_11_out),
    .sel(\重定向流水接口id_ex_1_ex_alusrc ));
  Shifter #(.width(32), .shift("ll")) shifter_1 (
    .in(\重定向流水接口id_ex_1_ex_signimm ), .\dist (5'b00010), .out(shifter_1_out));
  or or_2 (BranchTaken, Branch, EX_JMP);
  Multiplexer #(.select(1), .width(5), .disabled("Z"), .enable("false")) multiplexer_12 (
    .in0(\重定向流水接口id_ex_1_ex_shamt ), .in1(EX_RS[4:0]), .out(multiplexer_12_out),
    .sel(\重定向流水接口id_ex_1_ex_srav ));
  Adder #(.width(32)) adder_2 (.a(shifter_1_out), .b(\重定向流水接口id_ex_1_ex_pc_2 ), .out(adder_2_out));  // open: cin, cout
  // Probe on adder_2_out
  // Probe on EX_RS
  MIPS_ALU mips_alu_1 (
    .X(EX_RS), .Y(multiplexer_11_out), .AluOP(\重定向流水接口id_ex_1_ex_aluop ), .Equal(Equal),
    .Result(mips_alu_1_result), .shamt(multiplexer_12_out));  // open: Result_2
  \重定向流水接口EX_MEM  \u_重定向流水接口ex_mem_1  (
    .EX_RegWrite(\重定向流水接口id_ex_1_ex_regwrite ), .EX_MemToReg(\重定向流水接口id_ex_1_ex_memtoreg ),
    .EX_JAL(\重定向流水接口id_ex_1_ex_jal ), .EX_LB(\重定向流水接口id_ex_1_ex_lb ),
    .EX_MemWrite(\重定向流水接口id_ex_1_ex_memwrite ), .EX_Syscall(\重定向流水接口id_ex_1_ex_syscall ), .EX_RS(EX_RS),
    .EX_result(mips_alu_1_result), .EX_MDin(multiplexer_10_out), .EX_PC(\重定向流水接口id_ex_1_ex_pc_2 ),
    .EX_WriteReg(EX_WriteReg), .EX_IR(EX_IR), .EX_monitor(EX_PC), .CLK(CLK),
    .MEM_RegWrite(\重定向流水接口ex_mem_1_mem_regwrite ), .MEM_MemToReg(\重定向流水接口ex_mem_1_mem_memtoreg ),
    .MEM_JAL(\重定向流水接口ex_mem_1_mem_jal ), .MEM_LB(\重定向流水接口ex_mem_1_mem_lb ), .MEM_MemWrite(MemWrite),
    .MEM_Syscall(\重定向流水接口ex_mem_1_mem_syscall ), .MEM_RS(\重定向流水接口ex_mem_1_mem_rs ),
    .MEM_result(MEM_AluResult), .MEM_MDin(MDin), .MEM_PC(\重定向流水接口ex_mem_1_mem_pc ),
    .MEM_WriteReg(MEM_WriteReg), .MEM_IR(MEM_IR), .MEM_monitor(M_PC));  // open: 同步清零_气泡_高电平有效, 使能端_低电平有效_stall_高电平有效
  Register #(.width(32), .trigger("rising"), .Select("low")) register_1 (
    .D(MDin), .en(Ledin), .Q(LedData), .clk(CLK));  // open: clr
  // Probe on MEM_WriteReg
  RAM #(.addrWidth(10), .dataWidth(32), .bus("separate"), .Select("high")) ram_1 (
    .addr(MEM_AluResult[11:2]), .din(MDin), .data(ram_1_data), .str(MemWrite), .clk(CLK), .ld(1'b1),
    .clr(halt));  // open: sel
  // Probe on RDin
  Multiplexer #(.select(1), .width(32), .disabled("Z"), .enable("false")) multiplexer_13 (
    .in0({multiplexer_16_out_4, multiplexer_16_out_3, multiplexer_16_out_2, multiplexer_16_out}),
    .in1(bit_extender_3_out), .out(RDin), .sel(WB_LB));
  \重定向流水接口MEM_WB  \u_重定向流水接口mem_wb_1  (
    .MEM_RegWrite(\重定向流水接口ex_mem_1_mem_regwrite ), .MEM_MemToReg(\重定向流水接口ex_mem_1_mem_memtoreg ),
    .MEM_JAL(\重定向流水接口ex_mem_1_mem_jal ), .MEM_LB(\重定向流水接口ex_mem_1_mem_lb ), .MEM_AluResult(MEM_AluResult),
    .MEM_MemResult(ram_1_data), .MEM_PC(\重定向流水接口ex_mem_1_mem_pc ), .MEM_WriteReg(MEM_WriteReg),
    .MEM_IR(MEM_IR), .MEM_monitor(M_PC), .CLK(CLK), .WB_RegWrite(RegWrite),
    .WB_MemToReg(\重定向流水接口mem_wb_1_wb_memtoreg ), .WB_JAL(\重定向流水接口mem_wb_1_wb_jal ), .WB_LB(WB_LB),
    .WB_AluResult(result), .WB_MemResult(\重定向流水接口mem_wb_1_wb_memresult ), .WB_PC(\重定向流水接口mem_wb_1_wb_pc ),
    .WB_WriteReg(\重定向流水接口mem_wb_1_wb_writereg ), .WB_IR(WB_IR), .WB_monitor(WB_PC));  // open: 同步清零_气泡_高电平有效, 使能端_为高电平时忽略时钟输入
  Comparator #(.width(32), .mode("twosComplement")) comparator_3 (
    .a(32'h22), .b(\重定向流水接口ex_mem_1_mem_rs ), .eq(comparator_3_eq));  // open: gt, lt
  Multiplexer #(.select(1), .width(32), .disabled("Z"), .enable("false")) multiplexer_14 (
    .in0(result), .in1(\重定向流水接口mem_wb_1_wb_memresult ), .out(multiplexer_14_out),
    .sel(\重定向流水接口mem_wb_1_wb_memtoreg ));
  Multiplexer #(.select(2), .width(8), .disabled("Z"), .enable("false")) multiplexer_15 (
    .in0(multiplexer_16_out), .in1(multiplexer_16_out_2), .in2(multiplexer_16_out_3),
    .in3(multiplexer_16_out_4), .out(multiplexer_15_out), .sel(result[1:0]));
  assign bit_extender_3_out = {{24{multiplexer_15_out[7]}}, multiplexer_15_out};  // Bit_Extender bit_extender_3
  and and_5 (Ledin, \重定向流水接口ex_mem_1_mem_syscall , comparator_3_eq);
  and and_6 (and_6_out, \重定向流水接口ex_mem_1_mem_syscall , not_3_out);
  not not_3 (not_3_out, comparator_3_eq);
  Multiplexer #(.select(1), .width(32), .disabled("Z"), .enable("false")) multiplexer_16 (
    .in0(multiplexer_14_out), .in1(\重定向流水接口mem_wb_1_wb_pc ),
    .out({multiplexer_16_out_4, multiplexer_16_out_3, multiplexer_16_out_2, multiplexer_16_out}),
    .sel(\重定向流水接口mem_wb_1_wb_jal ));
  Register #(.width(1), .trigger("rising"), .Select("low")) register_2 (
    .D(\重定向流水接口ex_mem_1_mem_syscall ), .en(and_6_out), .Q(halt), .clk(CLK), .clr(Go));

  // Other names for the same wires on the sheet: ID_IR[5:0] = Func; OP[5:0] = ID_IR[31:26]; IR[31:0] = IF_IR;
  //   MEM_PC[31:0] = M_PC; PC[31:0] = IF_PC

  // Notes on the sheet:
  //   中断源
  //   时空图监测，可删除
  //   中断等待指示
  //   数码管输出
  //   指令存储器
  //   控制位
  //   指令字
  //   contents of rom_1 (hex, n*v repeats v):
  //   20110001 8000c05 20110001 20120002 20130003 8000c09 20110001 20120002 20130003 8000c0d 20110001
  //   20120002 20130003 8000c11 20110001 20120002 20130003 c000d09 20100001 20110001 118fc0 112020
  //   20020022 c 118882 12200001 8000c15 112020 20020022 c 20110001 118880 112020 20020022 c 12200001
  //   8000c1f 20110001 118fc0 112020 20020022 c 1188c3 112020 20020022 c 118903 112020 20020022 c 118903
  //   112020 20020022 c 118903 112020 20020022 c 118903 112020 20020022 c 118903 112020 20020022 c 118903
  //   112020 20020022 c 118903 112020 20020022 c 20100001 109fc0 139fc3 8021 2012000c 24160003 26100001
  //   3210000f 20080008 20090001 139900 2709825 132020 20020022 c 1094022 1500fff9 22100001 2018000f
  //   2188024 108700 20080008 20090001 139902 2709825 132021 20020022 c 1094022 1500fff9 108702 2c9b022
  //   12c00001 8000c50 4020 1084027 84400 3508ffff 82021 20020022 c 2010ffff 20110000 ae300000 22100001
  //   22310004 ae300000 22100001 22310004 ae300000 22100001 22310004 ae300000 22100001 22310004 ae300000
  //   22100001 22310004 ae300000 22100001 22310004 ae300000 22100001 22310004 ae300000 22100001 22310004
  //   ae300000 22100001 22310004 ae300000 22100001 22310004 ae300000 22100001 22310004 ae300000 22100001
  //   22310004 ae300000 22100001 22310004 ae300000 22100001 22310004 ae300000 22100001 22310004 ae300000
  //   22100001 22310004 22100001 8020 2011003c 8e130000 8e340000 274402a 11000002 ae330000 ae140000
  //   2231fffc 1611fff8 102020 20020022 c 22100004 2011003c 1611fff2 20020032 c 4*0 20080001 20090003
  //   20110876 118d00 112020 20020022 c 200b0008 1118807 1318807 112020 20020022 c 216bffff 1560fff9
  //   2002000a c 4*0 2008ffff 20117777 112020 20020022 c 200b0010 2288826 112020 20020022 c 216bffff
  //   1560fffa 2002000a c 4*0 20090000 200b0010 34118483 20120404 118c00 129400 36318281 22520404 ad310000
  //   2328820 21290004 216bffff 1560fffb 200b0020 20090000 81310000 112020 20020022 c 21290001 216bffff
  //   1560fff9 2002000a c 4*0 2011fff1 112020 20020022 c 22310001 620fffb 2002000a c 2002000a c 20100000
  //   22100001 102020 20020022 c 22100002 102020 20020022 c 22100003 102020 20020022 c 22100004 102020
  //   20020022 c 22100005 102020 20020022 c 22100006 102020 20020022 c 22100007 102020 20020022 c 22100008
  //   102020 20020022 20020022 c 3e00008
  //   流水调试日志用
  //   暂停节拍，不能为0
  //   戳工具置1进入计数暂停模式，ctrl+k时钟自动运行到对应节拍暂停
  //   ctrl+k关闭时钟连续运行，将控制位置零，进入单步调试模式调试
  //   Func
  //   OP
  //   rs
  //   rt
  //   shamt
  //   rt
  //   rd
  //   可计数暂停的时钟源
  //   为方便自动评测，需要输出流水线各段保存的PC值，注意是PC不是PC+4，另外ID段寄存器写入信息，Mem段内存写入信息也要输出
endmodule

module \动态分支预测  (
  output RegWrite,
  output MemWrite,
  output [31:0] IF_PC,
  output [31:0] ID_PC,
  output [31:0] EX_PC,
  output [31:0] M_PC,
  output [31:0] WB_PC,
  output [31:0] RDin,
  output [31:0] MDin,
  output [31:0] LedData
);

  wire and_1_out, and_2_out, and_3_out, and_4_out, and_5_out, and_6_out, and_8_out, Branch, BranchTaken,
       cBranch, CLK, clock_1_out, clock_2_out, comparator_1_eq, comparator_1_lt, comparator_2_lt,
       comparator_4_eq, d_ff_1_q, Equal, EX_Beq, EX_BLTZ, EX_Bne, EX_Branch, EX_JMP, EX_JR, EX_PredictJump,
       Go, halt, ID_Alu_SRC, ID_Beq, ID_BLTZ, ID_Bne, ID_JAL, ID_JMP, ID_JR, ID_LB, ID_MemToReg, ID_MemWrite,
       ID_RegDst, ID_RegWrite, ID_SRAV, ID_SysCall, IR1, IR2, IR3, Ledin, LoadUse, nand_1_out, not_1_out,
       not_2_out, not_4_out, PredictCor, PredictErr, PredictJump, RST, SignedExt, Stall, W1, W2, W3, WB_LB,
       \气泡流水接口if_id_1_id_predictjump , \相关处理逻辑_重定向_1_flush , \重定向流水接口ex_mem_1_mem_jal ,
       \重定向流水接口ex_mem_1_mem_lb , \重定向流水接口ex_mem_1_mem_memtoreg , \重定向流水接口ex_mem_1_mem_regwrite ,
       \重定向流水接口ex_mem_1_mem_syscall , \重定向流水接口id_ex_1_ex_alusrc , \重定向流水接口id_ex_1_ex_jal ,
       \重定向流水接口id_ex_1_ex_lb , \重定向流水接口id_ex_1_ex_memtoreg , \重定向流水接口id_ex_1_ex_memwrite ,
       \重定向流水接口id_ex_1_ex_regwrite , \重定向流水接口id_ex_1_ex_srav , \重定向流水接口id_ex_1_ex_syscall ,
       \重定向流水接口mem_wb_1_wb_jal , \重定向流水接口mem_wb_1_wb_memtoreg ;
  wire [1:0] \相关处理逻辑_重定向_1_rsf , \相关处理逻辑_重定向_1_rtf , \重定向流水接口id_ex_1_ex_rsf , \重定向流水接口id_ex_1_ex_rtf ;
  wire [3:0] ID_AluOP, \重定向流水接口id_ex_1_ex_aluop ;
  wire [4:0] EX_WriteReg, MEM_WriteReg, multiplexer_6_out, multiplexer_7_out, multiplexer_8_out,
       multiplexer_9_out, multiplexer_14_out, \重定向流水接口id_ex_1_ex_shamt , \重定向流水接口mem_wb_1_wb_writereg ;
  wire [5:0] Func;
  wire [7:0] multiplexer_17_out, multiplexer_18_out, multiplexer_18_out_2, multiplexer_18_out_3,
       multiplexer_18_out_4;
  wire [12:0] CNT_num;
  wire [15:0] \LoadUse次数 , \分支总数 , \总周期数 , \插入气泡数 , \无条件分支数 , \条件分支成功数 , \条件分支数 , \预测失败数 , \预测成功数 ;
  wire [31:0] adder_1_out, adder_2_out, adder_3_out, bit_extender_1_out, bit_extender_2_out,
       bit_extender_3_out, btb_1_jumpaddr, EX_BranchAddr, EX_IR, EX_RS, IF_IR, MEM_AluResult, MEM_IR,
       mips_alu_1_result, \mips_regifile_下降沿_1_r1 , \mips_regifile_下降沿_1_r2 , multiplexer_1_out,
       multiplexer_3_out, multiplexer_4_out, multiplexer_5_out, multiplexer_10_out, multiplexer_12_out,
       multiplexer_13_out, multiplexer_16_out, ram_1_data, result, shifter_1_out, WB_IR,
       \气泡流水接口if_id_1_id_pc , \重定向流水接口ex_mem_1_mem_pc , \重定向流水接口ex_mem_1_mem_rs , \重定向流水接口id_ex_1_ex_addr ,
       \重定向流水接口id_ex_1_ex_imm , \重定向流水接口id_ex_1_ex_pc_2 , \重定向流水接口id_ex_1_ex_rs , \重定向流水接口id_ex_1_ex_rt ,
       \重定向流水接口id_ex_1_ex_signimm , \重定向流水接口mem_wb_1_wb_memresult , \重定向流水接口mem_wb_1_wb_pc ;
  wire [31:6] ID_IR;

  Button \u_总复位  (.out(RST));
  Button _1 (.out(IR1));
  Button _2 (.out(IR2));
  Button _3 (.out(IR3));
  // Probe on \总周期数 
  // Probe on \总周期数 
  Button \u_继续运行  (.out(Go));
  LED #(.active("true")) led_1 (.in(W1));
  LED #(.active("true")) led_2 (.in(W2));
  LED #(.active("true")) led_3 (.in(W3));
  // Probe on \分支总数 
  Hex_Digit_Display hex_digit_display_1 (.value(LedData[31:28]));  // open: dp
  // Probe on IF_PC[19:0]
  // Mips_Probe mips_probe_1: pin names not known; wires that end beside it: IF_IR
  not not_1 (not_1_out, halt);
  Multiplexer #(.select(1), .width(32), .disabled("Z"), .enable("false")) multiplexer_1 (
    .in0(adder_3_out), .in1(\重定向流水接口id_ex_1_ex_addr ), .out(multiplexer_1_out), .sel(EX_JMP));
  Hex_Digit_Display hex_digit_display_2 (.value(LedData[23:20]));  // open: dp
  Hex_Digit_Display hex_digit_display_3 (.value(LedData[27:24]));  // open: dp
  // Probe on ID_PC[19:0]
  // Mips_Probe mips_probe_2: pin names not known; wires that end beside it: {ID_IR, Func}
  Counter #(.width(16), .max('hffff), .ongoal("stay"), .trigger("rising"), .behavior("old")) counter_1 (
    .count(not_1_out), .Q(\总周期数 ), .clk(CLK));  // open: load, D, carry, clr, preset
  Counter #(.width(16), .max('hffff), .ongoal("stay"), .trigger("rising"), .behavior("old")) counter_2 (
    .count(Stall), .Q(\插入气泡数 ), .clk(CLK));  // open: load, D, carry, clr, preset
  Counter #(.width(16), .max('hffff), .ongoal("stay"), .trigger("rising"), .behavior("old")) counter_3 (
    .count(Branch), .Q(\分支总数 ), .clk(CLK));  // open: load, D, carry, clr, preset
  Counter #(.width(16), .max('hffff), .ongoal("stay"), .trigger("rising"), .behavior("old")) counter_4 (
    .count(EX_JMP), .Q(\无条件分支数 ), .clk(CLK));  // open: load, D, carry, clr, preset
  Counter #(.width(16), .max('hffff), .ongoal("stay"), .trigger("rising"), .behavior("old")) counter_5 (
    .count(cBranch), .Q(\条件分支数 ), .clk(CLK));  // open: load, D, carry, clr, preset
  Counter #(.width(16), .max('hffff), .ongoal("stay"), .trigger("rising"), .behavior("old")) counter_6 (
    .count(EX_Branch), .Q(\条件分支成功数 ), .clk(CLK));  // open: load, D, carry, clr, preset
  Counter #(.width(16), .max('hffff), .ongoal("stay"), .trigger("rising"), .behavior("old")) counter_7 (
    .count(LoadUse), .Q(\LoadUse次数 ), .clk(CLK));  // open: load, D, carry, clr, preset
  // Probe on EX_BranchAddr
  Multiplexer #(.select(1), .width(32), .disabled("Z"), .enable("false")) multiplexer_2 (
    .in0(multiplexer_1_out), .in1(EX_RS), .out(EX_BranchAddr), .sel(EX_JR));
  Hex_Digit_Display hex_digit_display_4 (.value(LedData[15:12]));  // open: dp
  Hex_Digit_Display hex_digit_display_5 (.value(LedData[19:16]));  // open: dp
  // Probe on \条件分支数 
  Hex_Digit_Display hex_digit_display_6 (.value(LedData[11:8]));  // open: dp
  Hex_Digit_Display hex_digit_display_7 (.value(LedData[7:4]));  // open: dp
  Clock #(.highDuration(1), .lowDuration(1)) clock_1 (.out(clock_1_out));
  // Probe on EX_PC[19:0]
  // Mips_Probe mips_probe_3: pin names not known; wires that end beside it: clock_1_out, EX_IR, CLK
  Multiplexer #(.select(1), .width(32), .disabled("Z"), .enable("false")) multiplexer_3 (
    .in0(adder_1_out), .in1(EX_BranchAddr), .out(multiplexer_3_out), .sel(BranchTaken));
  Adder #(.width(32)) adder_1 (.a(EX_PC), .b(32'h4), .out(adder_1_out));  // open: cin, cout
  Hex_Digit_Display hex_digit_display_8 (.value(LedData[3:0]));  // open: dp
  // Probe on \预测成功数 
  and and_1 (and_1_out, Branch, PredictCor);
  and and_2 (and_2_out, Branch, PredictErr);
  Multiplexer #(.select(1), .width(32), .disabled("Z"), .enable("false")) multiplexer_4 (
    .in0(multiplexer_5_out), .in1(multiplexer_3_out), .out(multiplexer_4_out), .sel(PredictErr));
  // Probe on multiplexer_4_out
  Multiplexer #(.select(1), .width(32), .disabled("Z"), .enable("false")) multiplexer_5 (
    .in0(adder_2_out), .in1(btb_1_jumpaddr), .out(multiplexer_5_out), .sel(PredictJump));
  // Probe on \总周期数 
  // Probe on M_PC[19:0]
  // Mips_Probe mips_probe_4: pin names not known; wires that end beside it: MEM_IR
  Counter #(.width(16), .max('hffff), .ongoal("stay"), .trigger("rising"), .behavior("old")) counter_8 (
    .count(and_1_out), .Q(\预测成功数 ), .clk(CLK));  // open: load, D, carry, clr, preset
  Counter #(.width(16), .max('hffff), .ongoal("stay"), .trigger("rising"), .behavior("old")) counter_9 (
    .count(and_2_out), .Q(\预测失败数 ), .clk(CLK));  // open: load, D, carry, clr, preset
  and and_3 (and_3_out, ~halt, ~Stall);  // AND_Gate
  Register #(.width(32), .trigger("rising"), .Select("low")) PC (
    .D(multiplexer_4_out), .en(and_3_out), .Q(IF_PC), .clk(CLK));  // open: clr
  BTB btb_1 (
    .CLK(CLK), .EX_Branch(Branch), .PC(IF_PC), .EX_BranchTaken(BranchTaken), .EX_PC(EX_PC),
    .EX_BrachAddr(EX_BranchAddr), .JumpAddr(btb_1_jumpaddr), .PredictJump(PredictJump));
  // Probe on \总周期数 
  // Probe on \无条件分支数 
  // Probe on \条件分支成功数 
  // Probe on \插入气泡数 
  // Probe on \LoadUse次数 
  // Probe on \预测失败数 
  // Probe on IF_PC
  // Probe on IF_PC[11:0]
  // Probe on WB_PC[19:0]
  // Mips_Probe mips_probe_5: pin names not known; wires that end beside it: WB_IR
  \单周期硬布线控制器  \u_单周期硬布线控制器_1  (
    .Func(Func), .OP(ID_IR[31:26]), .ALU_OP(ID_AluOP), .MemToReg(ID_MemToReg), .MemWrite(ID_MemWrite),
    .ALU_SRC(ID_Alu_SRC), .RegWrite(ID_RegWrite), .SysCALL(ID_SysCall), .SignedExt(SignedExt),
    .RegDst(ID_RegDst), .JR(ID_JR), .JMP(ID_JMP), .Beq(ID_Beq), .JAL(ID_JAL), .Bne(ID_Bne), .SRAV(ID_SRAV),
    .LB(ID_LB), .BLTZ(ID_BLTZ));
  // Probe on ID_PC[11:0]
  // Probe on EX_PC[11:0]
  // Mips_Probe mips_probe_6: pin names not known; wires that end beside it: IF_IR
  ROM #(.addrWidth(10), .dataWidth(32), .Select("high")) rom_1 (.addr(IF_PC[11:2]), .data(IF_IR));
  Adder #(.width(32)) adder_2 (.a(IF_PC), .b(32'h4), .out(adder_2_out));  // open: cin, cout
  // Probe on M_PC[11:0]
  D_Flip_Flop #(.trigger("high"), .Pre_Clr_Positions("LEGACY"), .NegatePresetClear("false"), .enable("true"), .NewFFLayout("false")) d_ff_1 (.Q(d_ff_1_q));  // open: clk, D, Qn, preset, en, reset
  // Probe on 13'hc
  \相关处理逻辑_重定向  \u_相关处理逻辑_重定向_1  (
    .R1(multiplexer_6_out), .Instr({ID_IR, Func}), .R2(multiplexer_7_out),
    .EX_RegWrite(\重定向流水接口id_ex_1_ex_regwrite ), .EX_WriteReg_num(EX_WriteReg),
    .EX_MemtoReg(\重定向流水接口id_ex_1_ex_memtoreg ), .BranchTaken(PredictErr),
    .MEM_RegWrite(\重定向流水接口ex_mem_1_mem_regwrite ), .MEM_WriteReg_num(MEM_WriteReg), .Stall(Stall),
    .Flush(\相关处理逻辑_重定向_1_flush ), .RSF(\相关处理逻辑_重定向_1_rsf ), .RTF(\相关处理逻辑_重定向_1_rtf ), .LoadUse(LoadUse));
  \气泡流水接口IF_ID  \u_气泡流水接口if_id_1  (
    .IF_IR(IF_IR), .IF_PC(adder_2_out), .ID_IR({ID_IR, Func}), .ID_PC(\气泡流水接口if_id_1_id_pc ), .CLK(CLK),
    .\同步清零_气泡_高电平有效 (PredictErr), .\使能端_为高电平时忽略时钟输入 (Stall), .IF_monitor(IF_PC), .ID_monitor(ID_PC),
    .IF_PredictJump(PredictJump), .ID_PredictJump(\气泡流水接口if_id_1_id_predictjump ));
  // Probe on WB_PC[11:0]
  Comparator #(.width(13), .mode("twosComplement")) comparator_1 (
    .a(CNT_num), .b(13'hc), .eq(comparator_1_eq), .lt(comparator_1_lt));  // open: gt
  Clock #(.highDuration(1), .lowDuration(1)) clock_2 (.out(clock_2_out));
  nand nand_1 (nand_1_out, d_ff_1_q, comparator_1_eq);
  Counter #(.width(13), .max('h1fff), .ongoal("stay"), .trigger("rising"), .behavior("old")) counter_10 (
    .count(comparator_1_lt), .Q(CNT_num), .clk(clock_2_out));  // open: load, D, carry, clr, preset
  Comparator #(.width(32), .mode("twosComplement")) comparator_2 (
    .a(EX_RS), .b({32{1'b0}}), .lt(comparator_2_lt));  // open: gt, eq
  // Probe on {ID_IR, Func}
  assign CLK = nand_1_out ? clock_2_out : 1'bz;  // Controlled_Buffer controlled_buffer_1
  // Probe on \相关处理逻辑_重定向_1_rsf 
  // Probe on \相关处理逻辑_重定向_1_rtf 
  Multiplexer #(.select(1), .width(5), .disabled("Z"), .enable("false")) multiplexer_6 (
    .in0(ID_IR[25:21]), .in1(5'b00010), .out(multiplexer_6_out), .sel(ID_SysCall));
  Multiplexer #(.select(1), .width(5), .disabled("Z"), .enable("false")) multiplexer_7 (
    .in0(ID_IR[20:16]), .in1(5'b00100), .out(multiplexer_7_out), .sel(ID_SysCall));
  Multiplexer #(.select(1), .width(5), .disabled("Z"), .enable("false")) multiplexer_8 (
    .in0(ID_IR[20:16]), .in1(ID_IR[15:11]), .out(multiplexer_8_out), .sel(ID_RegDst));
  Pull_Resistor #(.pull(1)) pull_resistor_1 (.node(CLK));
  and and_4 (and_4_out, EX_BLTZ, comparator_2_lt);
  and and_5 (and_5_out, Equal, EX_Beq);
  not not_2 (not_2_out, Equal);
  and and_6 (and_6_out, not_2_out, EX_Bne);
  // Probe on multiplexer_6_out
  // Probe on multiplexer_7_out
  assign bit_extender_1_out = {{16{1'b0}}, {ID_IR[15:6], Func}};  // Bit_Extender bit_extender_1
  assign bit_extender_2_out = {{16{ID_IR[15]}}, {ID_IR[15:6], Func}};  // Bit_Extender bit_extender_2
  Multiplexer #(.select(1), .width(5), .disabled("Z"), .enable("false")) multiplexer_9 (
    .in0(multiplexer_8_out), .in1({5{1'b1}}), .out(multiplexer_9_out), .sel(ID_JAL));
  Multiplexer #(.select(1), .width(32), .disabled("Z"), .enable("false")) multiplexer_10 (
    .in0(bit_extender_1_out), .in1(bit_extender_2_out), .out(multiplexer_10_out), .sel(SignedExt));
  or or_1 (EX_Branch, and_4_out, and_5_out, and_6_out);
  \MIPS_Regifile_下降沿  \mips_regifile_下降沿_1  (
    .Din(RDin), .Clk(CLK), .R1(\mips_regifile_下降沿_1_r1 ), .R2(\mips_regifile_下降沿_1_r2 ), .WE(RegWrite),
    .W_num(\重定向流水接口mem_wb_1_wb_writereg ), .R1_num(multiplexer_6_out), .R2_num(multiplexer_7_out));
  // Probe on \气泡流水接口if_id_1_id_pc 
  or or_2 (BranchTaken, EX_Branch, EX_JMP);
  \重定向流水接口ID_EX  \u_重定向流水接口id_ex_1  (
    .ID_RegWrite(ID_RegWrite), .ID_MemToReg(ID_MemToReg), .ID_JAL(ID_JAL), .ID_LB(ID_LB),
    .ID_MemWrite(ID_MemWrite), .ID_Syscall(ID_SysCall), .ID_Beq(ID_Beq), .ID_Bne(ID_Bne), .ID_JMP(ID_JMP),
    .ID_JR(ID_JR), .ID_BLTZ(ID_BLTZ), .ID_AluOP(ID_AluOP), .ID_AluSRC(ID_Alu_SRC), .ID_SRAV(ID_SRAV),
    .ID_RSF(\相关处理逻辑_重定向_1_rsf ), .ID_RTF(\相关处理逻辑_重定向_1_rtf ), .ID_RS(\mips_regifile_下降沿_1_r1 ),
    .ID_RT(\mips_regifile_下降沿_1_r2 ), .ID_shamt(ID_IR[10:6]), .ID_Imm(multiplexer_10_out),
    .ID_SignImm(bit_extender_2_out), .ID_PC(\气泡流水接口if_id_1_id_pc ), .ID_WriteReg(multiplexer_9_out),
    .ID_IR({ID_IR, Func}), .ID_addr({4'b0000, ID_IR[25:6], Func, 2'b00}), .ID_monitor(ID_PC), .CLK(CLK),
    .EX_RegWrite(\重定向流水接口id_ex_1_ex_regwrite ), .EX_MemToReg(\重定向流水接口id_ex_1_ex_memtoreg ),
    .EX_JAL(\重定向流水接口id_ex_1_ex_jal ), .EX_LB(\重定向流水接口id_ex_1_ex_lb ),
    .EX_MemWrite(\重定向流水接口id_ex_1_ex_memwrite ), .EX_Syscall(\重定向流水接口id_ex_1_ex_syscall ), .EX_Beq(EX_Beq),
    .EX_PC(EX_Bne), .EX_JMP(EX_JMP), .EX_JR(EX_JR), .ID_BLTZ_2(EX_BLTZ),
    .EX_AluOP(\重定向流水接口id_ex_1_ex_aluop ), .EX_AluSRC(\重定向流水接口id_ex_1_ex_alusrc ),
    .EX_SRAV(\重定向流水接口id_ex_1_ex_srav ), .EX_RSF(\重定向流水接口id_ex_1_ex_rsf ), .EX_RTF(\重定向流水接口id_ex_1_ex_rtf ),
    .EX_RS(\重定向流水接口id_ex_1_ex_rs ), .EX_RT(\重定向流水接口id_ex_1_ex_rt ), .EX_shamt(\重定向流水接口id_ex_1_ex_shamt ),
    .EX_Imm(\重定向流水接口id_ex_1_ex_imm ), .EX_SignImm(\重定向流水接口id_ex_1_ex_signimm ),
    .EX_PC_2(\重定向流水接口id_ex_1_ex_pc_2 ), .EX_WriteReg(EX_WriteReg), .EX_IR(EX_IR),
    .EX_addr(\重定向流水接口id_ex_1_ex_addr ), .EX_monitor(EX_PC), .\同步清零_气泡_高电平有效 (\相关处理逻辑_重定向_1_flush ),
    .ID_PredictJump(\气泡流水接口if_id_1_id_predictjump ), .EX_PredictJump(EX_PredictJump));  // open: 使能端_为高电平时忽略时钟输入
  // Probe on \重定向流水接口id_ex_1_ex_rsf 
  // Probe on \重定向流水接口id_ex_1_ex_rtf 
  // Probe on EX_WriteReg
  Multiplexer #(.select(2), .width(32), .disabled("Z"), .enable("false")) multiplexer_11 (
    .in0(\重定向流水接口id_ex_1_ex_rs ), .in1(MEM_AluResult), .in2(RDin), .out(EX_RS), .sel(\重定向流水接口id_ex_1_ex_rsf ));  // open: in3
  Multiplexer #(.select(2), .width(32), .disabled("Z"), .enable("false")) multiplexer_12 (
    .in0(\重定向流水接口id_ex_1_ex_rt ), .in1(MEM_AluResult), .in2(RDin), .out(multiplexer_12_out),
    .sel(\重定向流水接口id_ex_1_ex_rtf ));  // open: in3
  // Probe on \重定向流水接口id_ex_1_ex_pc_2 
  or or_3 (Branch, EX_BLTZ, EX_Beq, EX_Bne, EX_JMP);
  Multiplexer #(.select(1), .width(32), .disabled("Z"), .enable("false")) multiplexer_13 (
    .in0(multiplexer_12_out), .in1(\重定向流水接口id_ex_1_ex_imm ), .out(multiplexer_13_out),
    .sel(\重定向流水接口id_ex_1_ex_alusrc ));
  Shifter #(.width(32), .shift("ll")) shifter_1 (
    .in(\重定向流水接口id_ex_1_ex_signimm ), .\dist (5'b00010), .out(shifter_1_out));
  Multiplexer #(.select(1), .width(5), .disabled("Z"), .enable("false")) multiplexer_14 (
    .in0(\重定向流水接口id_ex_1_ex_shamt ), .in1(EX_RS[4:0]), .out(multiplexer_14_out),
    .sel(\重定向流水接口id_ex_1_ex_srav ));
  Adder #(.width(32)) adder_3 (.a(shifter_1_out), .b(\重定向流水接口id_ex_1_ex_pc_2 ), .out(adder_3_out));  // open: cin, cout
  // Probe on adder_3_out
  not not_3 (PredictErr, PredictCor);
  Comparator #(.width(1), .mode("twosComplement")) comparator_3 (
    .a(EX_PredictJump), .b(BranchTaken), .eq(PredictCor));  // open: gt, lt
  // Probe on EX_RS
  MIPS_ALU mips_alu_1 (
    .X(EX_RS), .Y(multiplexer_13_out), .AluOP(\重定向流水接口id_ex_1_ex_aluop ), .Equal(Equal),
    .Result(mips_alu_1_result), .shamt(multiplexer_14_out));  // open: Result_2
  or or_4 (cBranch, EX_BLTZ, EX_Beq, EX_Bne);
  \重定向流水接口EX_MEM  \u_重定向流水接口ex_mem_1  (
    .EX_RegWrite(\重定向流水接口id_ex_1_ex_regwrite ), .EX_MemToReg(\重定向流水接口id_ex_1_ex_memtoreg ),
    .EX_JAL(\重定向流水接口id_ex_1_ex_jal ), .EX_LB(\重定向流水接口id_ex_1_ex_lb ),
    .EX_MemWrite(\重定向流水接口id_ex_1_ex_memwrite ), .EX_Syscall(\重定向流水接口id_ex_1_ex_syscall ), .EX_RS(EX_RS),
    .EX_result(mips_alu_1_result), .EX_MDin(multiplexer_12_out), .EX_PC(\重定向流水接口id_ex_1_ex_pc_2 ),
    .EX_WriteReg(EX_WriteReg), .EX_IR(EX_IR), .EX_monitor(EX_PC), .CLK(CLK),
    .MEM_RegWrite(\重定向流水接口ex_mem_1_mem_regwrite ), .MEM_MemToReg(\重定向流水接口ex_mem_1_mem_memtoreg ),
    .MEM_JAL(\重定向流水接口ex_mem_1_mem_jal ), .MEM_LB(\重定向流水接口ex_mem_1_mem_lb ), .MEM_MemWrite(MemWrite),
    .MEM_Syscall(\重定向流水接口ex_mem_1_mem_syscall ), .MEM_RS(\重定向流水接口ex_mem_1_mem_rs ),
    .MEM_result(MEM_AluResult), .MEM_MDin(MDin), .MEM_PC(\重定向流水接口ex_mem_1_mem_pc ),
    .MEM_WriteReg(MEM_WriteReg), .MEM_IR(MEM_IR), .MEM_monitor(M_PC));  // open: 同步清零_气泡_高电平有效, 使能端_低电平有效_stall_高电平有效
  Register #(.width(32), .trigger("rising"), .Select("low")) register_1 (
    .D(MDin), .en(Ledin), .Q(LedData), .clk(CLK));  // open: clr
  // Probe on MEM_WriteReg
  RAM #(.addrWidth(10), .dataWidth(32), .bus("separate"), .Select("high")) ram_1 (
    .addr(MEM_AluResult[11:2]), .din(MDin), .data(ram_1_data), .str(MemWrite), .clk(CLK), .ld(1'b1));  // open: sel, clr
  // Probe on RDin
  Multiplexer #(.select(1), .width(32), .disabled("Z"), .enable("false")) multiplexer_15 (
    .in0({multiplexer_18_out_4, multiplexer_18_out_3, multiplexer_18_out_2, multiplexer_18_out}),
    .in1(bit_extender_3_out), .out(RDin), .sel(WB_LB));
  \重定向流水接口MEM_WB  \u_重定向流水接口mem_wb_1  (
    .MEM_RegWrite(\重定向流水接口ex_mem_1_mem_regwrite ), .MEM_MemToReg(\重定向流水接口ex_mem_1_mem_memtoreg ),
    .MEM_JAL(\重定向流水接口ex_mem_1_mem_jal ), .MEM_LB(\重定向流水接口ex_mem_1_mem_lb ), .MEM_AluResult(MEM_AluResult),
    .MEM_MemResult(ram_1_data), .MEM_PC(\重定向流水接口ex_mem_1_mem_pc ), .MEM_WriteReg(MEM_WriteReg),
    .MEM_IR(MEM_IR), .MEM_monitor(M_PC), .CLK(CLK), .WB_RegWrite(RegWrite),
    .WB_MemToReg(\重定向流水接口mem_wb_1_wb_memtoreg ), .WB_JAL(\重定向流水接口mem_wb_1_wb_jal ), .WB_LB(WB_LB),
    .WB_AluResult(result), .WB_MemResult(\重定向流水接口mem_wb_1_wb_memresult ), .WB_PC(\重定向流水接口mem_wb_1_wb_pc ),
    .WB_WriteReg(\重定向流水接口mem_wb_1_wb_writereg ), .WB_IR(WB_IR), .WB_monitor(WB_PC));  // open: 同步清零_气泡_高电平有效, 使能端_为高电平时忽略时钟输入
  Comparator #(.width(32), .mode("twosComplement")) comparator_4 (
    .a(32'h22), .b(\重定向流水接口ex_mem_1_mem_rs ), .eq(comparator_4_eq));  // open: gt, lt
  Multiplexer #(.select(1), .width(32), .disabled("Z"), .enable("false")) multiplexer_16 (
    .in0(result), .in1(\重定向流水接口mem_wb_1_wb_memresult ), .out(multiplexer_16_out),
    .sel(\重定向流水接口mem_wb_1_wb_memtoreg ));
  Multiplexer #(.select(2), .width(8), .disabled("Z"), .enable("false")) multiplexer_17 (
    .in0(multiplexer_18_out), .in1(multiplexer_18_out_2), .in2(multiplexer_18_out_3),
    .in3(multiplexer_18_out_4), .out(multiplexer_17_out), .sel(result[1:0]));
  assign bit_extender_3_out = {{24{multiplexer_17_out[7]}}, multiplexer_17_out};  // Bit_Extender bit_extender_3
  and and_7 (Ledin, \重定向流水接口ex_mem_1_mem_syscall , comparator_4_eq);
  and and_8 (and_8_out, \重定向流水接口ex_mem_1_mem_syscall , not_4_out);
  not not_4 (not_4_out, comparator_4_eq);
  Multiplexer #(.select(1), .width(32), .disabled("Z"), .enable("false")) multiplexer_18 (
    .in0(multiplexer_16_out), .in1(\重定向流水接口mem_wb_1_wb_pc ),
    .out({multiplexer_18_out_4, multiplexer_18_out_3, multiplexer_18_out_2, multiplexer_18_out}),
    .sel(\重定向流水接口mem_wb_1_wb_jal ));
  Register #(.width(1), .trigger("rising"), .Select("low")) register_2 (
    .D(\重定向流水接口ex_mem_1_mem_syscall ), .en(and_8_out), .Q(halt), .clk(CLK), .clr(Go));

  // Other names for the same wires on the sheet: ID_IR[5:0] = Func; OP[5:0] = ID_IR[31:26]; IR[31:0] = IF_IR;
  //   MEM_PC[31:0] = M_PC; PC[31:0] = IF_PC

  // Notes on the sheet:
  //   中断源
  //   中断等待指示
  //   数码管输出
  //   指令存储器
  //   控制位
  //   指令字
  //   contents of rom_1 (hex, n*v repeats v):
  //   20110001 8000c05 20110001 20120002 20130003 8000c09 20110001 20120002 20130003 8000c0d 20110001
  //   20120002 20130003 8000c11 20110001 20120002 20130003 c000d09 20100001 20110001 118fc0 112020
  //   20020022 c 118882 12200001 8000c15 112020 20020022 c 20110001 118880 112020 20020022 c 12200001
  //   8000c1f 20110001 118fc0 112020 20020022 c 1188c3 112020 20020022 c 118903 112020 20020022 c 118903
  //   112020 20020022 c 118903 112020 20020022 c 118903 112020 20020022 c 118903 112020 20020022 c 118903
  //   112020 20020022 c 118903 112020 20020022 c 20100001 109fc0 139fc3 8021 2012000c 24160003 26100001
  //   3210000f 20080008 20090001 139900 2709825 132020 20020022 c 1094022 1500fff9 22100001 2018000f
  //   2188024 108700 20080008 20090001 139902 2709825 132021 20020022 c 1094022 1500fff9 108702 2c9b022
  //   12c00001 8000c50 4020 1084027 84400 3508ffff 82021 20020022 c 2010ffff 20110000 ae300000 22100001
  //   22310004 ae300000 22100001 22310004 ae300000 22100001 22310004 ae300000 22100001 22310004 ae300000
  //   22100001 22310004 ae300000 22100001 22310004 ae300000 22100001 22310004 ae300000 22100001 22310004
  //   ae300000 22100001 22310004 ae300000 22100001 22310004 ae300000 22100001 22310004 ae300000 22100001
  //   22310004 ae300000 22100001 22310004 ae300000 22100001 22310004 ae300000 22100001 22310004 ae300000
  //   22100001 22310004 22100001 8020 2011003c 8e130000 8e340000 274402a 11000002 ae330000 ae140000
  //   2231fffc 1611fff8 102020 20020022 c 22100004 2011003c 1611fff2 20020032 c 4*0 20080001 20090003
  //   20110876 118d00 112020 20020022 c 200b0008 1118807 1318807 112020 20020022 c 216bffff 1560fff9
  //   2002000a c 4*0 2008ffff 20117777 112020 20020022 c 200b0010 2288826 112020 20020022 c 216bffff
  //   1560fffa 2002000a c 4*0 20090000 200b0010 34118483 20120404 118c00 129400 36318281 22520404 ad310000
  //   2328820 21290004 216bffff 1560fffb 200b0020 20090000 81310000 112020 20020022 c 21290001 216bffff
  //   1560fff9 2002000a c 4*0 2011fff1 112020 20020022 c 22310001 620fffb 2002000a c 2002000a c 20100000
  //   22100001 102020 20020022 c 22100002 102020 20020022 c 22100003 102020 20020022 c 22100004 102020
  //   20020022 c 22100005 102020 20020022 c 22100006 102020 20020022 c 22100007 102020 20020022 c 22100008
  //   102020 20020022 20020022 c 3e00008
  //   流水调试日志用
  //   暂停节拍，不能为0
  //   戳工具置1进入计数暂停模式，ctrl+k时钟自动运行到对应节拍暂停
  //   ctrl+k关闭时钟连续运行，将控制位置零，进入单步调试模式调试
  //   Func
  //   OP
  //   rs
  //   rt
  //   shamt
  //   rt
  //   rd
  //   可计数暂停的时钟源
  //   为方便自动评测，需要输出流水线各段保存的PC值，注意是PC不是PC+4，另外ID段寄存器写入信息，Mem段内存写入信息也要输出
endmodule

module \中断按键参考电路  (
  input  \同步清零信号 ,
  output \与中断屏蔽位与 
);

  wire \_1号中断_out , and_1_out, clock_1_out, d_ff_1_q, or_1_out, or_2_out;

  Clock #(.highDuration(1), .lowDuration(1)) clock_1 (.out(clock_1_out));
  Button \_1号中断  (.out(\_1号中断_out ));
  or or_1 (or_1_out, \与中断屏蔽位与 , d_ff_1_q);
  LED #(.active("true")) \_1号中断等待指示灯  (.in(or_1_out));
  D_Flip_Flop #(.trigger("rising"), .Pre_Clr_Positions("LEGACY"), .NegatePresetClear("false"), .enable("true"), .NewFFLayout("false")) d_ff_1 (
    .clk(\_1号中断_out ), .D(1'b1), .Q(d_ff_1_q), .reset(\与中断屏蔽位与 ));  // open: Qn, preset, en
  or or_2 (or_2_out, d_ff_1_q, \与中断屏蔽位与 );
  and and_1 (and_1_out, or_2_out, ~\同步清零信号 );  // AND_Gate
  D_Flip_Flop #(.trigger("rising"), .Pre_Clr_Positions("LEGACY"), .NegatePresetClear("false"), .enable("true"), .NewFFLayout("false")) IR1 (
    .clk(clock_1_out), .D(and_1_out), .Q(\与中断屏蔽位与 ));  // open: Qn, preset, en, reset

  // Notes on the sheet:
  //   中断信号采样参考电路
  //   Reset 
endmodule

module \中断控制_单级  (
  input  \同步清零 ,
  input  CLK,
  input  IR1,
  input  \中断可接收 ,
  input  IR2,
  input  IR3,
  output [1:0] \优先中断编号 ,
  output \有中断 ,
  output W1,
  output W2,
  output W3
);

  wire and_1_out, and_2_out, and_3_out, Clr1, Clr2, Clr3, d_ff_1_q, d_ff_2_q, d_ff_3_q, IR1_q, IR2_q, IR3_q,
       or_4_out, or_5_out, or_6_out;
  wire [1:0] INT_q;

  D_Flip_Flop #(.trigger("rising"), .Pre_Clr_Positions("LEGACY"), .NegatePresetClear("false"), .enable("true"), .NewFFLayout("false")) d_ff_1 (
    .clk(IR1), .D(1'b1), .Q(d_ff_1_q), .reset(IR1_q));  // open: Qn, preset, en
  or or_1 (W1, IR1_q, d_ff_1_q);
  D_Flip_Flop #(.trigger("rising"), .Pre_Clr_Positions("LEGACY"), .NegatePresetClear("false"), .enable("true"), .NewFFLayout("false")) d_ff_2 (
    .clk(IR2), .D(1'b1), .Q(d_ff_2_q), .reset(IR2_q));  // open: Qn, preset, en
  or or_2 (W2, IR2_q, d_ff_2_q);
  D_Flip_Flop #(.trigger("rising"), .Pre_Clr_Positions("LEGACY"), .NegatePresetClear("false"), .enable("true"), .NewFFLayout("false")) d_ff_3 (
    .clk(IR3), .D(1'b1), .Q(d_ff_3_q), .reset(IR3_q));  // open: Qn, preset, en
  or or_3 (W3, IR3_q, d_ff_3_q);
  or or_4 (or_4_out, d_ff_1_q, IR1_q);
  or or_5 (or_5_out, d_ff_2_q, IR2_q);
  or or_6 (or_6_out, d_ff_3_q, IR3_q);
  and and_1 (and_1_out, or_4_out, ~Clr1);  // AND_Gate
  and and_2 (and_2_out, or_5_out, ~Clr2);  // AND_Gate
  and and_3 (and_3_out, or_6_out, ~Clr3);  // AND_Gate
  D_Flip_Flop #(.trigger("rising"), .Pre_Clr_Positions("LEGACY"), .NegatePresetClear("false"), .enable("true"), .NewFFLayout("false")) u_IR1 (
    .clk(CLK), .D(and_1_out), .Q(IR1_q));  // open: Qn, preset, en, reset
  D_Flip_Flop #(.trigger("rising"), .Pre_Clr_Positions("LEGACY"), .NegatePresetClear("false"), .enable("true"), .NewFFLayout("false")) u_IR2 (
    .clk(CLK), .D(and_2_out), .Q(IR2_q));  // open: Qn, preset, en, reset
  D_Flip_Flop #(.trigger("rising"), .Pre_Clr_Positions("LEGACY"), .NegatePresetClear("false"), .enable("true"), .NewFFLayout("false")) u_IR3 (
    .clk(CLK), .D(and_3_out), .Q(IR3_q));  // open: Qn, preset, en, reset
  Priority_Encoder #(.select(2), .disabled("Z")) priority_encoder_1 (
    .in0(1'b0), .in1(IR1_q), .in2(IR2_q), .in3(IR3_q), .out(\优先中断编号 ), .gs(\有中断 ));  // open: en_out, en_in
  Decoder #(.select(2), .tristate("false"), .disabled(0), .enable("true")) decoder_1 (
    .out1(Clr1), .out2(Clr2), .out3(Clr3), .sel(INT_q), .en(\同步清零 ));  // open: out0
  Register #(.width(2), .trigger("rising"), .Select("low")) INT (
    .D(\优先中断编号 ), .en(\中断可接收 ), .Q(INT_q), .clk(CLK));  // open: clr

  // Notes on the sheet:
  //   Reset 
  //   Reset 
  //   Reset 
endmodule

module \中断控制_多级  (
  input  \同步清零 ,
  input  CLK,
  input  IR1,
  input  \中断可接收 ,
  input  IR2,
  input  IR3,
  output [1:0] \优先中断编号 ,
  output W1,
  output \有新中断 ,
  output W2,
  output W3
);

  wire and_1_out, and_2_out, and_3_out, and_4_out, and_5_out, Clr1, Clr2, Clr3, comparator_1_gt,
       comparator_2_gt, comparator_3_eq, d_ff_1_q, d_ff_2_q, d_ff_3_q, INM1_qn, INM2_qn, IR1_q, IR2_q, IR3_q,
       not_1_out, not_2_out, or_4_out, or_5_out, or_6_out, or_7_out, priority_encoder_1_gs;
  wire [1:0] INT;
  wire [31:2] \硬件堆栈_1_pop ;

  D_Flip_Flop #(.trigger("rising"), .Pre_Clr_Positions("LEGACY"), .NegatePresetClear("false"), .enable("true"), .NewFFLayout("false")) d_ff_1 (
    .clk(IR1), .D(1'b1), .Q(d_ff_1_q), .reset(IR1_q));  // open: Qn, preset, en
  or or_1 (W1, IR1_q, d_ff_1_q);
  D_Flip_Flop #(.trigger("rising"), .Pre_Clr_Positions("LEGACY"), .NegatePresetClear("false"), .enable("true"), .NewFFLayout("false")) d_ff_2 (
    .clk(IR2), .D(1'b1), .Q(d_ff_2_q), .reset(IR2_q));  // open: Qn, preset, en
  or or_2 (W2, IR2_q, d_ff_2_q);
  D_Flip_Flop #(.trigger("rising"), .Pre_Clr_Positions("LEGACY"), .NegatePresetClear("false"), .enable("true"), .NewFFLayout("false")) d_ff_3 (
    .clk(IR3), .D(1'b1), .Q(d_ff_3_q), .reset(IR3_q));  // open: Qn, preset, en
  or or_3 (W3, IR3_q, d_ff_3_q);
  or or_4 (or_4_out, d_ff_1_q, IR1_q);
  or or_5 (or_5_out, d_ff_2_q, IR2_q);
  or or_6 (or_6_out, d_ff_3_q, IR3_q);
  and and_1 (and_1_out, or_4_out, ~Clr1);  // AND_Gate
  and and_2 (and_2_out, or_5_out, ~Clr2);  // AND_Gate
  and and_3 (and_3_out, or_6_out, ~Clr3);  // AND_Gate
  Comparator #(.width(2), .mode("unsigned")) comparator_1 (.a(INT), .b(2'b01), .gt(comparator_1_gt));  // open: eq, lt
  Comparator #(.width(2), .mode("unsigned")) comparator_2 (.a(INT), .b(2'b10), .gt(comparator_2_gt));  // open: eq, lt
  D_Flip_Flop #(.trigger("rising"), .Pre_Clr_Positions("LEGACY"), .NegatePresetClear("false"), .enable("true"), .NewFFLayout("false")) u_IR1 (
    .clk(CLK), .D(and_1_out), .Q(IR1_q));  // open: Qn, preset, en, reset
  D_Flip_Flop #(.trigger("rising"), .Pre_Clr_Positions("LEGACY"), .NegatePresetClear("false"), .enable("true"), .NewFFLayout("false")) u_IR2 (
    .clk(CLK), .D(and_2_out), .Q(IR2_q));  // open: Qn, preset, en, reset
  D_Flip_Flop #(.trigger("rising"), .Pre_Clr_Positions("LEGACY"), .NegatePresetClear("false"), .enable("true"), .NewFFLayout("false")) u_IR3 (
    .clk(CLK), .D(and_3_out), .Q(IR3_q));  // open: Qn, preset, en, reset
  D_Flip_Flop #(.trigger("rising"), .Pre_Clr_Positions("LEGACY"), .NegatePresetClear("false"), .enable("true"), .NewFFLayout("false")) INM1 (
    .clk(CLK), .Qn(INM1_qn), .preset(comparator_1_gt), .reset(not_1_out));  // open: D, Q, en
  not not_1 (not_1_out, comparator_1_gt);
  D_Flip_Flop #(.trigger("rising"), .Pre_Clr_Positions("LEGACY"), .NegatePresetClear("false"), .enable("true"), .NewFFLayout("false")) INM2 (
    .clk(CLK), .Qn(INM2_qn), .preset(comparator_2_gt), .reset(not_2_out));  // open: D, Q, en
  not not_2 (not_2_out, comparator_2_gt);
  and and_4 (and_4_out, IR1_q, INM1_qn);
  and and_5 (and_5_out, IR2_q, INM2_qn);
  Priority_Encoder #(.select(2), .disabled("Z")) priority_encoder_1 (
    .in0(1'b0), .in1(and_4_out), .in2(and_5_out), .in3(IR3_q), .out(\优先中断编号 ), .gs(priority_encoder_1_gs));  // open: en_out, en_in
  Pull_Resistor #(.pull(0)) pull_resistor_1 (.node(\优先中断编号 ));
  \硬件堆栈  \u_硬件堆栈_1  (
    .\使能_高电平有效 (or_7_out), .CLK(CLK), .push({{30{1'b0}}, \优先中断编号 }), .pop({\硬件堆栈_1_pop , INT}), .opt(\同步清零 ));
  or or_7 (or_7_out, \同步清零 , \中断可接收 );
  Decoder #(.select(2), .tristate("false"), .disabled(0), .enable("true")) decoder_1 (
    .out1(Clr1), .out2(Clr2), .out3(Clr3), .sel(INT), .en(\同步清零 ));  // open: out0
  Comparator #(.width(2), .mode("twosComplement")) comparator_3 (
    .a(INT), .b(\优先中断编号 ), .eq(comparator_3_eq));  // open: gt, lt
  and and_6 (\有新中断 , ~comparator_3_eq, priority_encoder_1_gs);  // AND_Gate

  // Notes on the sheet:
  //   Reset 
  //   Reset 
  //   Reset 
endmodule

module \硬件堆栈  (
  input  opt,
  input  [31:0] push,
  input  \使能_高电平有效 ,
  input  CLK,
  output [31:0] pop
);

  wire [31:0] multiplexer_1_out, multiplexer_2_out, multiplexer_3_out, multiplexer_4_out, multiplexer_5_out,
       multiplexer_6_out, multiplexer_7_out, multiplexer_8_out, register_2_q, register_3_q, register_4_q,
       register_5_q, register_6_q, register_7_q, register_8_q;

  Multiplexer #(.select(1), .width(32), .disabled("Z"), .enable("false")) multiplexer_1 (
    .in0(push), .in1(register_2_q), .out(multiplexer_1_out), .sel(opt));
  Multiplexer #(.select(1), .width(32), .disabled("Z"), .enable("false")) multiplexer_2 (
    .in0(pop), .in1(register_3_q), .out(multiplexer_2_out), .sel(opt));
  Register #(.width(32), .trigger("rising"), .Select("low")) register_1 (
    .D(multiplexer_1_out), .en(\使能_高电平有效 ), .Q(pop), .clk(CLK));  // open: clr
  Register #(.width(32), .trigger("rising"), .Select("low")) register_2 (
    .D(multiplexer_2_out), .en(\使能_高电平有效 ), .Q(register_2_q), .clk(CLK));  // open: clr
  Multiplexer #(.select(1), .width(32), .disabled("Z"), .enable("false")) multiplexer_3 (
    .in0(register_2_q), .in1(register_4_q), .out(multiplexer_3_out), .sel(opt));
  Register #(.width(32), .trigger("rising"), .Select("low")) register_3 (
    .D(multiplexer_3_out), .en(\使能_高电平有效 ), .Q(register_3_q), .clk(CLK));  // open: clr
  Multiplexer #(.select(1), .width(32), .disabled("Z"), .enable("false")) multiplexer_4 (
    .in0(register_3_q), .in1(register_5_q), .out(multiplexer_4_out), .sel(opt));
  Multiplexer #(.select(1), .width(32), .disabled("Z"), .enable("false")) multiplexer_5 (
    .in0(register_4_q), .in1(register_6_q), .out(multiplexer_5_out), .sel(opt));
  Register #(.width(32), .trigger("rising"), .Select("low")) register_4 (
    .D(multiplexer_4_out), .en(\使能_高电平有效 ), .Q(register_4_q), .clk(CLK));  // open: clr
  Register #(.width(32), .trigger("rising"), .Select("low")) register_5 (
    .D(multiplexer_5_out), .en(\使能_高电平有效 ), .Q(register_5_q), .clk(CLK));  // open: clr
  Multiplexer #(.select(1), .width(32), .disabled("Z"), .enable("false")) multiplexer_6 (
    .in0(register_5_q), .in1(register_7_q), .out(multiplexer_6_out), .sel(opt));
  Register #(.width(32), .trigger("rising"), .Select("low")) register_6 (
    .D(multiplexer_6_out), .en(\使能_高电平有效 ), .Q(register_6_q), .clk(CLK));  // open: clr
  Multiplexer #(.select(1), .width(32), .disabled("Z"), .enable("false")) multiplexer_7 (
    .in0(register_6_q), .in1(register_8_q), .out(multiplexer_7_out), .sel(opt));
  Multiplexer #(.select(1), .width(32), .disabled("Z"), .enable("false")) multiplexer_8 (
    .in0(register_7_q), .in1({32{1'b0}}), .out(multiplexer_8_out), .sel(opt));
  Register #(.width(32), .trigger("rising"), .Select("low")) register_7 (
    .D(multiplexer_7_out), .en(\使能_高电平有效 ), .Q(register_7_q), .clk(CLK));  // open: clr
  Register #(.width(32), .trigger("rising"), .Select("low")) register_8 (
    .D(multiplexer_8_out), .en(\使能_高电平有效 ), .Q(register_8_q), .clk(CLK));  // open: clr
endmodule

module \单周期MIPS_单级中断  (
  input  IR1,
  input  IR2,
  input  IR3,
  output RegWrite,
  output MemWrite,
  output [31:0] PC,
  output [31:0] IR,
  output [31:0] RDin,
  output [31:0] MDin,
  output [31:0] LedData
);

  wire Alu_SRC, and_2_out, and_3_out, and_4_out, and_6_out, Beq, BLTZ, Bne, Branch, CLK, clock_2_out,
       comparator_1_eq, comparator_2_eq, comparator_3_eq, comparator_4_eq, comparator_6_eq, comparator_6_lt,
       comparator_7_lt, comparator_8_eq, d_ff_1_q, d_ff_2_q, d_ff_3_q, Equal, ERET, Go, halt, IE_qn, INT,
       IR1_t, IR2_t, IR3_t, IRA, IRB, IRC, JAL, JMP, JR, LB, Ledin, MemToReg, nand_1_out, not_1_out,
       not_2_out, not_3_out, not_4_out, or_1_out, SignedExt, SRAV, SysCall, W1, W2, W3, \中断控制_单级_1_有中断 ,
       \单周期硬布线控制器_1_regdst ;
  wire [1:0] \中断控制_单级_1_优先中断编号 ;
  wire [3:0] AluOP;
  wire [4:0] multiplexer_7_out, multiplexer_8_out, multiplexer_9_out, multiplexer_10_out, multiplexer_13_out;
  wire [7:0] multiplexer_15_out, multiplexer_17_out, multiplexer_17_out_2, multiplexer_17_out_3,
       multiplexer_17_out_4;
  wire [12:0] CNT_num;
  wire [15:0] \总周期数 ;
  wire [31:0] adder_1_out, adder_2_out, bit_extender_1_out, bit_extender_2_out, bit_extender_3_out, EPC,
       IntPC, multiplexer_2_out, multiplexer_3_out, multiplexer_5_out, multiplexer_6_out, multiplexer_11_out,
       multiplexer_12_out, multiplexer_16_out, NextPC, ram_1_data, result, rs, shifter_1_out;

  Clock #(.highDuration(1), .lowDuration(1)) clock_1 ();  // open: out
  Button _1 ();  // open: out
  Button _2 ();  // open: out
  Button _3 ();  // open: out
  Button \u_继续运行  (.out(Go));
  LED #(.active("true")) led_1 (.in(W1));
  LED #(.active("true")) led_2 (.in(W2));
  LED #(.active("true")) led_3 (.in(W3));
  Hex_Digit_Display hex_digit_display_1 (.value(LedData[31:28]));  // open: dp
  Comparator #(.width(16), .mode("twosComplement")) comparator_1 (
    .a(16'h23b), .b(\总周期数 ), .eq(comparator_1_eq));  // open: gt, lt
  Comparator #(.width(16), .mode("twosComplement")) comparator_2 (
    .a(\总周期数 ), .b(16'h1), .eq(comparator_2_eq));  // open: gt, lt
  Comparator #(.width(16), .mode("twosComplement")) comparator_3 (
    .a(\总周期数 ), .b(16'h4), .eq(comparator_3_eq));  // open: gt, lt
  Comparator #(.width(16), .mode("twosComplement")) comparator_4 (
    .a(\总周期数 ), .b(16'h7), .eq(comparator_4_eq));  // open: gt, lt
  Hex_Digit_Display hex_digit_display_2 (.value(LedData[27:24]));  // open: dp
  Hex_Digit_Display hex_digit_display_3 (.value(LedData[23:20]));  // open: dp
  or or_1 (or_1_out, comparator_1_eq, comparator_2_eq);
  assign IRA = or_1_out ? ~CLK : 1'bz;  // Controlled_Inverter controlled_inverter_1
  assign IRB = comparator_3_eq ? ~CLK : 1'bz;  // Controlled_Inverter controlled_inverter_2
  assign IRC = comparator_4_eq ? ~CLK : 1'bz;  // Controlled_Inverter controlled_inverter_3
  \中断控制_单级  \u_中断控制_单级_1  (
    .\同步清零 (ERET), .CLK(CLK), .IR1(IR1_t), .W1(W1), .IR2(IR2_t), .W2(W2), .IR3(IR3_t), .W3(W3),
    .\有中断 (\中断控制_单级_1_有中断 ), .\中断可接收 (INT), .\优先中断编号 (\中断控制_单级_1_优先中断编号 ));
  Hex_Digit_Display hex_digit_display_4 (.value(LedData[15:12]));  // open: dp
  Hex_Digit_Display hex_digit_display_5 (.value(LedData[19:16]));  // open: dp
  Pull_Resistor #(.pull(0)) pull_resistor_1 (.node(IRA));
  Pull_Resistor #(.pull(0)) pull_resistor_2 (.node(IRB));
  Pull_Resistor #(.pull(0)) pull_resistor_3 (.node(IRC));
  Comparator #(.width(32), .mode("twosComplement")) comparator_5 (.a(IR), .b(32'h42000018), .eq(ERET));  // open: gt, lt
  // Probe on \中断控制_单级_1_优先中断编号 
  D_Flip_Flop #(.trigger("rising"), .Pre_Clr_Positions("LEGACY"), .NegatePresetClear("false"), .enable("true"), .NewFFLayout("false")) d_ff_1 (
    .clk(CLK), .D(INT), .Q(d_ff_1_q));  // open: Qn, preset, en, reset
  D_Flip_Flop #(.trigger("rising"), .Pre_Clr_Positions("LEGACY"), .NegatePresetClear("false"), .enable("true"), .NewFFLayout("false")) d_ff_2 (
    .clk(CLK), .D(ERET), .Q(d_ff_2_q));  // open: Qn, preset, en, reset
  Hex_Digit_Display hex_digit_display_6 (.value(LedData[11:8]));  // open: dp
  Hex_Digit_Display hex_digit_display_7 (.value(LedData[7:4]));  // open: dp
  // Probe on \总周期数 
  D_Flip_Flop #(.trigger("rising"), .Pre_Clr_Positions("LEGACY"), .NegatePresetClear("false"), .enable("true"), .NewFFLayout("false")) IE (
    .Qn(IE_qn), .preset(d_ff_1_q), .reset(d_ff_2_q));  // open: clk, D, Q, en
  Hex_Digit_Display hex_digit_display_8 (.value(LedData[3:0]));  // open: dp
  Multiplexer #(.select(2), .width(32), .disabled("Z"), .enable("false")) multiplexer_1 (
    .in1(32'h30ac), .in2(32'h3150), .in3(32'h31f4), .out(IntPC), .sel(\中断控制_单级_1_优先中断编号 ));  // open: in0
  D_Flip_Flop #(.trigger("high"), .Pre_Clr_Positions("LEGACY"), .NegatePresetClear("false"), .enable("true"), .NewFFLayout("false")) d_ff_3 (.Q(d_ff_3_q));  // open: clk, D, Qn, preset, en, reset
  // Probe on 13'h368
  and and_1 (INT, \中断控制_单级_1_有中断 , IE_qn);
  // Probe on NextPC
  or or_2 (IR1_t, IR1, IRA);
  Clock #(.highDuration(1), .lowDuration(1)) clock_2 (.out(clock_2_out));
  // Probe on EPC
  Register #(.width(32), .trigger("rising"), .Select("low")) u_EPC (
    .D(NextPC), .en(INT), .Q(EPC), .clk(CLK));  // open: clr
  or or_3 (IR2_t, IR2, IRB);
  Comparator #(.width(13), .mode("twosComplement")) comparator_6 (
    .a(CNT_num), .b(13'h368), .eq(comparator_6_eq), .lt(comparator_6_lt));  // open: gt
  nand nand_1 (nand_1_out, d_ff_3_q, comparator_6_eq);
  Counter #(.width(13), .max('h1fff), .ongoal("stay"), .trigger("rising"), .behavior("old")) counter_1 (
    .count(comparator_6_lt), .Q(CNT_num), .clk(clock_2_out));  // open: load, D, carry, clr, preset
  or or_4 (IR3_t, IR3, IRC);
  assign CLK = nand_1_out ? clock_2_out : 1'bz;  // Controlled_Buffer controlled_buffer_1
  Pull_Resistor #(.pull(1)) pull_resistor_4 (.node(CLK));
  Multiplexer #(.select(1), .width(32), .disabled("Z"), .enable("false")) multiplexer_2 (
    .in0(adder_1_out), .in1(adder_2_out), .out(multiplexer_2_out), .sel(Branch));
  Multiplexer #(.select(1), .width(32), .disabled("Z"), .enable("false")) multiplexer_3 (
    .in0(multiplexer_2_out), .in1({4'b0000, IR[25:0], 2'b00}), .out(multiplexer_3_out), .sel(JMP));
  not not_1 (not_1_out, halt);
  Multiplexer #(.select(1), .width(32), .disabled("Z"), .enable("false")) multiplexer_4 (
    .in0(multiplexer_3_out), .in1(rs), .out(NextPC), .sel(JR));
  Counter #(.width(16), .max('hffff), .ongoal("stay"), .trigger("rising"), .behavior("old")) counter_2 (
    .count(not_1_out), .Q(\总周期数 ), .clk(CLK));  // open: load, D, carry, clr, preset
  Multiplexer #(.select(1), .width(32), .disabled("Z"), .enable("false")) multiplexer_5 (
    .in0(NextPC), .in1(IntPC), .out(multiplexer_5_out), .sel(INT));
  // Probe on multiplexer_6_out
  Multiplexer #(.select(1), .width(32), .disabled("Z"), .enable("false")) multiplexer_6 (
    .in0(multiplexer_5_out), .in1(EPC), .out(multiplexer_6_out), .sel(ERET));
  not not_2 (not_2_out, halt);
  Register #(.width(32), .trigger("rising"), .Select("low")) u_PC (
    .D(multiplexer_6_out), .en(not_2_out), .Q(PC), .clk(CLK));  // open: clr
  // Probe on PC
  Adder #(.width(32)) adder_1 (.a(PC), .b(32'h4), .out(adder_1_out));  // open: cin, cout
  // Probe on IR
  // Mips_Probe mips_probe_1: pin names not known; wires that end beside it: IR, IR[20:16]
  ROM #(.addrWidth(10), .dataWidth(32), .Select("high")) rom_1 (.addr(PC[11:2]), .data(IR));
  \单周期硬布线控制器  \u_单周期硬布线控制器_1  (
    .Func(IR[5:0]), .OP(IR[31:26]), .ALU_OP(AluOP), .MemToReg(MemToReg), .MemWrite(MemWrite),
    .ALU_SRC(Alu_SRC), .RegWrite(RegWrite), .SysCALL(SysCall), .SignedExt(SignedExt),
    .RegDst(\单周期硬布线控制器_1_regdst ), .JR(JR), .JMP(JMP), .Beq(Beq), .JAL(JAL), .Bne(Bne), .SRAV(SRAV), .LB(LB),
    .BLTZ(BLTZ));
  Multiplexer #(.select(1), .width(5), .disabled("Z"), .enable("false")) multiplexer_7 (
    .in0(IR[25:21]), .in1(5'b00010), .out(multiplexer_7_out), .sel(SysCall));
  Multiplexer #(.select(1), .width(5), .disabled("Z"), .enable("false")) multiplexer_8 (
    .in0(IR[20:16]), .in1(5'b00100), .out(multiplexer_8_out), .sel(SysCall));
  Multiplexer #(.select(1), .width(5), .disabled("Z"), .enable("false")) multiplexer_9 (
    .in0(IR[20:16]), .in1(IR[15:11]), .out(multiplexer_9_out), .sel(\单周期硬布线控制器_1_regdst ));
  // Probe on multiplexer_8_out
  // Probe on multiplexer_10_out
  Multiplexer #(.select(1), .width(5), .disabled("Z"), .enable("false")) multiplexer_10 (
    .in0(multiplexer_9_out), .in1({5{1'b1}}), .out(multiplexer_10_out), .sel(JAL));
  assign bit_extender_1_out = {{16{1'b0}}, IR[15:0]};  // Bit_Extender bit_extender_1
  assign bit_extender_2_out = {{16{IR[15]}}, IR[15:0]};  // Bit_Extender bit_extender_2
  // Probe on RDin
  // Probe on multiplexer_7_out
  Multiplexer #(.select(1), .width(32), .disabled("Z"), .enable("false")) multiplexer_11 (
    .in0(bit_extender_1_out), .in1(bit_extender_2_out), .out(multiplexer_11_out), .sel(SignedExt));
  Shifter #(.width(32), .shift("ll")) shifter_1 (.in(bit_extender_2_out), .\dist (5'b00010), .out(shifter_1_out));
  MIPS_Regifile mips_regifile_1 (
    .Din(RDin), .Clk(CLK), .R1(rs), .R2(MDin), .WE(RegWrite), .W_num(multiplexer_10_out),
    .R1_num(multiplexer_7_out), .R2_num(multiplexer_8_out));
  Adder #(.width(32)) adder_2 (.a(shifter_1_out), .b(adder_1_out), .out(adder_2_out));  // open: cin, cout
  Multiplexer #(.select(1), .width(32), .disabled("Z"), .enable("false")) multiplexer_12 (
    .in0(MDin), .in1(multiplexer_11_out), .out(multiplexer_12_out), .sel(Alu_SRC));
  Comparator #(.width(32), .mode("twosComplement")) comparator_7 (
    .a(rs), .b({32{1'b0}}), .lt(comparator_7_lt));  // open: gt, eq
  // Probe on rs
  // Probe on multiplexer_12_out
  Multiplexer #(.select(1), .width(5), .disabled("Z"), .enable("false")) multiplexer_13 (
    .in0(IR[10:6]), .in1(rs[4:0]), .out(multiplexer_13_out), .sel(SRAV));
  MIPS_ALU mips_alu_1 (
    .X(rs), .Y(multiplexer_12_out), .AluOP(AluOP), .Equal(Equal), .Result(result), .shamt(multiplexer_13_out));  // open: Result_2
  Multiplexer #(.select(1), .width(32), .disabled("Z"), .enable("false")) multiplexer_14 (
    .in0({multiplexer_17_out_4, multiplexer_17_out_3, multiplexer_17_out_2, multiplexer_17_out}),
    .in1(bit_extender_3_out), .out(RDin), .sel(LB));
  and and_2 (and_2_out, BLTZ, comparator_7_lt);
  and and_3 (and_3_out, Equal, Beq);
  not not_3 (not_3_out, Equal);
  and and_4 (and_4_out, not_3_out, Bne);
  Comparator #(.width(32), .mode("twosComplement")) comparator_8 (
    .a(32'h22), .b(rs), .eq(comparator_8_eq));  // open: gt, lt
  // Probe on result
  or or_5 (Branch, and_2_out, and_3_out, and_4_out);
  not not_4 (not_4_out, comparator_8_eq);
  Register #(.width(32), .trigger("rising"), .Select("low")) register_1 (
    .D(MDin), .en(Ledin), .Q(LedData), .clk(CLK));  // open: clr
  assign bit_extender_3_out = {{24{multiplexer_15_out[7]}}, multiplexer_15_out};  // Bit_Extender bit_extender_3
  and and_5 (Ledin, SysCall, comparator_8_eq);
  Register #(.width(1), .trigger("rising"), .Select("low")) register_2 (
    .D(SysCall), .en(and_6_out), .Q(halt), .clk(CLK), .clr(Go));
  and and_6 (and_6_out, SysCall, not_4_out);
  RAM #(.addrWidth(10), .dataWidth(32), .bus("separate"), .Select("high")) ram_1 (
    .addr(result[11:2]), .din(MDin), .data(ram_1_data), .str(MemWrite), .clk(CLK), .ld(1'b1));  // open: sel, clr
  Multiplexer #(.select(2), .width(8), .disabled("Z"), .enable("false")) multiplexer_15 (
    .in0(multiplexer_17_out), .in1(multiplexer_17_out_2), .in2(multiplexer_17_out_3),
    .in3(multiplexer_17_out_4), .out(multiplexer_15_out), .sel(result[1:0]));
  Multiplexer #(.select(1), .width(32), .disabled("Z"), .enable("false")) multiplexer_16 (
    .in0(result), .in1(ram_1_data), .out(multiplexer_16_out), .sel(MemToReg));
  Multiplexer #(.select(1), .width(32), .disabled("Z"), .enable("false")) multiplexer_17 (
    .in0(multiplexer_16_out), .in1(adder_1_out),
    .out({multiplexer_17_out_4, multiplexer_17_out_3, multiplexer_17_out_2, multiplexer_17_out}), .sel(JAL));

  // Notes on the sheet:
  //   中断源
  //   中断等待指示
  //   总复位信号应将除ROM以外所有存储组件全部清零
  //   单级中断测试信号模拟器
  //   数码管输出
  //   数码管输出应该用寄存器锁存，否则显示数据只能一闪而过
  //   控制位
  //   暂停节拍，不能为0
  //   用这个时钟源需要去掉电路中的其他时钟源
  //   戳工具置1进入计数暂停模式，ctrl+k时钟自动运行到对应节拍暂停
  //   ctrl+k关闭时钟连续运行，将控制位置零，进入单步调试模式调试
  //   可计数暂停的时钟源
  //   为方便自动评测，需要输出PC，IR，寄存器堆写如数据RDin
  //   RAM写使能MemWrite、RAM写入数据MDin等信号
  //   指令存储器
  //   contents of rom_1 (hex, n*v repeats v):
  //   201d07d0 20100001 109fc0 139fc3 8021 2012000c 24160008 26100001 3210000f 20080008 20090001 139900
  //   2709825 132020 20020022 c 1094022 1500fff9 22100001 2018000f 2188024 108700 20080008 20090001 139902
  //   2709825 132021 20020022 c 1094022 1500fff9 108702 2c9b022 12c00001 8000c07 4020 1084027 84400
  //   3508ffff 82021 20020022 c 8000c01 afa20000 23bd0004 afa40000 23bd0004 afb00000 23bd0004 afb30000
  //   23bd0004 afb40000 23bd0004 afb50000 23bd0004 afb60000 23bd0004 20160001 20140003 20150001 168020
  //   108100 2149825 132020 20020022 c 1600fffa 295a022 1680fff7 23bdfffc 8fb60000 23bdfffc 8fb50000
  //   23bdfffc 8fb40000 23bdfffc 8fb30000 23bdfffc 8fb00000 23bdfffc 8fa40000 23bdfffc 8fa20000 42000018
  //   afa20000 23bd0004 afa40000 23bd0004 afb00000 23bd0004 afb30000 23bd0004 afb40000 23bd0004 afb50000
  //   23bd0004 afb60000 23bd0004 20160002 20140003 20150001 168020 108100 2149825 132020 20020022 c
  //   1600fffa 295a022 1680fff7 23bdfffc 8fb60000 23bdfffc 8fb50000 23bdfffc 8fb40000 23bdfffc 8fb30000
  //   23bdfffc 8fb00000 23bdfffc 8fa40000 23bdfffc 8fa20000 42000018 afa20000 23bd0004 afa40000 23bd0004
  //   afb00000 23bd0004 afb30000 23bd0004 afb40000 23bd0004 afb50000 23bd0004 afb60000 23bd0004 20160003
  //   20140003 20150001 168020 108100 2149825 132020 20020022 c 1600fffa 295a022 1680fff7 23bdfffc
  //   8fb60000 23bdfffc 8fb50000 23bdfffc 8fb40000 23bdfffc 8fb30000 23bdfffc 8fb00000 23bdfffc 8fa40000
  //   23bdfffc 8fa20000 42000018
  //   指令字
  //   rs
  //   rt
  //   rd
  //   OP
  //   Func
  //   RegDst
endmodule

module \单周期MIPS_多级中断  (
  input  IR1,
  input  IR2,
  input  IR3,
  output RegWrite,
  output MemWrite,
  output [31:0] PC,
  output [31:0] IR,
  output [31:0] RDin,
  output [31:0] MDin,
  output [31:0] LedData
);

  wire Alu_SRC, and_2_out, and_3_out, and_4_out, and_6_out, Beq, BLTZ, Bne, Branch, CLK, clock_2_out,
       comparator_1_eq, comparator_2_eq, comparator_3_eq, comparator_4_eq, comparator_5_eq, comparator_9_eq,
       comparator_9_lt, comparator_10_lt, comparator_11_eq, d_ff_1_q, d_ff_2_q, d_ff_3_q, Equal, ERET, Go,
       halt, IE_qn, INT, IR1_t, IR2_t, IR3_t, IRA, IRB, IRC, JAL, JMP, JR, LB, Ledin, MemToReg, MFC0, MTC0,
       nand_1_out, not_1_out, not_2_out, not_3_out, not_4_out, or_1_out, or_2_out, or_3_out, or_4_out,
       or_5_out, SignedExt, SRAV, SysCall, W1, W2, W3, \中断控制_多级_1_有新中断 , \单周期硬布线控制器_1_regdst ;
  wire [1:0] \中断控制_多级_1_优先中断编号 ;
  wire [3:0] AluOP;
  wire [4:0] multiplexer_7_out, multiplexer_8_out, multiplexer_9_out, multiplexer_10_out, multiplexer_13_out;
  wire [7:0] multiplexer_15_out, multiplexer_17_out, multiplexer_17_out_2, multiplexer_17_out_3,
       multiplexer_17_out_4;
  wire [12:0] CNT_num;
  wire [15:0] \总周期数 ;
  wire [31:0] adder_1_out, adder_2_out, bit_extender_1_out, bit_extender_2_out, bit_extender_3_out, EPC,
       IntPC, multiplexer_2_out, multiplexer_3_out, multiplexer_5_out, multiplexer_6_out, multiplexer_11_out,
       multiplexer_12_out, multiplexer_16_out, NextPC, ram_1_data, result, rs, shifter_1_out;

  Clock #(.highDuration(1), .lowDuration(1)) clock_1 ();  // open: out
  Button _1 ();  // open: out
  Button _2 ();  // open: out
  Button _3 ();  // open: out
  Button \u_继续运行  (.out(Go));
  LED #(.active("true")) led_1 (.in(W1));
  LED #(.active("true")) led_2 (.in(W2));
  LED #(.active("true")) led_3 (.in(W3));
  Hex_Digit_Display hex_digit_display_1 (.value(LedData[31:28]));  // open: dp
  Comparator #(.width(16), .mode("twosComplement")) comparator_1 (
    .a(\总周期数 ), .b(16'h7), .eq(comparator_1_eq));  // open: gt, lt
  Comparator #(.width(16), .mode("twosComplement")) comparator_2 (
    .a(\总周期数 ), .b(16'h241), .eq(comparator_2_eq));  // open: gt, lt
  \中断控制_多级  \u_中断控制_多级_1  (
    .\同步清零 (ERET), .CLK(CLK), .IR1(IR1_t), .W1(W1), .IR2(IR2_t), .W2(W2), .IR3(IR3_t), .W3(W3),
    .\有新中断 (\中断控制_多级_1_有新中断 ), .\优先中断编号 (\中断控制_多级_1_优先中断编号 ), .\中断可接收 (INT));
  or or_1 (or_1_out, MTC0, INT);
  Hex_Digit_Display hex_digit_display_2 (.value(LedData[23:20]));  // open: dp
  Hex_Digit_Display hex_digit_display_3 (.value(LedData[27:24]));  // open: dp
  Comparator #(.width(16), .mode("twosComplement")) comparator_3 (
    .a(16'h258), .b(\总周期数 ), .eq(comparator_3_eq));  // open: gt, lt
  or or_2 (or_2_out, comparator_3_eq, comparator_4_eq);
  Comparator #(.width(16), .mode("twosComplement")) comparator_4 (
    .a(\总周期数 ), .b(16'h1), .eq(comparator_4_eq));  // open: gt, lt
  Comparator #(.width(16), .mode("twosComplement")) comparator_5 (
    .a(\总周期数 ), .b(16'h4), .eq(comparator_5_eq));  // open: gt, lt
  or or_3 (or_3_out, comparator_1_eq, comparator_2_eq);
  Comparator #(.width(32), .mode("twosComplement")) comparator_6 (.a(IR), .b(32'h42000018), .eq(ERET));  // open: gt, lt
  or or_4 (or_4_out, ERET, MFC0);
  \硬件堆栈  \u_硬件堆栈_1  (.\使能_高电平有效 (or_5_out), .CLK(CLK), .push(NextPC), .pop(EPC), .opt(ERET));
  // Probe on EPC
  or or_5 (or_5_out, ERET, INT);
  Hex_Digit_Display hex_digit_display_4 (.value(LedData[19:16]));  // open: dp
  Hex_Digit_Display hex_digit_display_5 (.value(LedData[15:12]));  // open: dp
  Pull_Resistor #(.pull(0)) pull_resistor_1 (.node(IRA));
  assign IRA = or_2_out ? ~CLK : 1'bz;  // Controlled_Inverter controlled_inverter_1
  Pull_Resistor #(.pull(0)) pull_resistor_2 (.node(IRB));
  assign IRB = comparator_5_eq ? ~CLK : 1'bz;  // Controlled_Inverter controlled_inverter_2
  Pull_Resistor #(.pull(0)) pull_resistor_3 (.node(IRC));
  assign IRC = or_3_out ? ~CLK : 1'bz;  // Controlled_Inverter controlled_inverter_3
  // Probe on \中断控制_多级_1_优先中断编号 
  D_Flip_Flop #(.trigger("rising"), .Pre_Clr_Positions("LEGACY"), .NegatePresetClear("false"), .enable("true"), .NewFFLayout("false")) d_ff_1 (
    .clk(CLK), .D(or_1_out), .Q(d_ff_1_q));  // open: Qn, preset, en, reset
  D_Flip_Flop #(.trigger("rising"), .Pre_Clr_Positions("LEGACY"), .NegatePresetClear("false"), .enable("true"), .NewFFLayout("false")) d_ff_2 (
    .clk(CLK), .D(or_4_out), .Q(d_ff_2_q));  // open: Qn, preset, en, reset
  Hex_Digit_Display hex_digit_display_6 (.value(LedData[7:4]));  // open: dp
  Hex_Digit_Display hex_digit_display_7 (.value(LedData[11:8]));  // open: dp
  // Probe on \总周期数 
  // Probe on IntPC
  D_Flip_Flop #(.trigger("rising"), .Pre_Clr_Positions("LEGACY"), .NegatePresetClear("false"), .enable("true"), .NewFFLayout("false")) IE (
    .Qn(IE_qn), .preset(d_ff_1_q), .reset(d_ff_2_q));  // open: clk, D, Q, en
  Hex_Digit_Display hex_digit_display_8 (.value(LedData[3:0]));  // open: dp
  Comparator #(.width(32), .mode("twosComplement")) comparator_7 (.a(IR), .b(32'h40800000), .eq(MTC0));  // open: gt, lt
  Multiplexer #(.select(2), .width(32), .disabled("Z"), .enable("false")) multiplexer_1 (
    .in1(32'h30ac), .in2(32'h3158), .in3(32'h3204), .out(IntPC), .sel(\中断控制_多级_1_优先中断编号 ));  // open: in0
  D_Flip_Flop #(.trigger("high"), .Pre_Clr_Positions("LEGACY"), .NegatePresetClear("false"), .enable("true"), .NewFFLayout("false")) d_ff_3 (.Q(d_ff_3_q));  // open: clk, D, Qn, preset, en, reset
  // Probe on 13'h10
  and and_1 (INT, \中断控制_多级_1_有新中断 , IE_qn);
  or or_6 (IR1_t, IR1, IRA);
  Clock #(.highDuration(1), .lowDuration(1)) clock_2 (.out(clock_2_out));
  Comparator #(.width(32), .mode("twosComplement")) comparator_8 (.a(IR), .b(32'h40000000), .eq(MFC0));  // open: gt, lt
  or or_7 (IR2_t, IR2, IRB);
  Comparator #(.width(13), .mode("twosComplement")) comparator_9 (
    .a(CNT_num), .b(13'h10), .eq(comparator_9_eq), .lt(comparator_9_lt));  // open: gt
  nand nand_1 (nand_1_out, d_ff_3_q, comparator_9_eq);
  Counter #(.width(13), .max('h1fff), .ongoal("stay"), .trigger("rising"), .behavior("old")) counter_1 (
    .count(comparator_9_lt), .Q(CNT_num), .clk(clock_2_out));  // open: load, D, carry, clr, preset
  or or_8 (IR3_t, IR3, IRC);
  assign CLK = nand_1_out ? clock_2_out : 1'bz;  // Controlled_Buffer controlled_buffer_1
  Pull_Resistor #(.pull(1)) pull_resistor_4 (.node(CLK));
  Multiplexer #(.select(1), .width(32), .disabled("Z"), .enable("false")) multiplexer_2 (
    .in0(adder_1_out), .in1(adder_2_out), .out(multiplexer_2_out), .sel(Branch));
  Multiplexer #(.select(1), .width(32), .disabled("Z"), .enable("false")) multiplexer_3 (
    .in0(multiplexer_2_out), .in1({4'b0000, IR[25:0], 2'b00}), .out(multiplexer_3_out), .sel(JMP));
  not not_1 (not_1_out, halt);
  Multiplexer #(.select(1), .width(32), .disabled("Z"), .enable("false")) multiplexer_4 (
    .in0(multiplexer_3_out), .in1(rs), .out(NextPC), .sel(JR));
  Counter #(.width(16), .max('hffff), .ongoal("stay"), .trigger("rising"), .behavior("old")) counter_2 (
    .count(not_1_out), .Q(\总周期数 ), .clk(CLK));  // open: load, D, carry, clr, preset
  Multiplexer #(.select(1), .width(32), .disabled("Z"), .enable("false")) multiplexer_5 (
    .in0(NextPC), .in1(IntPC), .out(multiplexer_5_out), .sel(INT));
  // Probe on multiplexer_6_out
  Multiplexer #(.select(1), .width(32), .disabled("Z"), .enable("false")) multiplexer_6 (
    .in0(multiplexer_5_out), .in1(EPC), .out(multiplexer_6_out), .sel(ERET));
  not not_2 (not_2_out, halt);
  Register #(.width(32), .trigger("rising"), .Select("low")) u_PC (
    .D(multiplexer_6_out), .en(not_2_out), .Q(PC), .clk(CLK));  // open: clr
  // Probe on PC
  Adder #(.width(32)) adder_1 (.a(PC), .b(32'h4), .out(adder_1_out));  // open: cin, cout
  // Probe on IR
  // Mips_Probe mips_probe_1: pin names not known; wires that end beside it: IR, IR[20:16]
  ROM #(.addrWidth(10), .dataWidth(32), .Select("high")) rom_1 (.addr(PC[11:2]), .data(IR));
  \单周期硬布线控制器  \u_单周期硬布线控制器_1  (
    .Func(IR[5:0]), .OP(IR[31:26]), .ALU_OP(AluOP), .MemToReg(MemToReg), .MemWrite(MemWrite),
    .ALU_SRC(Alu_SRC), .RegWrite(RegWrite), .SysCALL(SysCall), .SignedExt(SignedExt),
    .RegDst(\单周期硬布线控制器_1_regdst ), .JR(JR), .JMP(JMP), .Beq(Beq), .JAL(JAL), .Bne(Bne), .SRAV(SRAV), .LB(LB),
    .BLTZ(BLTZ));
  Multiplexer #(.select(1), .width(5), .disabled("Z"), .enable("false")) multiplexer_7 (
    .in0(IR[25:21]), .in1(5'b00010), .out(multiplexer_7_out), .sel(SysCall));
  Multiplexer #(.select(1), .width(5), .disabled("Z"), .enable("false")) multiplexer_8 (
    .in0(IR[20:16]), .in1(5'b00100), .out(multiplexer_8_out), .sel(SysCall));
  Multiplexer #(.select(1), .width(5), .disabled("Z"), .enable("false")) multiplexer_9 (
    .in0(IR[20:16]), .in1(IR[15:11]), .out(multiplexer_9_out), .sel(\单周期硬布线控制器_1_regdst ));
  // Probe on multiplexer_8_out
  // Probe on multiplexer_10_out
  Multiplexer #(.select(1), .width(5), .disabled("Z"), .enable("false")) multiplexer_10 (
    .in0(multiplexer_9_out), .in1({5{1'b1}}), .out(multiplexer_10_out), .sel(JAL));
  assign bit_extender_1_out = {{16{1'b0}}, IR[15:0]};  // Bit_Extender bit_extender_1
  assign bit_extender_2_out = {{16{IR[15]}}, IR[15:0]};  // Bit_Extender bit_extender_2
  // Probe on RDin
  // Probe on multiplexer_7_out
  Multiplexer #(.select(1), .width(32), .disabled("Z"), .enable("false")) multiplexer_11 (
    .in0(bit_extender_1_out), .in1(bit_extender_2_out), .out(multiplexer_11_out), .sel(SignedExt));
  Shifter #(.width(32), .shift("ll")) shifter_1 (.in(bit_extender_2_out), .\dist (5'b00010), .out(shifter_1_out));
  MIPS_Regifile mips_regifile_1 (
    .Din(RDin), .Clk(CLK), .R1(rs), .R2(MDin), .WE(RegWrite), .W_num(multiplexer_10_out),
    .R1_num(multiplexer_7_out), .R2_num(multiplexer_8_out));
  Adder #(.width(32)) adder_2 (.a(shifter_1_out), .b(adder_1_out), .out(adder_2_out));  // open: cin, cout
  Multiplexer #(.select(1), .width(32), .disabled("Z"), .enable("false")) multiplexer_12 (
    .in0(MDin), .in1(multiplexer_11_out), .out(multiplexer_12_out), .sel(Alu_SRC));
  Comparator #(.width(32), .mode("twosComplement")) comparator_10 (
    .a(rs), .b({32{1'b0}}), .lt(comparator_10_lt));  // open: gt, eq
  // Probe on rs
  // Probe on multiplexer_12_out
  Multiplexer #(.select(1), .width(5), .disabled("Z"), .enable("false")) multiplexer_13 (
    .in0(IR[10:6]), .in1(rs[4:0]), .out(multiplexer_13_out), .sel(SRAV));
  MIPS_ALU mips_alu_1 (
    .X(rs), .Y(multiplexer_12_out), .AluOP(AluOP), .Equal(Equal), .Result(result), .shamt(multiplexer_13_out));  // open: Result_2
  Multiplexer #(.select(1), .width(32), .disabled("Z"), .enable("false")) multiplexer_14 (
    .in0({multiplexer_17_out_4, multiplexer_17_out_3, multiplexer_17_out_2, multiplexer_17_out}),
    .in1(bit_extender_3_out), .out(RDin), .sel(LB));
  and and_2 (and_2_out, BLTZ, comparator_10_lt);
  and and_3 (and_3_out, Equal, Beq);
  not not_3 (not_3_out, Equal);
  and and_4 (and_4_out, not_3_out, Bne);
  Comparator #(.width(32), .mode("twosComplement")) comparator_11 (
    .a(32'h22), .b(rs), .eq(comparator_11_eq));  // open: gt, lt
  // Probe on result
  or or_9 (Branch, and_2_out, and_3_out, and_4_out);
  not not_4 (not_4_out, comparator_11_eq);
  Register #(.width(32), .trigger("rising"), .Select("low")) register_1 (
    .D(MDin), .en(Ledin), .Q(LedData), .clk(CLK));  // open: clr
  assign bit_extender_3_out = {{24{multiplexer_15_out[7]}}, multiplexer_15_out};  // Bit_Extender bit_extender_3
  and and_5 (Ledin, SysCall, comparator_11_eq);
  Register #(.width(1), .trigger("rising"), .Select("low")) register_2 (
    .D(SysCall), .en(and_6_out), .Q(halt), .clk(CLK), .clr(Go));
  and and_6 (and_6_out, SysCall, not_4_out);
  RAM #(.addrWidth(10), .dataWidth(32), .bus("separate"), .Select("high")) ram_1 (
    .addr(result[11:2]), .din(MDin), .data(ram_1_data), .str(MemWrite), .clk(CLK), .ld(1'b1));  // open: sel, clr
  Multiplexer #(.select(2), .width(8), .disabled("Z"), .enable("false")) multiplexer_15 (
    .in0(multiplexer_17_out), .in1(multiplexer_17_out_2), .in2(multiplexer_17_out_3),
    .in3(multiplexer_17_out_4), .out(multiplexer_15_out), .sel(result[1:0]));
  Multiplexer #(.select(1), .width(32), .disabled("Z"), .enable("false")) multiplexer_16 (
    .in0(result), .in1(ram_1_data), .out(multiplexer_16_out), .sel(MemToReg));
  Multiplexer #(.select(1), .width(32), .disabled("Z"), .enable("false")) multiplexer_17 (
    .in0(multiplexer_16_out), .in1(adder_1_out),
    .out({multiplexer_17_out_4, multiplexer_17_out_3, multiplexer_17_out_2, multiplexer_17_out}), .sel(JAL));

  // Notes on the sheet:
  //   中断源
  //   中断等待指示
  //   总复位信号应将除ROM以外所有存储组件全部清零
  //   多级中断测试信号模拟器
  //   数码管输出
  //   数码管输出应该用寄存器锁存，否则显示数据只能一闪而过
  //   控制位
  //   暂停节拍，不能为0
  //   用这个时钟源需要去掉电路中的其他时钟源
  //   戳工具置1进入计数暂停模式，ctrl+k时钟自动运行到对应节拍暂停
  //   ctrl+k关闭时钟连续运行，将控制位置零，进入单步调试模式调试
  //   可计数暂停的时钟源
  //   为方便自动评测，需要输出PC，IR，寄存器堆写如数据RDin
  //   RAM写使能MemWrite、RAM写入数据MDin等信号
  //   指令存储器
  //   contents of rom_1 (hex, n*v repeats v):
  //   201d07d0 20100001 109fc0 139fc3 8021 2012000c 24160008 26100001 3210000f 20080008 20090001 139900
  //   2709825 132020 20020022 c 1094022 1500fff9 22100001 2018000f 2188024 108700 20080008 20090001 139902
  //   2709825 132021 20020022 c 1094022 1500fff9 108702 2c9b022 12c00001 8000c07 4020 1084027 84400
  //   3508ffff 82021 20020022 c 8000c01 afa20000 23bd0004 afa40000 23bd0004 afb00000 23bd0004 afb30000
  //   23bd0004 afb40000 23bd0004 afb50000 23bd0004 afb60000 23bd0004 40000000 20160001 20140003 20150001
  //   168020 108100 2149825 132020 20020022 c 1600fffa 295a022 1680fff7 40800000 23bdfffc 8fb60000
  //   23bdfffc 8fb50000 23bdfffc 8fb40000 23bdfffc 8fb30000 23bdfffc 8fb00000 23bdfffc 8fa40000 23bdfffc
  //   8fa20000 42000018 afa20000 23bd0004 afa40000 23bd0004 afb00000 23bd0004 afb30000 23bd0004 afb40000
  //   23bd0004 afb50000 23bd0004 afb60000 23bd0004 40000000 20160002 20140003 20150001 168020 108100
  //   2149825 132020 20020022 c 1600fffa 295a022 1680fff7 40800000 23bdfffc 8fb60000 23bdfffc 8fb50000
  //   23bdfffc 8fb40000 23bdfffc 8fb30000 23bdfffc 8fb00000 23bdfffc 8fa40000 23bdfffc 8fa20000 42000018
  //   afa20000 23bd0004 afa40000 23bd0004 afb00000 23bd0004 afb30000 23bd0004 afb40000 23bd0004 afb50000
  //   23bd0004 afb60000 23bd0004 40000000 20160003 20140003 20150001 168020 108100 2149825 132020 20020022
  //   c 1600fffa 295a022 1680fff7 40800000 23bdfffc 8fb60000 23bdfffc 8fb50000 23bdfffc 8fb40000 23bdfffc
  //   8fb30000 23bdfffc 8fb00000 23bdfffc 8fa40000 23bdfffc 8fa20000 42000018
  //   指令字
  //   rs
  //   rt
  //   rd
  //   OP
  //   Func
  //   RegDst
endmodule
module \重定向流水线_单级中断  (
  output RegWrite,
  output MemWrite,
  output [31:0] IF_PC,
  output [31:0] ID_PC,
  output [31:0] EX_PC,
  output [31:0] M_PC,
  output [31:0] WB_PC,
  output [31:0] RDin,
  output [31:0] MDin,
  output [31:0] LedData
);

  wire and_3_out, and_4_out, and_5_out, and_6_out, and_8_out, Branch, BranchTaken, bub, CLK, clock_1_out,
       clock_2_out, comparator_2_eq, comparator_3_eq, comparator_4_eq, comparator_4_lt, comparator_5_lt,
       comparator_6_eq, d_ff_1_q, d_ff_2_q, d_ff_3_q, Equal, ERET, EX_Beq, EX_BLTZ, EX_Bne, EX_JMP, EX_JR,
       Go, halt, ID_Alu_SRC, ID_Beq, ID_BLTZ, ID_Bne, ID_JAL, ID_JMP, ID_JR, ID_LB, ID_MemToReg, ID_MemWrite,
       ID_RegDst, ID_RegWrite, ID_SRAV, ID_SysCall, IE_qn, INT, IR1, IR2, IR3, Ledin, LoadUse, nand_1_out,
       not_1_out, not_2_out, not_3_out, or_1_out, or_2_out, RST, SignedExt, Stall, W1, W2, W3, WB_LB,
       \中断控制_单级_1_有中断 , \相关处理逻辑_重定向_1_flush , \重定向流水接口ex_mem_1_mem_jal , \重定向流水接口ex_mem_1_mem_lb ,
       \重定向流水接口ex_mem_1_mem_memtoreg , \重定向流水接口ex_mem_1_mem_regwrite , \重定向流水接口ex_mem_1_mem_syscall ,
       \重定向流水接口id_ex_1_ex_alusrc , \重定向流水接口id_ex_1_ex_jal , \重定向流水接口id_ex_1_ex_lb ,
       \重定向流水接口id_ex_1_ex_memtoreg , \重定向流水接口id_ex_1_ex_memwrite , \重定向流水接口id_ex_1_ex_regwrite ,
       \重定向流水接口id_ex_1_ex_srav , \重定向流水接口id_ex_1_ex_syscall , \重定向流水接口mem_wb_1_wb_jal ,
       \重定向流水接口mem_wb_1_wb_memtoreg ;
  wire [1:0] \中断控制_单级_1_优先中断编号 , \相关处理逻辑_重定向_1_rsf , \相关处理逻辑_重定向_1_rtf , \重定向流水接口id_ex_1_ex_rsf ,
       \重定向流水接口id_ex_1_ex_rtf ;
  wire [3:0] ID_AluOP, \重定向流水接口id_ex_1_ex_aluop ;
  wire [4:0] EX_WriteReg, MEM_WriteReg, multiplexer_8_out, multiplexer_9_out, multiplexer_10_out,
       multiplexer_11_out, multiplexer_16_out, \重定向流水接口id_ex_1_ex_shamt , \重定向流水接口mem_wb_1_wb_writereg ;
  wire [5:0] Func;
  wire [7:0] multiplexer_19_out, multiplexer_20_out, multiplexer_20_out_2, multiplexer_20_out_3,
       multiplexer_20_out_4;
  wire [12:0] CNT_num;
  wire [15:0] \LoadUse次数 , \总周期数 , \插入气泡数 , \无条件分支数 , \条件分支成功数 ;
  wire [31:0] adder_1_out, adder_2_out, bit_extender_1_out, bit_extender_2_out, bit_extender_3_out, BranchPC,
       EPC, EX_IR, EX_RS, IF_IR, IntPC, MEM_AluResult, MEM_IR, mips_alu_1_result, \mips_regifile_下降沿_1_r1 ,
       \mips_regifile_下降沿_1_r2 , multiplexer_3_out, multiplexer_4_out, multiplexer_6_out, multiplexer_7_out,
       multiplexer_12_out, multiplexer_14_out, multiplexer_15_out, multiplexer_18_out, NextPC, ram_1_data,
       result, shifter_1_out, WB_IR, \气泡流水接口if_id_1_id_pc , \重定向流水接口ex_mem_1_mem_pc ,
       \重定向流水接口ex_mem_1_mem_rs , \重定向流水接口id_ex_1_ex_addr , \重定向流水接口id_ex_1_ex_imm , \重定向流水接口id_ex_1_ex_pc_2 ,
       \重定向流水接口id_ex_1_ex_rs , \重定向流水接口id_ex_1_ex_rt , \重定向流水接口id_ex_1_ex_signimm ,
       \重定向流水接口mem_wb_1_wb_memresult , \重定向流水接口mem_wb_1_wb_pc ;
  wire [31:6] ID_IR;

  Button \u_总复位  (.out(RST));
  Button _1 (.out(IR1));
  Button _2 (.out(IR2));
  Button _3 (.out(IR3));
  // Probe on \总周期数 
  // Probe on \总周期数 
  Button \u_继续运行  (.out(Go));
  LED #(.active("true")) led_1 (.in(W1));
  LED #(.active("true")) led_2 (.in(W2));
  LED #(.active("true")) led_3 (.in(W3));
  Hex_Digit_Display hex_digit_display_1 (.value(LedData[31:28]));  // open: dp
  // Probe on IF_PC[19:0]
  // Mips_Probe mips_probe_1: pin names not known; wires that end beside it: IF_IR
  // Probe on NextPC
  Hex_Digit_Display hex_digit_display_2 (.value(LedData[23:20]));  // open: dp
  Hex_Digit_Display hex_digit_display_3 (.value(LedData[27:24]));  // open: dp
  // Probe on ID_PC[19:0]
  // Mips_Probe mips_probe_2: pin names not known; wires that end beside it: {ID_IR, Func}
  \中断控制_单级  \u_中断控制_单级_1  (
    .\同步清零 (ERET), .CLK(CLK), .IR1(IR1), .W1(W1), .IR2(IR2), .W2(W2), .IR3(IR3), .W3(W3),
    .\有中断 (\中断控制_单级_1_有中断 ), .\中断可接收 (INT), .\优先中断编号 (\中断控制_单级_1_优先中断编号 ));
  // Probe on EPC
  Register #(.width(32), .trigger("rising"), .Select("low")) u_EPC (
    .D(NextPC), .en(INT), .Q(EPC), .clk(CLK));  // open: clr
  Hex_Digit_Display hex_digit_display_4 (.value(LedData[15:12]));  // open: dp
  Hex_Digit_Display hex_digit_display_5 (.value(LedData[19:16]));  // open: dp
  Comparator #(.width(32), .mode("twosComplement")) comparator_1 (
    .a(EX_IR), .b(32'h42000018), .eq(ERET));  // open: gt, lt
  // Probe on \中断控制_单级_1_优先中断编号 
  D_Flip_Flop #(.trigger("rising"), .Pre_Clr_Positions("LEGACY"), .NegatePresetClear("false"), .enable("true"), .NewFFLayout("false")) d_ff_1 (
    .clk(CLK), .D(INT), .Q(d_ff_1_q));  // open: Qn, preset, en, reset
  D_Flip_Flop #(.trigger("rising"), .Pre_Clr_Positions("LEGACY"), .NegatePresetClear("false"), .enable("true"), .NewFFLayout("false")) d_ff_2 (
    .clk(CLK), .D(ERET), .Q(d_ff_2_q));  // open: Qn, preset, en, reset
  Hex_Digit_Display hex_digit_display_6 (.value(LedData[7:4]));  // open: dp
  Hex_Digit_Display hex_digit_display_7 (.value(LedData[11:8]));  // open: dp
  Clock #(.highDuration(1), .lowDuration(1)) clock_1 (.out(clock_1_out));
  // Probe on EX_PC[19:0]
  // Mips_Probe mips_probe_3: pin names not known; wires that end beside it: clock_1_out, EX_IR, CLK
  D_Flip_Flop #(.trigger("rising"), .Pre_Clr_Positions("LEGACY"), .NegatePresetClear("false"), .enable("true"), .NewFFLayout("false")) IE (
    .Qn(IE_qn), .preset(d_ff_1_q), .reset(d_ff_2_q));  // open: clk, D, Q, en
  Hex_Digit_Display hex_digit_display_8 (.value(LedData[3:0]));  // open: dp
  Multiplexer #(.select(2), .width(32), .disabled("Z"), .enable("false")) multiplexer_1 (
    .in1(32'h30ac), .in2(32'h3150), .in3(32'h31f4), .out(IntPC), .sel(\中断控制_单级_1_优先中断编号 ));  // open: in0
  Multiplexer #(.select(1), .width(32), .disabled("Z"), .enable("false")) multiplexer_2 (
    .in0(ID_PC), .in1(BranchPC), .out(NextPC), .sel(BranchTaken));
  // Probe on \总周期数 
  // Probe on M_PC[19:0]
  // Mips_Probe mips_probe_4: pin names not known; wires that end beside it: MEM_IR
  Comparator #(.width(32), .mode("twosComplement")) comparator_2 (
    .a(EX_IR), .b({32{1'b0}}), .eq(comparator_2_eq));  // open: gt, lt
  Comparator #(.width(32), .mode("twosComplement")) comparator_3 (
    .a(EX_PC), .b({32{1'b0}}), .eq(comparator_3_eq));  // open: gt, lt
  and and_1 (INT, ~bub, \中断控制_单级_1_有中断 , IE_qn);  // AND_Gate
  // Probe on NextPC
  // Probe on \总周期数 
  // Probe on \无条件分支数 
  // Probe on \条件分支成功数 
  // Probe on \插入气泡数 
  // Probe on \LoadUse次数 
  and and_2 (bub, comparator_2_eq, comparator_3_eq);
  // Probe on IF_PC[11:0]
  // Probe on WB_PC[19:0]
  // Mips_Probe mips_probe_5: pin names not known; wires that end beside it: WB_IR
  // Probe on ID_PC[11:0]
  // Probe on EX_PC[11:0]
  // Probe on M_PC[11:0]
  D_Flip_Flop #(.trigger("high"), .Pre_Clr_Positions("LEGACY"), .NegatePresetClear("false"), .enable("true"), .NewFFLayout("false")) d_ff_3 (.Q(d_ff_3_q));  // open: clk, D, Qn, preset, en, reset
  // Probe on 13'hea
  Multiplexer #(.select(1), .width(32), .disabled("Z"), .enable("false")) multiplexer_3 (
    .in0(adder_1_out), .in1(adder_2_out), .out(multiplexer_3_out), .sel(Branch));
  // Probe on WB_PC[11:0]
  Comparator #(.width(13), .mode("twosComplement")) comparator_4 (
    .a(CNT_num), .b(13'hea), .eq(comparator_4_eq), .lt(comparator_4_lt));  // open: gt
  Clock #(.highDuration(1), .lowDuration(1)) clock_2 (.out(clock_2_out));
  Counter #(.width(16), .max('hffff), .ongoal("stay"), .trigger("rising"), .behavior("old")) counter_1 (
    .count(not_1_out), .Q(\总周期数 ), .clk(CLK));  // open: load, D, carry, clr, preset
  not not_1 (not_1_out, halt);
  Counter #(.width(16), .max('hffff), .ongoal("stay"), .trigger("rising"), .behavior("old")) counter_2 (
    .count(Stall), .Q(\插入气泡数 ), .clk(CLK));  // open: load, D, carry, clr, preset
  Counter #(.width(16), .max('hffff), .ongoal("stay"), .trigger("rising"), .behavior("old")) counter_3 (
    .count(EX_JMP), .Q(\无条件分支数 ), .clk(CLK));  // open: load, D, carry, clr, preset
  Counter #(.width(16), .max('hffff), .ongoal("stay"), .trigger("rising"), .behavior("old")) counter_4 (
    .count(Branch), .Q(\条件分支成功数 ), .clk(CLK));  // open: load, D, carry, clr, preset
  Counter #(.width(16), .max('hffff), .ongoal("stay"), .trigger("rising"), .behavior("old")) counter_5 (
    .count(LoadUse), .Q(\LoadUse次数 ), .clk(CLK));  // open: load, D, carry, clr, preset
  Multiplexer #(.select(1), .width(32), .disabled("Z"), .enable("false")) multiplexer_4 (
    .in0(multiplexer_3_out), .in1(\重定向流水接口id_ex_1_ex_addr ), .out(multiplexer_4_out), .sel(EX_JMP));
  nand nand_1 (nand_1_out, d_ff_3_q, comparator_4_eq);
  Counter #(.width(13), .max('h1fff), .ongoal("stay"), .trigger("rising"), .behavior("old")) counter_6 (
    .count(comparator_4_lt), .Q(CNT_num), .clk(clock_2_out));  // open: load, D, carry, clr, preset
  Multiplexer #(.select(1), .width(32), .disabled("Z"), .enable("false")) multiplexer_5 (
    .in0(multiplexer_4_out), .in1(EX_RS), .out(BranchPC), .sel(EX_JR));
  assign CLK = nand_1_out ? clock_2_out : 1'bz;  // Controlled_Buffer controlled_buffer_1
  Multiplexer #(.select(1), .width(32), .disabled("Z"), .enable("false")) multiplexer_6 (
    .in0(BranchPC), .in1(IntPC), .out(multiplexer_6_out), .sel(INT));
  Multiplexer #(.select(1), .width(32), .disabled("Z"), .enable("false")) multiplexer_7 (
    .in0(multiplexer_6_out), .in1(EPC), .out(multiplexer_7_out), .sel(ERET));
  Pull_Resistor #(.pull(1)) pull_resistor_1 (.node(CLK));
  and and_3 (and_3_out, ~halt, ~Stall);  // AND_Gate
  Register #(.width(32), .trigger("rising"), .Select("low")) PC (
    .D(multiplexer_7_out), .en(and_3_out), .Q(IF_PC), .clk(CLK));  // open: clr
  \单周期硬布线控制器  \u_单周期硬布线控制器_1  (
    .Func(Func), .OP(ID_IR[31:26]), .ALU_OP(ID_AluOP), .MemToReg(ID_MemToReg), .MemWrite(ID_MemWrite),
    .ALU_SRC(ID_Alu_SRC), .RegWrite(ID_RegWrite), .SysCALL(ID_SysCall), .SignedExt(SignedExt),
    .RegDst(ID_RegDst), .JR(ID_JR), .JMP(ID_JMP), .Beq(ID_Beq), .JAL(ID_JAL), .Bne(ID_Bne), .SRAV(ID_SRAV),
    .LB(ID_LB), .BLTZ(ID_BLTZ));
  Adder #(.width(32)) adder_1 (.a(IF_PC), .b(32'h4), .out(adder_1_out));  // open: cin, cout
  ROM #(.addrWidth(10), .dataWidth(32), .Select("high")) rom_1 (.addr(IF_PC[11:2]), .data(IF_IR));
  or or_1 (or_1_out, ERET, INT, BranchTaken);
  // Mips_Probe mips_probe_6: pin names not known; wires that end beside it: IF_IR
  \相关处理逻辑_重定向  \u_相关处理逻辑_重定向_1  (
    .R1(multiplexer_8_out), .Instr({ID_IR, Func}), .R2(multiplexer_9_out),
    .EX_RegWrite(\重定向流水接口id_ex_1_ex_regwrite ), .EX_WriteReg_num(EX_WriteReg),
    .EX_MemtoReg(\重定向流水接口id_ex_1_ex_memtoreg ), .BranchTaken(BranchTaken),
    .MEM_RegWrite(\重定向流水接口ex_mem_1_mem_regwrite ), .MEM_WriteReg_num(MEM_WriteReg), .Stall(Stall),
    .Flush(\相关处理逻辑_重定向_1_flush ), .RSF(\相关处理逻辑_重定向_1_rsf ), .RTF(\相关处理逻辑_重定向_1_rtf ), .LoadUse(LoadUse));
  \气泡流水接口IF_ID  \u_气泡流水接口if_id_1  (
    .IF_IR(IF_IR), .IF_PC(adder_1_out), .ID_IR({ID_IR, Func}), .ID_PC(\气泡流水接口if_id_1_id_pc ), .CLK(CLK),
    .\同步清零_气泡_高电平有效 (or_1_out), .\使能端_为高电平时忽略时钟输入 (Stall), .IF_monitor(IF_PC), .ID_monitor(ID_PC));  // open: IF_PredictJump, ID_PredictJump
  // Probe on {ID_IR, Func}
  // Probe on \相关处理逻辑_重定向_1_rsf 
  // Probe on \相关处理逻辑_重定向_1_rtf 
  // Probe on multiplexer_8_out
  // Probe on multiplexer_9_out
  Multiplexer #(.select(1), .width(5), .disabled("Z"), .enable("false")) multiplexer_8 (
    .in0(ID_IR[25:21]), .in1(5'b00010), .out(multiplexer_8_out), .sel(ID_SysCall));
  Multiplexer #(.select(1), .width(5), .disabled("Z"), .enable("false")) multiplexer_9 (
    .in0(ID_IR[20:16]), .in1(5'b00100), .out(multiplexer_9_out), .sel(ID_SysCall));
  assign bit_extender_1_out = {{16{1'b0}}, {ID_IR[15:6], Func}};  // Bit_Extender bit_extender_1
  assign bit_extender_2_out = {{16{ID_IR[15]}}, {ID_IR[15:6], Func}};  // Bit_Extender bit_extender_2
  Multiplexer #(.select(1), .width(5), .disabled("Z"), .enable("false")) multiplexer_10 (
    .in0(ID_IR[20:16]), .in1(ID_IR[15:11]), .out(multiplexer_10_out), .sel(ID_RegDst));
  Multiplexer #(.select(1), .width(5), .disabled("Z"), .enable("false")) multiplexer_11 (
    .in0(multiplexer_10_out), .in1({5{1'b1}}), .out(multiplexer_11_out), .sel(ID_JAL));
  Comparator #(.width(32), .mode("twosComplement")) comparator_5 (
    .a(EX_RS), .b({32{1'b0}}), .lt(comparator_5_lt));  // open: gt, eq
  \MIPS_Regifile_下降沿  \mips_regifile_下降沿_1  (
    .Din(RDin), .Clk(CLK), .R1(\mips_regifile_下降沿_1_r1 ), .R2(\mips_regifile_下降沿_1_r2 ), .WE(RegWrite),
    .W_num(\重定向流水接口mem_wb_1_wb_writereg ), .R1_num(multiplexer_8_out), .R2_num(multiplexer_9_out));
  Multiplexer #(.select(1), .width(32), .disabled("Z"), .enable("false")) multiplexer_12 (
    .in0(bit_extender_1_out), .in1(bit_extender_2_out), .out(multiplexer_12_out), .sel(SignedExt));
  // Probe on \气泡流水接口if_id_1_id_pc 
  and and_4 (and_4_out, EX_BLTZ, comparator_5_lt);
  and and_5 (and_5_out, Equal, EX_Beq);
  not not_2 (not_2_out, Equal);
  and and_6 (and_6_out, not_2_out, EX_Bne);
  or or_2 (or_2_out, ERET, INT, \相关处理逻辑_重定向_1_flush );
  \重定向流水接口ID_EX  \u_重定向流水接口id_ex_1  (
    .ID_RegWrite(ID_RegWrite), .ID_MemToReg(ID_MemToReg), .ID_JAL(ID_JAL), .ID_LB(ID_LB),
    .ID_MemWrite(ID_MemWrite), .ID_Syscall(ID_SysCall), .ID_Beq(ID_Beq), .ID_Bne(ID_Bne), .ID_JMP(ID_JMP),
    .ID_JR(ID_JR), .ID_BLTZ(ID_BLTZ), .ID_AluOP(ID_AluOP), .ID_AluSRC(ID_Alu_SRC), .ID_SRAV(ID_SRAV),
    .ID_RSF(\相关处理逻辑_重定向_1_rsf ), .ID_RTF(\相关处理逻辑_重定向_1_rtf ), .ID_RS(\mips_regifile_下降沿_1_r1 ),
    .ID_RT(\mips_regifile_下降沿_1_r2 ), .ID_shamt(ID_IR[10:6]), .ID_Imm(multiplexer_12_out),
    .ID_SignImm(bit_extender_2_out), .ID_PC(\气泡流水接口if_id_1_id_pc ), .ID_WriteReg(multiplexer_11_out),
    .ID_IR({ID_IR, Func}), .ID_addr({4'b0000, ID_IR[25:6], Func, 2'b00}), .ID_monitor(ID_PC), .CLK(CLK),
    .EX_RegWrite(\重定向流水接口id_ex_1_ex_regwrite ), .EX_MemToReg(\重定向流水接口id_ex_1_ex_memtoreg ),
    .EX_JAL(\重定向流水接口id_ex_1_ex_jal ), .EX_LB(\重定向流水接口id_ex_1_ex_lb ),
    .EX_MemWrite(\重定向流水接口id_ex_1_ex_memwrite ), .EX_Syscall(\重定向流水接口id_ex_1_ex_syscall ), .EX_Beq(EX_Beq),
    .EX_PC(EX_Bne), .EX_JMP(EX_JMP), .EX_JR(EX_JR), .ID_BLTZ_2(EX_BLTZ),
    .EX_AluOP(\重定向流水接口id_ex_1_ex_aluop ), .EX_AluSRC(\重定向流水接口id_ex_1_ex_alusrc ),
    .EX_SRAV(\重定向流水接口id_ex_1_ex_srav ), .EX_RSF(\重定向流水接口id_ex_1_ex_rsf ), .EX_RTF(\重定向流水接口id_ex_1_ex_rtf ),
    .EX_RS(\重定向流水接口id_ex_1_ex_rs ), .EX_RT(\重定向流水接口id_ex_1_ex_rt ), .EX_shamt(\重定向流水接口id_ex_1_ex_shamt ),
    .EX_Imm(\重定向流水接口id_ex_1_ex_imm ), .EX_SignImm(\重定向流水接口id_ex_1_ex_signimm ),
    .EX_PC_2(\重定向流水接口id_ex_1_ex_pc_2 ), .EX_WriteReg(EX_WriteReg), .EX_IR(EX_IR),
    .EX_addr(\重定向流水接口id_ex_1_ex_addr ), .EX_monitor(EX_PC), .\同步清零_气泡_高电平有效 (or_2_out));  // open: 使能端_为高电平时忽略时钟输入, ID_PredictJump, EX_PredictJump
  // Probe on \重定向流水接口id_ex_1_ex_rsf 
  // Probe on EX_WriteReg
  or or_3 (Branch, and_4_out, and_5_out, and_6_out);
  // Probe on \重定向流水接口id_ex_1_ex_rtf 
  Multiplexer #(.select(2), .width(32), .disabled("Z"), .enable("false")) multiplexer_13 (
    .in0(\重定向流水接口id_ex_1_ex_rs ), .in1(MEM_AluResult), .in2(RDin), .out(EX_RS), .sel(\重定向流水接口id_ex_1_ex_rsf ));  // open: in3
  Multiplexer #(.select(2), .width(32), .disabled("Z"), .enable("false")) multiplexer_14 (
    .in0(\重定向流水接口id_ex_1_ex_rt ), .in1(MEM_AluResult), .in2(RDin), .out(multiplexer_14_out),
    .sel(\重定向流水接口id_ex_1_ex_rtf ));  // open: in3
  // Probe on \重定向流水接口id_ex_1_ex_pc_2 
  or or_4 (BranchTaken, Branch, EX_JMP);
  Multiplexer #(.select(1), .width(32), .disabled("Z"), .enable("false")) multiplexer_15 (
    .in0(multiplexer_14_out), .in1(\重定向流水接口id_ex_1_ex_imm ), .out(multiplexer_15_out),
    .sel(\重定向流水接口id_ex_1_ex_alusrc ));
  Multiplexer #(.select(1), .width(5), .disabled("Z"), .enable("false")) multiplexer_16 (
    .in0(\重定向流水接口id_ex_1_ex_shamt ), .in1(EX_RS[4:0]), .out(multiplexer_16_out),
    .sel(\重定向流水接口id_ex_1_ex_srav ));
  Shifter #(.width(32), .shift("ll")) shifter_1 (
    .in(\重定向流水接口id_ex_1_ex_signimm ), .\dist (5'b00010), .out(shifter_1_out));
  Adder #(.width(32)) adder_2 (.a(shifter_1_out), .b(\重定向流水接口id_ex_1_ex_pc_2 ), .out(adder_2_out));  // open: cin, cout
  // Probe on adder_2_out
  // Probe on EX_RS
  MIPS_ALU mips_alu_1 (
    .X(EX_RS), .Y(multiplexer_15_out), .AluOP(\重定向流水接口id_ex_1_ex_aluop ), .Equal(Equal),
    .Result(mips_alu_1_result), .shamt(multiplexer_16_out));  // open: Result_2
  \重定向流水接口EX_MEM  \u_重定向流水接口ex_mem_1  (
    .EX_RegWrite(\重定向流水接口id_ex_1_ex_regwrite ), .EX_MemToReg(\重定向流水接口id_ex_1_ex_memtoreg ),
    .EX_JAL(\重定向流水接口id_ex_1_ex_jal ), .EX_LB(\重定向流水接口id_ex_1_ex_lb ),
    .EX_MemWrite(\重定向流水接口id_ex_1_ex_memwrite ), .EX_Syscall(\重定向流水接口id_ex_1_ex_syscall ), .EX_RS(EX_RS),
    .EX_result(mips_alu_1_result), .EX_MDin(multiplexer_14_out), .EX_PC(\重定向流水接口id_ex_1_ex_pc_2 ),
    .EX_WriteReg(EX_WriteReg), .EX_IR(EX_IR), .EX_monitor(EX_PC), .CLK(CLK),
    .MEM_RegWrite(\重定向流水接口ex_mem_1_mem_regwrite ), .MEM_MemToReg(\重定向流水接口ex_mem_1_mem_memtoreg ),
    .MEM_JAL(\重定向流水接口ex_mem_1_mem_jal ), .MEM_LB(\重定向流水接口ex_mem_1_mem_lb ), .MEM_MemWrite(MemWrite),
    .MEM_Syscall(\重定向流水接口ex_mem_1_mem_syscall ), .MEM_RS(\重定向流水接口ex_mem_1_mem_rs ),
    .MEM_result(MEM_AluResult), .MEM_MDin(MDin), .MEM_PC(\重定向流水接口ex_mem_1_mem_pc ),
    .MEM_WriteReg(MEM_WriteReg), .MEM_IR(MEM_IR), .MEM_monitor(M_PC));  // open: 同步清零_气泡_高电平有效, 使能端_低电平有效_stall_高电平有效
  // Probe on MEM_WriteReg
  Register #(.width(32), .trigger("rising"), .Select("low")) register_1 (
    .D(MDin), .en(Ledin), .Q(LedData), .clk(CLK));  // open: clr
  // Probe on RDin
  RAM #(.addrWidth(10), .dataWidth(32), .bus("separate"), .Select("high")) ram_1 (
    .addr(MEM_AluResult[11:2]), .din(MDin), .data(ram_1_data), .str(MemWrite), .clk(CLK), .ld(1'b1));  // open: sel, clr
  \重定向流水接口MEM_WB  \u_重定向流水接口mem_wb_1  (
    .MEM_RegWrite(\重定向流水接口ex_mem_1_mem_regwrite ), .MEM_MemToReg(\重定向流水接口ex_mem_1_mem_memtoreg ),
    .MEM_JAL(\重定向流水接口ex_mem_1_mem_jal ), .MEM_LB(\重定向流水接口ex_mem_1_mem_lb ), .MEM_AluResult(MEM_AluResult),
    .MEM_MemResult(ram_1_data), .MEM_PC(\重定向流水接口ex_mem_1_mem_pc ), .MEM_WriteReg(MEM_WriteReg),
    .MEM_IR(MEM_IR), .MEM_monitor(M_PC), .CLK(CLK), .WB_RegWrite(RegWrite),
    .WB_MemToReg(\重定向流水接口mem_wb_1_wb_memtoreg ), .WB_JAL(\重定向流水接口mem_wb_1_wb_jal ), .WB_LB(WB_LB),
    .WB_AluResult(result), .WB_MemResult(\重定向流水接口mem_wb_1_wb_memresult ), .WB_PC(\重定向流水接口mem_wb_1_wb_pc ),
    .WB_WriteReg(\重定向流水接口mem_wb_1_wb_writereg ), .WB_IR(WB_IR), .WB_monitor(WB_PC));  // open: 同步清零_气泡_高电平有效, 使能端_为高电平时忽略时钟输入
  Multiplexer #(.select(1), .width(32), .disabled("Z"), .enable("false")) multiplexer_17 (
    .in0({multiplexer_20_out_4, multiplexer_20_out_3, multiplexer_20_out_2, multiplexer_20_out}),
    .in1(bit_extender_3_out), .out(RDin), .sel(WB_LB));
  Comparator #(.width(32), .mode("twosComplement")) comparator_6 (
    .a(32'h22), .b(\重定向流水接口ex_mem_1_mem_rs ), .eq(comparator_6_eq));  // open: gt, lt
  assign bit_extender_3_out = {{24{multiplexer_19_out[7]}}, multiplexer_19_out};  // Bit_Extender bit_extender_3
  not not_3 (not_3_out, comparator_6_eq);
  Multiplexer #(.select(1), .width(32), .disabled("Z"), .enable("false")) multiplexer_18 (
    .in0(result), .in1(\重定向流水接口mem_wb_1_wb_memresult ), .out(multiplexer_18_out),
    .sel(\重定向流水接口mem_wb_1_wb_memtoreg ));
  Multiplexer #(.select(2), .width(8), .disabled("Z"), .enable("false")) multiplexer_19 (
    .in0(multiplexer_20_out), .in1(multiplexer_20_out_2), .in2(multiplexer_20_out_3),
    .in3(multiplexer_20_out_4), .out(multiplexer_19_out), .sel(result[1:0]));
  and and_7 (Ledin, \重定向流水接口ex_mem_1_mem_syscall , comparator_6_eq);
  Register #(.width(1), .trigger("rising"), .Select("low")) register_2 (
    .D(\重定向流水接口ex_mem_1_mem_syscall ), .en(and_8_out), .Q(halt), .clk(CLK), .clr(Go));
  and and_8 (and_8_out, \重定向流水接口ex_mem_1_mem_syscall , not_3_out);
  Multiplexer #(.select(1), .width(32), .disabled("Z"), .enable("false")) multiplexer_20 (
    .in0(multiplexer_18_out), .in1(\重定向流水接口mem_wb_1_wb_pc ),
    .out({multiplexer_20_out_4, multiplexer_20_out_3, multiplexer_20_out_2, multiplexer_20_out}),
    .sel(\重定向流水接口mem_wb_1_wb_jal ));

  // Other names for the same wires on the sheet: ID_IR[5:0] = Func; OP[5:0] = ID_IR[31:26]; IR[31:0] = IF_IR;
  //   MEM_PC[31:0] = M_PC; PC[31:0] = IF_PC

  // Notes on the sheet:
  //   中断源
  //   时空图监测，可删除
  //   中断等待指示
  //   数码管输出
  //   控制位
  //   流水调试日志用
  //   暂停节拍，不能为0
  //   戳工具置1进入计数暂停模式，ctrl+k时钟自动运行到对应节拍暂停
  //   ctrl+k关闭时钟连续运行，将控制位置零，进入单步调试模式调试
  //   可计数暂停的时钟源
  //   为方便自动评测，需要输出流水线各段保存的PC值，注意是PC不是PC+4，另外ID段寄存器写入信息，Mem段内存写入信息也要输出
  //   指令存储器
  //   contents of rom_1 (hex, n*v repeats v):
  //   201d07d0 20100001 109fc0 139fc3 8021 2012000c 24160008 26100001 3210000f 20080008 20090001 139900
  //   2709825 132020 20020022 c 1094022 1500fff9 22100001 2018000f 2188024 108700 20080008 20090001 139902
  //   2709825 132021 20020022 c 1094022 1500fff9 108702 2c9b022 12c00001 8000c07 4020 1084027 84400
  //   3508ffff 82021 20020022 c 8000c01 afa20000 23bd0004 afa40000 23bd0004 afb00000 23bd0004 afb30000
  //   23bd0004 afb40000 23bd0004 afb50000 23bd0004 afb60000 23bd0004 20160001 20140003 20150001 168020
  //   108100 2149825 132020 20020022 c 1600fffa 295a022 1680fff7 23bdfffc 8fb60000 23bdfffc 8fb50000
  //   23bdfffc 8fb40000 23bdfffc 8fb30000 23bdfffc 8fb00000 23bdfffc 8fa40000 23bdfffc 8fa20000 42000018
  //   afa20000 23bd0004 afa40000 23bd0004 afb00000 23bd0004 afb30000 23bd0004 afb40000 23bd0004 afb50000
  //   23bd0004 afb60000 23bd0004 20160002 20140003 20150001 168020 108100 2149825 132020 20020022 c
  //   1600fffa 295a022 1680fff7 23bdfffc 8fb60000 23bdfffc 8fb50000 23bdfffc 8fb40000 23bdfffc 8fb30000
  //   23bdfffc 8fb00000 23bdfffc 8fa40000 23bdfffc 8fa20000 42000018 afa20000 23bd0004 afa40000 23bd0004
  //   afb00000 23bd0004 afb30000 23bd0004 afb40000 23bd0004 afb50000 23bd0004 afb60000 23bd0004 20160003
  //   20140003 20150001 168020 108100 2149825 132020 20020022 c 1600fffa 295a022 1680fff7 23bdfffc
  //   8fb60000 23bdfffc 8fb50000 23bdfffc 8fb40000 23bdfffc 8fb30000 23bdfffc 8fb00000 23bdfffc 8fa40000
  //   23bdfffc 8fa20000 42000018
  //   指令字
  //   OP
  //   Func
  //   rs
  //   rt
  //   shamt
  //   rt
  //   rd
endmodule

module \封装正确性测试  (
);

  wire IR1, IR2, IR3, MemW, RegW;
  wire [31:0] EX_PC, ID_PC, IF_PC, IR, LED, MDin, MDinr, MEM_PC, PC, RDin, RDinr, WB_PC;

  \单周期MIPS  \u_单周期mips_1  (
    .RegWrite(RegW), .MemWrite(MemW), .PC(PC), .IR(IR), .RDin(RDin), .MDin(MDin), .LedData(LED));  // open: IR1, IR2, IR3
  \气泡流水线  \u_气泡流水线_1  (
    .RegWrite(RegW), .MemWrite(MemW), .IF_PC(IF_PC), .ID_PC(ID_PC), .EX_PC(EX_PC), .M_PC(MEM_PC),
    .WB_PC(WB_PC), .RDin(RDinr), .MDin(MDinr), .LedData(LED));
  \单周期MIPS_单级中断  \u_单周期mips_单级中断_1  (
    .IR1(IR1), .IR2(IR2), .IR3(IR3), .RegWrite(RegW), .MemWrite(MemW), .PC(PC), .IR(IR), .RDin(RDin),
    .MDin(MDin), .LedData(LED));
  \理想流水线  \u_理想流水线_1  (
    .RegWrite(RegW), .MemWrite(MemW), .IF_PC(IF_PC), .ID_PC(ID_PC), .EX_PC(EX_PC), .M_PC(MEM_PC),
    .WB_PC(WB_PC), .RDin(RDinr), .MDin(MDinr), .LedData(LED));
  \重定向流水线  \u_重定向流水线_1  (
    .RegWrite(RegW), .MemWrite(MemW), .IF_PC(IF_PC), .ID_PC(ID_PC), .EX_PC(EX_PC), .M_PC(MEM_PC),
    .WB_PC(WB_PC), .RDin(RDinr), .MDin(MDinr), .LedData(LED));
  \单周期MIPS_多级中断  \u_单周期mips_多级中断_1  (
    .IR1(IR1), .IR2(IR2), .IR3(IR3), .RegWrite(RegW), .MemWrite(MemW), .PC(PC), .IR(IR), .RDin(RDin),
    .MDin(MDin), .LedData(LED));

  // Notes on the sheet:
  //   单周期封装测试
  //   气泡流水封装测试
  //   单周期+单级中断封装测试
  //   请检查上面封装有无位宽不匹配，引脚标签是否和连接的标签相对应，否则无法在educoder平台上正确测试
  //   理想流水封装测试
  //   重定向流水封装测试
  //   单周期+多级中断封装测试
endmodule

module \理想流水接口IF_ID  (
  input  [31:0] IF_IR,
  input  [31:0] IF_PC,
  input  CLK,
  output [31:0] ID_IR,
  output [31:0] ID_PC
);

  Register #(.width(32), .trigger("rising"), .Select("low")) register_1 (
    .D(IF_IR), .Q(ID_IR), .clk(CLK));  // open: en, clr
  Register #(.width(32), .trigger("rising"), .Select("low")) register_2 (
    .D(IF_PC), .Q(ID_PC), .clk(CLK));  // open: en, clr
endmodule

module \理想流水接口ID_EX  (
  input  ID_RegWrite,
  input  ID_MemtoReg,
  input  ID_MemWrite,
  input  [3:0] ID_AluOP,
  input  ID_AluSrc,
  input  ID_Syscall,
  input  [31:0] ID_rs,
  input  [31:0] ID_rt,
  input  [4:0] ID_shamt,
  input  [31:0] ID_Imm,
  input  [31:0] ID_SignImm,
  input  [31:0] ID_PC,
  input  [4:0] ID_WriteReg,
  input  [31:0] ID_IR,
  input  CLK,
  output EX_RegWrite,
  output EX_MemtoReg,
  output EX_MemWrite,
  output [3:0] EX_AluOP,
  output EX_AluSrc,
  output EX_Syscall,
  output [31:0] EX_rs,
  output [31:0] EX_rt,
  output [4:0] EX_shamt,
  output [31:0] EX_Imm,
  output [31:0] EX_SignImm,
  output [31:0] EX_PC,
  output [4:0] EX_WriteReg,
  output [31:0] EX_IR
);

  Register #(.width(1), .trigger("rising"), .Select("low")) register_1 (
    .D(ID_RegWrite), .Q(EX_RegWrite), .clk(CLK));  // open: en, clr
  Register #(.width(1), .trigger("rising"), .Select("low")) register_2 (
    .D(ID_MemtoReg), .Q(EX_MemtoReg), .clk(CLK));  // open: en, clr
  Register #(.width(1), .trigger("rising"), .Select("low")) register_3 (
    .D(ID_MemWrite), .Q(EX_MemWrite), .clk(CLK));  // open: en, clr
  Register #(.width(4), .trigger("rising"), .Select("low")) register_4 (
    .D(ID_AluOP), .Q(EX_AluOP), .clk(CLK));  // open: en, clr
  Register #(.width(1), .trigger("rising"), .Select("low")) register_5 (
    .D(ID_AluSrc), .Q(EX_AluSrc), .clk(CLK));  // open: en, clr
  Register #(.width(32), .trigger("rising"), .Select("low")) register_6 (
    .D(ID_rs), .Q(EX_rs), .clk(CLK));  // open: en, clr
  Register #(.width(32), .trigger("rising"), .Select("low")) register_7 (
    .D(ID_rt), .Q(EX_rt), .clk(CLK));  // open: en, clr
  Register #(.width(5), .trigger("rising"), .Select("low")) register_8 (
    .D(ID_shamt), .Q(EX_shamt), .clk(CLK));  // open: en, clr
  Register #(.width(32), .trigger("rising"), .Select("low")) register_9 (
    .D(ID_Imm), .Q(EX_Imm), .clk(CLK));  // open: en, clr
  Register #(.width(32), .trigger("rising"), .Select("low")) register_10 (
    .D(ID_SignImm), .Q(EX_SignImm), .clk(CLK));  // open: en, clr
  Register #(.width(32), .trigger("rising"), .Select("low")) register_11 (
    .D(ID_PC), .Q(EX_PC), .clk(CLK));  // open: en, clr
  Register #(.width(5), .trigger("rising"), .Select("low")) register_12 (
    .D(ID_WriteReg), .Q(EX_WriteReg), .clk(CLK));  // open: en, clr
  Register #(.width(32), .trigger("rising"), .Select("low")) register_13 (
    .D(ID_IR), .Q(EX_IR), .clk(CLK));  // open: en, clr
  Register #(.width(1), .trigger("rising"), .Select("low")) register_14 (
    .D(ID_Syscall), .Q(EX_Syscall), .clk(CLK));  // open: en, clr
endmodule

module \理想流水接口EX_MEM  (
  input  ID_RegWrite,
  input  ID_MemtoReg,
  input  ID_MemWrite,
  input  ID_Syscall,
  input  [31:0] ID_rs,
  input  [31:0] ID_result,
  input  [31:0] ID_MDin,
  input  [31:0] ID_PC,
  input  [4:0] ID_WriteReg,
  input  [31:0] ID_IR,
  input  CLK,
  output EX_RegWrite,
  output EX_MemtoReg,
  output EX_MemWrite,
  output EX_Syscall,
  output [31:0] EX_rs,
  output [31:0] EX_result,
  output [31:0] EX_MDin,
  output [31:0] EX_PC,
  output [4:0] EX_WriteReg,
  output [31:0] EX_IR
);

  Register #(.width(1), .trigger("rising"), .Select("low")) register_1 (
    .D(ID_RegWrite), .Q(EX_RegWrite), .clk(CLK));  // open: en, clr
  Register #(.width(1), .trigger("rising"), .Select("low")) register_2 (
    .D(ID_MemtoReg), .Q(EX_MemtoReg), .clk(CLK));  // open: en, clr
  Register #(.width(1), .trigger("rising"), .Select("low")) register_3 (
    .D(ID_MemWrite), .Q(EX_MemWrite), .clk(CLK));  // open: en, clr
  Register #(.width(32), .trigger("rising"), .Select("low")) register_4 (
    .D(ID_rs), .Q(EX_rs), .clk(CLK));  // open: en, clr
  Register #(.width(32), .trigger("rising"), .Select("low")) register_5 (
    .D(ID_result), .Q(EX_result), .clk(CLK));  // open: en, clr
  Register #(.width(32), .trigger("rising"), .Select("low")) register_6 (
    .D(ID_MDin), .Q(EX_MDin), .clk(CLK));  // open: en, clr
  Register #(.width(32), .trigger("rising"), .Select("low")) register_7 (
    .D(ID_PC), .Q(EX_PC), .clk(CLK));  // open: en, clr
  Register #(.width(5), .trigger("rising"), .Select("low")) register_8 (
    .D(ID_WriteReg), .Q(EX_WriteReg), .clk(CLK));  // open: en, clr
  Register #(.width(32), .trigger("rising"), .Select("low")) register_9 (
    .D(ID_IR), .Q(EX_IR), .clk(CLK));  // open: en, clr
  Register #(.width(1), .trigger("rising"), .Select("low")) register_10 (
    .D(ID_Syscall), .Q(EX_Syscall), .clk(CLK));  // open: en, clr
endmodule

module \理想流水接口MEM_WB  (
  input  ID_RegWrite,
  input  ID_MemtoReg,
  input  [31:0] ID_rs,
  input  ID_Syscall,
  input  [31:0] ID_AluResult,
  input  [31:0] ID_MemResult,
  input  [31:0] ID_PC,
  input  [4:0] ID_WriteReg,
  input  [31:0] ID_IR,
  input  CLK,
  output EX_RegWrite,
  output EX_MemtoReg,
  output [31:0] EX_rs,
  output EX_Syscall,
  output [31:0] EX_AluResult,
  output [31:0] EX_MemResult,
  output [31:0] EX_PC,
  output [4:0] EX_WriteReg,
  output [31:0] EX_IR
);

  Register #(.width(1), .trigger("rising"), .Select("low")) register_1 (
    .D(ID_RegWrite), .Q(EX_RegWrite), .clk(CLK));  // open: en, clr
  Register #(.width(1), .trigger("rising"), .Select("low")) register_2 (
    .D(ID_MemtoReg), .Q(EX_MemtoReg), .clk(CLK));  // open: en, clr
  Register #(.width(32), .trigger("rising"), .Select("low")) register_3 (
    .D(ID_rs), .Q(EX_rs), .clk(CLK));  // open: en, clr
  Register #(.width(32), .trigger("rising"), .Select("low")) register_4 (
    .D(ID_AluResult), .Q(EX_AluResult), .clk(CLK));  // open: en, clr
  Register #(.width(32), .trigger("rising"), .Select("low")) register_5 (
    .D(ID_MemResult), .Q(EX_MemResult), .clk(CLK));  // open: en, clr
  Register #(.width(32), .trigger("rising"), .Select("low")) register_6 (
    .D(ID_PC), .Q(EX_PC), .clk(CLK));  // open: en, clr
  Register #(.width(5), .trigger("rising"), .Select("low")) register_7 (
    .D(ID_WriteReg), .Q(EX_WriteReg), .clk(CLK));  // open: en, clr
  Register #(.width(32), .trigger("rising"), .Select("low")) register_8 (
    .D(ID_IR), .Q(EX_IR), .clk(CLK));  // open: en, clr
  Register #(.width(1), .trigger("rising"), .Select("low")) register_9 (
    .D(ID_Syscall), .Q(EX_Syscall), .clk(CLK));  // open: en, clr
endmodule

// 源寄存器使用情况
module \源寄存器使用情况自动生成  (
  input  OP0,
  input  OP1,
  input  OP2,
  input  OP3,
  input  OP4,
  input  OP5,
  input  F0,
  input  F1,
  input  F2,
  input  F3,
  input  F4,
  input  F5,
  output R1_Used,
  output R2_Used
);

  wire and_1_out, and_2_out, and_3_out, and_4_out, and_5_out, and_6_out, and_7_out, and_8_out, and_9_out,
       and_10_out, and_11_out, and_12_out, and_13_out, and_14_out, and_15_out, and_16_out, and_17_out,
       and_18_out, and_19_out, and_20_out, and_21_out, and_22_out, and_23_out, and_24_out, and_25_out,
       and_26_out, and_27_out, and_28_out, and_29_out, and_30_out, and_31_out, and_32_out, and_33_out,
       and_34_out, and_35_out, and_36_out, and_37_out, and_38_out, and_39_out, and_40_out, not_1_out,
       not_2_out, not_3_out, not_4_out, not_5_out, not_6_out, not_7_out, not_8_out, not_9_out, not_10_out,
       not_11_out, not_12_out, not_13_out, not_14_out, not_15_out, not_16_out, not_17_out, not_18_out,
       not_19_out, not_20_out, not_21_out, not_22_out, not_23_out, not_24_out, not_25_out, not_26_out,
       not_27_out, not_28_out, not_29_out, not_30_out, not_31_out, not_32_out, not_33_out, not_34_out,
       not_35_out, not_36_out, not_37_out, not_38_out, not_39_out, not_40_out, not_41_out, not_42_out,
       not_43_out, not_44_out, not_45_out, not_46_out, not_47_out, not_48_out, not_49_out, not_50_out,
       not_51_out, not_52_out, not_53_out, not_54_out, not_55_out, not_56_out, not_57_out, not_58_out,
       not_59_out, not_60_out, not_61_out, not_62_out, not_63_out, not_64_out, not_65_out, not_66_out,
       not_67_out, not_68_out, not_69_out, not_70_out, not_71_out, not_72_out, not_73_out, not_74_out,
       not_75_out, not_76_out, not_77_out, not_78_out, not_79_out, not_80_out, not_81_out, not_82_out,
       not_83_out, not_84_out, not_85_out, not_86_out, not_87_out, not_88_out, not_89_out, not_90_out,
       not_91_out, not_92_out, not_93_out, not_94_out, not_95_out, not_96_out, not_97_out, not_98_out,
       not_99_out, not_100_out, not_101_out, not_102_out, not_103_out, not_104_out, not_105_out, not_106_out,
       not_107_out, not_108_out, not_109_out, not_110_out, not_111_out, not_112_out, not_113_out,
       not_114_out, not_115_out, not_116_out, not_117_out, not_118_out, not_119_out, not_120_out,
       not_121_out, not_122_out, not_123_out, not_124_out, not_125_out, not_126_out, not_127_out,
       not_128_out, not_129_out, not_130_out, not_131_out, not_132_out, not_133_out, not_134_out,
       not_135_out, not_136_out, not_137_out, not_138_out, not_139_out, not_140_out, not_141_out,
       not_142_out, not_143_out, not_144_out, not_145_out, not_146_out, not_147_out, not_148_out,
       not_149_out, not_150_out, not_151_out, not_152_out, not_153_out, not_154_out, not_155_out,
       not_156_out, not_157_out, not_158_out, not_159_out, not_160_out, not_161_out, not_162_out,
       not_163_out, not_164_out, not_165_out, not_166_out, not_167_out, not_168_out, not_169_out,
       not_170_out, not_171_out, not_172_out, not_173_out, not_174_out, not_175_out, not_176_out,
       not_177_out, not_178_out, not_179_out, not_180_out, not_181_out, not_182_out, not_183_out,
       not_184_out, not_185_out, not_186_out, not_187_out, not_188_out, not_189_out, not_190_out,
       not_191_out, not_192_out, not_193_out, not_194_out, not_195_out, not_196_out, not_197_out,
       not_198_out, not_199_out, not_200_out, not_201_out, not_202_out, not_203_out, not_204_out,
       not_205_out, not_206_out, not_207_out, not_208_out, not_209_out, not_210_out, not_211_out,
       not_212_out, not_213_out, not_214_out, not_215_out, not_216_out, not_217_out, not_218_out,
       not_219_out, not_220_out, not_221_out, not_222_out, not_223_out, not_224_out, not_225_out,
       not_226_out, not_227_out, not_228_out, not_229_out, not_230_out, not_231_out, not_232_out,
       not_233_out, not_234_out, not_235_out, not_236_out, not_237_out, not_238_out, not_239_out,
       not_240_out, not_241_out, not_242_out, not_243_out, not_244_out, not_245_out, not_246_out,
       not_247_out, not_248_out, not_249_out, not_250_out, not_251_out, not_252_out, not_253_out,
       not_254_out, not_255_out, not_256_out, not_257_out, not_258_out, not_259_out, not_260_out,
       not_261_out, not_262_out, not_263_out, not_264_out, not_265_out, not_266_out, not_267_out,
       not_268_out, not_269_out, not_270_out, not_271_out, not_272_out, not_273_out, not_274_out,
       not_275_out, not_276_out, not_277_out, not_278_out, not_279_out, not_280_out, not_281_out,
       not_282_out, not_283_out, not_284_out, not_285_out, not_286_out, not_287_out, not_288_out,
       not_289_out, not_290_out, not_291_out, not_292_out, not_293_out, not_294_out, not_295_out,
       not_296_out, not_297_out, not_298_out, not_299_out, not_300_out, not_301_out, not_302_out,
       not_303_out, not_304_out, not_305_out, not_306_out, not_307_out;

  not not_1 (not_1_out, OP5);
  not not_2 (not_2_out, OP4);
  not not_3 (not_3_out, OP3);
  not not_4 (not_4_out, OP2);
  not not_5 (not_5_out, OP1);
  not not_6 (not_6_out, OP0);
  not not_7 (not_7_out, F5);
  not not_8 (not_8_out, F4);
  not not_9 (not_9_out, F3);
  not not_10 (not_10_out, F2);
  not not_11 (not_11_out, OP5);
  not not_12 (not_12_out, OP4);
  not not_13 (not_13_out, OP3);
  not not_14 (not_14_out, OP2);
  not not_15 (not_15_out, OP1);
  not not_16 (not_16_out, OP0);
  not not_17 (not_17_out, F4);
  not not_18 (not_18_out, F3);
  not not_19 (not_19_out, F2);
  not not_20 (not_20_out, F1);
  not not_21 (not_21_out, F0);
  not not_22 (not_22_out, OP5);
  not not_23 (not_23_out, OP4);
  not not_24 (not_24_out, OP3);
  not not_25 (not_25_out, OP2);
  not not_26 (not_26_out, OP1);
  not not_27 (not_27_out, OP0);
  not not_28 (not_28_out, F4);
  not not_29 (not_29_out, F3);
  not not_30 (not_30_out, F2);
  not not_31 (not_31_out, F1);
  not not_32 (not_32_out, OP5);
  not not_33 (not_33_out, OP4);
  not not_34 (not_34_out, OP3);
  not not_35 (not_35_out, OP2);
  not not_36 (not_36_out, OP1);
  not not_37 (not_37_out, OP0);
  not not_38 (not_38_out, F4);
  not not_39 (not_39_out, F3);
  not not_40 (not_40_out, F2);
  not not_41 (not_41_out, F0);
  not not_42 (not_42_out, OP5);
  not not_43 (not_43_out, OP4);
  not not_44 (not_44_out, OP3);
  not not_45 (not_45_out, OP2);
  not not_46 (not_46_out, OP1);
  not not_47 (not_47_out, OP0);
  not not_48 (not_48_out, F4);
  not not_49 (not_49_out, F3);
  not not_50 (not_50_out, F1);
  not not_51 (not_51_out, F0);
  not not_52 (not_52_out, OP5);
  not not_53 (not_53_out, OP4);
  not not_54 (not_54_out, OP3);
  not not_55 (not_55_out, OP2);
  not not_56 (not_56_out, OP1);
  not not_57 (not_57_out, OP0);
  not not_58 (not_58_out, F4);
  not not_59 (not_59_out, F3);
  not not_60 (not_60_out, F1);
  not not_61 (not_61_out, OP5);
  not not_62 (not_62_out, OP4);
  not not_63 (not_63_out, OP3);
  not not_64 (not_64_out, OP2);
  not not_65 (not_65_out, OP1);
  not not_66 (not_66_out, OP0);
  not not_67 (not_67_out, F4);
  not not_68 (not_68_out, F3);
  not not_69 (not_69_out, OP5);
  not not_70 (not_70_out, OP4);
  not not_71 (not_71_out, OP3);
  not not_72 (not_72_out, OP2);
  not not_73 (not_73_out, OP1);
  not not_74 (not_74_out, OP0);
  not not_75 (not_75_out, F4);
  not not_76 (not_76_out, F2);
  not not_77 (not_77_out, F0);
  not not_78 (not_78_out, OP5);
  not not_79 (not_79_out, OP4);
  not not_80 (not_80_out, OP3);
  not not_81 (not_81_out, OP2);
  not not_82 (not_82_out, OP1);
  not not_83 (not_83_out, OP0);
  not not_84 (not_84_out, F4);
  not not_85 (not_85_out, F2);
  not not_86 (not_86_out, OP5);
  not not_87 (not_87_out, OP4);
  not not_88 (not_88_out, OP3);
  not not_89 (not_89_out, OP2);
  not not_90 (not_90_out, OP1);
  not not_91 (not_91_out, OP0);
  not not_92 (not_92_out, F5);
  not not_93 (not_93_out, F4);
  not not_94 (not_94_out, F2);
  not not_95 (not_95_out, F1);
  not not_96 (not_96_out, F0);
  not not_97 (not_97_out, OP5);
  not not_98 (not_98_out, OP4);
  not not_99 (not_99_out, OP3);
  not not_100 (not_100_out, OP2);
  not not_101 (not_101_out, OP1);
  not not_102 (not_102_out, OP0);
  not not_103 (not_103_out, F5);
  not not_104 (not_104_out, F4);
  not not_105 (not_105_out, F1);
  not not_106 (not_106_out, F0);
  not not_107 (not_107_out, OP5);
  not not_108 (not_108_out, OP4);
  not not_109 (not_109_out, OP3);
  not not_110 (not_110_out, OP1);
  not not_111 (not_111_out, OP0);
  not not_112 (not_112_out, OP5);
  not not_113 (not_113_out, OP4);
  not not_114 (not_114_out, OP3);
  not not_115 (not_115_out, OP1);
  not not_116 (not_116_out, OP5);
  not not_117 (not_117_out, OP4);
  not not_118 (not_118_out, OP2);
  not not_119 (not_119_out, OP1);
  not not_120 (not_120_out, OP0);
  not not_121 (not_121_out, OP5);
  not not_122 (not_122_out, OP4);
  not not_123 (not_123_out, OP1);
  not not_124 (not_124_out, OP0);
  not not_125 (not_125_out, OP5);
  not not_126 (not_126_out, OP4);
  not not_127 (not_127_out, OP2);
  not not_128 (not_128_out, OP1);
  not not_129 (not_129_out, OP5);
  not not_130 (not_130_out, OP4);
  not not_131 (not_131_out, OP2);
  not not_132 (not_132_out, OP0);
  not not_133 (not_133_out, OP5);
  not not_134 (not_134_out, OP4);
  not not_135 (not_135_out, OP1);
  not not_136 (not_136_out, OP4);
  not not_137 (not_137_out, OP3);
  not not_138 (not_138_out, OP2);
  not not_139 (not_139_out, OP4);
  not not_140 (not_140_out, OP2);
  not not_141 (not_141_out, OP5);
  not not_142 (not_142_out, OP4);
  not not_143 (not_143_out, OP3);
  not not_144 (not_144_out, OP2);
  not not_145 (not_145_out, OP1);
  not not_146 (not_146_out, OP0);
  not not_147 (not_147_out, F5);
  not not_148 (not_148_out, F4);
  not not_149 (not_149_out, F3);
  not not_150 (not_150_out, OP5);
  not not_151 (not_151_out, OP4);
  not not_152 (not_152_out, OP3);
  not not_153 (not_153_out, OP2);
  not not_154 (not_154_out, OP1);
  not not_155 (not_155_out, OP0);
  not not_156 (not_156_out, F4);
  not not_157 (not_157_out, F3);
  not not_158 (not_158_out, F0);
  not not_159 (not_159_out, OP4);
  not not_160 (not_160_out, OP3);
  not not_161 (not_161_out, OP2);
  not not_162 (not_162_out, OP1);
  not not_163 (not_163_out, OP0);
  not not_164 (not_164_out, OP5);
  not not_165 (not_165_out, OP4);
  not not_166 (not_166_out, OP3);
  not not_167 (not_167_out, OP2);
  not not_168 (not_168_out, OP1);
  not not_169 (not_169_out, OP5);
  not not_170 (not_170_out, OP4);
  not not_171 (not_171_out, OP3);
  not not_172 (not_172_out, OP2);
  not not_173 (not_173_out, OP1);
  not not_174 (not_174_out, OP0);
  not not_175 (not_175_out, F5);
  not not_176 (not_176_out, F4);
  not not_177 (not_177_out, F3);
  not not_178 (not_178_out, F2);
  not not_179 (not_179_out, F1);
  not not_180 (not_180_out, F0);
  not not_181 (not_181_out, OP5);
  not not_182 (not_182_out, OP4);
  not not_183 (not_183_out, OP3);
  not not_184 (not_184_out, OP2);
  not not_185 (not_185_out, OP1);
  not not_186 (not_186_out, OP0);
  not not_187 (not_187_out, F5);
  not not_188 (not_188_out, F4);
  not not_189 (not_189_out, F3);
  not not_190 (not_190_out, F2);
  not not_191 (not_191_out, OP5);
  not not_192 (not_192_out, OP4);
  not not_193 (not_193_out, OP3);
  not not_194 (not_194_out, OP2);
  not not_195 (not_195_out, OP1);
  not not_196 (not_196_out, OP0);
  not not_197 (not_197_out, F5);
  not not_198 (not_198_out, F4);
  not not_199 (not_199_out, F3);
  not not_200 (not_200_out, F2);
  not not_201 (not_201_out, F0);
  not not_202 (not_202_out, OP5);
  not not_203 (not_203_out, OP4);
  not not_204 (not_204_out, OP3);
  not not_205 (not_205_out, OP2);
  not not_206 (not_206_out, OP1);
  not not_207 (not_207_out, OP0);
  not not_208 (not_208_out, F4);
  not not_209 (not_209_out, F3);
  not not_210 (not_210_out, F2);
  not not_211 (not_211_out, F1);
  not not_212 (not_212_out, F0);
  not not_213 (not_213_out, OP5);
  not not_214 (not_214_out, OP4);
  not not_215 (not_215_out, OP3);
  not not_216 (not_216_out, OP2);
  not not_217 (not_217_out, OP1);
  not not_218 (not_218_out, OP0);
  not not_219 (not_219_out, F4);
  not not_220 (not_220_out, F3);
  not not_221 (not_221_out, F2);
  not not_222 (not_222_out, F1);
  not not_223 (not_223_out, OP5);
  not not_224 (not_224_out, OP4);
  not not_225 (not_225_out, OP3);
  not not_226 (not_226_out, OP2);
  not not_227 (not_227_out, OP1);
  not not_228 (not_228_out, OP0);
  not not_229 (not_229_out, F4);
  not not_230 (not_230_out, F3);
  not not_231 (not_231_out, F2);
  not not_232 (not_232_out, F0);
  not not_233 (not_233_out, OP5);
  not not_234 (not_234_out, OP4);
  not not_235 (not_235_out, OP3);
  not not_236 (not_236_out, OP2);
  not not_237 (not_237_out, OP1);
  not not_238 (not_238_out, OP0);
  not not_239 (not_239_out, F4);
  not not_240 (not_240_out, F3);
  not not_241 (not_241_out, F1);
  not not_242 (not_242_out, F0);
  not not_243 (not_243_out, OP5);
  not not_244 (not_244_out, OP4);
  not not_245 (not_245_out, OP3);
  not not_246 (not_246_out, OP2);
  not not_247 (not_247_out, OP1);
  not not_248 (not_248_out, OP0);
  not not_249 (not_249_out, F4);
  not not_250 (not_250_out, F3);
  not not_251 (not_251_out, F1);
  not not_252 (not_252_out, OP5);
  not not_253 (not_253_out, OP4);
  not not_254 (not_254_out, OP3);
  not not_255 (not_255_out, OP2);
  not not_256 (not_256_out, OP1);
  not not_257 (not_257_out, OP0);
  not not_258 (not_258_out, F4);
  not not_259 (not_259_out, F3);
  not not_260 (not_260_out, OP5);
  not not_261 (not_261_out, OP4);
  not not_262 (not_262_out, OP3);
  not not_263 (not_263_out, OP2);
  not not_264 (not_264_out, OP1);
  not not_265 (not_265_out, OP0);
  not not_266 (not_266_out, F4);
  not not_267 (not_267_out, F2);
  not not_268 (not_268_out, F0);
  not not_269 (not_269_out, OP5);
  not not_270 (not_270_out, OP4);
  not not_271 (not_271_out, OP3);
  not not_272 (not_272_out, OP2);
  not not_273 (not_273_out, OP1);
  not not_274 (not_274_out, OP0);
  not not_275 (not_275_out, F5);
  not not_276 (not_276_out, F4);
  not not_277 (not_277_out, F1);
  not not_278 (not_278_out, F0);
  not not_279 (not_279_out, OP5);
  not not_280 (not_280_out, OP4);
  not not_281 (not_281_out, OP3);
  not not_282 (not_282_out, OP1);
  not not_283 (not_283_out, OP0);
  not not_284 (not_284_out, OP5);
  not not_285 (not_285_out, OP4);
  not not_286 (not_286_out, OP3);
  not not_287 (not_287_out, OP1);
  not not_288 (not_288_out, OP4);
  not not_289 (not_289_out, OP2);
  not not_290 (not_290_out, OP5);
  not not_291 (not_291_out, OP4);
  not not_292 (not_292_out, OP3);
  not not_293 (not_293_out, OP2);
  not not_294 (not_294_out, OP1);
  not not_295 (not_295_out, OP0);
  not not_296 (not_296_out, F5);
  not not_297 (not_297_out, F4);
  not not_298 (not_298_out, F3);
  not not_299 (not_299_out, OP5);
  not not_300 (not_300_out, OP4);
  not not_301 (not_301_out, OP3);
  not not_302 (not_302_out, OP2);
  not not_303 (not_303_out, OP1);
  not not_304 (not_304_out, OP0);
  not not_305 (not_305_out, F4);
  not not_306 (not_306_out, F3);
  not not_307 (not_307_out, F0);
  and and_1 (and_1_out, not_1_out, not_2_out, not_3_out, not_4_out, not_5_out, not_6_out, not_7_out, not_8_out, not_9_out, not_10_out, F1, F0);
  and and_2 (and_2_out, not_11_out, not_12_out, not_13_out, not_14_out, not_15_out, not_16_out, F5, not_17_out, not_18_out, not_19_out, not_20_out, not_21_out);
  and and_3 (and_3_out, not_22_out, not_23_out, not_24_out, not_25_out, not_26_out, not_27_out, F5, not_28_out, not_29_out, not_30_out, not_31_out, F0);
  and and_4 (and_4_out, not_32_out, not_33_out, not_34_out, not_35_out, not_36_out, not_37_out, F5, not_38_out, not_39_out, not_40_out, F1, not_41_out);
  and and_5 (and_5_out, not_42_out, not_43_out, not_44_out, not_45_out, not_46_out, not_47_out, F5, not_48_out, not_49_out, F2, not_50_out, not_51_out);
  and and_6 (and_6_out, not_52_out, not_53_out, not_54_out, not_55_out, not_56_out, not_57_out, F5, not_58_out, not_59_out, F2, not_60_out, F0);
  and and_7 (and_7_out, not_61_out, not_62_out, not_63_out, not_64_out, not_65_out, not_66_out, F5, not_67_out, not_68_out, F2, F1, F0);
  and and_8 (and_8_out, not_69_out, not_70_out, not_71_out, not_72_out, not_73_out, not_74_out, F5, not_75_out, F3, not_76_out, F1, not_77_out);
  and and_9 (and_9_out, not_78_out, not_79_out, not_80_out, not_81_out, not_82_out, not_83_out, F5, not_84_out, F3, not_85_out, F1, F0);
  and and_10 (and_10_out, not_86_out, not_87_out, not_88_out, not_89_out, not_90_out, not_91_out, not_92_out, not_93_out, F3, not_94_out, not_95_out, not_96_out);
  and and_11 (and_11_out, not_97_out, not_98_out, not_99_out, not_100_out, not_101_out, not_102_out, not_103_out, not_104_out, F3, F2, not_105_out, not_106_out);
  and and_12 (and_12_out, not_107_out, not_108_out, not_109_out, OP2, not_110_out, not_111_out);
  and and_13 (and_13_out, not_112_out, not_113_out, not_114_out, OP2, not_115_out, OP0);
  and and_14 (and_14_out, not_116_out, not_117_out, OP3, not_118_out, not_119_out, not_120_out);
  and and_15 (and_15_out, not_121_out, not_122_out, OP3, OP2, not_123_out, not_124_out);
  and and_16 (and_16_out, not_125_out, not_126_out, OP3, not_127_out, not_128_out, OP0);
  and and_17 (and_17_out, not_129_out, not_130_out, OP3, not_131_out, OP1, not_132_out);
  and and_18 (and_18_out, not_133_out, not_134_out, OP3, OP2, not_135_out, OP0);
  and and_19 (and_19_out, OP5, not_136_out, not_137_out, not_138_out, OP1, OP0);
  and and_20 (and_20_out, OP5, not_139_out, OP3, not_140_out, OP1, OP0);
  and and_21 (and_21_out, not_141_out, not_142_out, not_143_out, not_144_out, not_145_out, not_146_out, not_147_out, not_148_out, not_149_out, F2, F1, F0);
  and and_22 (and_22_out, not_150_out, not_151_out, not_152_out, not_153_out, not_154_out, not_155_out, F5, not_156_out, not_157_out, F2, F1, not_158_out);
  and and_23 (and_23_out, OP5, not_159_out, not_160_out, not_161_out, not_162_out, not_163_out);
  and and_24 (and_24_out, not_164_out, not_165_out, not_166_out, not_167_out, not_168_out, OP0);
  and and_25 (and_25_out, not_169_out, not_170_out, not_171_out, not_172_out, not_173_out, not_174_out, not_175_out, not_176_out, not_177_out, not_178_out, not_179_out, not_180_out);
  and and_26 (and_26_out, not_181_out, not_182_out, not_183_out, not_184_out, not_185_out, not_186_out, not_187_out, not_188_out, not_189_out, not_190_out, F1, F0);
  and and_27 (and_27_out, not_191_out, not_192_out, not_193_out, not_194_out, not_195_out, not_196_out, not_197_out, not_198_out, not_199_out, not_200_out, F1, not_201_out);
  and and_28 (and_28_out, not_202_out, not_203_out, not_204_out, not_205_out, not_206_out, not_207_out, F5, not_208_out, not_209_out, not_210_out, not_211_out, not_212_out);
  and and_29 (and_29_out, not_213_out, not_214_out, not_215_out, not_216_out, not_217_out, not_218_out, F5, not_219_out, not_220_out, not_221_out, not_222_out, F0);
  and and_30 (and_30_out, not_223_out, not_224_out, not_225_out, not_226_out, not_227_out, not_228_out, F5, not_229_out, not_230_out, not_231_out, F1, not_232_out);
  and and_31 (and_31_out, not_233_out, not_234_out, not_235_out, not_236_out, not_237_out, not_238_out, F5, not_239_out, not_240_out, F2, not_241_out, not_242_out);
  and and_32 (and_32_out, not_243_out, not_244_out, not_245_out, not_246_out, not_247_out, not_248_out, F5, not_249_out, not_250_out, F2, not_251_out, F0);
  and and_33 (and_33_out, not_252_out, not_253_out, not_254_out, not_255_out, not_256_out, not_257_out, F5, not_258_out, not_259_out, F2, F1, F0);
  and and_34 (and_34_out, not_260_out, not_261_out, not_262_out, not_263_out, not_264_out, not_265_out, F5, not_266_out, F3, not_267_out, F1, not_268_out);
  and and_35 (and_35_out, not_269_out, not_270_out, not_271_out, not_272_out, not_273_out, not_274_out, not_275_out, not_276_out, F3, F2, not_277_out, not_278_out);
  and and_36 (and_36_out, not_279_out, not_280_out, not_281_out, OP2, not_282_out, not_283_out);
  and and_37 (and_37_out, not_284_out, not_285_out, not_286_out, OP2, not_287_out, OP0);
  and and_38 (and_38_out, OP5, not_288_out, OP3, not_289_out, OP1, OP0);
  and and_39 (and_39_out, not_290_out, not_291_out, not_292_out, not_293_out, not_294_out, not_295_out, not_296_out, not_297_out, not_298_out, F2, F1, F0);
  and and_40 (and_40_out, not_299_out, not_300_out, not_301_out, not_302_out, not_303_out, not_304_out, F5, not_305_out, not_306_out, F2, F1, not_307_out);
  or or_1 (R1_Used, and_1_out, and_2_out, and_3_out, and_4_out, and_5_out, and_6_out, and_7_out, and_8_out, and_9_out, and_10_out, and_11_out, and_12_out, and_13_out, and_14_out, and_15_out, and_16_out, and_17_out, and_18_out, and_19_out, and_20_out, and_21_out, and_22_out, and_23_out, and_24_out);
  or or_2 (R2_Used, and_25_out, and_26_out, and_27_out, and_28_out, and_29_out, and_30_out, and_31_out, and_32_out, and_33_out, and_34_out, and_35_out, and_36_out, and_37_out, and_38_out, and_39_out, and_40_out);
endmodule

module \相关处理逻辑  (
  input  [4:0] R1,
  input  [31:0] Instr,
  input  [4:0] R2,
  input  EX_RegWrite,
  input  [4:0] EX_WriteReg_num,
  input  BranchTaken,
  input  MEM_RegWrite,
  input  [4:0] MEM_WriteReg_num,
  output Stall,
  output Flush
);

  wire and_1_out, and_2_out, and_3_out, and_4_out, comparator_1_eq, comparator_2_eq, comparator_3_eq,
       comparator_4_eq, comparator_5_eq, comparator_6_eq, comparator_7_eq, comparator_8_eq, not_1_out,
       not_2_out, not_3_out, not_4_out, or_2_out, or_3_out, R1_Used, R2_Used;

  or or_1 (Flush, BranchTaken, Stall);
  \源寄存器使用情况自动生成  \u_源寄存器使用情况自动生成_1  (
    .OP0(Instr[26]), .OP1(Instr[27]), .OP2(Instr[28]), .OP3(Instr[29]), .OP4(Instr[30]), .OP5(Instr[31]),
    .F0(Instr[0]), .F1(Instr[1]), .F2(Instr[2]), .F3(Instr[3]), .F4(Instr[4]), .F5(Instr[5]),
    .R1_Used(R1_Used), .R2_Used(R2_Used));
  not not_1 (not_1_out, comparator_1_eq);
  Comparator #(.width(5), .mode("twosComplement")) comparator_1 (
    .a(R1), .b({5{1'b0}}), .eq(comparator_1_eq));  // open: gt, lt
  Comparator #(.width(5), .mode("twosComplement")) comparator_2 (
    .a(R1), .b(EX_WriteReg_num), .eq(comparator_2_eq));  // open: gt, lt
  Comparator #(.width(5), .mode("twosComplement")) comparator_3 (
    .a(R2), .b({5{1'b0}}), .eq(comparator_3_eq));  // open: gt, lt
  not not_2 (not_2_out, comparator_3_eq);
  Comparator #(.width(5), .mode("twosComplement")) comparator_4 (
    .a(R2), .b(EX_WriteReg_num), .eq(comparator_4_eq));  // open: gt, lt
  Comparator #(.width(5), .mode("twosComplement")) comparator_5 (
    .a(R1), .b({5{1'b0}}), .eq(comparator_5_eq));  // open: gt, lt
  not not_3 (not_3_out, comparator_5_eq);
  Comparator #(.width(5), .mode("twosComplement")) comparator_6 (
    .a(R1), .b(MEM_WriteReg_num), .eq(comparator_6_eq));  // open: gt, lt
  Comparator #(.width(5), .mode("twosComplement")) comparator_7 (
    .a(R2), .b({5{1'b0}}), .eq(comparator_7_eq));  // open: gt, lt
  not not_4 (not_4_out, comparator_7_eq);
  Comparator #(.width(5), .mode("twosComplement")) comparator_8 (
    .a(R2), .b(MEM_WriteReg_num), .eq(comparator_8_eq));  // open: gt, lt
  and and_1 (and_1_out, not_1_out, comparator_2_eq, R1_Used, EX_RegWrite);
  and and_2 (and_2_out, not_2_out, comparator_4_eq, R2_Used, EX_RegWrite);
  and and_3 (and_3_out, not_3_out, comparator_6_eq, R1_Used, MEM_RegWrite);
  and and_4 (and_4_out, not_4_out, comparator_8_eq, R2_Used, MEM_RegWrite);
  or or_2 (or_2_out, and_1_out, and_2_out);
  or or_3 (or_3_out, and_3_out, and_4_out);
  or or_4 (Stall, or_2_out, or_3_out);

  // Other names for the same wires on the sheet: EX_WriteReg[4:0] = EX_WriteReg_num; FUNC[5:0] = Instr[5:0];
  //   OP_CODE[5:0] = Instr[31:26]; MEM_WriteReg[4:0] = MEM_WriteReg_num
endmodule

// IF/ID
module \气泡流水接口IF_ID  (
  input  [31:0] IF_IR,
  input  [31:0] IF_PC,
  input  [31:0] IF_monitor,
  input  IF_PredictJump,
  input  CLK,
  input  \同步清零_气泡_高电平有效 ,
  input  \使能端_为高电平时忽略时钟输入 ,
  output [31:0] ID_IR,
  output [31:0] ID_PC,
  output [31:0] ID_monitor,
  output ID_PredictJump
);

  wire multiplexer_4_out, not_1_out;
  wire [31:0] multiplexer_1_out, multiplexer_2_out, multiplexer_3_out;

  Multiplexer #(.select(1), .width(32), .disabled("Z"), .enable("false")) multiplexer_1 (
    .in0(IF_IR), .in1({32{1'b0}}), .out(multiplexer_1_out), .sel(\同步清零_气泡_高电平有效 ));
  Multiplexer #(.select(1), .width(32), .disabled("Z"), .enable("false")) multiplexer_2 (
    .in0(IF_PC), .in1({32{1'b0}}), .out(multiplexer_2_out), .sel(\同步清零_气泡_高电平有效 ));
  Multiplexer #(.select(1), .width(32), .disabled("Z"), .enable("false")) multiplexer_3 (
    .in0(IF_monitor), .in1({32{1'b0}}), .out(multiplexer_3_out), .sel(\同步清零_气泡_高电平有效 ));
  Multiplexer #(.select(1), .width(1), .disabled("Z"), .enable("false")) multiplexer_4 (
    .in0(IF_PredictJump), .in1(1'b0), .out(multiplexer_4_out), .sel(\同步清零_气泡_高电平有效 ));
  Pull_Resistor #(.pull(0)) pull_resistor_1 (.node(\同步清零_气泡_高电平有效 ));
  not not_1 (not_1_out, \使能端_为高电平时忽略时钟输入 );
  Register #(.width(32), .trigger("rising"), .Select("low")) register_1 (
    .D(multiplexer_1_out), .en(not_1_out), .Q(ID_IR), .clk(CLK));  // open: clr
  Register #(.width(32), .trigger("rising"), .Select("low")) register_2 (
    .D(multiplexer_2_out), .en(not_1_out), .Q(ID_PC), .clk(CLK));  // open: clr
  Register #(.width(32), .trigger("rising"), .Select("low")) register_3 (
    .D(multiplexer_3_out), .en(not_1_out), .Q(ID_monitor), .clk(CLK));  // open: clr
  Register #(.width(1), .trigger("rising"), .Select("low")) register_4 (
    .D(multiplexer_4_out), .en(not_1_out), .Q(ID_PredictJump), .clk(CLK));  // open: clr
  Pull_Resistor #(.pull(0)) pull_resistor_2 (.node(not_1_out));
endmodule

// ID/EX
module \气泡流水接口ID_EX  (
  input  ID_RegWrite,
  input  ID_MemToReg,
  input  ID_JAL,
  input  ID_LB,
  input  ID_MemWrite,
  input  ID_Beq,
  input  ID_Bne,
  input  ID_JMP,
  input  ID_JR,
  input  ID_BLTZ,
  input  ID_Syscall,
  input  [3:0] ID_AluOP,
  input  ID_AluSRC,
  input  ID_SRAV,
  input  [31:0] ID_RS,
  input  [31:0] ID_RT,
  input  [4:0] ID_shamt,
  input  [31:0] ID_Imm,
  input  [31:0] ID_SignImm,
  input  [31:0] ID_PC,
  input  [4:0] ID_WriteReg,
  input  [31:0] ID_IR,
  input  [31:0] ID_addr,
  input  [31:0] ID_monitor,
  input  CLK,
  input  \同步清零_气泡_高电平有效 ,
  input  \使能端_为高电平时忽略时钟输入 ,
  output EX_RegWrite,
  output EX_MemToReg,
  output EX_JAL,
  output EX_LB,
  output EX_MemWrite,
  output EX_Beq,
  output EX_PC,
  output EX_JMP,
  output EX_JR,
  output ID_BLTZ_2,
  output EX_Syscall,
  output [3:0] EX_AluOP,
  output EX_AluSRC,
  output EX_SRAV,
  output [31:0] EX_RS,
  output [31:0] EX_RT,
  output [4:0] EX_shamt,
  output [31:0] EX_Imm,
  output [31:0] EX_SignImm,
  output [31:0] EX_PC_2,
  output [4:0] EX_WriteReg,
  output [31:0] EX_IR,
  output [31:0] EX_addr,
  output [31:0] EX_monitor
);

  wire multiplexer_1_out, multiplexer_2_out, multiplexer_3_out, multiplexer_4_out, multiplexer_5_out,
       multiplexer_6_out, multiplexer_7_out, multiplexer_8_out, multiplexer_9_out, multiplexer_10_out,
       multiplexer_11_out, multiplexer_13_out, multiplexer_14_out, not_1_out;
  wire [3:0] multiplexer_12_out;
  wire [4:0] multiplexer_17_out, multiplexer_21_out;
  wire [31:0] multiplexer_15_out, multiplexer_16_out, multiplexer_18_out, multiplexer_19_out,
       multiplexer_20_out, multiplexer_22_out, multiplexer_23_out, multiplexer_24_out;

  Multiplexer #(.select(1), .width(1), .disabled("Z"), .enable("false")) multiplexer_1 (
    .in0(ID_RegWrite), .in1(1'b0), .out(multiplexer_1_out), .sel(\同步清零_气泡_高电平有效 ));
  Multiplexer #(.select(1), .width(1), .disabled("Z"), .enable("false")) multiplexer_2 (
    .in0(ID_MemToReg), .in1(1'b0), .out(multiplexer_2_out), .sel(\同步清零_气泡_高电平有效 ));
  Multiplexer #(.select(1), .width(1), .disabled("Z"), .enable("false")) multiplexer_3 (
    .in0(ID_JAL), .in1(1'b0), .out(multiplexer_3_out), .sel(\同步清零_气泡_高电平有效 ));
  Multiplexer #(.select(1), .width(1), .disabled("Z"), .enable("false")) multiplexer_4 (
    .in0(ID_LB), .in1(1'b0), .out(multiplexer_4_out), .sel(\同步清零_气泡_高电平有效 ));
  Multiplexer #(.select(1), .width(1), .disabled("Z"), .enable("false")) multiplexer_5 (
    .in0(ID_MemWrite), .in1(1'b0), .out(multiplexer_5_out), .sel(\同步清零_气泡_高电平有效 ));
  Multiplexer #(.select(1), .width(1), .disabled("Z"), .enable("false")) multiplexer_6 (
    .in0(ID_Beq), .in1(1'b0), .out(multiplexer_6_out), .sel(\同步清零_气泡_高电平有效 ));
  Multiplexer #(.select(1), .width(1), .disabled("Z"), .enable("false")) multiplexer_7 (
    .in0(ID_Bne), .in1(1'b0), .out(multiplexer_7_out), .sel(\同步清零_气泡_高电平有效 ));
  Multiplexer #(.select(1), .width(1), .disabled("Z"), .enable("false")) multiplexer_8 (
    .in0(ID_JMP), .in1(1'b0), .out(multiplexer_8_out), .sel(\同步清零_气泡_高电平有效 ));
  Multiplexer #(.select(1), .width(1), .disabled("Z"), .enable("false")) multiplexer_9 (
    .in0(ID_JR), .in1(1'b0), .out(multiplexer_9_out), .sel(\同步清零_气泡_高电平有效 ));
  Multiplexer #(.select(1), .width(1), .disabled("Z"), .enable("false")) multiplexer_10 (
    .in0(ID_BLTZ), .in1(1'b0), .out(multiplexer_10_out), .sel(\同步清零_气泡_高电平有效 ));
  Multiplexer #(.select(1), .width(1), .disabled("Z"), .enable("false")) multiplexer_11 (
    .in0(ID_Syscall), .in1(1'b0), .out(multiplexer_11_out), .sel(\同步清零_气泡_高电平有效 ));
  Multiplexer #(.select(1), .width(4), .disabled("Z"), .enable("false")) multiplexer_12 (
    .in0(ID_AluOP), .in1(4'b0000), .out(multiplexer_12_out), .sel(\同步清零_气泡_高电平有效 ));
  Multiplexer #(.select(1), .width(1), .disabled("Z"), .enable("false")) multiplexer_13 (
    .in0(ID_AluSRC), .in1(1'b0), .out(multiplexer_13_out), .sel(\同步清零_气泡_高电平有效 ));
  Multiplexer #(.select(1), .width(1), .disabled("Z"), .enable("false")) multiplexer_14 (
    .in0(ID_SRAV), .in1(1'b0), .out(multiplexer_14_out), .sel(\同步清零_气泡_高电平有效 ));
  Multiplexer #(.select(1), .width(32), .disabled("Z"), .enable("false")) multiplexer_15 (
    .in0(ID_RS), .in1({32{1'b0}}), .out(multiplexer_15_out), .sel(\同步清零_气泡_高电平有效 ));
  Multiplexer #(.select(1), .width(32), .disabled("Z"), .enable("false")) multiplexer_16 (
    .in0(ID_RT), .in1({32{1'b0}}), .out(multiplexer_16_out), .sel(\同步清零_气泡_高电平有效 ));
  Multiplexer #(.select(1), .width(5), .disabled("Z"), .enable("false")) multiplexer_17 (
    .in0(ID_shamt), .in1({5{1'b0}}), .out(multiplexer_17_out), .sel(\同步清零_气泡_高电平有效 ));
  Multiplexer #(.select(1), .width(32), .disabled("Z"), .enable("false")) multiplexer_18 (
    .in0(ID_Imm), .in1({32{1'b0}}), .out(multiplexer_18_out), .sel(\同步清零_气泡_高电平有效 ));
  Multiplexer #(.select(1), .width(32), .disabled("Z"), .enable("false")) multiplexer_19 (
    .in0(ID_SignImm), .in1({32{1'b0}}), .out(multiplexer_19_out), .sel(\同步清零_气泡_高电平有效 ));
  Multiplexer #(.select(1), .width(32), .disabled("Z"), .enable("false")) multiplexer_20 (
    .in0(ID_PC), .in1({32{1'b0}}), .out(multiplexer_20_out), .sel(\同步清零_气泡_高电平有效 ));
  Multiplexer #(.select(1), .width(5), .disabled("Z"), .enable("false")) multiplexer_21 (
    .in0(ID_WriteReg), .in1({5{1'b0}}), .out(multiplexer_21_out), .sel(\同步清零_气泡_高电平有效 ));
  Multiplexer #(.select(1), .width(32), .disabled("Z"), .enable("false")) multiplexer_22 (
    .in0(ID_IR), .in1({32{1'b0}}), .out(multiplexer_22_out), .sel(\同步清零_气泡_高电平有效 ));
  Multiplexer #(.select(1), .width(32), .disabled("Z"), .enable("false")) multiplexer_23 (
    .in0(ID_addr), .in1({32{1'b0}}), .out(multiplexer_23_out), .sel(\同步清零_气泡_高电平有效 ));
  Multiplexer #(.select(1), .width(32), .disabled("Z"), .enable("false")) multiplexer_24 (
    .in0(ID_monitor), .in1({32{1'b0}}), .out(multiplexer_24_out), .sel(\同步清零_气泡_高电平有效 ));
  Pull_Resistor #(.pull(0)) pull_resistor_1 (.node(\同步清零_气泡_高电平有效 ));
  not not_1 (not_1_out, \使能端_为高电平时忽略时钟输入 );
  Register #(.width(1), .trigger("rising"), .Select("low")) register_1 (
    .D(multiplexer_1_out), .en(not_1_out), .Q(EX_RegWrite), .clk(CLK));  // open: clr
  Register #(.width(1), .trigger("rising"), .Select("low")) register_2 (
    .D(multiplexer_2_out), .en(not_1_out), .Q(EX_MemToReg), .clk(CLK));  // open: clr
  Register #(.width(1), .trigger("rising"), .Select("low")) register_3 (
    .D(multiplexer_3_out), .en(not_1_out), .Q(EX_JAL), .clk(CLK));  // open: clr
  Register #(.width(1), .trigger("rising"), .Select("low")) register_4 (
    .D(multiplexer_4_out), .en(not_1_out), .Q(EX_LB), .clk(CLK));  // open: clr
  Register #(.width(1), .trigger("rising"), .Select("low")) register_5 (
    .D(multiplexer_5_out), .en(not_1_out), .Q(EX_MemWrite), .clk(CLK));  // open: clr
  Register #(.width(1), .trigger("rising"), .Select("low")) register_6 (
    .D(multiplexer_6_out), .en(not_1_out), .Q(EX_Beq), .clk(CLK));  // open: clr
  Register #(.width(1), .trigger("rising"), .Select("low")) register_7 (
    .D(multiplexer_7_out), .en(not_1_out), .Q(EX_PC), .clk(CLK));  // open: clr
  Register #(.width(1), .trigger("rising"), .Select("low")) register_8 (
    .D(multiplexer_8_out), .en(not_1_out), .Q(EX_JMP), .clk(CLK));  // open: clr
  Register #(.width(1), .trigger("rising"), .Select("low")) register_9 (
    .D(multiplexer_9_out), .en(not_1_out), .Q(EX_JR), .clk(CLK));  // open: clr
  Register #(.width(1), .trigger("rising"), .Select("low")) register_10 (
    .D(multiplexer_10_out), .en(not_1_out), .Q(ID_BLTZ_2), .clk(CLK));  // open: clr
  Register #(.width(1), .trigger("rising"), .Select("low")) register_11 (
    .D(multiplexer_11_out), .en(not_1_out), .Q(EX_Syscall), .clk(CLK));  // open: clr
  Register #(.width(4), .trigger("rising"), .Select("low")) register_12 (
    .D(multiplexer_12_out), .en(not_1_out), .Q(EX_AluOP), .clk(CLK));  // open: clr
  Register #(.width(1), .trigger("rising"), .Select("low")) register_13 (
    .D(multiplexer_13_out), .en(not_1_out), .Q(EX_AluSRC), .clk(CLK));  // open: clr
  Register #(.width(1), .trigger("rising"), .Select("low")) register_14 (
    .D(multiplexer_14_out), .en(not_1_out), .Q(EX_SRAV), .clk(CLK));  // open: clr
  Register #(.width(32), .trigger("rising"), .Select("low")) register_15 (
    .D(multiplexer_15_out), .en(not_1_out), .Q(EX_RS), .clk(CLK));  // open: clr
  Register #(.width(32), .trigger("rising"), .Select("low")) register_16 (
    .D(multiplexer_16_out), .en(not_1_out), .Q(EX_RT), .clk(CLK));  // open: clr
  Register #(.width(5), .trigger("rising"), .Select("low")) register_17 (
    .D(multiplexer_17_out), .en(not_1_out), .Q(EX_shamt), .clk(CLK));  // open: clr
  Register #(.width(32), .trigger("rising"), .Select("low")) register_18 (
    .D(multiplexer_18_out), .en(not_1_out), .Q(EX_Imm), .clk(CLK));  // open: clr
  Register #(.width(32), .trigger("rising"), .Select("low")) register_19 (
    .D(multiplexer_19_out), .en(not_1_out), .Q(EX_SignImm), .clk(CLK));  // open: clr
  Register #(.width(32), .trigger("rising"), .Select("low")) register_20 (
    .D(multiplexer_20_out), .en(not_1_out), .Q(EX_PC_2), .clk(CLK));  // open: clr
  Register #(.width(5), .trigger("rising"), .Select("low")) register_21 (
    .D(multiplexer_21_out), .en(not_1_out), .Q(EX_WriteReg), .clk(CLK));  // open: clr
  Register #(.width(32), .trigger("rising"), .Select("low")) register_22 (
    .D(multiplexer_22_out), .en(not_1_out), .Q(EX_IR), .clk(CLK));  // open: clr
  Register #(.width(32), .trigger("rising"), .Select("low")) register_23 (
    .D(multiplexer_23_out), .en(not_1_out), .Q(EX_addr), .clk(CLK));  // open: clr
  Register #(.width(32), .trigger("rising"), .Select("low")) register_24 (
    .D(multiplexer_24_out), .en(not_1_out), .Q(EX_monitor), .clk(CLK));  // open: clr
  Pull_Resistor #(.pull(0)) pull_resistor_2 (.node(not_1_out));
endmodule

// EX/MEM
module \气泡流水接口EX_MEM  (
  input  EX_RegWrite,
  input  EX_MemToReg,
  input  EX_JAL,
  input  EX_LB,
  input  EX_MemWrite,
  input  EX_Syscall,
  input  [31:0] EX_RS,
  input  [31:0] EX_result,
  input  [31:0] EX_MDin,
  input  [31:0] EX_PC,
  input  [4:0] EX_WriteReg,
  input  [31:0] EX_IR,
  input  [31:0] EX_monitor,
  input  CLK,
  input  \同步清零_气泡_高电平有效 ,
  input  \使能端_低电平有效_stall_高电平有效 ,
  output MEM_RegWrite,
  output MEM_MemToReg,
  output MEM_JAL,
  output MEM_LB,
  output MEM_MemWrite,
  output MEM_Syscall,
  output [31:0] MEM_RS,
  output [31:0] MEM_result,
  output [31:0] MEM_MDin,
  output [31:0] MEM_PC,
  output [4:0] MEM_WriteReg,
  output [31:0] MEM_IR,
  output [31:0] MEM_monitor
);

  wire multiplexer_1_out, multiplexer_2_out, multiplexer_3_out, multiplexer_4_out, multiplexer_5_out,
       multiplexer_6_out, not_1_out;
  wire [4:0] multiplexer_11_out;
  wire [31:0] multiplexer_7_out, multiplexer_8_out, multiplexer_9_out, multiplexer_10_out,
       multiplexer_12_out, multiplexer_13_out;

  Multiplexer #(.select(1), .width(1), .disabled("Z"), .enable("false")) multiplexer_1 (
    .in0(EX_RegWrite), .in1(1'b0), .out(multiplexer_1_out), .sel(\同步清零_气泡_高电平有效 ));
  Multiplexer #(.select(1), .width(1), .disabled("Z"), .enable("false")) multiplexer_2 (
    .in0(EX_MemToReg), .in1(1'b0), .out(multiplexer_2_out), .sel(\同步清零_气泡_高电平有效 ));
  Multiplexer #(.select(1), .width(1), .disabled("Z"), .enable("false")) multiplexer_3 (
    .in0(EX_JAL), .in1(1'b0), .out(multiplexer_3_out), .sel(\同步清零_气泡_高电平有效 ));
  Multiplexer #(.select(1), .width(1), .disabled("Z"), .enable("false")) multiplexer_4 (
    .in0(EX_LB), .in1(1'b0), .out(multiplexer_4_out), .sel(\同步清零_气泡_高电平有效 ));
  Multiplexer #(.select(1), .width(1), .disabled("Z"), .enable("false")) multiplexer_5 (
    .in0(EX_MemWrite), .in1(1'b0), .out(multiplexer_5_out), .sel(\同步清零_气泡_高电平有效 ));
  Multiplexer #(.select(1), .width(1), .disabled("Z"), .enable("false")) multiplexer_6 (
    .in0(EX_Syscall), .in1(1'b0), .out(multiplexer_6_out), .sel(\同步清零_气泡_高电平有效 ));
  Multiplexer #(.select(1), .width(32), .disabled("Z"), .enable("false")) multiplexer_7 (
    .in0(EX_RS), .in1({32{1'b0}}), .out(multiplexer_7_out), .sel(\同步清零_气泡_高电平有效 ));
  Multiplexer #(.select(1), .width(32), .disabled("Z"), .enable("false")) multiplexer_8 (
    .in0(EX_result), .in1({32{1'b0}}), .out(multiplexer_8_out), .sel(\同步清零_气泡_高电平有效 ));
  Multiplexer #(.select(1), .width(32), .disabled("Z"), .enable("false")) multiplexer_9 (
    .in0(EX_MDin), .in1({32{1'b0}}), .out(multiplexer_9_out), .sel(\同步清零_气泡_高电平有效 ));
  Multiplexer #(.select(1), .width(32), .disabled("Z"), .enable("false")) multiplexer_10 (
    .in0(EX_PC), .in1({32{1'b0}}), .out(multiplexer_10_out), .sel(\同步清零_气泡_高电平有效 ));
  Multiplexer #(.select(1), .width(5), .disabled("Z"), .enable("false")) multiplexer_11 (
    .in0(EX_WriteReg), .in1({5{1'b0}}), .out(multiplexer_11_out), .sel(\同步清零_气泡_高电平有效 ));
  Multiplexer #(.select(1), .width(32), .disabled("Z"), .enable("false")) multiplexer_12 (
    .in0(EX_IR), .in1({32{1'b0}}), .out(multiplexer_12_out), .sel(\同步清零_气泡_高电平有效 ));
  Multiplexer #(.select(1), .width(32), .disabled("Z"), .enable("false")) multiplexer_13 (
    .in0(EX_monitor), .in1({32{1'b0}}), .out(multiplexer_13_out), .sel(\同步清零_气泡_高电平有效 ));
  Pull_Resistor #(.pull(0)) pull_resistor_1 (.node(\同步清零_气泡_高电平有效 ));
  not not_1 (not_1_out, \使能端_低电平有效_stall_高电平有效 );
  Register #(.width(1), .trigger("rising"), .Select("low")) register_1 (
    .D(multiplexer_1_out), .en(not_1_out), .Q(MEM_RegWrite), .clk(CLK));  // open: clr
  Register #(.width(1), .trigger("rising"), .Select("low")) register_2 (
    .D(multiplexer_2_out), .en(not_1_out), .Q(MEM_MemToReg), .clk(CLK));  // open: clr
  Register #(.width(1), .trigger("rising"), .Select("low")) register_3 (
    .D(multiplexer_3_out), .en(not_1_out), .Q(MEM_JAL), .clk(CLK));  // open: clr
  Register #(.width(1), .trigger("rising"), .Select("low")) register_4 (
    .D(multiplexer_4_out), .en(not_1_out), .Q(MEM_LB), .clk(CLK));  // open: clr
  Register #(.width(1), .trigger("rising"), .Select("low")) register_5 (
    .D(multiplexer_5_out), .en(not_1_out), .Q(MEM_MemWrite), .clk(CLK));  // open: clr
  Register #(.width(1), .trigger("rising"), .Select("low")) register_6 (
    .D(multiplexer_6_out), .en(not_1_out), .Q(MEM_Syscall), .clk(CLK));  // open: clr
  Register #(.width(32), .trigger("rising"), .Select("low")) register_7 (
    .D(multiplexer_7_out), .en(not_1_out), .Q(MEM_RS), .clk(CLK));  // open: clr
  Register #(.width(32), .trigger("rising"), .Select("low")) register_8 (
    .D(multiplexer_8_out), .en(not_1_out), .Q(MEM_result), .clk(CLK));  // open: clr
  Register #(.width(32), .trigger("rising"), .Select("low")) register_9 (
    .D(multiplexer_9_out), .en(not_1_out), .Q(MEM_MDin), .clk(CLK));  // open: clr
  Register #(.width(32), .trigger("rising"), .Select("low")) register_10 (
    .D(multiplexer_10_out), .en(not_1_out), .Q(MEM_PC), .clk(CLK));  // open: clr
  Register #(.width(5), .trigger("rising"), .Select("low")) register_11 (
    .D(multiplexer_11_out), .en(not_1_out), .Q(MEM_WriteReg), .clk(CLK));  // open: clr
  Register #(.width(32), .trigger("rising"), .Select("low")) register_12 (
    .D(multiplexer_12_out), .en(not_1_out), .Q(MEM_IR), .clk(CLK));  // open: clr
  Register #(.width(32), .trigger("rising"), .Select("low")) register_13 (
    .D(multiplexer_13_out), .en(not_1_out), .Q(MEM_monitor), .clk(CLK));  // open: clr
  Pull_Resistor #(.pull(0)) pull_resistor_2 (.node(not_1_out));
endmodule

// MEM/WB
module \气泡流水接口MEM_WB  (
  input  MEM_RegWrite,
  input  MEM_MemToReg,
  input  MEM_JAL,
  input  MEM_LB,
  input  [31:0] MEM_AluResult,
  input  [31:0] MEM_MemResult,
  input  [31:0] MEM_PC,
  input  [4:0] MEM_WriteReg,
  input  [31:0] MEM_IR,
  input  [31:0] MEM_monitor,
  input  CLK,
  input  \同步清零_气泡_高电平有效 ,
  input  \使能端_为高电平时忽略时钟输入 ,
  output WB_RegWrite,
  output WB_MemToReg,
  output WB_JAL,
  output WB_LB,
  output [31:0] WB_AluResult,
  output [31:0] WB_MemResult,
  output [31:0] WB_PC,
  output [4:0] WB_WriteReg,
  output [31:0] WB_IR,
  output [31:0] WB_monitor
);

  wire multiplexer_1_out, multiplexer_2_out, multiplexer_3_out, multiplexer_4_out, not_1_out;
  wire [4:0] multiplexer_8_out;
  wire [31:0] multiplexer_5_out, multiplexer_6_out, multiplexer_7_out, multiplexer_9_out, multiplexer_10_out;

  Multiplexer #(.select(1), .width(1), .disabled("Z"), .enable("false")) multiplexer_1 (
    .in0(MEM_RegWrite), .in1(1'b0), .out(multiplexer_1_out), .sel(\同步清零_气泡_高电平有效 ));
  Multiplexer #(.select(1), .width(1), .disabled("Z"), .enable("false")) multiplexer_2 (
    .in0(MEM_MemToReg), .in1(1'b0), .out(multiplexer_2_out), .sel(\同步清零_气泡_高电平有效 ));
  Multiplexer #(.select(1), .width(1), .disabled("Z"), .enable("false")) multiplexer_3 (
    .in0(MEM_JAL), .in1(1'b0), .out(multiplexer_3_out), .sel(\同步清零_气泡_高电平有效 ));
  Multiplexer #(.select(1), .width(1), .disabled("Z"), .enable("false")) multiplexer_4 (
    .in0(MEM_LB), .in1(1'b0), .out(multiplexer_4_out), .sel(\同步清零_气泡_高电平有效 ));
  Multiplexer #(.select(1), .width(32), .disabled("Z"), .enable("false")) multiplexer_5 (
    .in0(MEM_AluResult), .in1({32{1'b0}}), .out(multiplexer_5_out), .sel(\同步清零_气泡_高电平有效 ));
  Multiplexer #(.select(1), .width(32), .disabled("Z"), .enable("false")) multiplexer_6 (
    .in0(MEM_MemResult), .in1({32{1'b0}}), .out(multiplexer_6_out), .sel(\同步清零_气泡_高电平有效 ));
  Multiplexer #(.select(1), .width(32), .disabled("Z"), .enable("false")) multiplexer_7 (
    .in0(MEM_PC), .in1({32{1'b0}}), .out(multiplexer_7_out), .sel(\同步清零_气泡_高电平有效 ));
  Multiplexer #(.select(1), .width(5), .disabled("Z"), .enable("false")) multiplexer_8 (
    .in0(MEM_WriteReg), .in1({5{1'b0}}), .out(multiplexer_8_out), .sel(\同步清零_气泡_高电平有效 ));
  Multiplexer #(.select(1), .width(32), .disabled("Z"), .enable("false")) multiplexer_9 (
    .in0(MEM_IR), .in1({32{1'b0}}), .out(multiplexer_9_out), .sel(\同步清零_气泡_高电平有效 ));
  Multiplexer #(.select(1), .width(32), .disabled("Z"), .enable("false")) multiplexer_10 (
    .in0(MEM_monitor), .in1({32{1'b0}}), .out(multiplexer_10_out), .sel(\同步清零_气泡_高电平有效 ));
  Pull_Resistor #(.pull(0)) pull_resistor_1 (.node(\同步清零_气泡_高电平有效 ));
  not not_1 (not_1_out, \使能端_为高电平时忽略时钟输入 );
  Register #(.width(1), .trigger("rising"), .Select("low")) register_1 (
    .D(multiplexer_1_out), .en(not_1_out), .Q(WB_RegWrite), .clk(CLK));  // open: clr
  Register #(.width(1), .trigger("rising"), .Select("low")) register_2 (
    .D(multiplexer_2_out), .en(not_1_out), .Q(WB_MemToReg), .clk(CLK));  // open: clr
  Register #(.width(1), .trigger("rising"), .Select("low")) register_3 (
    .D(multiplexer_3_out), .en(not_1_out), .Q(WB_JAL), .clk(CLK));  // open: clr
  Register #(.width(1), .trigger("rising"), .Select("low")) register_4 (
    .D(multiplexer_4_out), .en(not_1_out), .Q(WB_LB), .clk(CLK));  // open: clr
  Register #(.width(32), .trigger("rising"), .Select("low")) register_5 (
    .D(multiplexer_5_out), .en(not_1_out), .Q(WB_AluResult), .clk(CLK));  // open: clr
  Register #(.width(32), .trigger("rising"), .Select("low")) register_6 (
    .D(multiplexer_6_out), .en(not_1_out), .Q(WB_MemResult), .clk(CLK));  // open: clr
  Register #(.width(32), .trigger("rising"), .Select("low")) register_7 (
    .D(multiplexer_7_out), .en(not_1_out), .Q(WB_PC), .clk(CLK));  // open: clr
  Register #(.width(5), .trigger("rising"), .Select("low")) register_8 (
    .D(multiplexer_8_out), .en(not_1_out), .Q(WB_WriteReg), .clk(CLK));  // open: clr
  Register #(.width(32), .trigger("rising"), .Select("low")) register_9 (
    .D(multiplexer_9_out), .en(not_1_out), .Q(WB_IR), .clk(CLK));  // open: clr
  Register #(.width(32), .trigger("rising"), .Select("low")) register_10 (
    .D(multiplexer_10_out), .en(not_1_out), .Q(WB_monitor), .clk(CLK));  // open: clr
  Pull_Resistor #(.pull(0)) pull_resistor_2 (.node(not_1_out));
endmodule

module \相关处理逻辑_重定向  (
  input  [4:0] R1,
  input  [31:0] Instr,
  input  [4:0] R2,
  input  EX_RegWrite,
  input  [4:0] EX_WriteReg_num,
  input  EX_MemtoReg,
  input  BranchTaken,
  input  MEM_RegWrite,
  input  [4:0] MEM_WriteReg_num,
  output Stall,
  output Flush,
  output [1:0] RSF,
  output [1:0] RTF,
  output LoadUse
);

  wire and_2_out, and_4_out, and_7_out, and_8_out, comparator_1_eq, comparator_2_eq, comparator_3_eq,
       comparator_4_eq, comparator_5_eq, comparator_6_eq, comparator_7_eq, comparator_8_eq, comparator_9_eq,
       comparator_10_eq, comparator_11_eq, comparator_12_eq, not_1_out, not_2_out, not_3_out, not_4_out,
       not_5_out, not_6_out, R1_Used, R2_Used;

  \源寄存器使用情况自动生成  \u_源寄存器使用情况自动生成_1  (
    .OP0(Instr[26]), .OP1(Instr[27]), .OP2(Instr[28]), .OP3(Instr[29]), .OP4(Instr[30]), .OP5(Instr[31]),
    .F0(Instr[0]), .F1(Instr[1]), .F2(Instr[2]), .F3(Instr[3]), .F4(Instr[4]), .F5(Instr[5]),
    .R1_Used(R1_Used), .R2_Used(R2_Used));
  not not_1 (not_1_out, comparator_1_eq);
  Comparator #(.width(5), .mode("twosComplement")) comparator_1 (
    .a(R1), .b({5{1'b0}}), .eq(comparator_1_eq));  // open: gt, lt
  Comparator #(.width(5), .mode("twosComplement")) comparator_2 (
    .a(R1), .b(EX_WriteReg_num), .eq(comparator_2_eq));  // open: gt, lt
  Comparator #(.width(5), .mode("twosComplement")) comparator_3 (
    .a(R1), .b({5{1'b0}}), .eq(comparator_3_eq));  // open: gt, lt
  not not_2 (not_2_out, comparator_3_eq);
  Comparator #(.width(5), .mode("twosComplement")) comparator_4 (
    .a(R1), .b(MEM_WriteReg_num), .eq(comparator_4_eq));  // open: gt, lt
  not not_3 (not_3_out, comparator_5_eq);
  Comparator #(.width(5), .mode("twosComplement")) comparator_5 (
    .a(R2), .b({5{1'b0}}), .eq(comparator_5_eq));  // open: gt, lt
  Comparator #(.width(5), .mode("twosComplement")) comparator_6 (
    .a(R2), .b(EX_WriteReg_num), .eq(comparator_6_eq));  // open: gt, lt
  Comparator #(.width(5), .mode("twosComplement")) comparator_7 (
    .a(R2), .b({5{1'b0}}), .eq(comparator_7_eq));  // open: gt, lt
  not not_4 (not_4_out, comparator_7_eq);
  Comparator #(.width(5), .mode("twosComplement")) comparator_8 (
    .a(R2), .b(MEM_WriteReg_num), .eq(comparator_8_eq));  // open: gt, lt
  and and_1 (RSF[0], not_1_out, comparator_2_eq, R1_Used, EX_RegWrite);
  and and_2 (and_2_out, not_2_out, comparator_4_eq, R1_Used, MEM_RegWrite);
  and and_3 (RTF[0], not_3_out, comparator_6_eq, R2_Used, EX_RegWrite);
  and and_4 (and_4_out, not_4_out, comparator_8_eq, R2_Used, MEM_RegWrite);
  and and_5 (RSF[1], ~RSF[0], and_2_out);  // AND_Gate
  and and_6 (RTF[1], ~RTF[0], and_4_out);  // AND_Gate
  Comparator #(.width(5), .mode("twosComplement")) comparator_9 (
    .a(R1), .b({5{1'b0}}), .eq(comparator_9_eq));  // open: gt, lt
  Comparator #(.width(5), .mode("twosComplement")) comparator_10 (
    .a(R1), .b(EX_WriteReg_num), .eq(comparator_10_eq));  // open: gt, lt
  Comparator #(.width(5), .mode("twosComplement")) comparator_11 (
    .a(R2), .b({5{1'b0}}), .eq(comparator_11_eq));  // open: gt, lt
  Comparator #(.width(5), .mode("twosComplement")) comparator_12 (
    .a(R2), .b(EX_WriteReg_num), .eq(comparator_12_eq));  // open: gt, lt
  not not_5 (not_5_out, comparator_9_eq);
  and and_7 (and_7_out, not_5_out, comparator_10_eq, R1_Used, EX_MemtoReg);
  not not_6 (not_6_out, comparator_11_eq);
  and and_8 (and_8_out, not_6_out, comparator_12_eq, R2_Used, EX_MemtoReg);
  or or_1 (Flush, BranchTaken, LoadUse);
  or or_2 (LoadUse, and_7_out, and_8_out);

  assign Stall = LoadUse;

  // Other names for the same wires on the sheet: EX_WriteReg[4:0] = EX_WriteReg_num; FUNC[5:0] = Instr[5:0];
  //   OP_CODE[5:0] = Instr[31:26]; MEM_WriteReg[4:0] = MEM_WriteReg_num
endmodule

// ID/EX
module \重定向流水接口ID_EX  (
  input  ID_RegWrite,
  input  ID_MemToReg,
  input  ID_JAL,
  input  ID_LB,
  input  ID_MemWrite,
  input  ID_Syscall,
  input  ID_Beq,
  input  ID_Bne,
  input  ID_JMP,
  input  ID_JR,
  input  ID_BLTZ,
  input  [3:0] ID_AluOP,
  input  ID_AluSRC,
  input  ID_SRAV,
  input  [1:0] ID_RSF,
  input  [1:0] ID_RTF,
  input  [31:0] ID_RS,
  input  [31:0] ID_RT,
  input  [4:0] ID_shamt,
  input  [31:0] ID_Imm,
  input  [31:0] ID_SignImm,
  input  [31:0] ID_PC,
  input  [4:0] ID_WriteReg,
  input  [31:0] ID_IR,
  input  [31:0] ID_addr,
  input  [31:0] ID_monitor,
  input  ID_PredictJump,
  input  CLK,
  input  \同步清零_气泡_高电平有效 ,
  input  \使能端_为高电平时忽略时钟输入 ,
  output EX_RegWrite,
  output EX_MemToReg,
  output EX_JAL,
  output EX_LB,
  output EX_MemWrite,
  output EX_Syscall,
  output EX_Beq,
  output EX_PC,
  output EX_JMP,
  output EX_JR,
  output ID_BLTZ_2,
  output [3:0] EX_AluOP,
  output EX_AluSRC,
  output EX_SRAV,
  output [1:0] EX_RSF,
  output [1:0] EX_RTF,
  output [31:0] EX_RS,
  output [31:0] EX_RT,
  output [4:0] EX_shamt,
  output [31:0] EX_Imm,
  output [31:0] EX_SignImm,
  output [31:0] EX_PC_2,
  output [4:0] EX_WriteReg,
  output [31:0] EX_IR,
  output [31:0] EX_addr,
  output [31:0] EX_monitor,
  output EX_PredictJump
);

  wire multiplexer_1_out, multiplexer_2_out, multiplexer_3_out, multiplexer_4_out, multiplexer_5_out,
       multiplexer_6_out, multiplexer_7_out, multiplexer_8_out, multiplexer_9_out, multiplexer_10_out,
       multiplexer_11_out, multiplexer_13_out, multiplexer_14_out, multiplexer_27_out, not_1_out;
  wire [1:0] multiplexer_15_out, multiplexer_16_out;
  wire [3:0] multiplexer_12_out;
  wire [4:0] multiplexer_19_out, multiplexer_23_out;
  wire [31:0] multiplexer_17_out, multiplexer_18_out, multiplexer_20_out, multiplexer_21_out,
       multiplexer_22_out, multiplexer_24_out, multiplexer_25_out, multiplexer_26_out;

  Multiplexer #(.select(1), .width(1), .disabled("Z"), .enable("false")) multiplexer_1 (
    .in0(ID_RegWrite), .in1(1'b0), .out(multiplexer_1_out), .sel(\同步清零_气泡_高电平有效 ));
  Multiplexer #(.select(1), .width(1), .disabled("Z"), .enable("false")) multiplexer_2 (
    .in0(ID_MemToReg), .in1(1'b0), .out(multiplexer_2_out), .sel(\同步清零_气泡_高电平有效 ));
  Multiplexer #(.select(1), .width(1), .disabled("Z"), .enable("false")) multiplexer_3 (
    .in0(ID_JAL), .in1(1'b0), .out(multiplexer_3_out), .sel(\同步清零_气泡_高电平有效 ));
  Multiplexer #(.select(1), .width(1), .disabled("Z"), .enable("false")) multiplexer_4 (
    .in0(ID_LB), .in1(1'b0), .out(multiplexer_4_out), .sel(\同步清零_气泡_高电平有效 ));
  Multiplexer #(.select(1), .width(1), .disabled("Z"), .enable("false")) multiplexer_5 (
    .in0(ID_MemWrite), .in1(1'b0), .out(multiplexer_5_out), .sel(\同步清零_气泡_高电平有效 ));
  Multiplexer #(.select(1), .width(1), .disabled("Z"), .enable("false")) multiplexer_6 (
    .in0(ID_Syscall), .in1(1'b0), .out(multiplexer_6_out), .sel(\同步清零_气泡_高电平有效 ));
  Multiplexer #(.select(1), .width(1), .disabled("Z"), .enable("false")) multiplexer_7 (
    .in0(ID_Beq), .in1(1'b0), .out(multiplexer_7_out), .sel(\同步清零_气泡_高电平有效 ));
  Multiplexer #(.select(1), .width(1), .disabled("Z"), .enable("false")) multiplexer_8 (
    .in0(ID_Bne), .in1(1'b0), .out(multiplexer_8_out), .sel(\同步清零_气泡_高电平有效 ));
  Multiplexer #(.select(1), .width(1), .disabled("Z"), .enable("false")) multiplexer_9 (
    .in0(ID_JMP), .in1(1'b0), .out(multiplexer_9_out), .sel(\同步清零_气泡_高电平有效 ));
  Multiplexer #(.select(1), .width(1), .disabled("Z"), .enable("false")) multiplexer_10 (
    .in0(ID_JR), .in1(1'b0), .out(multiplexer_10_out), .sel(\同步清零_气泡_高电平有效 ));
  Multiplexer #(.select(1), .width(1), .disabled("Z"), .enable("false")) multiplexer_11 (
    .in0(ID_BLTZ), .in1(1'b0), .out(multiplexer_11_out), .sel(\同步清零_气泡_高电平有效 ));
  Multiplexer #(.select(1), .width(4), .disabled("Z"), .enable("false")) multiplexer_12 (
    .in0(ID_AluOP), .in1(4'b0000), .out(multiplexer_12_out), .sel(\同步清零_气泡_高电平有效 ));
  Multiplexer #(.select(1), .width(1), .disabled("Z"), .enable("false")) multiplexer_13 (
    .in0(ID_AluSRC), .in1(1'b0), .out(multiplexer_13_out), .sel(\同步清零_气泡_高电平有效 ));
  Multiplexer #(.select(1), .width(1), .disabled("Z"), .enable("false")) multiplexer_14 (
    .in0(ID_SRAV), .in1(1'b0), .out(multiplexer_14_out), .sel(\同步清零_气泡_高电平有效 ));
  Multiplexer #(.select(1), .width(2), .disabled("Z"), .enable("false")) multiplexer_15 (
    .in0(ID_RSF), .in1(2'b00), .out(multiplexer_15_out), .sel(\同步清零_气泡_高电平有效 ));
  Multiplexer #(.select(1), .width(2), .disabled("Z"), .enable("false")) multiplexer_16 (
    .in0(ID_RTF), .in1(2'b00), .out(multiplexer_16_out), .sel(\同步清零_气泡_高电平有效 ));
  Multiplexer #(.select(1), .width(32), .disabled("Z"), .enable("false")) multiplexer_17 (
    .in0(ID_RS), .in1({32{1'b0}}), .out(multiplexer_17_out), .sel(\同步清零_气泡_高电平有效 ));
  Multiplexer #(.select(1), .width(32), .disabled("Z"), .enable("false")) multiplexer_18 (
    .in0(ID_RT), .in1({32{1'b0}}), .out(multiplexer_18_out), .sel(\同步清零_气泡_高电平有效 ));
  Multiplexer #(.select(1), .width(5), .disabled("Z"), .enable("false")) multiplexer_19 (
    .in0(ID_shamt), .in1({5{1'b0}}), .out(multiplexer_19_out), .sel(\同步清零_气泡_高电平有效 ));
  Multiplexer #(.select(1), .width(32), .disabled("Z"), .enable("false")) multiplexer_20 (
    .in0(ID_Imm), .in1({32{1'b0}}), .out(multiplexer_20_out), .sel(\同步清零_气泡_高电平有效 ));
  Multiplexer #(.select(1), .width(32), .disabled("Z"), .enable("false")) multiplexer_21 (
    .in0(ID_SignImm), .in1({32{1'b0}}), .out(multiplexer_21_out), .sel(\同步清零_气泡_高电平有效 ));
  Multiplexer #(.select(1), .width(32), .disabled("Z"), .enable("false")) multiplexer_22 (
    .in0(ID_PC), .in1({32{1'b0}}), .out(multiplexer_22_out), .sel(\同步清零_气泡_高电平有效 ));
  Multiplexer #(.select(1), .width(5), .disabled("Z"), .enable("false")) multiplexer_23 (
    .in0(ID_WriteReg), .in1({5{1'b0}}), .out(multiplexer_23_out), .sel(\同步清零_气泡_高电平有效 ));
  Multiplexer #(.select(1), .width(32), .disabled("Z"), .enable("false")) multiplexer_24 (
    .in0(ID_IR), .in1({32{1'b0}}), .out(multiplexer_24_out), .sel(\同步清零_气泡_高电平有效 ));
  Multiplexer #(.select(1), .width(32), .disabled("Z"), .enable("false")) multiplexer_25 (
    .in0(ID_addr), .in1({32{1'b0}}), .out(multiplexer_25_out), .sel(\同步清零_气泡_高电平有效 ));
  Multiplexer #(.select(1), .width(32), .disabled("Z"), .enable("false")) multiplexer_26 (
    .in0(ID_monitor), .in1({32{1'b0}}), .out(multiplexer_26_out), .sel(\同步清零_气泡_高电平有效 ));
  Multiplexer #(.select(1), .width(1), .disabled("Z"), .enable("false")) multiplexer_27 (
    .in0(ID_PredictJump), .in1(1'b0), .out(multiplexer_27_out), .sel(\同步清零_气泡_高电平有效 ));
  Pull_Resistor #(.pull(0)) pull_resistor_1 (.node(\同步清零_气泡_高电平有效 ));
  not not_1 (not_1_out, \使能端_为高电平时忽略时钟输入 );
  Register #(.width(1), .trigger("rising"), .Select("low")) register_1 (
    .D(multiplexer_1_out), .en(not_1_out), .Q(EX_RegWrite), .clk(CLK));  // open: clr
  Register #(.width(1), .trigger("rising"), .Select("low")) register_2 (
    .D(multiplexer_2_out), .en(not_1_out), .Q(EX_MemToReg), .clk(CLK));  // open: clr
  Register #(.width(1), .trigger("rising"), .Select("low")) register_3 (
    .D(multiplexer_3_out), .en(not_1_out), .Q(EX_JAL), .clk(CLK));  // open: clr
  Register #(.width(1), .trigger("rising"), .Select("low")) register_4 (
    .D(multiplexer_4_out), .en(not_1_out), .Q(EX_LB), .clk(CLK));  // open: clr
  Register #(.width(1), .trigger("rising"), .Select("low")) register_5 (
    .D(multiplexer_5_out), .en(not_1_out), .Q(EX_MemWrite), .clk(CLK));  // open: clr
  Register #(.width(1), .trigger("rising"), .Select("low")) register_6 (
    .D(multiplexer_6_out), .en(not_1_out), .Q(EX_Syscall), .clk(CLK));  // open: clr
  Register #(.width(1), .trigger("rising"), .Select("low")) register_7 (
    .D(multiplexer_7_out), .en(not_1_out), .Q(EX_Beq), .clk(CLK));  // open: clr
  Register #(.width(1), .trigger("rising"), .Select("low")) register_8 (
    .D(multiplexer_8_out), .en(not_1_out), .Q(EX_PC), .clk(CLK));  // open: clr
  Register #(.width(1), .trigger("rising"), .Select("low")) register_9 (
    .D(multiplexer_9_out), .en(not_1_out), .Q(EX_JMP), .clk(CLK));  // open: clr
  Register #(.width(1), .trigger("rising"), .Select("low")) register_10 (
    .D(multiplexer_10_out), .en(not_1_out), .Q(EX_JR), .clk(CLK));  // open: clr
  Register #(.width(1), .trigger("rising"), .Select("low")) register_11 (
    .D(multiplexer_11_out), .en(not_1_out), .Q(ID_BLTZ_2), .clk(CLK));  // open: clr
  Register #(.width(4), .trigger("rising"), .Select("low")) register_12 (
    .D(multiplexer_12_out), .en(not_1_out), .Q(EX_AluOP), .clk(CLK));  // open: clr
  Register #(.width(1), .trigger("rising"), .Select("low")) register_13 (
    .D(multiplexer_13_out), .en(not_1_out), .Q(EX_AluSRC), .clk(CLK));  // open: clr
  Register #(.width(1), .trigger("rising"), .Select("low")) register_14 (
    .D(multiplexer_14_out), .en(not_1_out), .Q(EX_SRAV), .clk(CLK));  // open: clr
  Register #(.width(2), .trigger("rising"), .Select("low")) register_15 (
    .D(multiplexer_15_out), .en(not_1_out), .Q(EX_RSF), .clk(CLK));  // open: clr
  Register #(.width(2), .trigger("rising"), .Select("low")) register_16 (
    .D(multiplexer_16_out), .en(not_1_out), .Q(EX_RTF), .clk(CLK));  // open: clr
  Register #(.width(32), .trigger("rising"), .Select("low")) register_17 (
    .D(multiplexer_17_out), .en(not_1_out), .Q(EX_RS), .clk(CLK));  // open: clr
  Register #(.width(32), .trigger("rising"), .Select("low")) register_18 (
    .D(multiplexer_18_out), .en(not_1_out), .Q(EX_RT), .clk(CLK));  // open: clr
  Register #(.width(5), .trigger("rising"), .Select("low")) register_19 (
    .D(multiplexer_19_out), .en(not_1_out), .Q(EX_shamt), .clk(CLK));  // open: clr
  Register #(.width(32), .trigger("rising"), .Select("low")) register_20 (
    .D(multiplexer_20_out), .en(not_1_out), .Q(EX_Imm), .clk(CLK));  // open: clr
  Register #(.width(32), .trigger("rising"), .Select("low")) register_21 (
    .D(multiplexer_21_out), .en(not_1_out), .Q(EX_SignImm), .clk(CLK));  // open: clr
  Register #(.width(32), .trigger("rising"), .Select("low")) register_22 (
    .D(multiplexer_22_out), .en(not_1_out), .Q(EX_PC_2), .clk(CLK));  // open: clr
  Register #(.width(5), .trigger("rising"), .Select("low")) register_23 (
    .D(multiplexer_23_out), .en(not_1_out), .Q(EX_WriteReg), .clk(CLK));  // open: clr
  Register #(.width(32), .trigger("rising"), .Select("low")) register_24 (
    .D(multiplexer_24_out), .en(not_1_out), .Q(EX_IR), .clk(CLK));  // open: clr
  Register #(.width(32), .trigger("rising"), .Select("low")) register_25 (
    .D(multiplexer_25_out), .en(not_1_out), .Q(EX_addr), .clk(CLK));  // open: clr
  Register #(.width(32), .trigger("rising"), .Select("low")) register_26 (
    .D(multiplexer_26_out), .en(not_1_out), .Q(EX_monitor), .clk(CLK));  // open: clr
  Register #(.width(1), .trigger("rising"), .Select("low")) register_27 (
    .D(multiplexer_27_out), .en(not_1_out), .Q(EX_PredictJump), .clk(CLK));  // open: clr
  Pull_Resistor #(.pull(0)) pull_resistor_2 (.node(not_1_out));
endmodule

module \重定向流水接口EX_MEM  (
  input  EX_RegWrite,
  input  EX_MemToReg,
  input  EX_JAL,
  input  EX_LB,
  input  EX_MemWrite,
  input  EX_Syscall,
  input  [31:0] EX_RS,
  input  [31:0] EX_result,
  input  [31:0] EX_MDin,
  input  [31:0] EX_PC,
  input  [4:0] EX_WriteReg,
  input  [31:0] EX_IR,
  input  [31:0] EX_monitor,
  input  CLK,
  input  \同步清零_气泡_高电平有效 ,
  input  \使能端_低电平有效_stall_高电平有效 ,
  output MEM_RegWrite,
  output MEM_MemToReg,
  output MEM_JAL,
  output MEM_LB,
  output MEM_MemWrite,
  output MEM_Syscall,
  output [31:0] MEM_RS,
  output [31:0] MEM_result,
  output [31:0] MEM_MDin,
  output [31:0] MEM_PC,
  output [4:0] MEM_WriteReg,
  output [31:0] MEM_IR,
  output [31:0] MEM_monitor
);

  wire multiplexer_1_out, multiplexer_2_out, multiplexer_3_out, multiplexer_4_out, multiplexer_5_out,
       multiplexer_6_out, not_1_out;
  wire [4:0] multiplexer_11_out;
  wire [31:0] multiplexer_7_out, multiplexer_8_out, multiplexer_9_out, multiplexer_10_out,
       multiplexer_12_out, multiplexer_13_out;

  Multiplexer #(.select(1), .width(1), .disabled("Z"), .enable("false")) multiplexer_1 (
    .in0(EX_RegWrite), .in1(1'b0), .out(multiplexer_1_out), .sel(\同步清零_气泡_高电平有效 ));
  Multiplexer #(.select(1), .width(1), .disabled("Z"), .enable("false")) multiplexer_2 (
    .in0(EX_MemToReg), .in1(1'b0), .out(multiplexer_2_out), .sel(\同步清零_气泡_高电平有效 ));
  Multiplexer #(.select(1), .width(1), .disabled("Z"), .enable("false")) multiplexer_3 (
    .in0(EX_JAL), .in1(1'b0), .out(multiplexer_3_out), .sel(\同步清零_气泡_高电平有效 ));
  Multiplexer #(.select(1), .width(1), .disabled("Z"), .enable("false")) multiplexer_4 (
    .in0(EX_LB), .in1(1'b0), .out(multiplexer_4_out), .sel(\同步清零_气泡_高电平有效 ));
  Multiplexer #(.select(1), .width(1), .disabled("Z"), .enable("false")) multiplexer_5 (
    .in0(EX_MemWrite), .in1(1'b0), .out(multiplexer_5_out), .sel(\同步清零_气泡_高电平有效 ));
  Multiplexer #(.select(1), .width(1), .disabled("Z"), .enable("false")) multiplexer_6 (
    .in0(EX_Syscall), .in1(1'b0), .out(multiplexer_6_out), .sel(\同步清零_气泡_高电平有效 ));
  Multiplexer #(.select(1), .width(32), .disabled("Z"), .enable("false")) multiplexer_7 (
    .in0(EX_RS), .in1({32{1'b0}}), .out(multiplexer_7_out), .sel(\同步清零_气泡_高电平有效 ));
  Multiplexer #(.select(1), .width(32), .disabled("Z"), .enable("false")) multiplexer_8 (
    .in0(EX_result), .in1({32{1'b0}}), .out(multiplexer_8_out), .sel(\同步清零_气泡_高电平有效 ));
  Multiplexer #(.select(1), .width(32), .disabled("Z"), .enable("false")) multiplexer_9 (
    .in0(EX_MDin), .in1({32{1'b0}}), .out(multiplexer_9_out), .sel(\同步清零_气泡_高电平有效 ));
  Multiplexer #(.select(1), .width(32), .disabled("Z"), .enable("false")) multiplexer_10 (
    .in0(EX_PC), .in1({32{1'b0}}), .out(multiplexer_10_out), .sel(\同步清零_气泡_高电平有效 ));
  Multiplexer #(.select(1), .width(5), .disabled("Z"), .enable("false")) multiplexer_11 (
    .in0(EX_WriteReg), .in1({5{1'b0}}), .out(multiplexer_11_out), .sel(\同步清零_气泡_高电平有效 ));
  Multiplexer #(.select(1), .width(32), .disabled("Z"), .enable("false")) multiplexer_12 (
    .in0(EX_IR), .in1({32{1'b0}}), .out(multiplexer_12_out), .sel(\同步清零_气泡_高电平有效 ));
  Multiplexer #(.select(1), .width(32), .disabled("Z"), .enable("false")) multiplexer_13 (
    .in0(EX_monitor), .in1({32{1'b0}}), .out(multiplexer_13_out), .sel(\同步清零_气泡_高电平有效 ));
  Pull_Resistor #(.pull(0)) pull_resistor_1 (.node(\同步清零_气泡_高电平有效 ));
  not not_1 (not_1_out, \使能端_低电平有效_stall_高电平有效 );
  Register #(.width(1), .trigger("rising"), .Select("low")) register_1 (
    .D(multiplexer_1_out), .en(not_1_out), .Q(MEM_RegWrite), .clk(CLK));  // open: clr
  Register #(.width(1), .trigger("rising"), .Select("low")) register_2 (
    .D(multiplexer_2_out), .en(not_1_out), .Q(MEM_MemToReg), .clk(CLK));  // open: clr
  Register #(.width(1), .trigger("rising"), .Select("low")) register_3 (
    .D(multiplexer_3_out), .en(not_1_out), .Q(MEM_JAL), .clk(CLK));  // open: clr
  Register #(.width(1), .trigger("rising"), .Select("low")) register_4 (
    .D(multiplexer_4_out), .en(not_1_out), .Q(MEM_LB), .clk(CLK));  // open: clr
  Register #(.width(1), .trigger("rising"), .Select("low")) register_5 (
    .D(multiplexer_5_out), .en(not_1_out), .Q(MEM_MemWrite), .clk(CLK));  // open: clr
  Register #(.width(1), .trigger("rising"), .Select("low")) register_6 (
    .D(multiplexer_6_out), .en(not_1_out), .Q(MEM_Syscall), .clk(CLK));  // open: clr
  Register #(.width(32), .trigger("rising"), .Select("low")) register_7 (
    .D(multiplexer_7_out), .en(not_1_out), .Q(MEM_RS), .clk(CLK));  // open: clr
  Register #(.width(32), .trigger("rising"), .Select("low")) register_8 (
    .D(multiplexer_8_out), .en(not_1_out), .Q(MEM_result), .clk(CLK));  // open: clr
  Register #(.width(32), .trigger("rising"), .Select("low")) register_9 (
    .D(multiplexer_9_out), .en(not_1_out), .Q(MEM_MDin), .clk(CLK));  // open: clr
  Register #(.width(32), .trigger("rising"), .Select("low")) register_10 (
    .D(multiplexer_10_out), .en(not_1_out), .Q(MEM_PC), .clk(CLK));  // open: clr
  Register #(.width(5), .trigger("rising"), .Select("low")) register_11 (
    .D(multiplexer_11_out), .en(not_1_out), .Q(MEM_WriteReg), .clk(CLK));  // open: clr
  Register #(.width(32), .trigger("rising"), .Select("low")) register_12 (
    .D(multiplexer_12_out), .en(not_1_out), .Q(MEM_IR), .clk(CLK));  // open: clr
  Register #(.width(32), .trigger("rising"), .Select("low")) register_13 (
    .D(multiplexer_13_out), .en(not_1_out), .Q(MEM_monitor), .clk(CLK));  // open: clr
  Pull_Resistor #(.pull(0)) pull_resistor_2 (.node(not_1_out));
endmodule
module \重定向流水接口MEM_WB  (
  input  MEM_RegWrite,
  input  MEM_MemToReg,
  input  MEM_JAL,
  input  MEM_LB,
  input  [31:0] MEM_AluResult,
  input  [31:0] MEM_MemResult,
  input  [31:0] MEM_PC,
  input  [4:0] MEM_WriteReg,
  input  [31:0] MEM_IR,
  input  [31:0] MEM_monitor,
  input  CLK,
  input  \同步清零_气泡_高电平有效 ,
  input  \使能端_为高电平时忽略时钟输入 ,
  output WB_RegWrite,
  output WB_MemToReg,
  output WB_JAL,
  output WB_LB,
  output [31:0] WB_AluResult,
  output [31:0] WB_MemResult,
  output [31:0] WB_PC,
  output [4:0] WB_WriteReg,
  output [31:0] WB_IR,
  output [31:0] WB_monitor
);

  wire multiplexer_1_out, multiplexer_2_out, multiplexer_3_out, multiplexer_4_out, not_1_out;
  wire [4:0] multiplexer_8_out;
  wire [31:0] multiplexer_5_out, multiplexer_6_out, multiplexer_7_out, multiplexer_9_out, multiplexer_10_out;

  Multiplexer #(.select(1), .width(1), .disabled("Z"), .enable("false")) multiplexer_1 (
    .in0(MEM_RegWrite), .in1(1'b0), .out(multiplexer_1_out), .sel(\同步清零_气泡_高电平有效 ));
  Multiplexer #(.select(1), .width(1), .disabled("Z"), .enable("false")) multiplexer_2 (
    .in0(MEM_MemToReg), .in1(1'b0), .out(multiplexer_2_out), .sel(\同步清零_气泡_高电平有效 ));
  Multiplexer #(.select(1), .width(1), .disabled("Z"), .enable("false")) multiplexer_3 (
    .in0(MEM_JAL), .in1(1'b0), .out(multiplexer_3_out), .sel(\同步清零_气泡_高电平有效 ));
  Multiplexer #(.select(1), .width(1), .disabled("Z"), .enable("false")) multiplexer_4 (
    .in0(MEM_LB), .in1(1'b0), .out(multiplexer_4_out), .sel(\同步清零_气泡_高电平有效 ));
  Multiplexer #(.select(1), .width(32), .disabled("Z"), .enable("false")) multiplexer_5 (
    .in0(MEM_AluResult), .in1({32{1'b0}}), .out(multiplexer_5_out), .sel(\同步清零_气泡_高电平有效 ));
  Multiplexer #(.select(1), .width(32), .disabled("Z"), .enable("false")) multiplexer_6 (
    .in0(MEM_MemResult), .in1({32{1'b0}}), .out(multiplexer_6_out), .sel(\同步清零_气泡_高电平有效 ));
  Multiplexer #(.select(1), .width(32), .disabled("Z"), .enable("false")) multiplexer_7 (
    .in0(MEM_PC), .in1({32{1'b0}}), .out(multiplexer_7_out), .sel(\同步清零_气泡_高电平有效 ));
  Multiplexer #(.select(1), .width(5), .disabled("Z"), .enable("false")) multiplexer_8 (
    .in0(MEM_WriteReg), .in1({5{1'b0}}), .out(multiplexer_8_out), .sel(\同步清零_气泡_高电平有效 ));
  Multiplexer #(.select(1), .width(32), .disabled("Z"), .enable("false")) multiplexer_9 (
    .in0(MEM_IR), .in1({32{1'b0}}), .out(multiplexer_9_out), .sel(\同步清零_气泡_高电平有效 ));
  Multiplexer #(.select(1), .width(32), .disabled("Z"), .enable("false")) multiplexer_10 (
    .in0(MEM_monitor), .in1({32{1'b0}}), .out(multiplexer_10_out), .sel(\同步清零_气泡_高电平有效 ));
  Pull_Resistor #(.pull(0)) pull_resistor_1 (.node(\同步清零_气泡_高电平有效 ));
  not not_1 (not_1_out, \使能端_为高电平时忽略时钟输入 );
  Register #(.width(1), .trigger("rising"), .Select("low")) register_1 (
    .D(multiplexer_1_out), .en(not_1_out), .Q(WB_RegWrite), .clk(CLK));  // open: clr
  Register #(.width(1), .trigger("rising"), .Select("low")) register_2 (
    .D(multiplexer_2_out), .en(not_1_out), .Q(WB_MemToReg), .clk(CLK));  // open: clr
  Register #(.width(1), .trigger("rising"), .Select("low")) register_3 (
    .D(multiplexer_3_out), .en(not_1_out), .Q(WB_JAL), .clk(CLK));  // open: clr
  Register #(.width(1), .trigger("rising"), .Select("low")) register_4 (
    .D(multiplexer_4_out), .en(not_1_out), .Q(WB_LB), .clk(CLK));  // open: clr
  Register #(.width(32), .trigger("rising"), .Select("low")) register_5 (
    .D(multiplexer_5_out), .en(not_1_out), .Q(WB_AluResult), .clk(CLK));  // open: clr
  Register #(.width(32), .trigger("rising"), .Select("low")) register_6 (
    .D(multiplexer_6_out), .en(not_1_out), .Q(WB_MemResult), .clk(CLK));  // open: clr
  Register #(.width(32), .trigger("rising"), .Select("low")) register_7 (
    .D(multiplexer_7_out), .en(not_1_out), .Q(WB_PC), .clk(CLK));  // open: clr
  Register #(.width(5), .trigger("rising"), .Select("low")) register_8 (
    .D(multiplexer_8_out), .en(not_1_out), .Q(WB_WriteReg), .clk(CLK));  // open: clr
  Register #(.width(32), .trigger("rising"), .Select("low")) register_9 (
    .D(multiplexer_9_out), .en(not_1_out), .Q(WB_IR), .clk(CLK));  // open: clr
  Register #(.width(32), .trigger("rising"), .Select("low")) register_10 (
    .D(multiplexer_10_out), .en(not_1_out), .Q(WB_monitor), .clk(CLK));  // open: clr
  Pull_Resistor #(.pull(0)) pull_resistor_2 (.node(not_1_out));
endmodule

module BTB (
  input  CLK,
  input  EX_Branch,
  input  [31:0] PC,
  input  EX_BranchTaken,
  input  [31:0] EX_PC,
  input  [31:0] EX_BrachAddr,
  output [31:0] JumpAddr,
  output PredictJump
);

  wire and_10_out, comparator_1_eq, comparator_2_eq, comparator_3_eq, comparator_4_eq, comparator_5_eq,
       comparator_6_eq, comparator_7_eq, comparator_8_eq, full, Hit, L0, L1, L2, L3, L4, L5, L6, L7, Miss,
       not_2_out, not_3_out, not_4_out, not_5_out, not_6_out, not_7_out, not_8_out, not_9_out, upd, V0, V1,
       V2, V3, V4, V5, V6, V7, W0, W1, W2, W3, W4, W5, W6, W7;
  wire [1:0] History, register_17_q, register_18_q, register_19_q, register_20_q, register_21_q,
       register_22_q, register_23_q, register_24_q, \双位预测状态转换_1_s0 , \双位预测状态转换_2_s0 , \双位预测状态转换_3_s0 ,
       \双位预测状态转换_4_s0 , \双位预测状态转换_5_s0 , \双位预测状态转换_6_s0 , \双位预测状态转换_7_s0 , \双位预测状态转换_8_s0 ;
  wire [2:0] change, \max3_归并比较_1_max_num , \max3_归并比较_2_max_num , \max3_归并比较_3_max_num ,
       \max3_归并比较_4_max_num , \max3_归并比较_5_max_num , \max3_归并比较_6_max_num , multiplexer_3_out, row;
  wire [15:0] C0, C1, C2, C3, C4, C5, C6, C7, \max3_归并比较_1_max , \max3_归并比较_2_max , \max3_归并比较_3_max ,
       \max3_归并比较_4_max , \max3_归并比较_5_max , \max3_归并比较_6_max ;
  wire [31:0] register_25_q, register_26_q, register_27_q, register_28_q, register_29_q, register_30_q,
       register_31_q, register_32_q, tag, tag0, tag1, tag2, tag3, tag4, tag5, tag6, tag7;

  Multiplexer #(.select(1), .width(32), .disabled("Z"), .enable("false")) multiplexer_1 (
    .in0(PC), .in1(EX_PC), .out(tag), .sel(EX_Branch));
  Comparator #(.width(32), .mode("twosComplement")) comparator_1 (
    .a(tag), .b(tag0), .eq(comparator_1_eq));  // open: gt, lt
  Comparator #(.width(32), .mode("twosComplement")) comparator_2 (
    .a(tag), .b(tag1), .eq(comparator_2_eq));  // open: gt, lt
  Comparator #(.width(32), .mode("twosComplement")) comparator_3 (
    .a(tag), .b(tag2), .eq(comparator_3_eq));  // open: gt, lt
  Comparator #(.width(32), .mode("twosComplement")) comparator_4 (
    .a(tag), .b(tag3), .eq(comparator_4_eq));  // open: gt, lt
  Comparator #(.width(32), .mode("twosComplement")) comparator_5 (
    .a(tag), .b(tag4), .eq(comparator_5_eq));  // open: gt, lt
  Comparator #(.width(32), .mode("twosComplement")) comparator_6 (
    .a(tag), .b(tag5), .eq(comparator_6_eq));  // open: gt, lt
  Comparator #(.width(32), .mode("twosComplement")) comparator_7 (
    .a(tag), .b(tag6), .eq(comparator_7_eq));  // open: gt, lt
  Comparator #(.width(32), .mode("twosComplement")) comparator_8 (
    .a(tag), .b(tag7), .eq(comparator_8_eq));  // open: gt, lt
  and and_1 (L0, V0, comparator_1_eq);
  and and_2 (L1, V1, comparator_2_eq);
  and and_3 (L2, V2, comparator_3_eq);
  and and_4 (L3, V3, comparator_4_eq);
  and and_5 (L4, V4, comparator_5_eq);
  and and_6 (L5, V5, comparator_6_eq);
  and and_7 (L6, V6, comparator_7_eq);
  and and_8 (L7, V7, comparator_8_eq);
  Register #(.width(1), .trigger("rising"), .Select("low")) register_1 (
    .D(1'b1), .en(W0), .Q(V0), .clk(CLK));  // open: clr
  Register #(.width(1), .trigger("rising"), .Select("low")) register_2 (
    .D(1'b1), .en(W1), .Q(V1), .clk(CLK));  // open: clr
  Register #(.width(1), .trigger("rising"), .Select("low")) register_3 (
    .D(1'b1), .en(W2), .Q(V2), .clk(CLK));  // open: clr
  Register #(.width(1), .trigger("rising"), .Select("low")) register_4 (
    .D(1'b1), .en(W3), .Q(V3), .clk(CLK));  // open: clr
  Register #(.width(1), .trigger("rising"), .Select("low")) register_5 (
    .D(1'b1), .en(W4), .Q(V4), .clk(CLK));  // open: clr
  Register #(.width(1), .trigger("rising"), .Select("low")) register_6 (
    .D(1'b1), .en(W5), .Q(V5), .clk(CLK));  // open: clr
  Register #(.width(1), .trigger("rising"), .Select("low")) register_7 (
    .D(1'b1), .en(W6), .Q(V6), .clk(CLK));  // open: clr
  Register #(.width(1), .trigger("rising"), .Select("low")) register_8 (
    .D(1'b1), .en(W7), .Q(V7), .clk(CLK));  // open: clr
  Register #(.width(32), .trigger("rising"), .Select("low")) register_9 (
    .D(tag), .en(W0), .Q(tag0), .clk(CLK));  // open: clr
  Register #(.width(32), .trigger("rising"), .Select("low")) register_10 (
    .D(tag), .en(W1), .Q(tag1), .clk(CLK));  // open: clr
  Register #(.width(32), .trigger("rising"), .Select("low")) register_11 (
    .D(tag), .en(W2), .Q(tag2), .clk(CLK));  // open: clr
  Register #(.width(32), .trigger("rising"), .Select("low")) register_12 (
    .D(tag), .en(W3), .Q(tag3), .clk(CLK));  // open: clr
  Register #(.width(32), .trigger("rising"), .Select("low")) register_13 (
    .D(tag), .en(W4), .Q(tag4), .clk(CLK));  // open: clr
  Register #(.width(32), .trigger("rising"), .Select("low")) register_14 (
    .D(tag), .en(W5), .Q(tag5), .clk(CLK));  // open: clr
  Register #(.width(32), .trigger("rising"), .Select("low")) register_15 (
    .D(tag), .en(W6), .Q(tag6), .clk(CLK));  // open: clr
  Register #(.width(32), .trigger("rising"), .Select("low")) register_16 (
    .D(tag), .en(W7), .Q(tag7), .clk(CLK));  // open: clr
  or or_1 (Hit, L0, L1, L2, L3, L4, L5, L6, L7);
  not not_1 (Miss, Hit);
  Counter #(.width(16), .max('hffff), .ongoal("wrap"), .trigger("rising"), .behavior("new")) counter_1 (
    .Q(C0), .clk(CLK), .clr(L0));  // open: load, D, count, carry, preset, down
  Counter #(.width(16), .max('hffff), .ongoal("wrap"), .trigger("rising"), .behavior("new")) counter_2 (
    .Q(C1), .clk(CLK), .clr(L1));  // open: load, D, count, carry, preset, down
  Counter #(.width(16), .max('hffff), .ongoal("wrap"), .trigger("rising"), .behavior("new")) counter_3 (
    .Q(C2), .clk(CLK), .clr(L2));  // open: load, D, count, carry, preset, down
  Counter #(.width(16), .max('hffff), .ongoal("wrap"), .trigger("rising"), .behavior("new")) counter_4 (
    .Q(C3), .clk(CLK), .clr(L3));  // open: load, D, count, carry, preset, down
  Counter #(.width(16), .max('hffff), .ongoal("wrap"), .trigger("rising"), .behavior("new")) counter_5 (
    .Q(C4), .clk(CLK), .clr(L4));  // open: load, D, count, carry, preset, down
  Counter #(.width(16), .max('hffff), .ongoal("wrap"), .trigger("rising"), .behavior("new")) counter_6 (
    .Q(C5), .clk(CLK), .clr(L5));  // open: load, D, count, carry, preset, down
  Counter #(.width(16), .max('hffff), .ongoal("wrap"), .trigger("rising"), .behavior("new")) counter_7 (
    .Q(C6), .clk(CLK), .clr(L6));  // open: load, D, count, carry, preset, down
  Counter #(.width(16), .max('hffff), .ongoal("wrap"), .trigger("rising"), .behavior("new")) counter_8 (
    .Q(C7), .clk(CLK), .clr(L7));  // open: load, D, count, carry, preset, down
  not not_2 (not_2_out, V0);
  not not_3 (not_3_out, V1);
  not not_4 (not_4_out, V2);
  not not_5 (not_5_out, V3);
  not not_6 (not_6_out, V4);
  not not_7 (not_7_out, V5);
  not not_8 (not_8_out, V6);
  not not_9 (not_9_out, V7);
  and and_9 (upd, Hit, EX_Branch);
  \双位预测状态转换  \u_双位预测状态转换_1  (
    .P1(register_17_q[1]), .P0(register_17_q[0]), .realJump(EX_BranchTaken), .S1(\双位预测状态转换_1_s0 [1]),
    .S0(\双位预测状态转换_1_s0 [0]));
  \双位预测状态转换  \u_双位预测状态转换_2  (
    .P1(register_18_q[1]), .P0(register_18_q[0]), .realJump(EX_BranchTaken), .S1(\双位预测状态转换_2_s0 [1]),
    .S0(\双位预测状态转换_2_s0 [0]));
  \双位预测状态转换  \u_双位预测状态转换_3  (
    .P1(register_19_q[1]), .P0(register_19_q[0]), .realJump(EX_BranchTaken), .S1(\双位预测状态转换_3_s0 [1]),
    .S0(\双位预测状态转换_3_s0 [0]));
  \双位预测状态转换  \u_双位预测状态转换_4  (
    .P1(register_20_q[1]), .P0(register_20_q[0]), .realJump(EX_BranchTaken), .S1(\双位预测状态转换_4_s0 [1]),
    .S0(\双位预测状态转换_4_s0 [0]));
  \双位预测状态转换  \u_双位预测状态转换_5  (
    .P1(register_21_q[1]), .P0(register_21_q[0]), .realJump(EX_BranchTaken), .S1(\双位预测状态转换_5_s0 [1]),
    .S0(\双位预测状态转换_5_s0 [0]));
  \双位预测状态转换  \u_双位预测状态转换_6  (
    .P1(register_22_q[1]), .P0(register_22_q[0]), .realJump(EX_BranchTaken), .S1(\双位预测状态转换_6_s0 [1]),
    .S0(\双位预测状态转换_6_s0 [0]));
  \双位预测状态转换  \u_双位预测状态转换_7  (
    .P1(register_23_q[1]), .P0(register_23_q[0]), .realJump(EX_BranchTaken), .S1(\双位预测状态转换_7_s0 [1]),
    .S0(\双位预测状态转换_7_s0 [0]));
  \双位预测状态转换  \u_双位预测状态转换_8  (
    .P1(register_24_q[1]), .P0(register_24_q[0]), .realJump(EX_BranchTaken), .S1(\双位预测状态转换_8_s0 [1]),
    .S0(\双位预测状态转换_8_s0 [0]));
  Priority_Encoder #(.select(3), .disabled("Z")) priority_encoder_1 (
    .in0(not_2_out), .in1(not_3_out), .in2(not_4_out), .in3(not_5_out), .in4(not_6_out), .in5(not_7_out),
    .in6(not_8_out), .in7(not_9_out), .out(row), .en_out(full), .en_in(1'b1));  // open: gs
  Register #(.width(2), .trigger("rising"), .Select("low")) register_17 (
    .D(\双位预测状态转换_1_s0 ), .en(upd), .Q(register_17_q), .clk(CLK), .clr(W0));
  assign History = L0 ? register_17_q : 2'bz;  // Controlled_Buffer controlled_buffer_1
  Register #(.width(2), .trigger("rising"), .Select("low")) register_18 (
    .D(\双位预测状态转换_2_s0 ), .en(upd), .Q(register_18_q), .clk(CLK), .clr(W1));
  assign History = L1 ? register_18_q : 2'bz;  // Controlled_Buffer controlled_buffer_2
  Register #(.width(2), .trigger("rising"), .Select("low")) register_19 (
    .D(\双位预测状态转换_3_s0 ), .en(upd), .Q(register_19_q), .clk(CLK), .clr(W2));
  Register #(.width(2), .trigger("rising"), .Select("low")) register_20 (
    .D(\双位预测状态转换_4_s0 ), .en(upd), .Q(register_20_q), .clk(CLK), .clr(W3));
  Register #(.width(2), .trigger("rising"), .Select("low")) register_21 (
    .D(\双位预测状态转换_5_s0 ), .en(upd), .Q(register_21_q), .clk(CLK), .clr(W4));
  Register #(.width(2), .trigger("rising"), .Select("low")) register_22 (
    .D(\双位预测状态转换_6_s0 ), .en(upd), .Q(register_22_q), .clk(CLK), .clr(W5));
  Register #(.width(2), .trigger("rising"), .Select("low")) register_23 (
    .D(\双位预测状态转换_7_s0 ), .en(upd), .Q(register_23_q), .clk(CLK), .clr(W6));
  Register #(.width(2), .trigger("rising"), .Select("low")) register_24 (
    .D(\双位预测状态转换_8_s0 ), .en(upd), .Q(register_24_q), .clk(CLK), .clr(W7));
  Multiplexer #(.select(1), .width(1), .disabled("Z"), .enable("false")) multiplexer_2 (
    .in0(History[1]), .in1(1'b0), .out(PredictJump), .sel(Miss));
  assign History = L2 ? register_19_q : 2'bz;  // Controlled_Buffer controlled_buffer_3
  assign History = L3 ? register_20_q : 2'bz;  // Controlled_Buffer controlled_buffer_4
  assign History = L4 ? register_21_q : 2'bz;  // Controlled_Buffer controlled_buffer_5
  assign History = L5 ? register_22_q : 2'bz;  // Controlled_Buffer controlled_buffer_6
  assign History = L6 ? register_23_q : 2'bz;  // Controlled_Buffer controlled_buffer_7
  assign History = L7 ? register_24_q : 2'bz;  // Controlled_Buffer controlled_buffer_8
  \Max3_归并比较  \max3_归并比较_1  (
    .Y(C1), .X(C0), .Y_num(3'b001), .X_num(3'b000), .MAX(\max3_归并比较_1_max ), .Max_num(\max3_归并比较_1_max_num ));
  \Max3_归并比较  \max3_归并比较_2  (
    .Y(C3), .X(C2), .Y_num(3'b011), .X_num(3'b010), .MAX(\max3_归并比较_2_max ), .Max_num(\max3_归并比较_2_max_num ));
  \Max3_归并比较  \max3_归并比较_3  (
    .Y(C5), .X(C4), .Y_num(3'b101), .X_num(3'b100), .MAX(\max3_归并比较_3_max ), .Max_num(\max3_归并比较_3_max_num ));
  \Max3_归并比较  \max3_归并比较_4  (
    .Y(C7), .X(C6), .Y_num(3'b111), .X_num(3'b110), .MAX(\max3_归并比较_4_max ), .Max_num(\max3_归并比较_4_max_num ));
  \Max3_归并比较  \max3_归并比较_5  (
    .Y(\max3_归并比较_2_max ), .X(\max3_归并比较_1_max ), .Y_num(\max3_归并比较_2_max_num ),
    .X_num(\max3_归并比较_1_max_num ), .MAX(\max3_归并比较_5_max ), .Max_num(\max3_归并比较_5_max_num ));
  \Max3_归并比较  \max3_归并比较_6  (
    .Y(\max3_归并比较_4_max ), .X(\max3_归并比较_3_max ), .Y_num(\max3_归并比较_4_max_num ),
    .X_num(\max3_归并比较_3_max_num ), .MAX(\max3_归并比较_6_max ), .Max_num(\max3_归并比较_6_max_num ));
  assign JumpAddr = L0 ? register_25_q : 32'bz;  // Controlled_Buffer controlled_buffer_9
  Register #(.width(32), .trigger("rising"), .Select("low")) register_25 (
    .D(EX_BrachAddr), .en(W0), .Q(register_25_q), .clk(CLK));  // open: clr
  Register #(.width(32), .trigger("rising"), .Select("low")) register_26 (
    .D(EX_BrachAddr), .en(W1), .Q(register_26_q), .clk(CLK));  // open: clr
  assign JumpAddr = L1 ? register_26_q : 32'bz;  // Controlled_Buffer controlled_buffer_10
  assign JumpAddr = L2 ? register_27_q : 32'bz;  // Controlled_Buffer controlled_buffer_11
  Register #(.width(32), .trigger("rising"), .Select("low")) register_27 (
    .D(EX_BrachAddr), .en(W2), .Q(register_27_q), .clk(CLK));  // open: clr
  assign JumpAddr = L3 ? register_28_q : 32'bz;  // Controlled_Buffer controlled_buffer_12
  Register #(.width(32), .trigger("rising"), .Select("low")) register_28 (
    .D(EX_BrachAddr), .en(W3), .Q(register_28_q), .clk(CLK));  // open: clr
  assign JumpAddr = L4 ? register_29_q : 32'bz;  // Controlled_Buffer controlled_buffer_13
  Register #(.width(32), .trigger("rising"), .Select("low")) register_29 (
    .D(EX_BrachAddr), .en(W4), .Q(register_29_q), .clk(CLK));  // open: clr
  assign JumpAddr = L5 ? register_30_q : 32'bz;  // Controlled_Buffer controlled_buffer_14
  Register #(.width(32), .trigger("rising"), .Select("low")) register_30 (
    .D(EX_BrachAddr), .en(W5), .Q(register_30_q), .clk(CLK));  // open: clr
  Register #(.width(32), .trigger("rising"), .Select("low")) register_31 (
    .D(EX_BrachAddr), .en(W6), .Q(register_31_q), .clk(CLK));  // open: clr
  assign JumpAddr = L6 ? register_31_q : 32'bz;  // Controlled_Buffer controlled_buffer_15
  Register #(.width(32), .trigger("rising"), .Select("low")) register_32 (
    .D(EX_BrachAddr), .en(W7), .Q(register_32_q), .clk(CLK));  // open: clr
  assign JumpAddr = L7 ? register_32_q : 32'bz;  // Controlled_Buffer controlled_buffer_16
  \Max3_归并比较  \max3_归并比较_7  (
    .Y(\max3_归并比较_6_max ), .X(\max3_归并比较_5_max ), .Y_num(\max3_归并比较_6_max_num ),
    .X_num(\max3_归并比较_5_max_num ), .Max_num(change));  // open: MAX
  Demultiplexer #(.select(3), .width(1), .tristate("false"), .disabled("Z"), .enable("false")) demultiplexer_1 (
    .out0(W0), .out1(W1), .out2(W2), .out3(W3), .out4(W4), .out5(W5), .out6(W6), .out7(W7), .in(and_10_out),
    .sel(multiplexer_3_out));
  and and_10 (and_10_out, Miss, EX_Branch);
  Multiplexer #(.select(1), .width(3), .disabled("Z"), .enable("false")) multiplexer_3 (
    .in0(row), .in1(change), .out(multiplexer_3_out), .sel(full));

  // Other names for the same wires on the sheet: Blk[31:0] = EX_BrachAddr; SlotData[31:0] = JumpAddr
endmodule

// Max3
module \Max3_归并比较  (
  input  [15:0] Y,
  input  [15:0] X,
  input  [2:0] Y_num,
  input  [2:0] X_num,
  output [15:0] MAX,
  output [2:0] Max_num
);

  wire comparator_1_eq, comparator_1_gt, or_1_out;

  Multiplexer #(.select(1), .width(16), .disabled("Z"), .enable("false")) multiplexer_1 (
    .in0(Y), .in1(X), .out(MAX), .sel(or_1_out));
  Comparator #(.width(16), .mode("unsigned")) comparator_1 (
    .a(X), .b(Y), .gt(comparator_1_gt), .eq(comparator_1_eq));  // open: lt
  or or_1 (or_1_out, comparator_1_gt, comparator_1_eq);
  Multiplexer #(.select(1), .width(3), .disabled("Z"), .enable("false")) multiplexer_2 (
    .in0(Y_num), .in1(X_num), .out(Max_num), .sel(or_1_out));

  // Notes on the sheet:
  //   输出两个输入中的较大值，并输出较大值的3位编号
endmodule

// 预测
module \双位预测状态转换  (
  input  P1,
  input  P0,
  input  realJump,
  output S1,
  output S0
);

  wire and_1_out, and_2_out, and_3_out, and_4_out, not_1_out, not_2_out, not_3_out, not_4_out, not_5_out;

  not not_1 (not_1_out, P0);
  not not_2 (not_2_out, P1);
  not not_3 (not_3_out, P0);
  not not_4 (not_4_out, P0);
  not not_5 (not_5_out, realJump);
  and and_1 (and_1_out, P0, realJump);
  and and_2 (and_2_out, P1, not_1_out);
  and and_3 (and_3_out, not_2_out, not_3_out, realJump);
  and and_4 (and_4_out, P1, not_4_out, not_5_out);
  or or_1 (S1, and_1_out, and_2_out);
  or or_2 (S0, and_3_out, and_4_out);
endmodule

module \扫雷_小组任务  (
  output RegWrite,
  output MemWrite,
  output [31:0] PC,
  output [31:0] IR,
  output [31:0] RDin,
  output [31:0] MDin,
  output [31:0] LedData
);

  wire Alu_SRC, and_2_out, and_3_out, and_4_out, and_7_out, Beq, BLTZ, Bne, Branch, button_33_out, ch, CLK,
       clock_2_out, comparator_1_eq, comparator_1_lt, comparator_3_lt, comparator_5_eq, d_ff_1_q, d_ff_2_q,
       d_ff_3_q, Equal, ERET, Go, halt, IE_qn, INT, IR1, IR2, IR3, IR4, IR5, IR6, IR7, IR8, IR9, IR10, IR11,
       IR12, IR13, IR14, IR15, IR16, IR17, IR18, IR19, IR20, IR21, IR22, IR23, IR24, IR25, IR26, IR27, IR28,
       IR29, IR30, IR31, IR32, JAL, JMP, JR, LB, Ledin1, Ledin2, MemToReg, nand_1_out, not_1_out, not_2_out,
       not_3_out, not_4_out, or_1_out, SignedExt, SRAV, SysCall, W1, W2, W3, W4, W5, W6, W7, W8, W9, W10,
       W11, W12, W13, W14, W15, W16, W17, W18, W19, W20, W21, W22, W23, W24, W25, W26, W27, W28, W29, W30,
       W31, W32, \中断控制_32_1_有中断 , \单周期硬布线控制器_1_regdst ;
  wire [2:0] \rand ;
  wire [3:0] _1, _2, _3, _4, _5, _6, _7, _8, _9, _10, _11, _12, _13, _14, _15, _16, AluOP, bit_extender_1_out;
  wire [4:0] multiplexer_7_out, multiplexer_8_out, multiplexer_9_out, multiplexer_10_out, multiplexer_13_out,
       \中断控制_32_1_优先中断编号 ;
  wire [7:0] multiplexer_15_out, multiplexer_17_out, multiplexer_17_out_2, multiplexer_17_out_3,
       multiplexer_17_out_4;
  wire [12:0] CNT_num;
  wire [15:0] \总周期数 ;
  wire [31:0] adder_1_out, adder_2_out, bit_extender_2_out, bit_extender_3_out, bit_extender_4_out,
       demultiplexer_1_out0, demultiplexer_1_out1, EPC, IntPC, multiplexer_2_out, multiplexer_3_out,
       multiplexer_5_out, multiplexer_6_out, multiplexer_11_out, multiplexer_12_out, multiplexer_16_out,
       NextPC, ram_1_data, result, rs, shifter_1_out;

  Clock #(.highDuration(1), .lowDuration(1)) clock_1 ();  // open: out
  Button \u_继续运行  (.out(Go));
  D_Flip_Flop #(.trigger("high"), .Pre_Clr_Positions("LEGACY"), .NegatePresetClear("false"), .enable("true"), .NewFFLayout("false")) d_ff_1 (.Q(d_ff_1_q));  // open: clk, D, Qn, preset, en, reset
  Hex_Digit_Display hex_digit_display_1 (.value(_1));  // open: dp
  Button button_1 (.out(IR1));
  Hex_Digit_Display hex_digit_display_2 (.value(_5));  // open: dp
  Button button_2 (.out(IR5));
  Hex_Digit_Display hex_digit_display_3 (.value(_9));  // open: dp
  Button button_3 (.out(IR9));
  Hex_Digit_Display hex_digit_display_4 (.value(_13));  // open: dp
  Button button_4 (.out(IR13));
  // Probe on 13'h73
  Clock #(.highDuration(1), .lowDuration(1)) clock_2 (.out(clock_2_out));
  Button button_5 (.out(IR17));
  Button button_6 (.out(IR2));
  Button button_7 (.out(IR21));
  Button button_8 (.out(IR6));
  Button button_9 (.out(IR10));
  Button button_10 (.out(IR25));
  Button button_11 (.out(IR29));
  Button button_12 (.out(IR14));
  \中断控制_32  \u_中断控制_32_1  (
    .CLK(CLK), .IR1(IR1), .W1(W1), .\同步清零 (ERET), .IR2(IR2), .W2(W2), .IR3(IR3), .W3(W3), .IR4(IR4), .W4(W4),
    .IR5(IR5), .W5(W5), .IR6(IR6), .W6(W6), .IR7(IR7), .W7(W7), .IR8(IR8), .W8(W8), .IR9(IR9), .W9(W9),
    .IR10(IR10), .W10(W10), .IR11(IR11), .W11(W11), .IR12(IR12), .W12(W12), .IR13(IR13), .W13(W13),
    .IR14(IR14), .W14(W14), .IR15(IR15), .W15(W15), .IR16(IR16), .W16(W16), .IR17(IR17), .W17(W17),
    .IR18(IR18), .W18(W18), .IR19(IR19), .W19(W19), .IR20(IR20), .W20(W20), .IR21(IR21), .W21(W21),
    .IR22(IR22), .W22(W22), .IR23(IR23), .W23(W23), .IR24(IR24), .W24(W24), .IR25(IR25), .W25(W25),
    .IR26(IR26), .W26(W26), .IR27(IR27), .W27(W27), .IR28(IR28), .W28(W28), .IR29(IR29), .W29(W29),
    .IR30(IR30), .W30(W30), .IR31(IR31), .W31(W31), .IR32(IR32), .W32(W32), .\优先中断编号 (\中断控制_32_1_优先中断编号 ),
    .\有中断 (\中断控制_32_1_有中断 ), .\中断可接收 (INT));
  // Probe on NextPC
  // Probe on \总周期数 
  Comparator #(.width(13), .mode("twosComplement")) comparator_1 (
    .a(CNT_num), .b(13'h73), .eq(comparator_1_eq), .lt(comparator_1_lt));  // open: gt
  Hex_Digit_Display hex_digit_display_5 (.value(_2));  // open: dp
  Button button_13 (.out(IR18));
  Hex_Digit_Display hex_digit_display_6 (.value(_6));  // open: dp
  Button button_14 (.out(IR22));
  Hex_Digit_Display hex_digit_display_7 (.value(_10));  // open: dp
  Button button_15 (.out(IR26));
  Hex_Digit_Display hex_digit_display_8 (.value(_14));  // open: dp
  Button button_16 (.out(IR30));
  Register #(.width(32), .trigger("rising"), .Select("low")) u_EPC (
    .D(NextPC), .en(INT), .Q(EPC), .clk(CLK));  // open: clr
  // Probe on \总周期数 
  nand nand_1 (nand_1_out, d_ff_1_q, comparator_1_eq);
  Counter #(.width(13), .max('h1fff), .ongoal("stay"), .trigger("rising"), .behavior("old")) counter_1 (
    .count(comparator_1_lt), .Q(CNT_num), .clk(clock_2_out));  // open: load, D, carry, clr, preset
  Hex_Digit_Display hex_digit_display_9 (.value(_3));  // open: dp
  Button button_17 (.out(IR3));
  Button button_18 (.out(IR19));
  Hex_Digit_Display hex_digit_display_10 (.value(_7));  // open: dp
  Button button_19 (.out(IR23));
  Button button_20 (.out(IR7));
  Hex_Digit_Display hex_digit_display_11 (.value(_11));  // open: dp
  Button button_21 (.out(IR11));
  Button button_22 (.out(IR27));
  Hex_Digit_Display hex_digit_display_12 (.value(_15));  // open: dp
  Button button_23 (.out(IR15));
  Button button_24 (.out(IR31));
  D_Flip_Flop #(.trigger("rising"), .Pre_Clr_Positions("LEGACY"), .NegatePresetClear("false"), .enable("true"), .NewFFLayout("false")) d_ff_2 (
    .clk(CLK), .D(INT), .Q(d_ff_2_q));  // open: Qn, preset, en, reset
  D_Flip_Flop #(.trigger("rising"), .Pre_Clr_Positions("LEGACY"), .NegatePresetClear("false"), .enable("true"), .NewFFLayout("false")) d_ff_3 (
    .clk(CLK), .D(ERET), .Q(d_ff_3_q));  // open: Qn, preset, en, reset
  // Probe on EPC
  assign CLK = nand_1_out ? clock_2_out : 1'bz;  // Controlled_Buffer controlled_buffer_1
  Pull_Resistor #(.pull(1)) pull_resistor_1 (.node(CLK));
  Hex_Digit_Display hex_digit_display_13 (.value(_4));  // open: dp
  Button button_25 (.out(IR20));
  Button button_26 (.out(IR4));
  Hex_Digit_Display hex_digit_display_14 (.value(_8));  // open: dp
  Button button_27 (.out(IR24));
  Button button_28 (.out(IR8));
  Hex_Digit_Display hex_digit_display_15 (.value(_12));  // open: dp
  Button button_29 (.out(IR12));
  Button button_30 (.out(IR28));
  Hex_Digit_Display hex_digit_display_16 (.value(_16));  // open: dp
  Button button_31 (.out(IR16));
  Button button_32 (.out(IR32));
  Multiplexer #(.select(5), .width(32), .disabled("Z"), .enable("false")) multiplexer_1 (
    .in0(32'h36a4), .in1(32'h36dc), .in2(32'h3714), .in3(32'h374c), .in4(32'h3784), .in5(32'h37bc),
    .in6(32'h37f4), .in7(32'h382c), .in8(32'h3864), .in9(32'h389c), .in10(32'h38d4), .in11(32'h390c),
    .in12(32'h3944), .in13(32'h397c), .in14(32'h39b4), .in15(32'h39ec), .in16(32'h3a24), .in17(32'h3a40),
    .in18(32'h3a5c), .in19(32'h3a78), .in20(32'h3a94), .in21(32'h3ab0), .in22(32'h3acc), .in23(32'h3ae8),
    .in24(32'h3b04), .in25(32'h3b20), .in26(32'h3b3c), .in27(32'h3b58), .in28(32'h3b74), .in29(32'h3b90),
    .in30(32'h3bac), .in31(32'h3bc8), .out(IntPC), .sel(\中断控制_32_1_优先中断编号 ));
  D_Flip_Flop #(.trigger("rising"), .Pre_Clr_Positions("LEGACY"), .NegatePresetClear("false"), .enable("true"), .NewFFLayout("false")) IE (
    .Qn(IE_qn), .preset(d_ff_2_q), .reset(d_ff_3_q));  // open: clk, D, Q, en
  LED #(.active("true")) led_1 (.in(W1));
  LED #(.active("true")) led_2 (.in(W17));
  LED #(.active("true")) led_3 (.in(W21));
  LED #(.active("true")) led_4 (.in(W5));
  LED #(.active("true")) led_5 (.in(W9));
  LED #(.active("true")) led_6 (.in(W25));
  LED #(.active("true")) led_7 (.in(W13));
  LED #(.active("true")) led_8 (.in(W29));
  and and_1 (INT, \中断控制_32_1_有中断 , IE_qn);
  Comparator #(.width(32), .mode("twosComplement")) comparator_2 (.a(IR), .b(32'h42000018), .eq(ERET));  // open: gt, lt
  LED #(.active("true")) led_9 (.in(W2));
  LED #(.active("true")) led_10 (.in(W3));
  LED #(.active("true")) led_11 (.in(W18));
  LED #(.active("true")) led_12 (.in(W22));
  LED #(.active("true")) led_13 (.in(W6));
  LED #(.active("true")) led_14 (.in(W7));
  LED #(.active("true")) led_15 (.in(W26));
  LED #(.active("true")) led_16 (.in(W10));
  LED #(.active("true")) led_17 (.in(W11));
  LED #(.active("true")) led_18 (.in(W14));
  LED #(.active("true")) led_19 (.in(W30));
  LED #(.active("true")) led_20 (.in(W15));
  LED #(.active("true")) led_21 (.in(W4));
  LED #(.active("true")) led_22 (.in(W20));
  LED #(.active("true")) led_23 (.in(W19));
  LED #(.active("true")) led_24 (.in(W8));
  LED #(.active("true")) led_25 (.in(W24));
  LED #(.active("true")) led_26 (.in(W23));
  LED #(.active("true")) led_27 (.in(W12));
  LED #(.active("true")) led_28 (.in(W27));
  LED #(.active("true")) led_29 (.in(W28));
  LED #(.active("true")) led_30 (.in(W16));
  LED #(.active("true")) led_31 (.in(W32));
  LED #(.active("true")) led_32 (.in(W31));
  Multiplexer #(.select(1), .width(32), .disabled("Z"), .enable("false")) multiplexer_2 (
    .in0(adder_1_out), .in1(adder_2_out), .out(multiplexer_2_out), .sel(Branch));
  Multiplexer #(.select(1), .width(32), .disabled("Z"), .enable("false")) multiplexer_3 (
    .in0(multiplexer_2_out), .in1({4'b0000, IR[25:0], 2'b00}), .out(multiplexer_3_out), .sel(JMP));
  Multiplexer #(.select(1), .width(32), .disabled("Z"), .enable("false")) multiplexer_4 (
    .in0(multiplexer_3_out), .in1(rs), .out(NextPC), .sel(JR));
  Counter #(.width(16), .max('hffff), .ongoal("stay"), .trigger("rising"), .behavior("old")) counter_2 (
    .count(not_1_out), .Q(\总周期数 ), .clk(CLK));  // open: load, D, carry, clr, preset
  not not_1 (not_1_out, halt);
  Multiplexer #(.select(1), .width(32), .disabled("Z"), .enable("false")) multiplexer_5 (
    .in0(NextPC), .in1(IntPC), .out(multiplexer_5_out), .sel(INT));
  Button button_33 (.out(button_33_out));
  // Probe on multiplexer_6_out
  Multiplexer #(.select(1), .width(32), .disabled("Z"), .enable("false")) multiplexer_6 (
    .in0(multiplexer_5_out), .in1(EPC), .out(multiplexer_6_out), .sel(ERET));
  Random #(.width(3), .seed(0), .trigger("rising")) random_1 (.clk(button_33_out), .out(\rand ));  // open: next, clr
  Register #(.width(32), .trigger("rising"), .Select("low")) u_PC (
    .D(multiplexer_6_out), .en(not_2_out), .Q(PC), .clk(CLK));  // open: clr
  not not_2 (not_2_out, halt);
  assign bit_extender_1_out = {{1{1'b0}}, \rand };  // Bit_Extender bit_extender_1
  // Probe on PC
  Hex_Digit_Display hex_digit_display_17 (.value(bit_extender_1_out));  // open: dp
  // Probe on IR
  // Mips_Probe mips_probe_1: pin names not known; wires that end beside it: IR, IR[20:16]
  \指令存储器封装  \u_指令存储器封装_1  (.in_1(\rand ), .in_2(PC[11:2]), .out_3(IR));
  Adder #(.width(32)) adder_1 (.a(PC), .b(32'h4), .out(adder_1_out));  // open: cin, cout
  \单周期硬布线控制器  \u_单周期硬布线控制器_1  (
    .Func(IR[5:0]), .OP(IR[31:26]), .ALU_OP(AluOP), .MemToReg(MemToReg), .MemWrite(MemWrite),
    .ALU_SRC(Alu_SRC), .RegWrite(RegWrite), .SysCALL(SysCall), .SignedExt(SignedExt),
    .RegDst(\单周期硬布线控制器_1_regdst ), .JR(JR), .JMP(JMP), .Beq(Beq), .JAL(JAL), .Bne(Bne), .SRAV(SRAV), .LB(LB),
    .BLTZ(BLTZ));
  Multiplexer #(.select(1), .width(5), .disabled("Z"), .enable("false")) multiplexer_7 (
    .in0(IR[25:21]), .in1(5'b00010), .out(multiplexer_7_out), .sel(SysCall));
  Multiplexer #(.select(1), .width(5), .disabled("Z"), .enable("false")) multiplexer_8 (
    .in0(IR[20:16]), .in1(5'b00100), .out(multiplexer_8_out), .sel(SysCall));
  Multiplexer #(.select(1), .width(5), .disabled("Z"), .enable("false")) multiplexer_9 (
    .in0(IR[20:16]), .in1(IR[15:11]), .out(multiplexer_9_out), .sel(\单周期硬布线控制器_1_regdst ));
  assign bit_extender_2_out = {{16{1'b0}}, IR[15:0]};  // Bit_Extender bit_extender_2
  assign bit_extender_3_out = {{16{IR[15]}}, IR[15:0]};  // Bit_Extender bit_extender_3
  // Probe on RDin
  // Probe on multiplexer_7_out
  // Probe on multiplexer_8_out
  // Probe on multiplexer_10_out
  Multiplexer #(.select(1), .width(5), .disabled("Z"), .enable("false")) multiplexer_10 (
    .in0(multiplexer_9_out), .in1({5{1'b1}}), .out(multiplexer_10_out), .sel(JAL));
  MIPS_Regifile mips_regifile_1 (
    .Din(RDin), .Clk(CLK), .R1(rs), .R2(MDin), .WE(RegWrite), .W_num(multiplexer_10_out),
    .R1_num(multiplexer_7_out), .R2_num(multiplexer_8_out));
  Multiplexer #(.select(1), .width(32), .disabled("Z"), .enable("false")) multiplexer_11 (
    .in0(bit_extender_2_out), .in1(bit_extender_3_out), .out(multiplexer_11_out), .sel(SignedExt));
  Shifter #(.width(32), .shift("ll")) shifter_1 (.in(bit_extender_3_out), .\dist (5'b00010), .out(shifter_1_out));
  Adder #(.width(32)) adder_2 (.a(shifter_1_out), .b(adder_1_out), .out(adder_2_out));  // open: cin, cout
  Multiplexer #(.select(1), .width(32), .disabled("Z"), .enable("false")) multiplexer_12 (
    .in0(MDin), .in1(multiplexer_11_out), .out(multiplexer_12_out), .sel(Alu_SRC));
  Comparator #(.width(32), .mode("twosComplement")) comparator_3 (
    .a(rs), .b({32{1'b0}}), .lt(comparator_3_lt));  // open: gt, eq
  Multiplexer #(.select(1), .width(5), .disabled("Z"), .enable("false")) multiplexer_13 (
    .in0(IR[10:6]), .in1(rs[4:0]), .out(multiplexer_13_out), .sel(SRAV));
  Multiplexer #(.select(1), .width(32), .disabled("Z"), .enable("false")) multiplexer_14 (
    .in0({multiplexer_17_out_4, multiplexer_17_out_3, multiplexer_17_out_2, multiplexer_17_out}),
    .in1(bit_extender_4_out), .out(RDin), .sel(LB));
  not not_3 (not_3_out, Equal);
  Comparator #(.width(32), .mode("twosComplement")) comparator_4 (.a(32'h23), .b(rs), .eq(ch));  // open: gt, lt
  Comparator #(.width(32), .mode("twosComplement")) comparator_5 (
    .a(32'h22), .b(rs), .eq(comparator_5_eq));  // open: gt, lt
  // Probe on result
  MIPS_ALU mips_alu_1 (
    .X(rs), .Y(multiplexer_12_out), .AluOP(AluOP), .Equal(Equal), .Result(result), .shamt(multiplexer_13_out));  // open: Result_2
  Demultiplexer #(.select(1), .width(32), .tristate("false"), .disabled("Z"), .enable("false")) demultiplexer_1 (
    .out0(demultiplexer_1_out0), .out1(demultiplexer_1_out1), .in(MDin), .sel(ch));
  and and_2 (and_2_out, BLTZ, comparator_3_lt);
  and and_3 (and_3_out, Equal, Beq);
  and and_4 (and_4_out, not_3_out, Bne);
  or or_1 (or_1_out, ch, comparator_5_eq);
  not not_4 (not_4_out, or_1_out);
  and and_5 (Ledin1, SysCall, comparator_5_eq);
  Register #(.width(32), .trigger("rising"), .Select("low")) Data2 (
    .D(demultiplexer_1_out1), .en(Ledin2), .Q({_16, _15, _14, _13, _12, _11, _10, _9}), .clk(CLK));  // open: clr
  or or_2 (Branch, and_2_out, and_3_out, and_4_out);
  and and_6 (Ledin2, ch, SysCall);
  and and_7 (and_7_out, SysCall, not_4_out);
  Register #(.width(32), .trigger("rising"), .Select("low")) Data1 (
    .D(demultiplexer_1_out0), .en(Ledin1), .Q({_8, _7, _6, _5, _4, _3, _2, _1}), .clk(CLK));  // open: clr
  Multiplexer #(.select(2), .width(8), .disabled("Z"), .enable("false")) multiplexer_15 (
    .in0(multiplexer_17_out), .in1(multiplexer_17_out_2), .in2(multiplexer_17_out_3),
    .in3(multiplexer_17_out_4), .out(multiplexer_15_out), .sel(result[1:0]));
  assign bit_extender_4_out = {{24{multiplexer_15_out[7]}}, multiplexer_15_out};  // Bit_Extender bit_extender_4
  Register #(.width(1), .trigger("rising"), .Select("low")) register_1 (
    .D(SysCall), .en(and_7_out), .Q(halt), .clk(CLK), .clr(Go));
  RAM #(.addrWidth(10), .dataWidth(32), .bus("separate"), .Select("high")) ram_1 (
    .addr(result[11:2]), .din(MDin), .data(ram_1_data), .str(MemWrite), .clk(CLK), .ld(1'b1));  // open: sel, clr
  Multiplexer #(.select(1), .width(32), .disabled("Z"), .enable("false")) multiplexer_16 (
    .in0(result), .in1(ram_1_data), .out(multiplexer_16_out), .sel(MemToReg));
  Multiplexer #(.select(1), .width(32), .disabled("Z"), .enable("false")) multiplexer_17 (
    .in0(multiplexer_16_out), .in1(adder_1_out),
    .out({multiplexer_17_out_4, multiplexer_17_out_3, multiplexer_17_out_2, multiplexer_17_out}), .sel(JAL));

  // Other names for the same wires on the sheet: LedData1[31:0] = {_8, _7, _6, _5, _4, _3, _2, _1};
  //   LedData2[31:0] = {_16, _15, _14, _13, _12, _11, _10, _9}

  // Notes on the sheet:
  //   控制位
  //   暂停节拍，不能为0
  //   可计数暂停的时钟源
  //   请点击下面的按钮生成随机地图，当选定随机数后，地图自动生成，就可以加入时钟运行游戏了，冲！
  //   指令字
  //   OP
  //   Func
  //   rs
  //   rt
  //   rd
  //   RegDst
endmodule

// 中断控制
module \中断控制_32  (
  input  CLK,
  input  IR1,
  input  \同步清零 ,
  input  IR2,
  input  \中断可接收 ,
  input  IR3,
  input  IR4,
  input  IR5,
  input  IR6,
  input  IR7,
  input  IR8,
  input  IR9,
  input  IR10,
  input  IR11,
  input  IR12,
  input  IR13,
  input  IR14,
  input  IR15,
  input  IR16,
  input  IR17,
  input  IR18,
  input  IR19,
  input  IR20,
  input  IR21,
  input  IR22,
  input  IR23,
  input  IR24,
  input  IR25,
  input  IR26,
  input  IR27,
  input  IR28,
  input  IR29,
  input  IR30,
  input  IR31,
  input  IR32,
  output [4:0] \优先中断编号 ,
  output W1,
  output \有中断 ,
  output W2,
  output W3,
  output W4,
  output W5,
  output W6,
  output W7,
  output W8,
  output W9,
  output W10,
  output W11,
  output W12,
  output W13,
  output W14,
  output W15,
  output W16,
  output W17,
  output W18,
  output W19,
  output W20,
  output W21,
  output W22,
  output W23,
  output W24,
  output W25,
  output W26,
  output W27,
  output W28,
  output W29,
  output W30,
  output W31,
  output W32
);

  wire and_1_out, and_2_out, and_3_out, and_4_out, and_5_out, and_6_out, and_7_out, and_8_out, and_9_out,
       and_10_out, and_11_out, and_12_out, and_13_out, and_14_out, and_15_out, and_16_out, and_17_out,
       and_18_out, and_19_out, and_20_out, and_21_out, and_22_out, and_23_out, and_24_out, and_25_out,
       and_26_out, and_27_out, and_28_out, and_29_out, and_30_out, and_31_out, and_32_out, Clr1, Clr2, Clr3,
       Clr4, Clr5, Clr6, Clr7, Clr8, Clr9, Clr10, Clr11, Clr12, Clr13, Clr14, Clr15, Clr16, Clr17, Clr18,
       Clr19, Clr20, Clr21, Clr22, Clr23, Clr24, Clr25, Clr26, Clr27, Clr28, Clr29, Clr30, Clr31, Clr32,
       d_ff_1_q, d_ff_2_q, d_ff_3_q, d_ff_4_q, d_ff_5_q, d_ff_6_q, d_ff_7_q, d_ff_8_q, d_ff_9_q, d_ff_10_q,
       d_ff_11_q, d_ff_12_q, d_ff_13_q, d_ff_14_q, d_ff_15_q, d_ff_16_q, d_ff_17_q, d_ff_18_q, d_ff_19_q,
       d_ff_20_q, d_ff_21_q, d_ff_22_q, d_ff_23_q, d_ff_24_q, d_ff_25_q, d_ff_26_q, d_ff_27_q, d_ff_28_q,
       d_ff_29_q, d_ff_30_q, d_ff_31_q, d_ff_32_q, IR1_q, IR2_q, IR3_q, IR4_q, IR5_q, IR6_q, IR7_q, IR8_q,
       IR9_q, IR10_q, IR11_q, IR12_q, IR13_q, IR14_q, IR15_q, IR16_q, IR17_q, IR18_q, IR19_q, IR20_q, IR21_q,
       IR22_q, IR23_q, IR24_q, IR25_q, IR26_q, IR27_q, IR28_q, IR29_q, IR30_q, IR31_q, IR32_q, or_33_out,
       or_34_out, or_35_out, or_36_out, or_37_out, or_38_out, or_39_out, or_40_out, or_41_out, or_42_out,
       or_43_out, or_44_out, or_45_out, or_46_out, or_47_out, or_48_out, or_49_out, or_50_out, or_51_out,
       or_52_out, or_53_out, or_54_out, or_55_out, or_56_out, or_57_out, or_58_out, or_59_out, or_60_out,
       or_61_out, or_62_out, or_63_out, or_64_out;
  wire [4:0] INT_q;

  D_Flip_Flop #(.trigger("rising"), .Pre_Clr_Positions("LEGACY"), .NegatePresetClear("false"), .enable("true"), .NewFFLayout("false")) d_ff_1 (
    .clk(IR1), .D(1'b1), .Q(d_ff_1_q), .reset(IR1_q));  // open: Qn, preset, en
  or or_1 (W1, IR1_q, d_ff_1_q);
  D_Flip_Flop #(.trigger("rising"), .Pre_Clr_Positions("LEGACY"), .NegatePresetClear("false"), .enable("true"), .NewFFLayout("false")) d_ff_2 (
    .clk(IR2), .D(1'b1), .Q(d_ff_2_q), .reset(IR2_q));  // open: Qn, preset, en
  or or_2 (W2, IR2_q, d_ff_2_q);
  D_Flip_Flop #(.trigger("rising"), .Pre_Clr_Positions("LEGACY"), .NegatePresetClear("false"), .enable("true"), .NewFFLayout("false")) d_ff_3 (
    .clk(IR3), .D(1'b1), .Q(d_ff_3_q), .reset(IR3_q));  // open: Qn, preset, en
  or or_3 (W3, IR3_q, d_ff_3_q);
  D_Flip_Flop #(.trigger("rising"), .Pre_Clr_Positions("LEGACY"), .NegatePresetClear("false"), .enable("true"), .NewFFLayout("false")) d_ff_4 (
    .clk(IR4), .D(1'b1), .Q(d_ff_4_q), .reset(IR4_q));  // open: Qn, preset, en
  or or_4 (W4, IR4_q, d_ff_4_q);
  D_Flip_Flop #(.trigger("rising"), .Pre_Clr_Positions("LEGACY"), .NegatePresetClear("false"), .enable("true"), .NewFFLayout("false")) d_ff_5 (
    .clk(IR5), .D(1'b1), .Q(d_ff_5_q), .reset(IR5_q));  // open: Qn, preset, en
  or or_5 (W5, IR5_q, d_ff_5_q);
  D_Flip_Flop #(.trigger("rising"), .Pre_Clr_Positions("LEGACY"), .NegatePresetClear("false"), .enable("true"), .NewFFLayout("false")) d_ff_6 (
    .clk(IR6), .D(1'b1), .Q(d_ff_6_q), .reset(IR6_q));  // open: Qn, preset, en
  or or_6 (W6, IR6_q, d_ff_6_q);
  D_Flip_Flop #(.trigger("rising"), .Pre_Clr_Positions("LEGACY"), .NegatePresetClear("false"), .enable("true"), .NewFFLayout("false")) d_ff_7 (
    .clk(IR7), .D(1'b1), .Q(d_ff_7_q), .reset(IR7_q));  // open: Qn, preset, en
  or or_7 (W7, IR7_q, d_ff_7_q);
  D_Flip_Flop #(.trigger("rising"), .Pre_Clr_Positions("LEGACY"), .NegatePresetClear("false"), .enable("true"), .NewFFLayout("false")) d_ff_8 (
    .clk(IR8), .D(1'b1), .Q(d_ff_8_q), .reset(IR8_q));  // open: Qn, preset, en
  or or_8 (W8, IR8_q, d_ff_8_q);
  D_Flip_Flop #(.trigger("rising"), .Pre_Clr_Positions("LEGACY"), .NegatePresetClear("false"), .enable("true"), .NewFFLayout("false")) d_ff_9 (
    .clk(IR9), .D(1'b1), .Q(d_ff_9_q), .reset(IR9_q));  // open: Qn, preset, en
  or or_9 (W9, IR9_q, d_ff_9_q);
  D_Flip_Flop #(.trigger("rising"), .Pre_Clr_Positions("LEGACY"), .NegatePresetClear("false"), .enable("true"), .NewFFLayout("false")) d_ff_10 (
    .clk(IR10), .D(1'b1), .Q(d_ff_10_q), .reset(IR10_q));  // open: Qn, preset, en
  or or_10 (W10, IR10_q, d_ff_10_q);
  D_Flip_Flop #(.trigger("rising"), .Pre_Clr_Positions("LEGACY"), .NegatePresetClear("false"), .enable("true"), .NewFFLayout("false")) d_ff_11 (
    .clk(IR11), .D(1'b1), .Q(d_ff_11_q), .reset(IR11_q));  // open: Qn, preset, en
  or or_11 (W11, IR11_q, d_ff_11_q);
  D_Flip_Flop #(.trigger("rising"), .Pre_Clr_Positions("LEGACY"), .NegatePresetClear("false"), .enable("true"), .NewFFLayout("false")) d_ff_12 (
    .clk(IR12), .D(1'b1), .Q(d_ff_12_q), .reset(IR12_q));  // open: Qn, preset, en
  or or_12 (W12, IR12_q, d_ff_12_q);
  D_Flip_Flop #(.trigger("rising"), .Pre_Clr_Positions("LEGACY"), .NegatePresetClear("false"), .enable("true"), .NewFFLayout("false")) d_ff_13 (
    .clk(IR13), .D(1'b1), .Q(d_ff_13_q), .reset(IR13_q));  // open: Qn, preset, en
  or or_13 (W13, IR13_q, d_ff_13_q);
  D_Flip_Flop #(.trigger("rising"), .Pre_Clr_Positions("LEGACY"), .NegatePresetClear("false"), .enable("true"), .NewFFLayout("false")) d_ff_14 (
    .clk(IR14), .D(1'b1), .Q(d_ff_14_q), .reset(IR14_q));  // open: Qn, preset, en
  or or_14 (W14, IR14_q, d_ff_14_q);
  D_Flip_Flop #(.trigger("rising"), .Pre_Clr_Positions("LEGACY"), .NegatePresetClear("false"), .enable("true"), .NewFFLayout("false")) d_ff_15 (
    .clk(IR15), .D(1'b1), .Q(d_ff_15_q), .reset(IR15_q));  // open: Qn, preset, en
  or or_15 (W15, IR15_q, d_ff_15_q);
  D_Flip_Flop #(.trigger("rising"), .Pre_Clr_Positions("LEGACY"), .NegatePresetClear("false"), .enable("true"), .NewFFLayout("false")) d_ff_16 (
    .clk(IR16), .D(1'b1), .Q(d_ff_16_q), .reset(IR16_q));  // open: Qn, preset, en
  or or_16 (W16, IR16_q, d_ff_16_q);
  D_Flip_Flop #(.trigger("rising"), .Pre_Clr_Positions("LEGACY"), .NegatePresetClear("false"), .enable("true"), .NewFFLayout("false")) d_ff_17 (
    .clk(IR17), .D(1'b1), .Q(d_ff_17_q), .reset(IR17_q));  // open: Qn, preset, en
  or or_17 (W17, IR17_q, d_ff_17_q);
  D_Flip_Flop #(.trigger("rising"), .Pre_Clr_Positions("LEGACY"), .NegatePresetClear("false"), .enable("true"), .NewFFLayout("false")) d_ff_18 (
    .clk(IR18), .D(1'b1), .Q(d_ff_18_q), .reset(IR18_q));  // open: Qn, preset, en
  or or_18 (W18, IR18_q, d_ff_18_q);
  D_Flip_Flop #(.trigger("rising"), .Pre_Clr_Positions("LEGACY"), .NegatePresetClear("false"), .enable("true"), .NewFFLayout("false")) d_ff_19 (
    .clk(IR19), .D(1'b1), .Q(d_ff_19_q), .reset(IR19_q));  // open: Qn, preset, en
  or or_19 (W19, IR19_q, d_ff_19_q);
  D_Flip_Flop #(.trigger("rising"), .Pre_Clr_Positions("LEGACY"), .NegatePresetClear("false"), .enable("true"), .NewFFLayout("false")) d_ff_20 (
    .clk(IR20), .D(1'b1), .Q(d_ff_20_q), .reset(IR20_q));  // open: Qn, preset, en
  or or_20 (W20, IR20_q, d_ff_20_q);
  D_Flip_Flop #(.trigger("rising"), .Pre_Clr_Positions("LEGACY"), .NegatePresetClear("false"), .enable("true"), .NewFFLayout("false")) d_ff_21 (
    .clk(IR21), .D(1'b1), .Q(d_ff_21_q), .reset(IR21_q));  // open: Qn, preset, en
  or or_21 (W21, IR21_q, d_ff_21_q);
  D_Flip_Flop #(.trigger("rising"), .Pre_Clr_Positions("LEGACY"), .NegatePresetClear("false"), .enable("true"), .NewFFLayout("false")) d_ff_22 (
    .clk(IR22), .D(1'b1), .Q(d_ff_22_q), .reset(IR22_q));  // open: Qn, preset, en
  or or_22 (W22, IR22_q, d_ff_22_q);
  D_Flip_Flop #(.trigger("rising"), .Pre_Clr_Positions("LEGACY"), .NegatePresetClear("false"), .enable("true"), .NewFFLayout("false")) d_ff_23 (
    .clk(IR23), .D(1'b1), .Q(d_ff_23_q), .reset(IR23_q));  // open: Qn, preset, en
  or or_23 (W23, IR23_q, d_ff_23_q);
  D_Flip_Flop #(.trigger("rising"), .Pre_Clr_Positions("LEGACY"), .NegatePresetClear("false"), .enable("true"), .NewFFLayout("false")) d_ff_24 (
    .clk(IR24), .D(1'b1), .Q(d_ff_24_q), .reset(IR24_q));  // open: Qn, preset, en
  or or_24 (W24, IR24_q, d_ff_24_q);
  D_Flip_Flop #(.trigger("rising"), .Pre_Clr_Positions("LEGACY"), .NegatePresetClear("false"), .enable("true"), .NewFFLayout("false")) d_ff_25 (
    .clk(IR25), .D(1'b1), .Q(d_ff_25_q), .reset(IR25_q));  // open: Qn, preset, en
  or or_25 (W25, IR25_q, d_ff_25_q);
  D_Flip_Flop #(.trigger("rising"), .Pre_Clr_Positions("LEGACY"), .NegatePresetClear("false"), .enable("true"), .NewFFLayout("false")) d_ff_26 (
    .clk(IR26), .D(1'b1), .Q(d_ff_26_q), .reset(IR26_q));  // open: Qn, preset, en
  or or_26 (W26, IR26_q, d_ff_26_q);
  D_Flip_Flop #(.trigger("rising"), .Pre_Clr_Positions("LEGACY"), .NegatePresetClear("false"), .enable("true"), .NewFFLayout("false")) d_ff_27 (
    .clk(IR27), .D(1'b1), .Q(d_ff_27_q), .reset(IR27_q));  // open: Qn, preset, en
  or or_27 (W27, IR27_q, d_ff_27_q);
  D_Flip_Flop #(.trigger("rising"), .Pre_Clr_Positions("LEGACY"), .NegatePresetClear("false"), .enable("true"), .NewFFLayout("false")) d_ff_28 (
    .clk(IR28), .D(1'b1), .Q(d_ff_28_q), .reset(IR28_q));  // open: Qn, preset, en
  or or_28 (W28, IR28_q, d_ff_28_q);
  D_Flip_Flop #(.trigger("rising"), .Pre_Clr_Positions("LEGACY"), .NegatePresetClear("false"), .enable("true"), .NewFFLayout("false")) d_ff_29 (
    .clk(IR29), .D(1'b1), .Q(d_ff_29_q), .reset(IR29_q));  // open: Qn, preset, en
  or or_29 (W29, IR29_q, d_ff_29_q);
  D_Flip_Flop #(.trigger("rising"), .Pre_Clr_Positions("LEGACY"), .NegatePresetClear("false"), .enable("true"), .NewFFLayout("false")) d_ff_30 (
    .clk(IR30), .D(1'b1), .Q(d_ff_30_q), .reset(IR30_q));  // open: Qn, preset, en
  or or_30 (W30, IR30_q, d_ff_30_q);
  D_Flip_Flop #(.trigger("rising"), .Pre_Clr_Positions("LEGACY"), .NegatePresetClear("false"), .enable("true"), .NewFFLayout("false")) d_ff_31 (
    .clk(IR31), .D(1'b1), .Q(d_ff_31_q), .reset(IR31_q));  // open: Qn, preset, en
  or or_31 (W31, IR31_q, d_ff_31_q);
  D_Flip_Flop #(.trigger("rising"), .Pre_Clr_Positions("LEGACY"), .NegatePresetClear("false"), .enable("true"), .NewFFLayout("false")) d_ff_32 (
    .clk(IR32), .D(1'b1), .Q(d_ff_32_q), .reset(IR32_q));  // open: Qn, preset, en
  or or_32 (W32, IR32_q, d_ff_32_q);
  or or_33 (or_33_out, d_ff_1_q, IR1_q);
  or or_34 (or_34_out, d_ff_2_q, IR2_q);
  or or_35 (or_35_out, d_ff_3_q, IR3_q);
  or or_36 (or_36_out, d_ff_4_q, IR4_q);
  or or_37 (or_37_out, d_ff_5_q, IR5_q);
  or or_38 (or_38_out, d_ff_6_q, IR6_q);
  or or_39 (or_39_out, d_ff_7_q, IR7_q);
  or or_40 (or_40_out, d_ff_8_q, IR8_q);
  or or_41 (or_41_out, d_ff_9_q, IR9_q);
  or or_42 (or_42_out, d_ff_10_q, IR10_q);
  or or_43 (or_43_out, d_ff_11_q, IR11_q);
  or or_44 (or_44_out, d_ff_12_q, IR12_q);
  or or_45 (or_45_out, d_ff_13_q, IR13_q);
  or or_46 (or_46_out, d_ff_14_q, IR14_q);
  or or_47 (or_47_out, d_ff_15_q, IR15_q);
  or or_48 (or_48_out, d_ff_16_q, IR16_q);
  or or_49 (or_49_out, d_ff_17_q, IR17_q);
  or or_50 (or_50_out, d_ff_18_q, IR18_q);
  or or_51 (or_51_out, d_ff_19_q, IR19_q);
  or or_52 (or_52_out, d_ff_20_q, IR20_q);
  or or_53 (or_53_out, d_ff_21_q, IR21_q);
  or or_54 (or_54_out, d_ff_22_q, IR22_q);
  or or_55 (or_55_out, d_ff_23_q, IR23_q);
  or or_56 (or_56_out, d_ff_24_q, IR24_q);
  or or_57 (or_57_out, d_ff_25_q, IR25_q);
  or or_58 (or_58_out, d_ff_26_q, IR26_q);
  or or_59 (or_59_out, d_ff_27_q, IR27_q);
  or or_60 (or_60_out, d_ff_28_q, IR28_q);
  or or_61 (or_61_out, d_ff_29_q, IR29_q);
  or or_62 (or_62_out, d_ff_30_q, IR30_q);
  or or_63 (or_63_out, d_ff_31_q, IR31_q);
  or or_64 (or_64_out, d_ff_32_q, IR32_q);
  and and_1 (and_1_out, or_33_out, ~Clr1);  // AND_Gate
  and and_2 (and_2_out, or_34_out, ~Clr2);  // AND_Gate
  and and_3 (and_3_out, or_35_out, ~Clr3);  // AND_Gate
  and and_4 (and_4_out, or_36_out, ~Clr4);  // AND_Gate
  and and_5 (and_5_out, or_37_out, ~Clr5);  // AND_Gate
  and and_6 (and_6_out, or_38_out, ~Clr6);  // AND_Gate
  and and_7 (and_7_out, or_39_out, ~Clr7);  // AND_Gate
  and and_8 (and_8_out, or_40_out, ~Clr8);  // AND_Gate
  and and_9 (and_9_out, or_41_out, ~Clr9);  // AND_Gate
  and and_10 (and_10_out, or_42_out, ~Clr10);  // AND_Gate
  and and_11 (and_11_out, or_43_out, ~Clr11);  // AND_Gate
  and and_12 (and_12_out, or_44_out, ~Clr12);  // AND_Gate
  and and_13 (and_13_out, or_45_out, ~Clr13);  // AND_Gate
  and and_14 (and_14_out, or_46_out, ~Clr14);  // AND_Gate
  and and_15 (and_15_out, or_47_out, ~Clr15);  // AND_Gate
  and and_16 (and_16_out, or_48_out, ~Clr16);  // AND_Gate
  and and_17 (and_17_out, or_49_out, ~Clr17);  // AND_Gate
  and and_18 (and_18_out, or_50_out, ~Clr18);  // AND_Gate
  and and_19 (and_19_out, or_51_out, ~Clr19);  // AND_Gate
  and and_20 (and_20_out, or_52_out, ~Clr20);  // AND_Gate
  and and_21 (and_21_out, or_53_out, ~Clr21);  // AND_Gate
  and and_22 (and_22_out, or_54_out, ~Clr22);  // AND_Gate
  and and_23 (and_23_out, or_55_out, ~Clr23);  // AND_Gate
  and and_24 (and_24_out, or_56_out, ~Clr24);  // AND_Gate
  and and_25 (and_25_out, or_57_out, ~Clr25);  // AND_Gate
  and and_26 (and_26_out, or_58_out, ~Clr26);  // AND_Gate
  and and_27 (and_27_out, or_59_out, ~Clr27);  // AND_Gate
  and and_28 (and_28_out, or_60_out, ~Clr28);  // AND_Gate
  and and_29 (and_29_out, or_61_out, ~Clr29);  // AND_Gate
  and and_30 (and_30_out, or_62_out, ~Clr30);  // AND_Gate
  and and_31 (and_31_out, or_63_out, ~Clr31);  // AND_Gate
  and and_32 (and_32_out, or_64_out, ~Clr32);  // AND_Gate
  D_Flip_Flop #(.trigger("rising"), .Pre_Clr_Positions("LEGACY"), .NegatePresetClear("false"), .enable("true"), .NewFFLayout("false")) u_IR1 (
    .clk(CLK), .D(and_1_out), .Q(IR1_q));  // open: Qn, preset, en, reset
  D_Flip_Flop #(.trigger("rising"), .Pre_Clr_Positions("LEGACY"), .NegatePresetClear("false"), .enable("true"), .NewFFLayout("false")) u_IR2 (
    .clk(CLK), .D(and_2_out), .Q(IR2_q));  // open: Qn, preset, en, reset
  D_Flip_Flop #(.trigger("rising"), .Pre_Clr_Positions("LEGACY"), .NegatePresetClear("false"), .enable("true"), .NewFFLayout("false")) u_IR3 (
    .clk(CLK), .D(and_3_out), .Q(IR3_q));  // open: Qn, preset, en, reset
  D_Flip_Flop #(.trigger("rising"), .Pre_Clr_Positions("LEGACY"), .NegatePresetClear("false"), .enable("true"), .NewFFLayout("false")) u_IR4 (
    .clk(CLK), .D(and_4_out), .Q(IR4_q));  // open: Qn, preset, en, reset
  D_Flip_Flop #(.trigger("rising"), .Pre_Clr_Positions("LEGACY"), .NegatePresetClear("false"), .enable("true"), .NewFFLayout("false")) u_IR5 (
    .clk(CLK), .D(and_5_out), .Q(IR5_q));  // open: Qn, preset, en, reset
  D_Flip_Flop #(.trigger("rising"), .Pre_Clr_Positions("LEGACY"), .NegatePresetClear("false"), .enable("true"), .NewFFLayout("false")) u_IR6 (
    .clk(CLK), .D(and_6_out), .Q(IR6_q));  // open: Qn, preset, en, reset
  D_Flip_Flop #(.trigger("rising"), .Pre_Clr_Positions("LEGACY"), .NegatePresetClear("false"), .enable("true"), .NewFFLayout("false")) u_IR7 (
    .clk(CLK), .D(and_7_out), .Q(IR7_q));  // open: Qn, preset, en, reset
  D_Flip_Flop #(.trigger("rising"), .Pre_Clr_Positions("LEGACY"), .NegatePresetClear("false"), .enable("true"), .NewFFLayout("false")) u_IR8 (
    .clk(CLK), .D(and_8_out), .Q(IR8_q));  // open: Qn, preset, en, reset
  D_Flip_Flop #(.trigger("rising"), .Pre_Clr_Positions("LEGACY"), .NegatePresetClear("false"), .enable("true"), .NewFFLayout("false")) u_IR9 (
    .clk(CLK), .D(and_9_out), .Q(IR9_q));  // open: Qn, preset, en, reset
  D_Flip_Flop #(.trigger("rising"), .Pre_Clr_Positions("LEGACY"), .NegatePresetClear("false"), .enable("true"), .NewFFLayout("false")) u_IR10 (
    .clk(CLK), .D(and_10_out), .Q(IR10_q));  // open: Qn, preset, en, reset
  D_Flip_Flop #(.trigger("rising"), .Pre_Clr_Positions("LEGACY"), .NegatePresetClear("false"), .enable("true"), .NewFFLayout("false")) u_IR11 (
    .clk(CLK), .D(and_11_out), .Q(IR11_q));  // open: Qn, preset, en, reset
  D_Flip_Flop #(.trigger("rising"), .Pre_Clr_Positions("LEGACY"), .NegatePresetClear("false"), .enable("true"), .NewFFLayout("false")) u_IR12 (
    .clk(CLK), .D(and_12_out), .Q(IR12_q));  // open: Qn, preset, en, reset
  D_Flip_Flop #(.trigger("rising"), .Pre_Clr_Positions("LEGACY"), .NegatePresetClear("false"), .enable("true"), .NewFFLayout("false")) u_IR13 (
    .clk(CLK), .D(and_13_out), .Q(IR13_q));  // open: Qn, preset, en, reset
  D_Flip_Flop #(.trigger("rising"), .Pre_Clr_Positions("LEGACY"), .NegatePresetClear("false"), .enable("true"), .NewFFLayout("false")) u_IR14 (
    .clk(CLK), .D(and_14_out), .Q(IR14_q));  // open: Qn, preset, en, reset
  D_Flip_Flop #(.trigger("rising"), .Pre_Clr_Positions("LEGACY"), .NegatePresetClear("false"), .enable("true"), .NewFFLayout("false")) u_IR15 (
    .clk(CLK), .D(and_15_out), .Q(IR15_q));  // open: Qn, preset, en, reset
  D_Flip_Flop #(.trigger("rising"), .Pre_Clr_Positions("LEGACY"), .NegatePresetClear("false"), .enable("true"), .NewFFLayout("false")) u_IR16 (
    .clk(CLK), .D(and_16_out), .Q(IR16_q));  // open: Qn, preset, en, reset
  D_Flip_Flop #(.trigger("rising"), .Pre_Clr_Positions("LEGACY"), .NegatePresetClear("false"), .enable("true"), .NewFFLayout("false")) u_IR17 (
    .clk(CLK), .D(and_17_out), .Q(IR17_q));  // open: Qn, preset, en, reset
  D_Flip_Flop #(.trigger("rising"), .Pre_Clr_Positions("LEGACY"), .NegatePresetClear("false"), .enable("true"), .NewFFLayout("false")) u_IR18 (
    .clk(CLK), .D(and_18_out), .Q(IR18_q));  // open: Qn, preset, en, reset
  D_Flip_Flop #(.trigger("rising"), .Pre_Clr_Positions("LEGACY"), .NegatePresetClear("false"), .enable("true"), .NewFFLayout("false")) u_IR19 (
    .clk(CLK), .D(and_19_out), .Q(IR19_q));  // open: Qn, preset, en, reset
  D_Flip_Flop #(.trigger("rising"), .Pre_Clr_Positions("LEGACY"), .NegatePresetClear("false"), .enable("true"), .NewFFLayout("false")) u_IR20 (
    .clk(CLK), .D(and_20_out), .Q(IR20_q));  // open: Qn, preset, en, reset
  D_Flip_Flop #(.trigger("rising"), .Pre_Clr_Positions("LEGACY"), .NegatePresetClear("false"), .enable("true"), .NewFFLayout("false")) u_IR21 (
    .clk(CLK), .D(and_21_out), .Q(IR21_q));  // open: Qn, preset, en, reset
  D_Flip_Flop #(.trigger("rising"), .Pre_Clr_Positions("LEGACY"), .NegatePresetClear("false"), .enable("true"), .NewFFLayout("false")) u_IR22 (
    .clk(CLK), .D(and_22_out), .Q(IR22_q));  // open: Qn, preset, en, reset
  D_Flip_Flop #(.trigger("rising"), .Pre_Clr_Positions("LEGACY"), .NegatePresetClear("false"), .enable("true"), .NewFFLayout("false")) u_IR23 (
    .clk(CLK), .D(and_23_out), .Q(IR23_q));  // open: Qn, preset, en, reset
  D_Flip_Flop #(.trigger("rising"), .Pre_Clr_Positions("LEGACY"), .NegatePresetClear("false"), .enable("true"), .NewFFLayout("false")) u_IR24 (
    .clk(CLK), .D(and_24_out), .Q(IR24_q));  // open: Qn, preset, en, reset
  D_Flip_Flop #(.trigger("rising"), .Pre_Clr_Positions("LEGACY"), .NegatePresetClear("false"), .enable("true"), .NewFFLayout("false")) u_IR25 (
    .clk(CLK), .D(and_25_out), .Q(IR25_q));  // open: Qn, preset, en, reset
  D_Flip_Flop #(.trigger("rising"), .Pre_Clr_Positions("LEGACY"), .NegatePresetClear("false"), .enable("true"), .NewFFLayout("false")) u_IR26 (
    .clk(CLK), .D(and_26_out), .Q(IR26_q));  // open: Qn, preset, en, reset
  D_Flip_Flop #(.trigger("rising"), .Pre_Clr_Positions("LEGACY"), .NegatePresetClear("false"), .enable("true"), .NewFFLayout("false")) u_IR27 (
    .clk(CLK), .D(and_27_out), .Q(IR27_q));  // open: Qn, preset, en, reset
  D_Flip_Flop #(.trigger("rising"), .Pre_Clr_Positions("LEGACY"), .NegatePresetClear("false"), .enable("true"), .NewFFLayout("false")) u_IR28 (
    .clk(CLK), .D(and_28_out), .Q(IR28_q));  // open: Qn, preset, en, reset
  D_Flip_Flop #(.trigger("rising"), .Pre_Clr_Positions("LEGACY"), .NegatePresetClear("false"), .enable("true"), .NewFFLayout("false")) u_IR29 (
    .clk(CLK), .D(and_29_out), .Q(IR29_q));  // open: Qn, preset, en, reset
  D_Flip_Flop #(.trigger("rising"), .Pre_Clr_Positions("LEGACY"), .NegatePresetClear("false"), .enable("true"), .NewFFLayout("false")) u_IR30 (
    .clk(CLK), .D(and_30_out), .Q(IR30_q));  // open: Qn, preset, en, reset
  D_Flip_Flop #(.trigger("rising"), .Pre_Clr_Positions("LEGACY"), .NegatePresetClear("false"), .enable("true"), .NewFFLayout("false")) u_IR31 (
    .clk(CLK), .D(and_31_out), .Q(IR31_q));  // open: Qn, preset, en, reset
  D_Flip_Flop #(.trigger("rising"), .Pre_Clr_Positions("LEGACY"), .NegatePresetClear("false"), .enable("true"), .NewFFLayout("false")) u_IR32 (
    .clk(CLK), .D(and_32_out), .Q(IR32_q));  // open: Qn, preset, en, reset
  Priority_Encoder #(.select(5), .disabled("Z")) priority_encoder_1 (
    .in0(IR1_q), .in1(IR2_q), .in2(IR3_q), .in3(IR4_q), .in4(IR5_q), .in5(IR6_q), .in6(IR7_q), .in7(IR8_q),
    .in8(IR9_q), .in9(IR10_q), .in10(IR11_q), .in11(IR12_q), .in12(IR13_q), .in13(IR14_q), .in14(IR15_q),
    .in15(IR16_q), .in16(IR17_q), .in17(IR18_q), .in18(IR19_q), .in19(IR20_q), .in20(IR21_q), .in21(IR22_q),
    .in22(IR23_q), .in23(IR24_q), .in24(IR25_q), .in25(IR26_q), .in26(IR27_q), .in27(IR28_q), .in28(IR29_q),
    .in29(IR30_q), .in30(IR31_q), .in31(IR32_q), .out(\优先中断编号 ), .gs(\有中断 ));  // open: en_out, en_in
  Register #(.width(5), .trigger("rising"), .Select("low")) INT (
    .D(\优先中断编号 ), .en(\中断可接收 ), .Q(INT_q), .clk(CLK));  // open: clr
  Decoder #(.select(5), .tristate("false"), .disabled(0), .enable("true")) decoder_1 (
    .out0(Clr1), .out1(Clr2), .out2(Clr3), .out3(Clr4), .out4(Clr5), .out5(Clr6), .out6(Clr7), .out7(Clr8),
    .out8(Clr9), .out9(Clr10), .out10(Clr11), .out11(Clr12), .out12(Clr13), .out13(Clr14), .out14(Clr15),
    .out15(Clr16), .out16(Clr17), .out17(Clr18), .out18(Clr19), .out19(Clr20), .out20(Clr21), .out21(Clr22),
    .out22(Clr23), .out23(Clr24), .out24(Clr25), .out25(Clr26), .out26(Clr27), .out27(Clr28), .out28(Clr29),
    .out29(Clr30), .out30(Clr31), .out31(Clr32), .sel(INT_q), .en(\同步清零 ));

  // Notes on the sheet:
  //   Reset 
  //   Reset 
  //   Reset 
  //   Reset 
  //   Reset 
  //   Reset 
  //   Reset 
  //   Reset 
  //   Reset 
  //   Reset 
  //   Reset 
  //   Reset 
  //   Reset 
  //   Reset 
  //   Reset 
  //   Reset 
  //   Reset 
  //   Reset 
  //   Reset 
  //   Reset 
  //   Reset 
  //   Reset 
  //   Reset 
  //   Reset 
  //   Reset 
  //   Reset 
  //   Reset 
  //   Reset 
  //   Reset 
  //   Reset 
  //   Reset 
  //   Reset 
endmodule

// 指令存储器
module \指令存储器封装  (
  input  [2:0] in_1,
  input  [9:0] in_2,
  output [31:0] out_3
);

  wire [9:0] demultiplexer_1_out0, demultiplexer_1_out1, demultiplexer_1_out2, demultiplexer_1_out3,
       demultiplexer_1_out4, demultiplexer_1_out5, demultiplexer_1_out6, demultiplexer_1_out7;
  wire [31:0] rom_1_data, rom_2_data, rom_3_data, rom_4_data, rom_5_data, rom_6_data, rom_7_data, rom_8_data;

  Demultiplexer #(.select(3), .width(10), .tristate("false"), .disabled("Z"), .enable("false")) demultiplexer_1 (
    .out0(demultiplexer_1_out0), .out1(demultiplexer_1_out1), .out2(demultiplexer_1_out2),
    .out3(demultiplexer_1_out3), .out4(demultiplexer_1_out4), .out5(demultiplexer_1_out5),
    .out6(demultiplexer_1_out6), .out7(demultiplexer_1_out7), .in(in_2), .sel(in_1));
  ROM #(.addrWidth(10), .dataWidth(32), .Select("high")) rom_1 (.addr(demultiplexer_1_out0), .data(rom_1_data));
  ROM #(.addrWidth(10), .dataWidth(32), .Select("high")) rom_2 (.addr(demultiplexer_1_out1), .data(rom_2_data));
  ROM #(.addrWidth(10), .dataWidth(32), .Select("high")) rom_3 (.addr(demultiplexer_1_out2), .data(rom_3_data));
  ROM #(.addrWidth(10), .dataWidth(32), .Select("high")) rom_4 (.addr(demultiplexer_1_out3), .data(rom_4_data));
  ROM #(.addrWidth(10), .dataWidth(32), .Select("high")) rom_5 (.addr(demultiplexer_1_out4), .data(rom_5_data));
  ROM #(.addrWidth(10), .dataWidth(32), .Select("high")) rom_6 (.addr(demultiplexer_1_out5), .data(rom_6_data));
  ROM #(.addrWidth(10), .dataWidth(32), .Select("high")) rom_7 (.addr(demultiplexer_1_out6), .data(rom_7_data));
  ROM #(.addrWidth(10), .dataWidth(32), .Select("high")) rom_8 (.addr(demultiplexer_1_out7), .data(rom_8_data));
  Multiplexer #(.select(3), .width(32), .disabled("Z"), .enable("false")) multiplexer_1 (
    .in0(rom_1_data), .in1(rom_2_data), .in2(rom_3_data), .in3(rom_4_data), .in4(rom_5_data),
    .in5(rom_6_data), .in6(rom_7_data), .in7(rom_8_data), .out(out_3), .sel(in_1));

  // Notes on the sheet:
  //   contents of rom_1 (hex, n*v repeats v):
  //   2011000e 200b0040 ad71ffff 216bfffc 11600001 8000c02 2005000c 20064182 200b003f 20120000 63b82
  //   30e70001 2479020 63ac2 30e70001 2479020 63a82 30e70001 2479020 ad720040 216bfffc 20120000 63bc2
  //   30e70001 2479020 63b42 30e70001 2479020 63ac2 30e70001 2479020 63a82 30e70001 2479020 63a42 30e70001
  //   2479020 ad720040 216bfffc 20120000 63b82 30e70001 2479020 63b02 30e70001 2479020 63a82 30e70001
  //   2479020 63a42 30e70001 2479020 63a02 30e70001 2479020 ad720040 216bfffc 20120000 63b42 30e70001
  //   2479020 63a42 30e70001 2479020 63a02 30e70001 2479020 ad720040 216bfffc 20120000 63bc2 30e70001
  //   2479020 63b82 30e70001 2479020 63a82 30e70001 2479020 639c2 30e70001 2479020 63982 30e70001 2479020
  //   ad720040 216bfffc 20120000 63bc2 30e70001 2479020 63b82 30e70001 2479020 63b42 30e70001 2479020
  //   63ac2 30e70001 2479020 63a42 30e70001 2479020 639c2 30e70001 2479020 63982 30e70001 2479020 63942
  //   30e70001 2479020 ad720040 216bfffc 20120000 63b82 30e70001 2479020 63b42 30e70001 2479020 63b02
  //   30e70001 2479020 63a82 30e70001 2479020 63a02 30e70001 2479020 63982 30e70001 2479020 63942 30e70001
  //   2479020 63902 30e70001 2479020 ad720040 216bfffc 20120000 63b42 30e70001 2479020 63b02 30e70001
  //   2479020 63a42 30e70001 2479020 63942 30e70001 2479020 63902 30e70001 2479020 ad720040 216bfffc
  //   20120000 63ac2 30e70001 2479020 63a82 30e70001 2479020 63982 30e70001 2479020 638c2 30e70001 2479020
  //   63882 30e70001 2479020 ad720040 216bfffc 20120000 63ac2 30e70001 2479020 63a82 30e70001 2479020
  //   63a42 30e70001 2479020 639c2 30e70001 2479020 63942 30e70001 2479020 638c2 30e70001 2479020 63882
  //   30e70001 2479020 63842 30e70001 2479020 ad720040 216bfffc 20120000 63a82 30e70001 2479020 63a42
  //   30e70001 2479020 63a02 30e70001 2479020 63982 30e70001 2479020 63902 30e70001 2479020 63882 30e70001
  //   2479020 63842 30e70001 2479020 63802 30e70001 2479020 ad720040 216bfffc 20120000 63a42 30e70001
  //   2479020 63a02 30e70001 2479020 63942 30e70001 2479020 63842 30e70001 2479020 63802 30e70001 2479020
  //   ad720040 216bfffc 20120000 639c2 30e70001 2479020 63982 30e70001 2479020 63882 30e70001 2479020
  //   ad72003f 216bfffc 20120000 639c2 30e70001 2479020 63982 30e70001 2479020 63942 30e70001 2479020
  //   638c2 30e70001 2479020 63842 30e70001 2479020 ad720040 216bfffc 20120000 63982 30e70001 2479020
  //   63942 30e70001 2479020 63902 30e70001 2479020 63882 30e70001 2479020 63802 30e70001 2479020 ad720040
  //   216bfffc 20120000 63942 30e70001 2479020 63902 30e70001 2479020 63842 30e70001 2479020 ad720040
  //   20040000 200b0040 8d71ffff 118f00 912025 216bfffc 8d71ffff 118e00 912025 216bfffc 8d71ffff 118d00
  //   912025 216bfffc 8d71ffff 118c00 912025 216bfffc 8d71ffff 118b00 912025 216bfffc 8d71ffff 118a00
  //   912025 216bfffc 8d71ffff 118900 912025 216bfffc 8d71ffff 912025 20020023 c 20040000 216bfffc
  //   8d71ffff 118f00 912025 216bfffc 8d71ffff 118e00 912025 216bfffc 8d71ffff 118d00 912025 216bfffc
  //   8d71ffff 118c00 912025 216bfffc 8d71ffff 118b00 912025 216bfffc 8d71ffff 118a00 912025 216bfffc
  //   8d71ffff 118900 912025 216bfffc 8d71ffff 912025 20020022 c 14a00002 c000d86 8000d84 2007fffe
  //   14a70002 c000d94 8000d84 2007ffff 10a70019 2007fffd 10a70017 8000d34 20a5ffff 8000d34 200b0040
  //   200a000f 1463807 30e70001 14e00003 20110000 ad71ffff 8000d90 2011000f ad71ffff 216bfffc 214affff
  //   1560fff5 3e00008 2011000f 200b0040 ad71ffff 216bfffc 1560fffd 3e00008 2002000a c 10*0 2005fffe
  //   42000018 42000018 66802 31ad0001 200e0001 11aefff9 200d0003 8db30000 200e000d 1d3782a 11e0fff6
  //   200e0003 8dd30040 add30000 20a5ffff 42000018 6684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
  //   contents of rom_2 (hex, n*v repeats v):
  //   2011000e 200b0040 ad71ffff 216bfffc 11600001 8000c02 2005000c 20064182 200b003f 20120000 63b82
  //   30e70001 2479020 63ac2 30e70001 2479020 63a82 30e70001 2479020 ad720040 216bfffc 20120000 63bc2
  //   30e70001 2479020 63b42 30e70001 2479020 63ac2 30e70001 2479020 63a82 30e70001 2479020 63a42 30e70001
  //   2479020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
  //   contents of rom_3 (hex, n*v repeats v):
  //   2011000e 200b0040 ad71ffff 216bfffc 11600001 8100002 2005000d 20060418 200b003f 20120000 63b82
  //   30e70001 2479020 63ac2 30e70001 2479020 63a82 30e70001 2479020 ad720040 216bfffc 20120000 63bc2
  //   30e70001 2479020 63b42 30e70001 2479020 63ac2 30e70001 2479020 63a82 30e70001 2479020 63a42 30e70001
  //   2479020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
  //   contents of rom_4 (hex, n*v repeats v):
  //   2011000e 200b0040 ad71ffff 216bfffc 11600001 8100002 2005000d 20060504 200b003f 20120000 63b82
  //   30e70001 2479020 63ac2 30e70001 2479020 63a82 30e70001 2479020 ad720040 216bfffc 20120000 63bc2
  //   30e70001 2479020 63b42 30e70001 2479020 63ac2 30e70001 2479020 63a82 30e70001 2479020 63a42 30e70001
  //   2479020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
  //   contents of rom_5 (hex, n*v repeats v):
  //   2011000e 200b0040 ad71ffff 216bfffc 11600001 8000c02 2005000c 20064182 200b003f 20120000 63b82
  //   30e70001 2479020 63ac2 30e70001 2479020 63a82 30e70001 2479020 ad720040 216bfffc 20120000 63bc2
  //   30e70001 2479020 63b42 30e70001 2479020 63ac2 30e70001 2479020 63a82 30e70001 2479020 63a42 30e70001
  //   2479020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
  //   contents of rom_6 (hex, n*v repeats v):
  //   2011000e 200b0040 ad71ffff 216bfffc 11600001 8100002 2005000c 20060660 200b003f 20120000 63b82
  //   30e70001 2479020 63ac2 30e70001 2479020 63a82 30e70001 2479020 ad720040 216bfffc 20120000 63bc2
  //   30e70001 2479020 63b42 30e70001 2479020 63ac2 30e70001 2479020 63a82 30e70001 2479020 63a42 30e70001
  //   2479020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
  //   contents of rom_7 (hex, n*v repeats v):
  //   2011000e 200b0040 ad71ffff 216bfffc 11600001 8000c02 2005000c 20064182 200b003f 20120000 63b82
  //   30e70001 2479020 63ac2 30e70001 2479020 63a82 30e70001 2479020 ad720040 216bfffc 20120000 63bc2
  //   30e70001 2479020 63b42 30e70001 2479020 63ac2 30e70001 2479020 63a82 30e70001 2479020 63a42 30e70001
  //   2479020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
  //   contents of rom_8 (hex, n*v repeats v):
  //   2011000e 200b0040 ad71ffff 216bfffc 11600001 8100002 2005000c 20060906 200b003f 20120000 63b82
  //   30e70001 2479020 63ac2 30e70001 2479020 63a82 30e70001 2479020 ad720040 216bfffc 20120000 63bc2
  //   30e70001 2479020 63b42 30e70001 2479020 63ac2 30e70001 2479020 63a82 30e70001 2479020 63a42 30e70001
  //   2479020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
endmodule
